// Logisim project YM6045C.circ as structural Verilog: 3 circuits, main circuit main
module main (
  input  MCLK,
  input  VCLK,
  input  ZCLK,
  input  nM1,
  input  nM3,
  input  RW,
  input  nBG,
  input  nBGACK,
  input  nAS,
  input  nDTACK,
  input  ZD0,
  input  VA8,
  input  VA9,
  input  VA10,
  input  VA11,
  input  VA12,
  input  VA13,
  input  VA14,
  input  VA15,
  input  VA16,
  input  VA17,
  input  VA18,
  input  VA19,
  input  VA20,
  input  VA21,
  input  VA22,
  input  VA23,
  input  ZA0,
  input  ZA7,
  input  ZA8,
  input  ZA9,
  input  ZA10,
  input  ZA11,
  input  ZA12,
  input  ZA13,
  input  ZA14,
  input  ZA15,
  input  nSRES,
  input  TPAL,
  input  D8,
  input  nCAS0,
  input  nCART,
  input  FC0,
  input  FC1,
  input  nWRES,
  input  nLDS,
  input  nUDS,
  input  nOE0,
  input  nHSYNC,
  input  nZWR,
  input  nZRD,
  input  nZWR_2,
  input  nZBAK,
  input  nIREQ,
  input  nMREQ,
  input  nWAIT,
  output PIN100,
  output nVDPM,
  output ZA15_2,
  output PIN99,
  output ZA14_2,
  output ZA13_2,
  output nZRAM,
  output ZA12_2,
  output ZA11_2,
  output ZA10_2,
  output nSOUND,
  output ZA9_2,
  output ZA8_2,
  output ZA8_3,
  output ZA0_2,
  output nUDS_2,
  output nLDS_2,
  output nAS_o,
  output nWAIT_2,
  output nIA14,
  output nVTOZ,
  output nZTOV,
  output RW_2,
  output nBR,
  output nBGACK_2,
  output VA23_2,
  output VA22_2,
  output VA21_2,
  output VA20_2,
  output VA19_2,
  output VA18_2,
  output VA17_2,
  output VA16_2,
  output VA15_2,
  output VA14_2,
  output VA13_2,
  output VA12_2,
  output VA11_2,
  output VA10_2,
  output VA9_2,
  output VA8_2,
  output EDCLK,
  output nZ_RES,
  output nRESET,
  output nHALT,
  output nZBR,
  output nZNMI,
  output nCAS2,
  output nRAS2,
  output nCE0,
  output nZWR_3,
  output nZRD_2,
  output nINTACK,
  output nVPA,
  output nROM,
  output nIO,
  output nFDC,
  output nDTACK_2,
  output nFDWR,
  output nTIME,
  output nASEL,
  output nZREF,
  output nMREQ_o,
  output nNOE,
  output nEOE
);

  wire _2_out, _6_out, _13_out, _15_out, _28_out, _29_out, _30_out, _32_out, _35_out, _38_out, _41_out,
       _45_out, _47_out, _49_out, _51_out, _52_out, _56_out, _57_out, _61_out, _68_out, _70_out, _71_out,
       _73_out, _76_out, _77_out, _79_out, _80_out, _82_out, _83_out, _87_out, _88_out, _91_out, _94_out,
       _95_out, _100_out, _102_out, _105_out, _106_out, _107_out, _110_out, _111_out, _115_out, _120_out,
       _122_out, _123_out, _124_out, _127_out, _128_out, _129_out, _130_out, _132_out, _133_out, _134_out,
       _135_out, _137_out, _138_out, _141_out, _143_out, _151_out, _156_out, _157_out, _158_out, _163_out,
       _164_out, _165_out, _167_out, _168_out, _169_out, _170_2_out, _170_out, _171_out, _172_out, _173_out,
       _176_2_out, _176_out, _177_out, _178_out, _179_out, _182_out, _187_out, _189_out, _190_out, _192_out,
       _194_out, _195_out, _196_out, _197_out, _201_out, _202_out, _203_out, _205_out, _206_out, _207_out,
       _211_out, _212_out, _213_out, _214_out, _216_out, _218_out, _219_out, _224_out, _225_out, _229_out,
       _234_out, _235_out, _239_out, _240_out, _241_out, _244_out, _248_out, _251_2_out, _251_out, _257_out,
       _262_out, _263_out, _270_out, _273_out, _274_out, _275_out, _276_out, _281_out, _282_out, _283_out,
       _284_out, _285_out, _286_out, _287_out, _288_out, _292_out, _295_out, _296_out, _302_out, _304_out,
       _306_out, _310_out, _316_out, _317_out, _319_out, _323_out, _325_out, _326_out, _327_out, _336_out,
       _339_out, _342_out, _343_out, buffer_1_out, buffer_2_out, buffer_3_out, buffer_4_out, buffer_5_out,
       buffer_7_out, buffer_8_out, buffer_10_out, buffer_11_out, buffer_12_out, buffer_13_out, buffer_14_out,
       CAS0, d_ff_1_q, d_ff_2_q, d_ff_3_qn, d_ff_4_q, d_ff_5_q, d_ff_6_q, d_ff_7_q, d_ff_8_q, d_ff_9_q,
       d_ff_10_q, d_ff_11_q, d_ff_12_q, d_ff_14_q, d_ff_14_qn, d_ff_15_q, d_ff_16_q, d_ff_16_qn, d_ff_17_q,
       d_ff_18_q, d_ff_19_q, d_ff_20_q, d_ff_21_q, d_ff_22_q, d_ff_22_qn, d_ff_23_q, d_ff_23_qn, d_ff_24_q,
       d_ff_25_q, d_ff_26_q, d_ff_26_qn, d_ff_27_q, d_ff_28_q, d_ff_29_q, d_ff_30_q, d_ff_31_q, d_ff_31_qn,
       d_ff_32_q, d_ff_32_qn, d_ff_33_q, d_ff_34_q, d_ff_35_q, d_ff_35_qn, d_ff_36_qn, d_ff_37_qn, d_ff_38_q,
       d_ff_38_qn, d_ff_39_q, d_ff_40_q, d_ff_41_q, d_ff_41_qn, d_ff_42_q, d_ff_45_qn, d_ff_46_q, d_ff_46_qn,
       d_ff_48_q, d_ff_49_q, d_ff_50_q, d_ff_50_qn, d_ff_51_q, d_ff_52_qn, d_ff_53_qn, d_ff_54_qn, d_ff_55_q,
       DCA0, DCA1, DCA2, DCA3, DCA4, DCA5, DCA6, DCA7, decoder_1_out0, decoder_1_out1, decoder_1_out2,
       decoder_1_out3, decoder_2_out0, decoder_2_out1, decoder_2_out2, decoder_3_out0, decoder_3_out1,
       decoder_3_out2, decoder_3_out3, FFRES, j_k_ff_1_q, j_k_ff_1_qn, M1DELAY, M1DELAY2, multiplexer_5_out,
       n1_bit_cnt_1_nq, n1_bit_cnt_1_q, n1_bit_cnt_2_nq, n1_bit_cnt_2_q, n1_bit_cnt_3_nq, n1_bit_cnt_3_q,
       n4_bit_cnt_1_nq0, n4_bit_cnt_1_nq1, n4_bit_cnt_1_nq2, n4_bit_cnt_1_nq3, n4_bit_cnt_2_nq0,
       n4_bit_cnt_2_nq1, n4_bit_cnt_2_nq2, n4_bit_cnt_2_nq3, n4_bit_cnt_3_nq0, n4_bit_cnt_3_nq1,
       n4_bit_cnt_3_nq2, n4_bit_cnt_3_nq3, nFFRES, not_6_out, not_7_out, not_8_out, not_9_out, not_10_out,
       not_11_out, not_12_out, not_13_out, not_14_out, not_15_out, not_16_out, not_17_out, not_18_out,
       not_19_out, not_20_out, not_21_out, not_22_out, not_23_out, not_24_out, not_25_out, not_26_out,
       not_27_out, not_28_out, not_29_out, not_30_out, not_31_out, not_32_out, not_33_out, not_34_out,
       not_35_out, not_36_out, not_37_out, not_38_out, not_39_out, not_40_out, not_41_out, not_42_out,
       not_43_out, not_44_out, not_45_out, not_46_out, not_47_out, not_48_out, not_49_out, not_50_out,
       not_51_out, not_52_out, not_53_out, not_54_out, not_55_out, not_56_out, not_57_out, not_58_out,
       not_59_out, not_60_out, not_61_out, not_62_out, not_63_out, not_64_out, not_65_out, not_66_out,
       not_67_out, not_68_out, not_69_out, not_70_out, not_71_out, not_72_out, not_73_out, not_74_out,
       not_75_out, not_76_out, not_77_out, not_78_out, not_79_out, not_80_out, not_81_out, not_82_out,
       not_83_out, not_84_out, not_85_out, not_86_out, not_87_out, not_88_out, not_89_out, not_90_out,
       not_91_out, not_93_out, not_94_out, not_95_out, not_96_out, not_97_out, not_98_out, not_99_out,
       not_100_out, not_101_out, nTPAL, nVCLK, nZA15, RWd, SRES, t_ff_1_qn, t_ff_2_qn, t_ff_3_qn, t_ff_4_qn,
       t_ff_5_qn, t_ff_6_qn, t_ff_7_qn, t_ff_8_qn, t_ff_9_qn, VA7;
  wire [0:0] _50_out;
  wire [2:2] _299_out;
  wire [3:0] _221_out, _312_out, multiplexer_1_out, multiplexer_2_out, multiplexer_3_out, multiplexer_4_out;

  not not_1 (nVCLK, VCLK);
  not not_2 (nZA15, ZA15);
  not not_3 (SRES, nSRES);
  not not_4 (nTPAL, TPAL);
  not not_5 (CAS0, nCAS0);
  D_Flip_Flop d_ff_1 (.clk(ZCLK), .D(nM1), .Q(d_ff_1_q));  // open: Qn, preset, en, reset
  Decoder #(.select(2), .disabled(0), .enable("false")) decoder_1 (
    .out0(decoder_1_out0), .out1(decoder_1_out1), .out2(decoder_1_out2), .out3(decoder_1_out3),
    .sel({FC1, FC0}));
  not not_6 (not_6_out, ZCLK);
  D_Flip_Flop d_ff_2 (.clk(ZCLK), .D(d_ff_1_q), .Q(d_ff_2_q));  // open: Qn, preset, en, reset
  not not_7 (not_7_out, decoder_1_out0);
  not not_8 (not_8_out, decoder_1_out1);
  not not_9 (not_9_out, decoder_1_out2);
  buf buffer_1 (buffer_1_out, nM3);
  not not_10 (not_10_out, ZA8);
  not not_11 (not_11_out, ZA9);
  not not_12 (not_12_out, ZA10);
  not not_13 (not_13_out, ZA11);
  not not_14 (not_14_out, ZA12);
  nor _240 (_240_out, _295_out, _319_out);
  nor _319 (_319_out, not_7_out, buffer_1_out);
  nor _327 (_327_out, not_8_out, buffer_1_out);
  nor _325 (_325_out, not_9_out, buffer_1_out);
  nand _332 (nINTACK, decoder_1_out3, nZTOV);
  D_Flip_Flop d_ff_3 (.clk(not_6_out), .D(d_ff_2_q), .Q(M1DELAY2), .Qn(d_ff_3_qn));  // open: preset, en, reset
  nand _38 (_38_out, not_10_out, not_11_out, 1'b1, not_12_out, not_13_out, not_14_out);
  nor _239 (_239_out, nFFRES, _295_out);
  not not_15 (not_15_out, _257_out);
  or _318 (M1DELAY, d_ff_3_qn, nMREQ);
  buf buffer_2 (buffer_2_out, _239_out);
  nor _302 (_302_out, d_ff_14_q, _336_out, not_15_out, d_ff_16_q);
  not not_16 (not_16_out, nM3);
  nor _310 (_310_out, d_ff_14_qn, _325_out);
  or _52 (_52_out, M1DELAY, nZWR, _38_out, _51_out);
  not not_17 (not_17_out, ZA15);
  not not_18 (not_18_out, VA22);
  and _342 (_342_out, 1'b1, 1'b1, buffer_2_out);
  or _292 (_292_out, nAS, not_16_out);
  T_Flip_Flop t_ff_1 (.clk(_310_out), .T(not_23_out), .Qn(t_ff_1_qn));  // open: Q, preset, reset, en
  D_Flip_Flop d_ff_4 (.clk(_52_out), .D(ZD0), .Q(d_ff_4_q), .reset(nFFRES));  // open: Qn, preset, en
  D_Flip_Flop d_ff_5 (.clk(_52_out), .D(d_ff_4_q), .Q(d_ff_5_q), .reset(nFFRES));  // open: Qn, preset, en
  D_Flip_Flop d_ff_6 (.clk(_52_out), .D(d_ff_5_q), .Q(d_ff_6_q), .reset(nFFRES));  // open: Qn, preset, en
  D_Flip_Flop d_ff_7 (.clk(_52_out), .D(d_ff_6_q), .Q(d_ff_7_q), .reset(nFFRES));  // open: Qn, preset, en
  D_Flip_Flop d_ff_8 (.clk(_52_out), .D(d_ff_7_q), .Q(d_ff_8_q), .reset(nFFRES));  // open: Qn, preset, en
  D_Flip_Flop d_ff_9 (.clk(_52_out), .D(d_ff_8_q), .Q(d_ff_9_q), .reset(nFFRES));  // open: Qn, preset, en
  D_Flip_Flop d_ff_10 (.clk(_52_out), .D(d_ff_9_q), .Q(d_ff_10_q), .reset(nFFRES));  // open: Qn, preset, en
  D_Flip_Flop d_ff_11 (.clk(_52_out), .D(d_ff_10_q), .Q(d_ff_11_q), .reset(nFFRES));  // open: Qn, preset, en
  D_Flip_Flop d_ff_12 (.clk(_52_out), .D(d_ff_11_q), .Q(d_ff_12_q), .reset(nFFRES));  // open: Qn, preset, en
  D_Flip_Flop d_ff_13 (.clk(VCLK), .D(nSRES), .Q(FFRES), .Qn(nFFRES));  // open: preset, en, reset
  nand _51 (_51_out, nM3, not_17_out, ZA14, ZA13);
  nand _41 (_41_out, ZA12, ZA11, ZA10, 1'b1, ZA9, ZA8);
  or _216 (_216_out, VA10, VA11, VA14, VA15);
  nand _306 (_306_out, VA21, not_18_out, VA23, nM3);
  or _225 (_225_out, VA17, VA18, VA19, VA20);
  _4_bit_cnt u_4_bit_cnt_1 (
    .C(VCLK), .nLD(buffer_2_out), .nRES(1'b1), .CIN(_342_out), .VAL0(1'b0), .VAL1(1'b0), .VAL2(1'b0),
    .VAL3(1'b0), .nQ0(n4_bit_cnt_1_nq0), .nQ1(n4_bit_cnt_1_nq1), .nQ2(n4_bit_cnt_1_nq2),
    .nQ3(n4_bit_cnt_1_nq3));  // open: CO
  nor _304 (_304_out, _295_out, _302_out, _319_out);
  or _213 (_213_out, VA23, _292_out, _214_out);
  T_Flip_Flop t_ff_2 (.clk(t_ff_1_qn), .T(not_23_out), .Qn(t_ff_2_qn));  // open: Q, preset, reset, en
  or _190 (_190_out, nBGACK, _189_out);
  not not_19 (not_19_out, nAS);
  not not_20 (not_20_out, nM3);
  or _49 (_49_out, _51_out, _41_out);
  Decoder #(.select(2), .disabled(0), .enable("false")) decoder_2 (
    .out0(decoder_2_out0), .out1(decoder_2_out1), .out2(decoder_2_out2), .sel({VA9, VA8}));  // open: out3
  nor _229 (_229_out, _216_out, _306_out, _225_out);
  or _230 (DCA6, _306_out, _225_out, VA16);
  D_Flip_Flop d_ff_14 (.clk(VCLK), .D(_304_out), .Q(d_ff_14_q), .Qn(d_ff_14_qn), .preset(FFRES));  // open: en, reset
  D_Flip_Flop d_ff_15 (.clk(VCLK), .D(_213_out), .Q(d_ff_15_q));  // open: Qn, preset, en, reset
  not not_21 (not_21_out, _292_out);
  D_Flip_Flop d_ff_16 (
    .clk(not_21_out), .D(d_ff_14_qn), .Q(d_ff_16_q), .Qn(d_ff_16_qn), .reset(not_22_out));  // open: preset, en
  not not_22 (not_22_out, d_ff_14_qn);
  T_Flip_Flop t_ff_3 (.clk(t_ff_2_qn), .T(not_23_out), .Qn(t_ff_3_qn));  // open: Q, preset, reset, en
  not not_23 (not_23_out, nFFRES);
  and _189 (_189_out, _190_out, nZTOV);
  or _151 (_151_out, nZA15, not_20_out, M1DELAY);
  or _156 (_156_out, M1DELAY, _49_out);
  not not_24 (not_24_out, _49_out);
  and _234 (_234_out, d_ff_4_q, _49_out);
  and _235 (_235_out, d_ff_5_q, _49_out);
  and _236 (_312_out[2], d_ff_6_q, _49_out);
  and _237 (_312_out[3], d_ff_7_q, _49_out);
  and _221 (_221_out[0], d_ff_8_q, _49_out);
  and _222 (_221_out[1], d_ff_9_q, _49_out);
  and _223 (_221_out[2], d_ff_10_q, _49_out);
  and _220 (_221_out[3], d_ff_11_q, _49_out);
  and _50 (_50_out[0], d_ff_12_q, _49_out);
  nor _339 (_339_out, n4_bit_cnt_1_nq3, n4_bit_cnt_1_nq2, n4_bit_cnt_1_nq1, n4_bit_cnt_1_nq0);
  T_Flip_Flop t_ff_4 (.clk(t_ff_3_qn), .T(not_23_out), .Qn(t_ff_4_qn));  // open: Q, preset, reset, en
  not not_25 (not_25_out, nM3);
  not not_26 (not_26_out, _189_out);
  not not_27 (not_27_out, _257_out);
  not not_28 (not_28_out, not_27_out);
  not not_29 (not_29_out, not_28_out);
  not not_30 (not_30_out, _257_out);
  not not_31 (not_31_out, nM1);
  nor _77 (_77_out, d_ff_22_q, nAS);
  nor _241 (_241_out, _240_out, nFFRES);
  nand _87 (_87_out, nLDS, nUDS);
  not not_32 (not_32_out, VA21);
  and _157 (_157_out, _151_out, _156_out);
  or _312 (_312_out[0], _234_out, not_24_out);
  or _313 (_312_out[1], _235_out, not_24_out);
  or _65 (nVTOZ, DCA6, nZBAK);
  or _205 (_205_out, d_ff_15_q, _213_out);
  or _207 (_207_out, d_ff_16_qn, VA23);
  nand _196 (_196_out, d_ff_26_qn, d_ff_31_q);
  or _257 (_257_out, not_25_out, nBGACK, not_26_out);
  not not_33 (not_33_out, not_35_out);
  not not_34 (not_34_out, not_33_out);
  not not_35 (not_35_out, not_29_out);
  not not_36 (not_36_out, not_30_out);
  or _70 (_70_out, nM3, not_31_out, nIREQ);
  nor _158 (_158_out, _77_out, _241_out);
  or _82 (_82_out, nZBR, nZBAK);
  D_Flip_Flop d_ff_17 (.clk(VCLK), .D(_87_out), .Q(d_ff_17_q));  // open: Qn, preset, en, reset
  D_Flip_Flop d_ff_18 (.clk(VCLK), .D(d_ff_46_q), .Q(d_ff_18_q), .reset(not_55_out));  // open: Qn, preset, en
  nand _209 (PIN100, not_32_out, VA22, VA23, not_19_out);
  nor _224 (_224_out, VA22, VA20, VA19, VA18, VA17, VA15, VA13, VA12);
  and _13 (_13_out, not_19_out, 1'b1, VA14, VA16, VA21, VA23);
  not not_37 (not_37_out, nAS);
  not not_38 (not_38_out, nBGACK);
  and _187 (_187_out, _157_out, d_ff_24_q);
  Decoder #(.select(2), .disabled(0), .enable("false")) decoder_3 (
    .out0(decoder_3_out0), .out1(decoder_3_out1), .out2(decoder_3_out2), .out3(decoder_3_out3),
    .sel({VA13, VA12}));
  and _336 (_336_out, _339_out, 1'b1);
  and _295 (_295_out, _336_out, _195_out);
  and _197 (_197_out, _207_out, _196_out);
  nor _326 (_326_out, _327_out, t_ff_4_qn);
  or _244 (_244_out, nCAS0, _257_out);
  D_Flip_Flop d_ff_19 (.clk(CAS0), .D(VA23), .Q(d_ff_19_q), .preset(not_36_out));  // open: Qn, en, reset
  D_Flip_Flop d_ff_20 (.clk(ZCLK), .D(_70_out), .Q(d_ff_20_q));  // open: Qn, preset, en, reset
  D_Flip_Flop d_ff_21 (.clk(nVCLK), .D(_178_out), .Q(d_ff_21_q));  // open: Qn, preset, en, reset
  D_Flip_Flop d_ff_22 (
    .clk(nVCLK), .D(_158_out), .Q(d_ff_22_q), .Qn(d_ff_22_qn), .preset(not_39_out));  // open: en, reset
  not not_39 (not_39_out, _83_out);
  nand _83 (_83_out, nZ_RES, _82_out);
  buf buffer_3 (buffer_3_out, buffer_4_out);
  buf buffer_4 (buffer_4_out, nSRES);
  D_Flip_Flop d_ff_23 (.clk(not_63_out), .D(d_ff_18_q), .Q(d_ff_23_q), .Qn(d_ff_23_qn));  // open: preset, en, reset
  nand _61 (_61_out, _224_out, _13_out);
  D_Flip_Flop d_ff_24 (.clk(ZCLK), .D(_157_out), .Q(d_ff_24_q));  // open: Qn, preset, en, reset
  or _299 (_299_out[2], nMREQ, VA21);
  not not_40 (not_40_out, nUDS);
  nor _73 (_73_out, nUDS, RW);
  and _285 (_285_out, buffer_2_out, _336_out, _336_out);
  nand _288 (_288_out, _336_out, d_ff_14_qn, d_ff_16_qn);
  nand _286 (_286_out, VA23, d_ff_16_q);
  or _203 (_203_out, _213_out, d_ff_25_q);
  D_Flip_Flop d_ff_25 (.clk(nVCLK), .D(_205_out), .Q(d_ff_25_q));  // open: Qn, preset, en, reset
  D_Flip_Flop d_ff_26 (
    .clk(VCLK), .D(_197_out), .Q(d_ff_26_q), .Qn(d_ff_26_qn), .preset(not_78_out));  // open: en, reset
  T_Flip_Flop t_ff_5 (.clk(_326_out), .T(not_50_out), .Qn(t_ff_5_qn));  // open: Q, preset, reset, en
  not not_41 (not_41_out, _244_out);
  nand _270 (_270_out, _257_out, not_34_out);
  D_Flip_Flop d_ff_27 (.clk(nVCLK), .D(_110_out), .Q(d_ff_27_q));  // open: Qn, preset, en, reset
  D_Flip_Flop d_ff_28 (.clk(VCLK), .D(_102_out), .Q(d_ff_28_q));  // open: Qn, preset, en, reset
  D_Flip_Flop d_ff_29 (.clk(VCLK), .D(_177_out), .Q(d_ff_29_q));  // open: Qn, preset, en, reset
  or _100 (_100_out, nBG, not_37_out, not_38_out, _187_out);
  nand _145 (DCA7, _229_out, VA16, decoder_3_out1);
  not not_42 (not_42_out, DCA7);
  nand _154 (DCA3, decoder_2_out0, not_42_out, _73_out);
  nand _160 (DCA4, decoder_2_out1, not_42_out, not_40_out);
  nand _153 (DCA5, decoder_2_out2, not_42_out, _73_out);
  _4_bit_cnt u_4_bit_cnt_2 (
    .C(VCLK), .nLD(buffer_2_out), .nRES(1'b1), .CIN(_285_out), .VAL0(1'b0), .VAL1(1'b0), .VAL2(1'b0),
    .VAL3(nM3), .nQ0(n4_bit_cnt_2_nq0), .nQ1(n4_bit_cnt_2_nq1), .nQ2(n4_bit_cnt_2_nq2), .nQ3(n4_bit_cnt_2_nq3));  // open: CO
  and _287 (_287_out, _288_out, _286_out);
  or _201 (_201_out, _203_out, d_ff_26_q);
  or _206 (_206_out, _205_out, d_ff_26_qn);
  T_Flip_Flop t_ff_6 (.clk(t_ff_5_qn), .T(not_50_out), .Qn(t_ff_6_qn));  // open: Q, preset, reset, en
  not not_43 (not_43_out, not_44_out);
  not not_44 (not_44_out, not_45_out);
  not not_45 (not_45_out, not_41_out);
  and _323 (_323_out, _270_out, VA23);
  not not_46 (not_46_out, _323_out);
  and _296 (_296_out, CAS0, d_ff_19_q, VA23);
  nand _178 (_178_out, d_ff_22_qn, nAS);
  or _251 (_251_out, d_ff_23_qn, d_ff_18_q);
  not not_47 (not_47_out, M1DELAY);
  or _95 (_95_out, d_ff_29_q, _187_out);
  and _182 (_182_out, _100_out, _177_out);
  or _177 (_177_out, _187_out, SRES, d_ff_34_q);
  or _176 (_176_out, d_ff_34_q, SRES);
  Multiplexer #(.width(4), .disabled(0), .enable("false")) multiplexer_1 (
    .in0(_312_out), .in1({nZ_RES, 3'b000}), .out(multiplexer_1_out), .sel(nM3));
  Multiplexer #(.width(4), .disabled(0), .enable("false")) multiplexer_2 (
    .in0(_221_out), .in1({ZA15, _299_out[2], nMREQ, nIREQ}), .out(multiplexer_2_out), .sel(nM3));
  Multiplexer #(.width(4), .disabled(0), .enable("false")) multiplexer_3 (
    .in0({ZA12, ZA13, ZA14, _50_out[0]}), .in1({ZA11, ZA12, ZA13, ZA14}), .out(multiplexer_3_out), .sel(nM3));
  Multiplexer #(.width(4), .disabled(0), .enable("false")) multiplexer_4 (
    .in0({ZA8, ZA9, ZA10, ZA11}), .in1({ZA7, ZA8, ZA9, ZA10}), .out(multiplexer_4_out), .sel(nM3));
  not not_48 (not_48_out, not_49_out);
  not not_49 (not_49_out, _49_out);
  nand _148 (DCA0, decoder_2_out0, decoder_3_out0, VA16, _229_out);
  nand _146 (DCA1, decoder_2_out0, decoder_3_out2, VA16, _229_out);
  nand _147 (DCA2, decoder_2_out0, decoder_3_out3, VA16, _229_out);
  D_Flip_Flop d_ff_30 (.clk(VCLK), .D(_287_out), .Q(d_ff_30_q), .preset(not_78_out));  // open: Qn, en, reset
  D_Flip_Flop d_ff_31 (.clk(nVCLK), .D(_201_out), .Q(d_ff_31_q), .Qn(d_ff_31_qn));  // open: preset, en, reset
  T_Flip_Flop t_ff_7 (.clk(t_ff_6_qn), .T(not_50_out), .Qn(t_ff_7_qn));  // open: Q, preset, reset, en
  not not_50 (not_50_out, nFFRES);
  buf buffer_5 (buffer_5_out, FFRES);
  not not_51 (not_51_out, not_43_out);
  not not_52 (not_52_out, not_51_out);
  D_Flip_Flop d_ff_32 (
    .clk(CAS0), .D(d_ff_32_qn), .Q(d_ff_32_q), .Qn(d_ff_32_qn), .preset(not_46_out));  // open: en, reset
  and _71 (_71_out, d_ff_20_q, _70_out);
  nand _262 (_262_out, d_ff_21_q, _178_out);
  nand _263 (_263_out, d_ff_37_qn, d_ff_21_q, _178_out);
  nand _80 (_80_out, d_ff_38_qn, d_ff_17_q, _87_out);
  not not_53 (not_53_out, nBGACK);
  not not_54 (not_54_out, _251_2_out);
  nand _251_2 (_251_2_out, buffer_3_out, _251_out);
  or _139 (PIN99, VA8, VA9, VA10, VA11, 1'b0, nUDS, nLDS, _61_out);
  and _57 (_57_out, d_ff_27_q, _110_out);
  or _106 (_106_out, nZRD, _102_out);
  and _107 (_107_out, _106_out, _105_out);
  or _105 (_105_out, nZWR, d_ff_28_q);
  D_Flip_Flop d_ff_33 (.clk(VCLK), .D(_95_out), .Q(d_ff_33_q));  // open: Qn, preset, en, reset
  nor _179 (_179_out, _177_out, nDTACK);
  D_Flip_Flop d_ff_34 (.clk(nVCLK), .D(_182_out), .Q(d_ff_34_q));  // open: Qn, preset, en, reset
  nor _195 (_195_out, n4_bit_cnt_2_nq3, n4_bit_cnt_2_nq2, n4_bit_cnt_2_nq1, n4_bit_cnt_2_nq0);
  D_Flip_Flop d_ff_35 (
    .clk(nVCLK), .D(d_ff_30_q), .Q(d_ff_35_q), .Qn(d_ff_35_qn), .preset(not_78_out));  // open: en, reset
  D_Flip_Flop d_ff_36 (.clk(nVCLK), .D(d_ff_31_qn), .Qn(d_ff_36_qn), .reset(not_78_out));  // open: Q, preset, en
  nor _202 (_202_out, d_ff_31_qn, _213_out);
  T_Flip_Flop t_ff_8 (.clk(t_ff_7_qn), .T(not_50_out), .Qn(t_ff_8_qn));  // open: Q, preset, reset, en
  or _79 (_79_out, DCA4, RW);
  nor _138 (_138_out, buffer_5_out, buffer_1_out);
  or _141 (_141_out, not_52_out, d_ff_32_q);
  xnor _120 (_120_out, nCART, VA22);
  D_Flip_Flop d_ff_37 (.clk(nVCLK), .D(_262_out), .Qn(d_ff_37_qn));  // open: Q, preset, en, reset
  D_Flip_Flop d_ff_38 (.clk(nVCLK), .D(_263_out), .Q(d_ff_38_q), .Qn(d_ff_38_qn));  // open: preset, en, reset
  D_Flip_Flop d_ff_39 (.clk(VCLK), .D(nAS), .Q(d_ff_39_q));  // open: Qn, preset, en, reset
  not not_55 (not_55_out, d_ff_40_q);
  D_Flip_Flop d_ff_40 (.clk(not_53_out), .D(nWAIT), .Q(d_ff_40_q), .reset(not_56_out));  // open: Qn, preset, en
  not not_56 (not_56_out, not_54_out);
  not not_57 (not_57_out, ZA0);
  not not_58 (not_58_out, _177_out);
  buf buffer_6 (RWd, _176_out);
  buf buffer_7 (buffer_7_out, _176_out);
  not not_59 (not_59_out, FFRES);
  nor _137 (_137_out, _138_out, buffer_1_out);
  not not_60 (not_60_out, not_61_out);
  not not_61 (not_61_out, _141_out);
  not not_62 (not_62_out, VA21);
  and _69 (nIO, _71_out, DCA0);
  not not_63 (not_63_out, VCLK);
  D_Flip_Flop d_ff_41 (
    .clk(VCLK), .D(not_53_out), .Q(d_ff_41_q), .Qn(d_ff_41_qn), .reset(not_55_out));  // open: preset, en
  or _171 (_171_out, nMREQ, nM3, D8, VA22);
  not not_64 (not_64_out, ZA14);
  not not_65 (not_65_out, ZA13);
  or _343 (_343_out, RWd, nTPAL);
  or _110 (_110_out, _107_out, ZA0);
  or _111 (_111_out, _107_out, not_57_out);
  or _102 (_102_out, d_ff_33_q, _187_out);
  or _94 (_94_out, nTPAL, _187_out, _179_out);
  or _176_2 (_176_2_out, SRES, d_ff_34_q);
  or _91 (_91_out, not_58_out, SRES, _187_out);
  or _115 (_115_out, RWd, nTPAL);
  or _317 (_317_out, buffer_7_out, nTPAL);
  or _316 (_316_out, nTPAL, nZTOV);
  and _284 (_284_out, multiplexer_3_out[0], not_48_out);
  and _283 (_283_out, multiplexer_3_out[1], not_48_out);
  and _282 (_282_out, multiplexer_3_out[2], not_48_out);
  and _281 (_281_out, multiplexer_3_out[3], not_48_out);
  and _273 (_273_out, multiplexer_4_out[0], not_48_out);
  and _276 (_276_out, multiplexer_4_out[1], not_48_out);
  and _275 (_275_out, multiplexer_4_out[2], not_48_out);
  and _274 (_274_out, multiplexer_4_out[3], not_48_out);
  not not_66 (not_66_out, buffer_12_out);
  not not_67 (not_67_out, nHSYNC);
  and _218 (_218_out, d_ff_30_q, d_ff_35_q);
  nor _211 (_211_out, d_ff_35_qn, d_ff_36_qn);
  not not_68 (not_68_out, d_ff_14_qn);
  T_Flip_Flop t_ff_9 (.clk(t_ff_8_qn), .T(buffer_5_out), .Qn(t_ff_9_qn));  // open: Q, preset, reset, en
  D_Flip_Flop d_ff_42 (.clk(DCA5), .D(D8), .Q(d_ff_42_q), .reset(not_69_out));  // open: Qn, preset, en
  not not_69 (not_69_out, _143_out);
  D_Flip_Flop d_ff_43 (.clk(_79_out), .D(D8), .Qn(nZBR), .reset(not_59_out));  // open: Q, preset, en
  D_Flip_Flop d_ff_44 (.clk(t_ff_9_qn), .D(VA23), .Q(nZNMI), .preset(_137_out));  // open: Qn, en, reset
  D_Flip_Flop d_ff_45 (.clk(DCA3), .D(D8), .Qn(d_ff_45_qn), .reset(nFFRES));  // open: Q, preset, en
  not not_70 (not_70_out, not_71_out);
  not not_71 (not_71_out, not_60_out);
  or _133 (_133_out, _257_out, VA23);
  or _212 (_212_out, _257_out, _296_out);
  or _127 (_127_out, _212_out, _120_out, VA21);
  or _124 (_124_out, VA21, _120_out, _135_out);
  or _134 (_134_out, _135_out, _206_out);
  or _192 (_192_out, d_ff_38_q, nAS, d_ff_39_q);
  D_Flip_Flop d_ff_46 (
    .clk(not_63_out), .D(d_ff_41_q), .Q(d_ff_46_q), .Qn(d_ff_46_qn), .reset(not_55_out));  // open: preset, en
  or _108 (nVDPM, _171_out, D8);
  nand _63 (nZRAM, not_64_out, nZA15, nM3, not_47_out);
  nand _62 (nSOUND, not_65_out, ZA14, 1'b1, nZA15, not_47_out, nM3);
  not not_72 (not_72_out, _343_out);
  assign nUDS_2 = not_72_out ? _110_out : 1'bz;  // Controlled_Buffer controlled_buffer_1
  assign nLDS_2 = not_72_out ? _111_out : 1'bz;  // Controlled_Buffer controlled_buffer_2
  assign nAS_o = not_72_out ? _102_out : 1'bz;  // Controlled_Buffer controlled_buffer_3
  assign nWAIT_2 = not_73_out ? 1'b0 : 1'bz;  // Controlled_Buffer controlled_buffer_4
  not not_73 (not_73_out, _94_out);
  nand _5 (nIA14, nM3, VA14);
  and _175 (nZTOV, _176_2_out, nM3);
  assign RW_2 = RWd ? nZWR : 1'bz;  // Controlled_Buffer controlled_buffer_5
  D_Flip_Flop d_ff_47 (.clk(VCLK), .D(_91_out), .Q(nBR));  // open: Qn, preset, en, reset
  assign nBGACK_2 = not_74_out ? 1'b0 : 1'bz;  // Controlled_Buffer controlled_buffer_6
  not not_74 (not_74_out, _115_out);
  assign VA23_2 = not_75_out ? multiplexer_1_out[0] : 1'bz;  // Controlled_Buffer controlled_buffer_7
  assign VA22_2 = not_75_out ? multiplexer_1_out[1] : 1'bz;  // Controlled_Buffer controlled_buffer_8
  assign VA21_2 = not_75_out ? multiplexer_1_out[2] : 1'bz;  // Controlled_Buffer controlled_buffer_9
  not not_75 (not_75_out, _317_out);
  not not_76 (not_76_out, _316_out);
  assign VA20_2 = not_76_out ? multiplexer_1_out[3] : 1'bz;  // Controlled_Buffer controlled_buffer_10
  assign VA19_2 = not_76_out ? multiplexer_2_out[0] : 1'bz;  // Controlled_Buffer controlled_buffer_11
  assign VA18_2 = not_76_out ? multiplexer_2_out[1] : 1'bz;  // Controlled_Buffer controlled_buffer_12
  assign VA17_2 = not_76_out ? multiplexer_2_out[2] : 1'bz;  // Controlled_Buffer controlled_buffer_13
  assign VA16_2 = not_76_out ? multiplexer_2_out[3] : 1'bz;  // Controlled_Buffer controlled_buffer_14
  assign VA15_2 = not_76_out ? _284_out : 1'bz;  // Controlled_Buffer controlled_buffer_15
  assign VA14_2 = not_76_out ? _283_out : 1'bz;  // Controlled_Buffer controlled_buffer_16
  assign VA13_2 = not_76_out ? _282_out : 1'bz;  // Controlled_Buffer controlled_buffer_17
  assign VA12_2 = not_76_out ? _281_out : 1'bz;  // Controlled_Buffer controlled_buffer_18
  assign VA11_2 = not_76_out ? _273_out : 1'bz;  // Controlled_Buffer controlled_buffer_19
  assign VA10_2 = not_76_out ? _276_out : 1'bz;  // Controlled_Buffer controlled_buffer_20
  assign VA9_2 = not_76_out ? _275_out : 1'bz;  // Controlled_Buffer controlled_buffer_21
  assign VA8_2 = not_76_out ? _274_out : 1'bz;  // Controlled_Buffer controlled_buffer_22
  buf buffer_8 (buffer_8_out, nSRES);
  buf buffer_9 (EDCLK, buffer_12_out);
  buf buffer_10 (buffer_10_out, buffer_12_out);
  buf buffer_11 (buffer_11_out, nSRES);
  J_K_Flip_Flop j_k_ff_1 (
    .J(1'b0), .clk(not_66_out), .K(not_67_out), .Q(j_k_ff_1_q), .Qn(j_k_ff_1_qn), .preset(not_77_out));  // open: en, reset
  not not_77 (not_77_out, buffer_13_out);
  D_Flip_Flop d_ff_48 (.clk(nVCLK), .D(_218_out), .Q(d_ff_48_q), .preset(not_78_out));  // open: Qn, en, reset
  not not_78 (not_78_out, _219_out);
  D_Flip_Flop d_ff_49 (.clk(not_68_out), .D(d_ff_50_q), .Q(d_ff_49_q), .reset(buffer_5_out));  // open: Qn, preset, en
  D_Flip_Flop d_ff_50 (
    .clk(t_ff_9_qn), .D(nWRES), .Q(d_ff_50_q), .Qn(d_ff_50_qn), .reset(buffer_5_out));  // open: preset, en
  D_Flip_Flop d_ff_51 (.clk(t_ff_9_qn), .D(buffer_5_out), .Q(d_ff_51_q), .reset(buffer_5_out));  // open: Qn, preset, en
  D_Flip_Flop d_ff_52 (.clk(t_ff_9_qn), .D(d_ff_51_q), .Qn(d_ff_52_qn), .reset(buffer_5_out));  // open: Q, preset, en
  Multiplexer #(.disabled(0), .enable("false")) multiplexer_5 (
    .in0(_133_out), .in1(_212_out), .out(multiplexer_5_out), .sel(d_ff_45_qn));
  not not_79 (not_79_out, _120_out);
  and _43 (nROM, _127_out, _124_out);
  D_Flip_Flop d_ff_53 (.clk(VCLK), .D(_192_out), .Qn(d_ff_53_qn));  // open: Q, preset, en, reset
  _1_bit_cnt u_1_bit_cnt_1 (
    .C(MCLK), .CIN(_2_out), .VAL(1'b1), .nLD(_6_out), .nRES(buffer_8_out), .Q(n1_bit_cnt_1_q),
    .nQ(n1_bit_cnt_1_nq));  // open: CO
  _1_bit_cnt u_1_bit_cnt_2 (
    .C(MCLK), .CIN(1'b1), .VAL(j_k_ff_1_q), .nLD(_6_out), .nRES(buffer_8_out), .Q(n1_bit_cnt_2_q),
    .nQ(n1_bit_cnt_2_nq));  // open: CO
  _1_bit_cnt u_1_bit_cnt_3 (
    .C(MCLK), .CIN(n1_bit_cnt_2_q), .VAL(1'b0), .nLD(_6_out), .nRES(buffer_8_out), .Q(n1_bit_cnt_3_q),
    .nQ(n1_bit_cnt_3_nq));  // open: CO
  nand _6 (_6_out, n1_bit_cnt_3_nq, n1_bit_cnt_2_nq, n1_bit_cnt_1_nq);
  _4_bit_cnt u_4_bit_cnt_3 (
    .C(buffer_10_out), .nLD(j_k_ff_1_qn), .nRES(buffer_11_out), .CIN(j_k_ff_1_qn), .VAL0(1'b1), .VAL1(1'b0),
    .VAL2(1'b0), .VAL3(1'b0), .nQ0(n4_bit_cnt_3_nq0), .nQ1(n4_bit_cnt_3_nq1), .nQ2(n4_bit_cnt_3_nq2),
    .nQ3(n4_bit_cnt_3_nq3));  // open: CO
  nand _214 (_214_out, d_ff_48_q, _218_out);
  and _129 (_129_out, _218_out, _203_out);
  and _219 (_219_out, FFRES, nM3);
  nor _68 (_68_out, d_ff_49_q, d_ff_50_qn);
  nor _143 (_143_out, _68_out, d_ff_52_qn);
  or _132 (_132_out, d_ff_45_qn, not_70_out);
  and _123 (_123_out, not_70_out, _122_out);
  or _130 (_130_out, multiplexer_5_out, not_79_out);
  or _122 (_122_out, _120_out, _133_out, not_62_out);
  or _163 (_163_out, DCA6, nAS);
  not not_80 (not_80_out, _133_out);
  and _88 (_88_out, nOE0, d_ff_46_qn);
  and _248 (_248_out, nCAS0, d_ff_18_q);
  D_Flip_Flop d_ff_54 (.clk(buffer_10_out), .D(_15_out), .Qn(d_ff_54_qn), .preset(not_81_out));  // open: Q, en, reset
  not not_81 (not_81_out, buffer_11_out);
  and _128 (_128_out, _132_out, _130_out);
  not not_82 (not_82_out, _120_out);
  not not_83 (not_83_out, nM3);
  or _149 (nFDC, DCA1, nAS);
  or _167 (_167_out, _163_out, _168_out);
  nand _168 (_168_out, d_ff_53_qn, nWAIT);
  or _164 (_164_out, DCA7, nAS);
  or _166 (nTIME, DCA2, nAS);
  not not_84 (not_84_out, not_85_out);
  not not_85 (not_85_out, not_86_out);
  not not_86 (not_86_out, not_80_out);
  or _169 (_169_out, _88_out, _248_out);
  or _170 (_170_out, d_ff_41_qn, d_ff_23_q);
  and _2 (_2_out, n1_bit_cnt_2_q, n1_bit_cnt_3_q);
  buf buffer_12 (buffer_12_out, n1_bit_cnt_3_q);
  nor _15 (_15_out, n4_bit_cnt_3_nq3, n4_bit_cnt_3_nq2, n4_bit_cnt_3_nq1, n4_bit_cnt_3_nq0);
  buf buffer_13 (buffer_13_out, buffer_14_out);
  buf buffer_14 (buffer_14_out, d_ff_54_qn);
  Multiplexer #(.disabled(0), .enable("false")) multiplexer_6 (
    .in0(_143_out), .in1(d_ff_42_q), .out(nZ_RES), .sel(nM3));
  not not_87 (not_87_out, _135_out);
  nor _29 (_29_out, d_ff_45_qn, _202_out);
  or _135 (_135_out, VA23, not_83_out, nAS);
  not not_88 (not_88_out, not_84_out);
  nand _170_2 (_170_2_out, _169_out, _170_out);
  or _28 (_28_out, _211_out, d_ff_45_qn);
  or _30 (_30_out, _29_out, not_82_out, _135_out);
  nand _165 (_165_out, _134_out, nFDC, DCA0, _167_out, _164_out, nTIME);
  not not_89 (not_89_out, not_91_out);
  not not_90 (not_90_out, not_88_out);
  not not_91 (not_91_out, not_90_out);
  not not_92 (nNOE, _170_2_out);
  not not_93 (not_93_out, not_94_out);
  not not_94 (not_94_out, not_89_out);
  not not_95 (not_95_out, nM3);
  and _335 (nHALT, nM3, _143_out);
  or _45 (_45_out, M1DELAY, ZA14, nZA15, nM3);
  nand _32 (_32_out, _202_out, not_87_out, VA21, not_82_out);
  or _35 (_35_out, nM3, M1DELAY, ZA15);
  not not_96 (not_96_out, RW);
  nor _47 (_47_out, d_ff_55_q, nFDC, RW);
  and _25 (nASEL, not_93_out, _205_out);
  nor _173 (_173_out, d_ff_21_q, not_95_out);
  nor _172 (_172_out, not_95_out, nMREQ, M1DELAY2);
  not not_97 (not_97_out, nNOE);
  nand _3 (nEOE, not_97_out, nM3);
  not not_98 (not_98_out, nVTOZ);
  assign ZA15_2 = not_98_out ? 1'b0 : 1'bz;  // Controlled_Buffer controlled_buffer_23
  assign ZA14_2 = not_98_out ? VA14 : 1'bz;  // Controlled_Buffer controlled_buffer_24
  assign ZA13_2 = not_98_out ? VA13 : 1'bz;  // Controlled_Buffer controlled_buffer_25
  assign ZA12_2 = not_98_out ? VA12 : 1'bz;  // Controlled_Buffer controlled_buffer_26
  assign ZA11_2 = not_98_out ? VA11 : 1'bz;  // Controlled_Buffer controlled_buffer_27
  assign ZA10_2 = not_98_out ? VA10 : 1'bz;  // Controlled_Buffer controlled_buffer_28
  assign ZA9_2 = not_98_out ? VA9 : 1'bz;  // Controlled_Buffer controlled_buffer_29
  assign ZA8_2 = not_98_out ? VA8 : 1'bz;  // Controlled_Buffer controlled_buffer_30
  assign ZA8_3 = not_98_out ? VA7 : 1'bz;  // Controlled_Buffer controlled_buffer_31
  assign ZA0_2 = not_98_out ? _57_out : 1'bz;  // Controlled_Buffer controlled_buffer_32
  and _44 (nCAS2, _129_out, _45_out, _244_out);
  and _33 (nRAS2, _211_out, _32_out, _123_out);
  and _27 (nCE0, _35_out, _28_out, _128_out, _30_out);
  not not_99 (not_99_out, nVTOZ);
  or _56 (_56_out, RW, nAS);
  assign nZWR_3 = not_99_out ? _56_out : 1'bz;  // Controlled_Buffer controlled_buffer_33
  assign nZRD_2 = not_99_out ? _76_out : 1'bz;  // Controlled_Buffer controlled_buffer_34
  or _76 (_76_out, not_96_out, nAS);
  or _333 (nVPA, nINTACK, nAS);
  assign nDTACK_2 = not_100_out ? 1'b0 : 1'bz;  // Controlled_Buffer controlled_buffer_35
  not not_100 (not_100_out, _194_out);
  nand _194 (_194_out, nINTACK, _165_out);
  D_Flip_Flop d_ff_55 (.clk(VCLK), .D(_47_out), .Q(d_ff_55_q), .Qn(nFDWR));  // open: preset, en, reset
  nor _85 (nZREF, _173_out, _172_out);
  not not_101 (not_101_out, nVTOZ);
  assign nMREQ_o = not_101_out ? _80_out : 1'bz;  // Controlled_Buffer controlled_buffer_36

  assign nRESET = nHALT;
  assign nZWR_2 = nZWR;

  // Notes on the sheet:
  //   84
  //   48
  //   90
  //   114
  //   243
  //   331
  //   180
  //   259
  //   181
  //   328
  //   329
  //   330
  //   324
  //   260
  //   36
  //   42
  //   37
  //   40
  //   39
  //   301
  //   238
  //   291
  //   309
  //   140
  //   D
  //   53
  //   75
  //   48
  //   305
  //   150
  //   Q7
  //   Q6
  //   Q5
  //   Q4
  //   Q3
  //   Q2
  //   Q1
  //   Q0
  //   290
  //   308
  //   96
  //   152
  //   337,338,340,341
  //   303
  //   204
  //   289
  //   307
  //   315
  //   298
  //   226
  //   311
  //   256
  //   258
  //   269
  //   !
  //   74
  //   208
  //   144
  //   297
  //   81
  //   321
  //   99
  //   185
  //   186
  //   199
  //   198
  //   334
  //   72
  //   264
  //   162
  //   !
  //   89
  //   12
  //   250
  //   161
  //   267
  //   58
  //   104
  //   93
  //   226
  //   159
  //   277-280
  //   142
  //   !
  //   255
  //   251
  //   60
  //   314
  //   300
  //   125
  //   118
  //   293
  //   294
  //   200
  //   268
  //   320
  //   232
  //   242
  //   247
  //   246
  //   101
  //   183
  //   188
  //   245
  //   217
  //   210
  //   322
  //   261
  //   184
  //   193
  //   !
  //   !
  //   109
  //   92
  //   233
  //   231
  //   266
  //   78
  //   !
  //   55
  //   54
  //   121
  //   254
  //   252
  //   64
  //   59
  //   !
  //   !
  //   10
  //   21
  //   11
  //   215
  //   67
  //   66
  //   227
  //   155
  //   131
  //   191
  //   249
  //   !
  //   113
  //   !
  //   !
  //   EDCLK DIVIDER
  //   22
  //   22
  //   14
  //   97
  //   !
  //   !
  //   228
  //   126
  //   9
  //   8
  //   19
  //   98,18,17,16
  //   !
  //   20
  //   112
  //   265
  //   119
  //   136
  //   34
  //   7
  //   4
  //   31
  //   170
  //   26
  //   1
  //   174
  //   86
  //   103
  //   !
  //   !
  //   !
  //   46
  //   !
endmodule

// CONTER 4 BIT
module _4_bit_cnt (
  input  C,
  input  nLD,
  input  nRES,
  input  CIN,
  input  VAL0,
  input  VAL1,
  input  VAL2,
  input  VAL3,
  output nQ0,
  output nQ1,
  output nQ2,
  output nQ3,
  output CO
);

  wire and_1_out, and_2_out, and_3_out, d_ff_1_q, d_ff_2_q, d_ff_3_q, d_ff_4_q, d_ff_5_q, d_ff_6_q, d_ff_7_q,
       d_ff_8_q, multiplexer_1_out, multiplexer_2_out, multiplexer_3_out, multiplexer_4_out, not_1_out,
       not_2_out, not_3_out, not_4_out, not_5_out, not_6_out, not_7_out, not_8_out, xor_1_out, xor_2_out,
       xor_3_out, xor_4_out;

  not not_1 (not_1_out, nRES);
  xor xor_1 (xor_1_out, d_ff_5_q, CIN);
  and and_1 (and_1_out, d_ff_5_q, CIN);
  not not_2 (not_2_out, nRES);
  xor xor_2 (xor_2_out, d_ff_6_q, and_1_out);
  and and_2 (and_2_out, d_ff_6_q, and_1_out);
  not not_3 (not_3_out, nRES);
  xor xor_3 (xor_3_out, d_ff_7_q, and_2_out);
  and and_3 (and_3_out, d_ff_7_q, and_2_out);
  not not_4 (not_4_out, nRES);
  xor xor_4 (xor_4_out, d_ff_8_q, and_3_out);
  and and_4 (CO, d_ff_8_q, and_3_out);
  Multiplexer #(.disabled(0), .enable("false")) multiplexer_1 (
    .in0(VAL0), .in1(xor_1_out), .out(multiplexer_1_out), .sel(nLD));
  Multiplexer #(.disabled(0), .enable("false")) multiplexer_2 (
    .in0(VAL1), .in1(xor_2_out), .out(multiplexer_2_out), .sel(nLD));
  Multiplexer #(.disabled(0), .enable("false")) multiplexer_3 (
    .in0(VAL2), .in1(xor_3_out), .out(multiplexer_3_out), .sel(nLD));
  Multiplexer #(.disabled(0), .enable("false")) multiplexer_4 (
    .in0(VAL3), .in1(xor_4_out), .out(multiplexer_4_out), .sel(nLD));
  not not_5 (not_5_out, C);
  D_Flip_Flop #(.trigger("high")) d_ff_1 (
    .clk(C), .D(multiplexer_1_out), .Q(d_ff_1_q), .reset(not_1_out));  // open: Qn, preset, en
  not not_6 (not_6_out, C);
  D_Flip_Flop #(.trigger("high")) d_ff_2 (
    .clk(C), .D(multiplexer_2_out), .Q(d_ff_2_q), .reset(not_2_out));  // open: Qn, preset, en
  not not_7 (not_7_out, C);
  D_Flip_Flop #(.trigger("high")) d_ff_3 (
    .clk(C), .D(multiplexer_3_out), .Q(d_ff_3_q), .reset(not_3_out));  // open: Qn, preset, en
  not not_8 (not_8_out, C);
  D_Flip_Flop #(.trigger("high")) d_ff_4 (
    .clk(C), .D(multiplexer_4_out), .Q(d_ff_4_q), .reset(not_4_out));  // open: Qn, preset, en
  D_Flip_Flop #(.trigger("high")) d_ff_5 (
    .clk(not_5_out), .D(d_ff_1_q), .Q(d_ff_5_q), .Qn(nQ0), .reset(not_1_out));  // open: preset, en
  D_Flip_Flop #(.trigger("high")) d_ff_6 (
    .clk(not_6_out), .D(d_ff_2_q), .Q(d_ff_6_q), .Qn(nQ1), .reset(not_2_out));  // open: preset, en
  D_Flip_Flop #(.trigger("high")) d_ff_7 (
    .clk(not_7_out), .D(d_ff_3_q), .Q(d_ff_7_q), .Qn(nQ2), .reset(not_3_out));  // open: preset, en
  D_Flip_Flop #(.trigger("high")) d_ff_8 (
    .clk(not_8_out), .D(d_ff_4_q), .Q(d_ff_8_q), .Qn(nQ3), .reset(not_4_out));  // open: preset, en

  // Notes on the sheet:
  //   C
  //   VAL
  //   LD
  //   /RES
  //   C
  //   VAL
  //   LD
  //   /RES
  //   C
  //   VAL
  //   LD
  //   /RES
  //   C
  //   VAL
  //   LD
  //   /RES
  //   CIN
  //   CO
  //   CIN
  //   CO
  //   CIN
  //   CO
  //   CIN
  //   CO
  //   CNT BIT
  //   Q
  //   nQ
  //   CNT BIT
  //   Q
  //   nQ
  //   CNT BIT
  //   Q
  //   nQ
  //   CNT BIT
  //   Q
  //   nQ
endmodule

// COUNTER 1BIT
module _1_bit_cnt (
  input  C,
  input  CIN,
  input  VAL,
  input  nLD,
  input  nRES,
  output Q,
  output nQ,
  output CO
);

  wire d_ff_1_q, multiplexer_1_out, not_1_out, not_2_out, xor_1_out;

  not not_1 (not_1_out, nRES);
  xor xor_1 (xor_1_out, Q, CIN);
  and and_1 (CO, Q, CIN);
  Multiplexer #(.disabled(0), .enable("false")) multiplexer_1 (
    .in0(VAL), .in1(xor_1_out), .out(multiplexer_1_out), .sel(nLD));
  not not_2 (not_2_out, C);
  D_Flip_Flop #(.trigger("high")) d_ff_1 (
    .clk(C), .D(multiplexer_1_out), .Q(d_ff_1_q), .reset(not_1_out));  // open: Qn, preset, en
  D_Flip_Flop #(.trigger("high")) d_ff_2 (
    .clk(not_2_out), .D(d_ff_1_q), .Q(Q), .Qn(nQ), .reset(not_1_out));  // open: preset, en

  // Notes on the sheet:
  //   C
  //   VAL
  //   LD
  //   /RES
  //   CIN
  //   CNT BIT
  //   Q
  //   nQ
  //   CO
endmodule
