// Logisim project cnt_bit.circ as structural Verilog: 1 circuit, main circuit main
module main (
  input  res,
  input  cin,
  input  clk,
  input  ld,
  input  val,
  output cout,
  output nq,
  output q
);

  wire multiplexer_1_out, multiplexer_2_out, multiplexer_3_out, multiplexer_4_out, nand_1_out, nand_2_out,
       nand_3_out, nor_1_out, not_1_out, not_3_out, not_4_out, not_5_out, not_6_out, not_7_out;

  nand nand_1 (nand_1_out, not_7_out, cin);
  Multiplexer multiplexer_1 (.in0(1'b1), .in1(nor_1_out), .out(multiplexer_1_out), .sel(nand_1_out));
  nor nor_1 (nor_1_out, not_7_out, cin);
  not not_1 (not_1_out, val);
  not not_2 (cout, nand_1_out);
  Multiplexer multiplexer_2 (.in0(multiplexer_1_out), .in1(not_1_out), .out(multiplexer_2_out), .sel(ld));
  not not_3 (not_3_out, nand_3_out);
  not not_4 (not_4_out, nand_2_out);
  not not_5 (not_5_out, nand_3_out);
  not not_6 (not_6_out, multiplexer_2_out);
  Multiplexer multiplexer_3 (.in0(not_3_out), .in1(not_4_out), .out(multiplexer_3_out), .sel(clk));
  Multiplexer multiplexer_4 (.in0(not_5_out), .in1(not_6_out), .out(multiplexer_4_out), .sel(clk));
  nand nand_2 (nand_2_out, res, multiplexer_3_out);
  nand nand_3 (nand_3_out, res, multiplexer_4_out);
  not not_7 (not_7_out, nand_2_out);
  not not_8 (q, nand_2_out);
  not not_9 (nq, not_7_out);
endmodule
