// Logisim project arbiter.circ as structural Verilog: 7 circuits, main circuit main
module main (
  input  MCLK,
  input  rw_in,
  input  as_in,
  input  w33,
  input  cas0,
  input  w38,
  input  VCLK,
  input  uds_in,
  input  lds_in,
  input  [22:0] va_in,
  input  w82,
  input  bgack_in,
  input  [15:0] vd_in,
  input  m3,
  input  iorq,
  input  [15:0] za,
  input  m1_in,
  input  ZCLK,
  input  w152,
  input  zwr_in,
  input  in_21,
  input  in_22,
  output w12,
  output zrd_out,
  output zwr_out,
  output VD8_out,
  output w226,
  output w24,
  output w35,
  output w115,
  output ZA0_out,
  output w162,
  output w120,
  output w32,
  output w160,
  output w123,
  output w47,
  output o_TIME,
  output FDC,
  output w196,
  output rw_dir,
  output rw_out,
  output w230
);

  wire and_1_out, and_2_out, and_3_out, cnt_bit_1_cout, cnt_bit_1_nq, cnt_bit_2_nq, cnt_bit_3_cout,
       cnt_bit_3_nq, cnt_bit_4_nq, cnt_bit_4_q, cnt_bit_5_cout, cnt_bit_5_nq, cnt_bit_6_nq, cnt_bit_6_q,
       cnt_bit_7_nq, d_ff_1_q, d_ff_1_qn, d_ff_2_qn, d_ff_3_q, d_ff_4_q, d_ff_5_q, d_ff_6_q, d_ff_7_q,
       d_ff_8_q, d_ff_9_q, d_ff_10_q, dff11_q, dff12_q, dff12_qn, dff13_qn, dff15_q, dff15_qn, dff16_q,
       dff17_q, dff19_q, dff20_q, dff20_qn, dff23_q, dff23_qn, dff24_q, dff26_qn, dff27_q, dff29_q, dff30_q,
       dff31_q, dff32_q, dff33_q, dff33_qn, dff44_qn, dff45_q, dff46_q, dff46_qn, multiplexer_2_out,
       nand_1_out, nor_1_out, nor_2_out, nor_3_out, nor_4_out, nor_5_out, not_1_out, not_2_out, not_3_out,
       not_4_out, not_5_out, not_6_out, not_7_out, not_8_out, not_9_out, not_10_out, not_11_out, not_13_out,
       not_14_out, not_16_out, not_17_out, not_18_out, not_19_out, not_20_out, not_21_out, not_22_out,
       not_23_out, not_24_out, not_25_out, not_26_out, not_27_out, not_28_out, not_29_out, not_30_out,
       not_31_out, not_32_out, not_33_out, not_34_out, not_35_out, not_36_out, not_37_out, not_39_out,
       not_43_out, not_44_out, not_46_out, not_47_out, not_49_out, not_50_out, not_51_out, not_52_out,
       not_53_out, not_54_out, not_55_out, not_56_out, not_57_out, not_58_out, not_59_out, not_63_out,
       not_64_out, not_65_out, not_66_out, or_5_out, pal_trap_out, undriven, undriven_2, undriven_3,
       undriven_4, undriven_5, undriven_6, undriven_7, undriven_8, undriven_9, undriven_10, undriven_11,
       undriven_12, undriven_13, undriven_14, undriven_15, undriven_16, undriven_17, undriven_18,
       undriven_19, undriven_20, undriven_21, undriven_22, undriven_23, undriven_24, undriven_25,
       undriven_26, undriven_27, undriven_28, undriven_29, undriven_30, undriven_31, undriven_32,
       undriven_33, undriven_34, undriven_35, undriven_36, w26_out, w27_out, w34_out, w36_out, w40_out,
       w41_out, w42_out, w43_out, w44_out, w45_out, w46_out, w48_out, w54_out, w58_out, w59_out, w60_out,
       w63_out, w64_out, w65_out, w66_out, w68_out, w69_out, w70_out, w71_out, w72_out, w73_out, w75_out,
       w83_out, w84_out, w94_out, w95_out, w96_out, w97_out, w101_out, w102_out, w103_out, w107_out,
       w112_out, w113_out, w118_out, w131_out, w132_out, w133_out, w134_out, w137_out, w142_out, w163_out,
       w164_out, w167_out, w169_out, w170_out, w171_out, w172_out, w173_out, w198_out, w200_out, w202_out,
       w204_out, w205_out, w206_out, w207_out, w211_out, w215_out, w220_out, w223_out, w228_out, w232_out,
       w234_out, w235_out, w238_out, w248_out, w249_out, w254_out, w269_out, w274_out, xor_delay_6x_1_out_2,
       xor_delay_6x_2_out_2, xor_delay_12x_1_out_2, xor_delay_36x_1_out_2, xor_delay_40x_1_out_2;

  not not_1 (not_1_out, VCLK);
  and w40 (w40_out, w26_out, w83_out);
  not pal_trap (pal_trap_out, 1'b1);
  D_Flip_Flop d_ff_1 (
    .D(nor_3_out), .clk(not_46_out), .Q(d_ff_1_q), .Qn(d_ff_1_qn), .reset(not_2_out));  // open: preset
  not not_2 (not_2_out, not_32_out);
  // NOR_Gate nor_1 has open pins: out=nor_1_out
  D_Flip_Flop dff13 (.D(uds_in), .clk(not_1_out), .Qn(dff13_qn));  // open: Q, preset, reset
  not not_3 (not_3_out, w73_out);
  D_Flip_Flop dff15 (.D(w40_out), .clk(VCLK), .Q(dff15_q), .Qn(dff15_qn), .preset(not_3_out));  // open: reset
  not not_4 (not_4_out, m3);
  not not_5 (not_5_out, ZCLK);
  // NOT_Gate not_6 has open pins: in=open, out=not_6_out
  D_Flip_Flop d_ff_2 (.D(nor_4_out), .clk(not_46_out), .Qn(d_ff_2_qn), .preset(not_13_out));  // open: Q, reset
  not not_7 (not_7_out, not_46_out);
  and and_1 (and_1_out, 1'b0, d_ff_1_q);
  nor nor_2 (nor_2_out, d_ff_1_q, w27_out);
  not not_8 (not_8_out, rw_in);
  not not_9 (not_9_out, undriven_2);
  D_Flip_Flop dff11 (.D(w43_out), .clk(not_1_out), .Q(dff11_q));  // open: Qn, preset, reset
  // NAND_Gate w257 has open pins: in0=uds_in, in1=lds_in, out=open
  nand w42 (w42_out, dff19_q, w71_out);
  or w44 (w44_out, w42_out, undriven, va_in[22]);
  D_Flip_Flop dff16 (.D(w44_out), .clk(VCLK), .Q(dff16_q));  // open: Qn, preset, reset
  or w59 (w59_out, as_in, not_4_out);
  xor_delay_6x xor_delay_6x_1 (.in_1(m1_in), .out_2(xor_delay_6x_1_out_2));
  not not_10 (not_10_out, not_6_out);
  not not_11 (not_11_out, not_7_out);
  nor nor_3 (nor_3_out, and_1_out, nor_2_out);
  not not_12 (w24, not_9_out);
  or w41 (w41_out, dff15_q, w27_out);
  or w36 (w36_out, undriven_3, rw_in);
  nand nand_1 (nand_1_out, cnt_bit_2_nq, cnt_bit_4_nq, cnt_bit_6_nq);
  not not_13 (not_13_out, not_10_out);
  not not_14 (not_14_out, not_11_out);
  // NOT_Gate not_15 has open pins: in=not_14_out, out=open
  buf or_1 (w12, not_8_out);  // OR_Gate
  or or_2 (zrd_out, as_in, not_8_out);
  or or_3 (zwr_out, rw_in, as_in);
  D_Flip_Flop dff12 (.D(w41_out), .clk(not_1_out), .Q(dff12_q), .Qn(dff12_qn));  // open: preset, reset
  not not_16 (not_16_out, w73_out);
  D_Flip_Flop dff19 (.D(w71_out), .clk(not_1_out), .Q(dff19_q), .preset(not_16_out));  // open: Qn, reset
  or w43 (w43_out, w44_out, dff16_q);
  and w45 (w45_out, undriven_4, w46_out);
  or w46 (w46_out, w45_out, bgack_in);
  not not_17 (not_17_out, w38);
  not not_18 (not_18_out, not_17_out);
  and and_2 (and_2_out, cnt_bit_6_q, cnt_bit_4_q);
  not not_19 (not_19_out, w73_out);
  D_Flip_Flop dff17 (.D(w58_out), .clk(VCLK), .Q(dff17_q), .preset(not_19_out));  // open: Qn, reset
  not w48 (w48_out, w45_out);
  not not_20 (not_20_out, za[14]);
  cnt_bit cnt_bit_1 (
    .cin(d_ff_1_q), .val(1'b1), .load(d_ff_1_q), .clk(not_50_out), .res(not_10_out), .cout(cnt_bit_1_cout),
    .nq(cnt_bit_1_nq));  // open: q
  not w26 (w26_out, dff12_q);  // NAND_Gate
  buf w27 (w27_out, dff11_q);  // OR_Gate
  not not_21 (not_21_out, dff17_q);
  not not_22 (not_22_out, m1_in);
  not not_23 (not_23_out, za[15]);
  not not_24 (not_24_out, w12);
  D_Flip_Flop dff14 (.D(undriven_5), .clk(w36_out), .Qn(w35), .reset(not_25_out));  // open: Q, preset
  not not_25 (not_25_out, dff32_q);
  not not_26 (not_26_out, not_21_out);
  not not_27 (not_27_out, not_26_out);
  not w54 (w54_out, va_in[22]);  // NAND_Gate
  not not_28 (not_28_out, d_ff_2_qn);
  assign VD8_out = not_24_out ? w33 : 1'bz;  // Controlled_Buffer controlled_buffer_1
  or w34 (w34_out, w33, w35);
  nor w69 (w69_out, dff12_qn, w44_out);
  not not_29 (not_29_out, not_27_out);
  and w58 (w58_out, w84_out, w54_out);
  not not_30 (not_30_out, not_28_out);
  not not_31 (not_31_out, not_30_out);
  buf w60 (w60_out, w33);  // OR_Gate
  cnt_bit cnt_bit_2 (
    .cin(and_2_out), .val(1'b1), .load(nand_1_out), .clk(MCLK), .res(not_18_out), .nq(cnt_bit_2_nq));  // open: cout, q
  cnt_bit cnt_bit_3 (
    .cin(cnt_bit_1_cout), .val(1'b0), .load(d_ff_1_q), .clk(not_50_out), .res(not_10_out),
    .cout(cnt_bit_3_cout), .nq(cnt_bit_3_nq));  // open: q
  not not_32 (not_32_out, not_31_out);
  or w107 (w107_out, m3, w220_out, not_20_out, not_23_out);
  not not_33 (not_33_out, dff32_q);
  or w113 (w113_out, m3, iorq, not_22_out);
  D_Flip_Flop dff27 (.D(xor_delay_6x_1_out_2), .clk(ZCLK), .Q(dff27_q));  // open: Qn, preset, reset
  D_Flip_Flop d_ff_3 (.D(in_21), .clk(undriven_24), .Q(d_ff_3_q), .reset(not_33_out));  // open: Qn, preset
  nor nor_4 (nor_4_out, cnt_bit_7_nq, cnt_bit_5_nq, cnt_bit_3_nq, cnt_bit_1_nq);
  or w131 (w131_out, undriven_6, pal_trap_out, w152);
  D_Flip_Flop d_ff_4 (.D(d_ff_3_q), .clk(undriven_24), .Q(d_ff_4_q), .reset(not_33_out));  // open: Qn, preset
  nor w95 (w95_out, rw_in, uds_in);
  and w73 (w73_out, dff32_q, m3);
  and w112 (w112_out, dff29_q, w113_out);
  xor_delay_6x xor_delay_6x_2 (.in_1(w113_out), .out_2(xor_delay_6x_2_out_2));
  cnt_bit cnt_bit_4 (
    .cin(1'b1), .val(d_ff_1_qn), .load(nand_1_out), .clk(MCLK), .res(not_18_out), .q(cnt_bit_4_q),
    .nq(cnt_bit_4_nq));  // open: cout
  cnt_bit cnt_bit_5 (
    .cin(cnt_bit_3_cout), .val(1'b0), .load(d_ff_1_q), .clk(not_50_out), .res(not_10_out),
    .cout(cnt_bit_5_cout), .nq(cnt_bit_5_nq));  // open: q
  not not_34 (not_34_out, uds_in);
  or w66 (w66_out, as_in, undriven_9);
  nor w68 (w68_out, vd_in[8], w163_out);
  and w71 (w71_out, dff20_q, not_29_out);
  not not_35 (not_35_out, w73_out);
  D_Flip_Flop dff20 (.D(not_29_out), .clk(not_1_out), .Q(dff20_q), .Qn(dff20_qn), .preset(not_35_out));  // open: reset
  D_Flip_Flop dff23 (.D(dff33_qn), .clk(not_36_out), .Q(dff23_q), .Qn(dff23_qn), .reset(not_37_out));  // open: preset
  not not_36 (not_36_out, w59_out);
  not not_37 (not_37_out, dff33_qn);
  or w126 (o_TIME, undriven_8, as_in);
  or w130 (FDC, as_in, undriven_7);
  D_Flip_Flop dff29 (.D(xor_delay_6x_2_out_2), .clk(ZCLK), .Q(dff29_q));  // open: Qn, preset, reset
  D_Flip_Flop dff30 (.D(dff27_q), .clk(ZCLK), .Q(dff30_q));  // open: Qn, preset, reset
  D_Flip_Flop d_ff_5 (.D(d_ff_4_q), .clk(undriven_24), .Q(d_ff_5_q), .reset(not_33_out));  // open: Qn, preset
  nand w65 (w65_out, uds_in, dff13_qn);
  not not_38 (w32, w68_out);
  and w70 (w70_out, w27_out, w71_out);
  or w72 (w72_out, dff15_qn, w43_out);
  D_Flip_Flop d_ff_6 (.D(d_ff_5_q), .clk(undriven_24), .Q(d_ff_6_q), .reset(not_33_out));  // open: Qn, preset
  not not_39 (not_39_out, not_18_out);
  xor_delay_40x xor_delay_40x_1 (.in_1(undriven_10), .out_2(xor_delay_40x_1_out_2));
  nor w101 (w101_out, undriven_12, dff20_qn);
  nand w75 (w75_out, w94_out, undriven_11);
  or w83 (w83_out, dff23_qn, va_in[22]);
  // NOT_Gate not_40 has open pins: in=not_39_out, out=open
  nand w96 (w96_out, w95_out, undriven_15, undriven_13);
  nand w97 (w97_out, w95_out, undriven_15, undriven_14);
  nand w63 (w63_out, not_34_out, undriven_17);
  nand w64 (w64_out, w43_out, xor_delay_40x_1_out_2);
  not not_41 (ZA0_out, w65_out);
  not not_42 (w47, w75_out);
  nand w84 (w84_out, dff23_qn, dff33_qn, undriven_16);
  D_Flip_Flop dff26 (.D(vd_in[8]), .clk(w97_out), .Qn(dff26_qn), .reset(not_43_out));  // open: Q, preset
  not not_43 (not_43_out, dff32_q);
  D_Flip_Flop d_ff_7 (.D(d_ff_6_q), .clk(undriven_24), .Q(d_ff_7_q), .reset(not_33_out));  // open: Qn, preset
  cnt_bit cnt_bit_6 (
    .cin(cnt_bit_4_q), .val(1'b0), .load(nand_1_out), .clk(MCLK), .res(not_18_out), .q(cnt_bit_6_q),
    .nq(cnt_bit_6_nq));  // open: cout
  cnt_bit cnt_bit_7 (
    .cin(cnt_bit_5_cout), .val(1'b0), .load(d_ff_1_q), .clk(not_50_out), .res(not_10_out), .nq(cnt_bit_7_nq));  // open: cout, q
  nand w102 (w102_out, w70_out, w238_out, w107_out);
  buf w94 (w94_out, as_in);  // OR_Gate
  not not_44 (not_44_out, cnt_bit_6_q);
  not not_45 (w115, w64_out);
  D_Flip_Flop d_ff_8 (.D(d_ff_7_q), .clk(undriven_24), .Q(d_ff_8_q), .reset(not_33_out));  // open: Qn, preset
  not not_46 (not_46_out, not_44_out);
  not w103 (w103_out, rw_in);  // NOR_Gate
  not not_47 (not_47_out, w73_out);
  not not_48 (w160, w102_out);
  nor w137 (w137_out, pal_trap_out, w152, undriven_18);
  or or_4 (rw_dir, undriven_19, w152);
  D_Flip_Flop d_ff_9 (.D(d_ff_8_q), .clk(undriven_24), .Q(d_ff_9_q), .reset(not_33_out));  // open: Qn, preset
  not not_49 (not_49_out, not_46_out);
  not not_50 (not_50_out, not_49_out);
  or w118 (w118_out, as_in, undriven_20);
  D_Flip_Flop dff24 (.D(w103_out), .clk(VCLK), .Q(dff24_q), .Qn(w120));  // open: preset, reset
  D_Flip_Flop dff25 (.D(dff12_qn), .clk(not_1_out), .reset(not_47_out));  // open: Q, Qn, preset
  or w132 (w132_out, w72_out, undriven_21);
  or w134 (w134_out, w66_out, undriven_22);
  not w142 (w142_out, w137_out);
  not not_51 (not_51_out, dff30_q);
  not not_52 (not_52_out, not_51_out);
  D_Flip_Flop d_ff_10 (.D(d_ff_9_q), .clk(undriven_24), .Q(d_ff_10_q), .reset(not_33_out));  // open: Qn, preset
  D_Flip_Flop dff31 (.D(vd_in[8]), .clk(w96_out), .Q(dff31_q), .reset(not_53_out));  // open: Qn, preset
  not not_53 (not_53_out, undriven_23);
  Multiplexer multiplexer_1 (.in0(undriven_23), .in1(dff31_q), .out(w226), .sel(m3));
  nand w133 (w133_out, w132_out, w118_out, FDC, o_TIME, w94_out, w134_out);
  not not_54 (not_54_out, not_52_out);
  nand w164 (w164_out, w226, w34_out);
  not w207 (w207_out, not_54_out);
  D_Flip_Flop d_ff_11 (.D(d_ff_10_q), .clk(undriven_24), .reset(not_33_out));  // open: Q, Qn, preset
  not not_55 (not_55_out, m3);
  or w211 (w211_out, not_55_out, va_in[22], as_in);
  nand w200 (w200_out, w133_out, w249_out);
  nor w163 (w163_out, w82, vd_in[8], va_in[21], m3);
  xor w228 (w228_out, va_in[21], in_22);
  // AND_Gate w266 has open pins: in0=undriven_25, in1=undriven_26, in2=undriven_26, out=open
  nor nor_5 (nor_5_out, w69_out, dff26_qn);
  or w171 (w171_out, m3, w220_out, va_in[22]);
  or w170 (w170_out, dff26_qn, xor_delay_12x_1_out_2);
  not not_56 (not_56_out, w228_out);
  not not_57 (not_57_out, dff32_q);
  D_Flip_Flop dff33 (.D(undriven_27), .clk(as_in), .Q(dff33_q), .Qn(dff33_qn), .preset(not_57_out));  // open: reset
  D_Flip_Flop dff32 (.D(w38), .clk(as_in), .Q(dff32_q));  // open: Qn, preset, reset
  or w169 (w169_out, nor_5_out, undriven_28, undriven_29);
  and w167 (w167_out, w170_out, w202_out);
  and and_3 (and_3_out, xor_delay_12x_1_out_2, w206_out);
  or w202 (w202_out, not_56_out, multiplexer_2_out);
  not not_58 (not_58_out, w211_out);
  not w205 (w205_out, w228_out);
  not not_59 (not_59_out, va_in[20]);
  Multiplexer multiplexer_2 (.in0(w248_out), .in1(w254_out), .out(multiplexer_2_out), .sel(dff26_qn));
  or w215 (w215_out, va_in[20], w82);
  or w220 (w220_out, w82, dff44_qn);
  or w232 (w232_out, w228_out, va_in[20], w248_out);
  or w234 (w234_out, w228_out, va_in[20], w211_out);
  or w173 (w173_out, w101_out, dff26_qn);
  nand w204 (w204_out, not_58_out, w69_out, w205_out, va_in[20]);
  or w206 (w206_out, not_59_out, w228_out, w254_out);
  nand w235 (w235_out, w232_out, w234_out);
  nand w172 (w172_out, w169_out, w167_out, w171_out, w173_out);
  // NOR_Gate w268 has open pins: in0=w152, in1=undriven_30, in2=pal_trap_out, out=open
  nand w198 (w198_out, and_3_out, w101_out, w204_out);
  not not_60 (w230, w235_out);
  // NOR_Gate w183 has open pins: in0=dff23_q, in1=undriven_31, in2=undriven_32, in3=dff33_q, out=open
  not not_61 (w162, w172_out);
  not not_62 (w196, w198_out);
  D_Flip_Flop dff44 (.D(w207_out), .clk(not_5_out), .Qn(dff44_qn));  // open: Q, preset, reset
  // NOR_Gate w222 has open pins: in0=w200_out, in1=w152, out=open
  not not_63 (not_63_out, m3);
  or w223 (w223_out, w48_out, not_63_out, undriven_33);
  // NOT_Gate w259 has open pins: in=w223_out, out=open
  or w254 (w254_out, va_in[22], w223_out);
  or w248 (w248_out, w269_out, w223_out);
  or w238 (w238_out, w223_out, cas0);
  not w274 (w274_out, cas0);
  nand w249 (w249_out, undriven_35, undriven_34);
  and w269 (w269_out, va_in[22], w274_out, dff45_q);
  not not_64 (not_64_out, w223_out);
  not not_65 (not_65_out, not_64_out);
  D_Flip_Flop dff45 (.D(va_in[22]), .clk(w274_out), .Q(dff45_q), .preset(not_65_out));  // open: Qn, reset
  xor_delay_36x xor_delay_36x_1 (.in_1(w238_out), .out_2(xor_delay_36x_1_out_2));
  not not_66 (not_66_out, undriven_36);
  D_Flip_Flop dff46 (.D(dff46_qn), .clk(w274_out), .Q(dff46_q), .Qn(dff46_qn), .preset(not_66_out));  // open: reset
  or or_5 (or_5_out, xor_delay_36x_1_out_2, dff46_q);
  xor_delay_12x xor_delay_12x_1 (.in_1(or_5_out), .out_2(xor_delay_12x_1_out_2));

  assign rw_out = zwr_in;
endmodule

module cnt_bit (
  input  cin,
  input  val,
  input  load,
  input  clk,
  input  res,
  output cout,
  output q,
  output nq
);

  wire multiplexer_1_out, not_1_out, xor_1_out;

  and and_1 (cout, cin, q);
  xor xor_1 (xor_1_out, cin, q);
  not not_1 (not_1_out, res);
  Multiplexer multiplexer_1 (.in0(val), .in1(xor_1_out), .out(multiplexer_1_out), .sel(load));
  D_Flip_Flop d_ff_1 (.D(multiplexer_1_out), .clk(clk), .Q(q), .Qn(nq), .reset(not_1_out));  // open: preset
endmodule

module xor_delay_6x (
  input  in_1,
  output out_2
);

  wire xor_1_out, xor_2_out, xor_3_out, xor_4_out, xor_5_out;

  xor xor_1 (xor_1_out, in_1, 1'b0);
  xor xor_2 (xor_2_out, xor_1_out, 1'b0);
  xor xor_3 (xor_3_out, xor_2_out, 1'b0);
  xor xor_4 (xor_4_out, xor_3_out, 1'b0);
  xor xor_5 (xor_5_out, xor_4_out, 1'b0);
  xor xor_6 (out_2, xor_5_out, 1'b0);
endmodule

module xor_delay_40x (
  input  in_1,
  output out_2
);

  wire xor_1_out, xor_2_out, xor_3_out, xor_4_out, xor_5_out, xor_6_out, xor_7_out, xor_8_out, xor_9_out,
       xor_10_out, xor_11_out, xor_12_out, xor_13_out, xor_14_out, xor_15_out, xor_16_out, xor_17_out,
       xor_18_out, xor_19_out, xor_20_out, xor_21_out, xor_22_out, xor_23_out, xor_24_out, xor_25_out,
       xor_26_out, xor_27_out, xor_28_out, xor_29_out, xor_30_out, xor_31_out, xor_33_out, xor_34_out,
       xor_35_out, xor_36_out, xor_37_out, xor_38_out, xor_39_out, xor_40_out;

  xor xor_1 (xor_1_out, in_1, 1'b0);
  xor xor_2 (xor_2_out, xor_40_out, 1'b0);
  xor xor_3 (xor_3_out, xor_1_out, 1'b0);
  xor xor_4 (xor_4_out, xor_2_out, 1'b0);
  xor xor_5 (xor_5_out, xor_3_out, 1'b0);
  xor xor_6 (xor_6_out, xor_4_out, 1'b0);
  xor xor_7 (xor_7_out, xor_5_out, 1'b0);
  xor xor_8 (xor_8_out, xor_6_out, 1'b0);
  xor xor_9 (xor_9_out, xor_7_out, 1'b0);
  xor xor_10 (xor_10_out, xor_8_out, 1'b0);
  xor xor_11 (xor_11_out, xor_9_out, 1'b0);
  xor xor_12 (xor_12_out, xor_10_out, 1'b0);
  xor xor_13 (xor_13_out, xor_11_out, 1'b0);
  xor xor_14 (xor_14_out, xor_12_out, 1'b0);
  xor xor_15 (xor_15_out, xor_13_out, 1'b0);
  xor xor_16 (xor_16_out, xor_14_out, 1'b0);
  xor xor_17 (xor_17_out, xor_15_out, 1'b0);
  xor xor_18 (xor_18_out, xor_16_out, 1'b0);
  xor xor_19 (xor_19_out, xor_17_out, 1'b0);
  xor xor_20 (xor_20_out, xor_18_out, 1'b0);
  xor xor_21 (xor_21_out, xor_19_out, 1'b0);
  xor xor_22 (xor_22_out, xor_20_out, 1'b0);
  xor xor_23 (xor_23_out, xor_21_out, 1'b0);
  xor xor_24 (xor_24_out, xor_22_out, 1'b0);
  xor xor_25 (xor_25_out, xor_23_out, 1'b0);
  xor xor_26 (xor_26_out, xor_24_out, 1'b0);
  xor xor_27 (xor_27_out, xor_25_out, 1'b0);
  xor xor_28 (xor_28_out, xor_26_out, 1'b0);
  xor xor_29 (xor_29_out, xor_27_out, 1'b0);
  xor xor_30 (xor_30_out, xor_28_out, 1'b0);
  xor xor_31 (xor_31_out, xor_29_out, 1'b0);
  xor xor_32 (out_2, xor_30_out, 1'b0);
  xor xor_33 (xor_33_out, xor_31_out, 1'b0);
  xor xor_34 (xor_34_out, xor_33_out, 1'b0);
  xor xor_35 (xor_35_out, xor_34_out, 1'b0);
  xor xor_36 (xor_36_out, xor_35_out, 1'b0);
  xor xor_37 (xor_37_out, xor_36_out, 1'b0);
  xor xor_38 (xor_38_out, xor_37_out, 1'b0);
  xor xor_39 (xor_39_out, xor_38_out, 1'b0);
  xor xor_40 (xor_40_out, xor_39_out, 1'b0);
endmodule

module xor_delay_48x (
  input  in_1,
  output out_2
);

  wire xor_1_out, xor_2_out, xor_3_out, xor_4_out, xor_5_out, xor_6_out, xor_7_out, xor_8_out, xor_9_out,
       xor_10_out, xor_11_out, xor_12_out, xor_13_out, xor_14_out, xor_15_out, xor_16_out, xor_17_out,
       xor_18_out, xor_19_out, xor_20_out, xor_21_out, xor_22_out, xor_23_out, xor_24_out, xor_25_out,
       xor_26_out, xor_27_out, xor_28_out, xor_29_out, xor_30_out, xor_31_out, xor_32_out, xor_33_out,
       xor_34_out, xor_35_out, xor_36_out, xor_37_out, xor_38_out, xor_39_out, xor_40_out, xor_41_out,
       xor_42_out, xor_43_out, xor_44_out, xor_45_out, xor_46_out, xor_47_out;

  xor xor_1 (xor_1_out, in_1, 1'b0);
  xor xor_2 (xor_2_out, xor_47_out, 1'b0);
  xor xor_3 (xor_3_out, xor_1_out, 1'b0);
  xor xor_4 (xor_4_out, xor_2_out, 1'b0);
  xor xor_5 (xor_5_out, xor_3_out, 1'b0);
  xor xor_6 (xor_6_out, xor_4_out, 1'b0);
  xor xor_7 (xor_7_out, xor_5_out, 1'b0);
  xor xor_8 (xor_8_out, xor_6_out, 1'b0);
  xor xor_9 (xor_9_out, xor_7_out, 1'b0);
  xor xor_10 (xor_10_out, xor_8_out, 1'b0);
  xor xor_11 (xor_11_out, xor_9_out, 1'b0);
  xor xor_12 (xor_12_out, xor_10_out, 1'b0);
  xor xor_13 (xor_13_out, xor_11_out, 1'b0);
  xor xor_14 (xor_14_out, xor_12_out, 1'b0);
  xor xor_15 (xor_15_out, xor_13_out, 1'b0);
  xor xor_16 (xor_16_out, xor_14_out, 1'b0);
  xor xor_17 (xor_17_out, xor_15_out, 1'b0);
  xor xor_18 (xor_18_out, xor_16_out, 1'b0);
  xor xor_19 (xor_19_out, xor_17_out, 1'b0);
  xor xor_20 (xor_20_out, xor_18_out, 1'b0);
  xor xor_21 (xor_21_out, xor_19_out, 1'b0);
  xor xor_22 (xor_22_out, xor_20_out, 1'b0);
  xor xor_23 (xor_23_out, xor_21_out, 1'b0);
  xor xor_24 (xor_24_out, xor_22_out, 1'b0);
  xor xor_25 (xor_25_out, xor_23_out, 1'b0);
  xor xor_26 (xor_26_out, xor_24_out, 1'b0);
  xor xor_27 (xor_27_out, xor_25_out, 1'b0);
  xor xor_28 (xor_28_out, xor_26_out, 1'b0);
  xor xor_29 (xor_29_out, xor_27_out, 1'b0);
  xor xor_30 (xor_30_out, xor_28_out, 1'b0);
  xor xor_31 (xor_31_out, xor_29_out, 1'b0);
  xor xor_32 (xor_32_out, xor_30_out, 1'b0);
  xor xor_33 (xor_33_out, xor_31_out, 1'b0);
  xor xor_34 (xor_34_out, xor_32_out, 1'b0);
  xor xor_35 (xor_35_out, xor_33_out, 1'b0);
  xor xor_36 (xor_36_out, xor_34_out, 1'b0);
  xor xor_37 (xor_37_out, xor_35_out, 1'b0);
  xor xor_38 (xor_38_out, xor_36_out, 1'b0);
  xor xor_39 (xor_39_out, xor_37_out, 1'b0);
  xor xor_40 (xor_40_out, xor_38_out, 1'b0);
  xor xor_41 (xor_41_out, xor_39_out, 1'b0);
  xor xor_42 (xor_42_out, xor_40_out, 1'b0);
  xor xor_43 (xor_43_out, xor_41_out, 1'b0);
  xor xor_44 (xor_44_out, xor_42_out, 1'b0);
  xor xor_45 (xor_45_out, xor_43_out, 1'b0);
  xor xor_46 (xor_46_out, xor_44_out, 1'b0);
  xor xor_47 (xor_47_out, xor_45_out, 1'b0);
  xor xor_48 (out_2, xor_46_out, 1'b0);
endmodule

module xor_delay_36x (
  input  in_1,
  output out_2
);

  wire xor_1_out, xor_2_out, xor_3_out, xor_4_out, xor_5_out, xor_6_out, xor_7_out, xor_8_out, xor_9_out,
       xor_10_out, xor_11_out, xor_12_out, xor_13_out, xor_14_out, xor_15_out, xor_16_out, xor_17_out,
       xor_18_out, xor_19_out, xor_20_out, xor_21_out, xor_22_out, xor_23_out, xor_25_out, xor_26_out,
       xor_27_out, xor_28_out, xor_29_out, xor_30_out, xor_31_out, xor_32_out, xor_33_out, xor_34_out,
       xor_35_out, xor_36_out;

  xor xor_1 (xor_1_out, in_1, 1'b0);
  xor xor_2 (xor_2_out, xor_36_out, 1'b0);
  xor xor_3 (xor_3_out, xor_1_out, 1'b0);
  xor xor_4 (xor_4_out, xor_2_out, 1'b0);
  xor xor_5 (xor_5_out, xor_3_out, 1'b0);
  xor xor_6 (xor_6_out, xor_4_out, 1'b0);
  xor xor_7 (xor_7_out, xor_5_out, 1'b0);
  xor xor_8 (xor_8_out, xor_6_out, 1'b0);
  xor xor_9 (xor_9_out, xor_7_out, 1'b0);
  xor xor_10 (xor_10_out, xor_8_out, 1'b0);
  xor xor_11 (xor_11_out, xor_9_out, 1'b0);
  xor xor_12 (xor_12_out, xor_10_out, 1'b0);
  xor xor_13 (xor_13_out, xor_11_out, 1'b0);
  xor xor_14 (xor_14_out, xor_12_out, 1'b0);
  xor xor_15 (xor_15_out, xor_13_out, 1'b0);
  xor xor_16 (xor_16_out, xor_14_out, 1'b0);
  xor xor_17 (xor_17_out, xor_15_out, 1'b0);
  xor xor_18 (xor_18_out, xor_16_out, 1'b0);
  xor xor_19 (xor_19_out, xor_17_out, 1'b0);
  xor xor_20 (xor_20_out, xor_18_out, 1'b0);
  xor xor_21 (xor_21_out, xor_19_out, 1'b0);
  xor xor_22 (xor_22_out, xor_20_out, 1'b0);
  xor xor_23 (xor_23_out, xor_21_out, 1'b0);
  xor xor_24 (out_2, xor_22_out, 1'b0);
  xor xor_25 (xor_25_out, xor_23_out, 1'b0);
  xor xor_26 (xor_26_out, xor_25_out, 1'b0);
  xor xor_27 (xor_27_out, xor_26_out, 1'b0);
  xor xor_28 (xor_28_out, xor_27_out, 1'b0);
  xor xor_29 (xor_29_out, xor_28_out, 1'b0);
  xor xor_30 (xor_30_out, xor_29_out, 1'b0);
  xor xor_31 (xor_31_out, xor_30_out, 1'b0);
  xor xor_32 (xor_32_out, xor_31_out, 1'b0);
  xor xor_33 (xor_33_out, xor_32_out, 1'b0);
  xor xor_34 (xor_34_out, xor_33_out, 1'b0);
  xor xor_35 (xor_35_out, xor_34_out, 1'b0);
  xor xor_36 (xor_36_out, xor_35_out, 1'b0);
endmodule

module xor_delay_12x (
  input  in_1,
  output out_2
);

  wire xor_1_out, xor_2_out, xor_3_out, xor_4_out, xor_5_out, xor_6_out, xor_7_out, xor_8_out, xor_9_out,
       xor_10_out, xor_11_out;

  xor xor_1 (xor_1_out, in_1, 1'b0);
  xor xor_2 (xor_2_out, xor_1_out, 1'b0);
  xor xor_3 (xor_3_out, xor_2_out, 1'b0);
  xor xor_4 (xor_4_out, xor_3_out, 1'b0);
  xor xor_5 (xor_5_out, xor_4_out, 1'b0);
  xor xor_6 (xor_6_out, xor_5_out, 1'b0);
  xor xor_7 (xor_7_out, xor_6_out, 1'b0);
  xor xor_8 (xor_8_out, xor_7_out, 1'b0);
  xor xor_9 (xor_9_out, xor_8_out, 1'b0);
  xor xor_10 (xor_10_out, xor_9_out, 1'b0);
  xor xor_11 (xor_11_out, xor_10_out, 1'b0);
  xor xor_12 (out_2, xor_11_out, 1'b0);
endmodule
