// Logisim project iochip.circ as structural Verilog: 4 circuits, main circuit main
module main (
  input  A6i,
  input  B0i,
  input  B2i,
  input  in_4,
  input  A4i,
  input  w2,
  input  A5i,
  input  in_8,
  input  in_9,
  input  TEST,
  input  SRES,
  input  VCLK,
  input  PAL,
  input  C0i,
  input  C1i,
  input  C2i,
  input  C3i,
  input  C4i,
  input  C5i,
  input  C6i,
  input  [7:0] ZD_in,
  input  [7:0] ZA_in,
  input  [6:0] VA_in,
  input  [15:0] VD_in,
  input  nM3,
  input  LWR,
  input  CAS0,
  input  IO,
  input  in_29,
  input  in_30,
  input  in_31,
  output C4o,
  output out_33,
  output C0d,
  output out_35,
  output out_36,
  output out_37,
  output out_38,
  output out_39,
  output out_40,
  output C0o,
  output C1o,
  output C2o,
  output C3o,
  output C5o,
  output C6o,
  output [6:0] VA_out,
  output bc1,
  output bc2,
  output bc3,
  output bc4,
  output bc5
);

  wire and_1_out, and_2_out, and_3_out, and_4_out, and_5_out, and_6_out, and_7_out, and_8_out, and_9_out,
       and_10_out, and_11_out, and_12_out, and_13_out, and_14_out, and_15_out, and_16_out, and_17_out,
       and_18_out, and_19_out, and_20_out, and_21_out, and_22_out, and_23_out, and_24_out, and_25_out,
       and_26_out, and_27_out, and_28_out, and_29_out, buffer_9_out, buffer_10_out, clk_div_1_out_4,
       d_ff_1_q, d_ff_1_qn, d_ff_2_q, d_ff_3_q, d_ff_4_q, d_ff_5_q, d_ff_6_q, d_ff_15_q, d_ff_16_q,
       d_ff_17_q, d_ff_18_q, d_ff_19_q, d_ff_20_q, d_ff_21_q, d_ff_23_q, d_ff_23_qn, d_ff_24_q, d_ff_24_qn,
       d_ff_25_qn, d_ff_26_qn, d_ff_27_qn, d_ff_28_qn, d_ff_29_qn, d_ff_30_qn, d_ff_31_qn, d_ff_32_qn,
       d_ff_33_q, d_ff_33_qn, d_ff_34_q, d_ff_34_qn, d_ff_35_q, d_ff_35_qn, d_ff_36_q, d_ff_36_qn, d_ff_37_q,
       d_ff_38_q, d_ff_39_q, d_ff_40_q, d_ff_41_q, d_ff_42_q, d_ff_43_q, d_ff_44_q, d_ff_45_q, d_ff_45_qn,
       d_ff_46_q, d_ff_46_qn, d_ff_47_q, d_ff_47_qn, d_ff_50_qn, d_ff_52_q, d_ff_52_qn, d_ff_53_q, d_ff_55_q,
       d_ff_55_qn, d_ff_56_q, d_ff_56_qn, d_ff_58_q, d_ff_58_qn, d_ff_59_q, d_ff_59_qn, d_ff_60_q,
       d_ff_60_qn, d_ff_62_q, d_ff_63_q, d_ff_64_q, d_ff_64_qn, d_ff_66_q, d_ff_67_q, d_ff_67_qn, d_ff_69_q,
       d_ff_71_q, d_ff_71_qn, d_ff_72_q, d_ff_74_q, d_ff_77_q, d_ff_79_q, d_ff_80_q, d_ff_80_qn, d_ff_82_q,
       d_ff_83_q, d_ff_83_qn, d_ff_85_q, d_ff_87_q, d_ff_88_q, d_ff_88_qn, d_ff_90_q, d_ff_91_q, d_ff_91_qn,
       d_ff_93_q, multiplexer_16_out, multiplexer_17_out, multiplexer_18_out, multiplexer_19_out,
       multiplexer_20_out, multiplexer_21_out, multiplexer_22_out, multiplexer_23_out, multiplexer_24_out,
       nand_1_out, nand_2_out, nand_3_out, nand_4_out, nand_5_out, nand_6_out, nand_7_out, nand_8_out,
       nand_9_out, nand_10_out, nand_11_out, nand_12_out, nand_13_out, nand_14_out, nand_15_out, nand_17_out,
       nand_18_out, nand_19_out, nand_20_out, nand_21_out, nand_22_out, nand_23_out, nand_24_out,
       nand_27_out, nand_30_out, nand_33_out, nand_34_out, nand_36_out, nand_37_out, nand_39_out,
       nand_40_out, nand_41_out, nand_42_out, nand_43_out, nand_44_out, nand_45_out, nand_46_out,
       nand_47_out, nand_48_out, nand_49_out, nand_50_out, nand_51_out, nand_52_out, nand_53_out,
       nand_54_out, nand_55_out, nand_56_out, nand_57_out, nand_58_out, nand_59_out, nand_60_out,
       nand_61_out, nand_62_out, nand_63_out, nand_64_out, nand_65_out, nand_66_out, nand_67_out,
       nand_68_out, nor_1_out, nor_2_out, nor_4_out, nor_5_out, nor_6_out, nor_7_out, nor_8_out, nor_9_out,
       nor_10_out, nor_11_out, nor_12_out, nor_13_out, nor_14_out, nor_15_out, nor_16_out, nor_17_out,
       not_1_out, not_2_out, not_3_out, not_4_out, not_5_out, not_6_out, not_7_out, not_8_out, not_9_out,
       not_10_out, not_11_out, not_12_out, not_13_out, not_14_out, not_15_out, not_16_out, not_17_out,
       not_20_out, not_21_out, not_22_out, not_23_out, not_24_out, not_25_out, not_26_out, not_27_out,
       not_28_out, not_29_out, not_30_out, not_31_out, not_32_out, not_33_out, not_34_out, not_35_out,
       not_36_out, not_37_out, not_38_out, not_39_out, not_40_out, not_41_out, not_42_out, not_43_out,
       not_44_out, not_45_out, not_46_out, not_47_out, not_48_out, not_49_out, not_50_out, not_51_out,
       not_52_out, not_53_out, not_54_out, not_55_out, not_56_out, not_57_out, not_58_out, not_59_out,
       not_60_out, or_1_out, or_2_out, or_3_out, or_6_out, or_7_out, or_8_out, or_9_out, or_10_out,
       or_11_out, or_12_out, or_13_out, or_14_out, or_15_out, or_16_out, or_17_out, or_18_out, or_19_out,
       or_20_out, or_21_out, undriven, xor_1_out, xor_delay_6x_1_out_2, xor_delay_6x_2_out_2,
       xor_delay_6x_3_out_2, xor_delay_6x_4_out_2, xor_delay_6x_5_out_2, xor_delay_6x_6_out_2,
       xor_delay_6x_7_out_2, xor_delay_6x_8_out_2;
  wire [6:0] multiplexer_26_out;
  wire [7:0] buffer_1_out, d_ff_7_q, d_ff_92_q, multiplexer_5_out, multiplexer_14_out, multiplexer_15_out,
       multiplexer_25_out, multiplexer_33_out, multiplexer_34_out;

  buf buffer_1 (buffer_1_out[0], C0i);
  buf buffer_2 (buffer_1_out[1], C1i);
  buf buffer_3 (buffer_1_out[2], C2i);
  buf buffer_4 (buffer_1_out[3], C3i);
  buf buffer_5 (buffer_1_out[4], C4i);
  buf buffer_6 (buffer_1_out[5], C5i);
  buf buffer_7 (buffer_1_out[6], C6i);
  and and_1 (and_1_out, or_1_out, nand_1_out, or_6_out);
  and and_2 (and_2_out, or_3_out, or_2_out);
  nand nand_1 (nand_1_out, nM3, and_6_out);
  Multiplexer multiplexer_1 (.in0(B0i), .in1(A6i), .sel(w2));  // open: out
  Multiplexer multiplexer_2 (.in0(A4i), .in1(A4i), .sel(w2));  // open: out
  buf and_3 (and_3_out, A5i);  // AND_Gate
  not not_1 (not_1_out, in_9);
  D_Flip_Flop d_ff_1 (.D(SRES), .clk(VCLK), .Q(d_ff_1_q), .Qn(d_ff_1_qn));  // open: preset, reset
  not not_2 (not_2_out, PAL);
  and and_4 (and_4_out, and_1_out, nM3);
  Multiplexer multiplexer_3 (.in0(B2i), .in1(in_4), .sel(w2));  // open: out
  D_Flip_Flop d_ff_2 (.D(buffer_1_out[3]), .clk(nand_39_out), .Q(d_ff_2_q), .reset(not_3_out));  // open: Qn, preset
  D_Flip_Flop d_ff_3 (.D(buffer_1_out[4]), .clk(nand_39_out), .Q(d_ff_3_q), .reset(not_3_out));  // open: Qn, preset
  D_Flip_Flop d_ff_4 (.D(buffer_1_out[5]), .clk(nand_39_out), .Q(d_ff_4_q), .reset(not_3_out));  // open: Qn, preset
  D_Flip_Flop d_ff_5 (.D(buffer_1_out[6]), .clk(nand_39_out), .Q(d_ff_5_q), .reset(not_3_out));  // open: Qn, preset
  D_Flip_Flop d_ff_6 (.D(buffer_1_out[7]), .clk(nand_39_out), .Q(d_ff_6_q), .reset(not_3_out));  // open: Qn, preset
  not not_3 (not_3_out, in_8);
  not not_4 (not_4_out, multiplexer_24_out);
  not not_5 (not_5_out, d_ff_46_q);
  D_Flip_Flop d_ff_7 (.D(buffer_1_out[0]), .clk(nand_22_out), .Q(d_ff_7_q[0]), .reset(not_9_out));  // open: Qn, preset
  D_Flip_Flop d_ff_8 (.D(buffer_1_out[1]), .clk(nand_22_out), .Q(d_ff_7_q[1]), .reset(not_9_out));  // open: Qn, preset
  D_Flip_Flop d_ff_9 (.D(buffer_1_out[2]), .clk(nand_22_out), .Q(d_ff_7_q[2]), .reset(not_9_out));  // open: Qn, preset
  D_Flip_Flop d_ff_10 (.D(buffer_1_out[3]), .clk(nand_22_out), .Q(d_ff_7_q[3]), .reset(not_9_out));  // open: Qn, preset
  D_Flip_Flop d_ff_11 (.D(buffer_1_out[4]), .clk(nand_22_out), .Q(d_ff_7_q[4]), .reset(not_9_out));  // open: Qn, preset
  D_Flip_Flop d_ff_12 (.D(buffer_1_out[5]), .clk(nand_22_out), .Q(d_ff_7_q[5]), .reset(not_9_out));  // open: Qn, preset
  D_Flip_Flop d_ff_13 (.D(buffer_1_out[6]), .clk(nand_22_out), .Q(d_ff_7_q[6]), .reset(not_9_out));  // open: Qn, preset
  D_Flip_Flop d_ff_14 (.D(buffer_1_out[7]), .clk(nand_22_out), .Q(d_ff_7_q[7]), .reset(not_9_out));  // open: Qn, preset
  D_Flip_Flop d_ff_15 (.D(buffer_1_out[0]), .clk(nand_19_out), .Q(d_ff_15_q), .reset(not_6_out));  // open: Qn, preset
  D_Flip_Flop d_ff_16 (.D(buffer_1_out[1]), .clk(nand_19_out), .Q(d_ff_16_q), .reset(not_6_out));  // open: Qn, preset
  D_Flip_Flop d_ff_17 (.D(buffer_1_out[2]), .clk(nand_19_out), .Q(d_ff_17_q), .reset(not_6_out));  // open: Qn, preset
  D_Flip_Flop d_ff_18 (.D(buffer_1_out[3]), .clk(nand_19_out), .Q(d_ff_18_q), .reset(not_6_out));  // open: Qn, preset
  D_Flip_Flop d_ff_19 (.D(buffer_1_out[4]), .clk(nand_19_out), .Q(d_ff_19_q), .reset(not_6_out));  // open: Qn, preset
  D_Flip_Flop d_ff_20 (.D(buffer_1_out[5]), .clk(nand_19_out), .Q(d_ff_20_q), .reset(not_6_out));  // open: Qn, preset
  D_Flip_Flop d_ff_21 (.D(buffer_1_out[6]), .clk(nand_19_out), .Q(d_ff_21_q), .reset(not_6_out));  // open: Qn, preset
  D_Flip_Flop d_ff_22 (
    .D(buffer_1_out[7]), .clk(nand_19_out), .Q(buffer_1_out[7]), .reset(not_6_out));  // open: Qn, preset
  // NOT_Gate not_6 has open pins: in=open, out=not_6_out
  and and_5 (and_5_out, CAS0, IO);
  not not_7 (not_7_out, ZA_in[0]);
  not not_8 (not_8_out, CAS0);
  Multiplexer multiplexer_4 (.in0(and_3_out), .in1(A5i), .sel(w2));  // open: out
  D_Flip_Flop d_ff_23 (
    .D(d_ff_23_qn), .clk(not_4_out), .Q(d_ff_23_q), .Qn(d_ff_23_qn), .reset(not_1_out));  // open: preset
  D_Flip_Flop d_ff_24 (
    .D(d_ff_24_qn), .clk(not_5_out), .Q(d_ff_24_q), .Qn(d_ff_24_qn), .reset(not_1_out));  // open: preset
  buf buffer_8 (out_33, d_ff_1_qn);
  // NOT_Gate not_9 has open pins: in=open, out=not_9_out
  nor nor_1 (nor_1_out, CAS0, IO, and_21_out);
  and and_6 (and_6_out, not_7_out, CAS0);
  or or_1 (or_1_out, CAS0, in_29);
  or or_2 (or_2_out, CAS0, in_31);
  or or_3 (or_3_out, not_8_out, in_29);
  nor nor_2 (nor_2_out, in_29, in_30);
  or or_4 (bc2, and_1_out, in_30);
  nor nor_3 (bc3, and_4_out, in_30);
  or or_5 (bc4, and_2_out, in_30);
  or or_6 (or_6_out, not_8_out, in_31);
  nor nor_4 (nor_4_out, in_31, in_30);
  not not_10 (not_10_out, d_ff_5_q);
  buf buffer_9 (buffer_9_out, d_ff_5_q);
  not not_11 (not_11_out, d_ff_6_q);
  buf buffer_10 (buffer_10_out, d_ff_6_q);
  not not_12 (not_12_out, nand_37_out);
  not not_13 (not_13_out, d_ff_23_q);
  not not_14 (not_14_out, d_ff_24_q);
  buf buffer_11 (C0o, d_ff_15_q);
  buf buffer_12 (C1o, d_ff_16_q);
  buf buffer_13 (C2o, d_ff_17_q);
  buf buffer_14 (C3o, d_ff_18_q);
  buf buffer_15 (C5o, d_ff_20_q);
  buf buffer_16 (C6o, d_ff_21_q);
  not not_15 (not_15_out, multiplexer_5_out[6]);
  not not_16 (not_16_out, multiplexer_5_out[7]);
  D_Flip_Flop #(.trigger("high")) d_ff_25 (
    .D(buffer_1_out[0]), .clk(not_12_out), .Qn(d_ff_25_qn));  // open: Q, preset, reset
  D_Flip_Flop #(.trigger("high")) d_ff_26 (
    .D(buffer_1_out[1]), .clk(not_12_out), .Qn(d_ff_26_qn));  // open: Q, preset, reset
  D_Flip_Flop #(.trigger("high")) d_ff_27 (
    .D(buffer_1_out[2]), .clk(not_12_out), .Qn(d_ff_27_qn));  // open: Q, preset, reset
  D_Flip_Flop #(.trigger("high")) d_ff_28 (
    .D(buffer_1_out[3]), .clk(not_12_out), .Qn(d_ff_28_qn));  // open: Q, preset, reset
  D_Flip_Flop #(.trigger("high")) d_ff_29 (
    .D(buffer_1_out[4]), .clk(not_12_out), .Qn(d_ff_29_qn));  // open: Q, preset, reset
  D_Flip_Flop #(.trigger("high")) d_ff_30 (
    .D(buffer_1_out[5]), .clk(not_12_out), .Qn(d_ff_30_qn));  // open: Q, preset, reset
  D_Flip_Flop #(.trigger("high")) d_ff_31 (
    .D(buffer_1_out[6]), .clk(not_12_out), .Qn(d_ff_31_qn));  // open: Q, preset, reset
  D_Flip_Flop #(.trigger("high")) d_ff_32 (
    .D(buffer_1_out[7]), .clk(not_12_out), .Qn(d_ff_32_qn));  // open: Q, preset, reset
  D_Flip_Flop d_ff_33 (
    .D(d_ff_33_qn), .clk(not_13_out), .Q(d_ff_33_q), .Qn(d_ff_33_qn), .reset(not_1_out));  // open: preset
  D_Flip_Flop d_ff_34 (
    .D(d_ff_34_qn), .clk(not_14_out), .Q(d_ff_34_q), .Qn(d_ff_34_qn), .reset(not_1_out));  // open: preset
  clk_div clk_div_1 (.VCLK(VCLK), .Reset(d_ff_1_qn), .PAL(not_2_out), .out_4(clk_div_1_out_4));
  not not_17 (not_17_out, d_ff_7_q[7]);
  Multiplexer multiplexer_5 (.in0(ZA_in[0]), .in1(VA_in[0]), .out(multiplexer_5_out[0]), .sel(nM3));
  Multiplexer multiplexer_6 (.in0(ZA_in[1]), .in1(VA_in[1]), .out(multiplexer_5_out[1]), .sel(nM3));
  Multiplexer multiplexer_7 (.in0(ZA_in[2]), .in1(VA_in[2]), .out(multiplexer_5_out[2]), .sel(nM3));
  Multiplexer multiplexer_8 (.in0(ZA_in[3]), .in1(VA_in[3]), .out(multiplexer_5_out[3]), .sel(nM3));
  Multiplexer multiplexer_9 (.in0(ZA_in[4]), .in1(VA_in[4]), .out(multiplexer_5_out[4]), .sel(nM3));
  Multiplexer multiplexer_10 (.in0(ZA_in[5]), .in1(VA_in[5]), .out(multiplexer_5_out[5]), .sel(nM3));
  Multiplexer multiplexer_11 (.in0(ZA_in[6]), .in1(VA_in[6]), .out(multiplexer_5_out[6]), .sel(nM3));
  Multiplexer multiplexer_12 (.in0(ZA_in[7]), .in1(1'b0), .out(multiplexer_5_out[7]), .sel(nM3));
  nor nor_5 (nor_5_out, multiplexer_5_out[4], multiplexer_5_out[5], multiplexer_5_out[6], multiplexer_5_out[7]);
  nand nand_2 (nand_2_out, 1'b1, multiplexer_5_out[1], multiplexer_5_out[2], multiplexer_5_out[3], multiplexer_5_out[4], multiplexer_5_out[5], not_15_out, not_16_out);
  nor nor_6 (nor_6_out, multiplexer_5_out[6], multiplexer_5_out[7]);
  nor nor_7 (nor_7_out, multiplexer_5_out[2], multiplexer_5_out[3], multiplexer_5_out[4]);
  and and_7 (and_7_out, multiplexer_5_out[2], multiplexer_5_out[3], multiplexer_5_out[4]);
  or or_7 (or_7_out, multiplexer_5_out[5], multiplexer_5_out[1]);
  not not_18 (bc1, nor_2_out);
  not not_19 (bc5, nor_4_out);
  nor nor_8 (nor_8_out, not_17_out, buffer_1_out[6]);
  nor nor_9 (nor_9_out, nor_7_out, and_7_out);
  and and_8 (and_8_out, multiplexer_24_out, not_10_out, not_11_out);
  and and_9 (and_9_out, d_ff_23_q, buffer_9_out, not_11_out);
  and and_10 (and_10_out, d_ff_33_q, not_10_out, buffer_10_out);
  and and_11 (and_11_out, d_ff_46_q, buffer_9_out, buffer_10_out);
  and and_12 (and_12_out, d_ff_46_q, not_10_out, not_11_out);
  and and_13 (and_13_out, d_ff_24_q, buffer_9_out, not_11_out);
  and and_14 (and_14_out, d_ff_34_q, not_10_out, buffer_10_out);
  and and_15 (and_15_out, d_ff_47_q, buffer_9_out, buffer_10_out);
  not not_20 (not_20_out, d_ff_33_q);
  not not_21 (not_21_out, d_ff_34_q);
  Multiplexer multiplexer_13 (.in0(not_2_out), .in1(clk_div_1_out_4), .sel(TEST));  // open: out
  not not_22 (not_22_out, d_ff_7_q[4]);
  not not_23 (not_23_out, d_ff_7_q[5]);
  not not_24 (not_24_out, multiplexer_5_out[0]);
  and and_16 (and_16_out, nM3, multiplexer_5_out[1]);
  and and_17 (and_17_out, nM3, multiplexer_5_out[2]);
  and and_18 (and_18_out, multiplexer_5_out[3], nM3);
  not not_25 (not_25_out, multiplexer_5_out[3]);
  nand nand_3 (nand_3_out, nM3, nor_5_out);
  not not_26 (not_26_out, multiplexer_5_out[3]);
  or or_8 (or_8_out, LWR, IO);
  Multiplexer #(.width(8)) multiplexer_14 (.in0(ZD_in), .in1(VD_in[7:0]), .out(multiplexer_14_out), .sel(nM3));
  Multiplexer #(.width(8)) multiplexer_15 (
    .in0(VD_in[7:0]), .in1(VD_in[15:8]), .out(multiplexer_15_out), .sel(and_6_out));
  Multiplexer multiplexer_16 (.in0(d_ff_25_qn), .in1(d_ff_38_q), .out(multiplexer_16_out), .sel(nand_4_out));
  Multiplexer multiplexer_17 (.in0(d_ff_26_qn), .in1(d_ff_39_q), .out(multiplexer_17_out), .sel(nand_4_out));
  Multiplexer multiplexer_18 (.in0(d_ff_27_qn), .in1(d_ff_40_q), .out(multiplexer_18_out), .sel(nand_4_out));
  Multiplexer multiplexer_19 (.in0(d_ff_28_qn), .in1(d_ff_41_q), .out(multiplexer_19_out), .sel(nand_4_out));
  Multiplexer multiplexer_20 (.in0(d_ff_29_qn), .in1(d_ff_42_q), .out(multiplexer_20_out), .sel(nand_4_out));
  Multiplexer multiplexer_21 (.in0(d_ff_30_qn), .in1(d_ff_43_q), .out(multiplexer_21_out), .sel(nand_4_out));
  Multiplexer multiplexer_22 (.in0(d_ff_31_qn), .in1(d_ff_44_q), .out(multiplexer_22_out), .sel(nand_4_out));
  Multiplexer multiplexer_23 (.in0(d_ff_32_qn), .in1(1'b0), .out(multiplexer_23_out), .sel(nand_4_out));
  D_Flip_Flop d_ff_35 (
    .D(d_ff_35_qn), .clk(not_20_out), .Q(d_ff_35_q), .Qn(d_ff_35_qn), .reset(not_1_out));  // open: preset
  D_Flip_Flop d_ff_36 (
    .D(d_ff_36_qn), .clk(not_21_out), .Q(d_ff_36_q), .Qn(d_ff_36_qn), .reset(not_1_out));  // open: preset
  Multiplexer multiplexer_24 (.in0(clk_div_1_out_4), .in1(VCLK), .out(multiplexer_24_out), .sel(TEST));
  not not_27 (not_27_out, d_ff_7_q[0]);
  not not_28 (not_28_out, d_ff_7_q[1]);
  not not_29 (not_29_out, d_ff_7_q[2]);
  not not_30 (not_30_out, d_ff_7_q[3]);
  and and_19 (and_19_out, not_22_out, not_47_out);
  or or_9 (or_9_out, not_23_out, d_ff_4_q);
  not not_31 (not_31_out, d_ff_7_q[6]);
  xor xor_1 (xor_1_out, multiplexer_5_out[0], nM3);
  nor nor_10 (nor_10_out, not_24_out, nM3);
  nor nor_11 (nor_11_out, not_25_out, nand_3_out, and_5_out);
  nor nor_12 (nor_12_out, not_26_out, or_8_out, nand_3_out);
  nor nor_13 (nor_13_out, multiplexer_5_out[3], or_8_out, nand_3_out);
  or or_10 (or_10_out, or_8_out, nM3, nand_2_out);
  or or_11 (or_11_out, nM3, nor_9_out, nor_6_out, or_7_out);
  D_Flip_Flop d_ff_37 (.D(multiplexer_16_out), .clk(or_12_out), .Q(d_ff_37_q), .reset(not_35_out));  // open: Qn, preset
  D_Flip_Flop d_ff_38 (.D(multiplexer_17_out), .clk(or_12_out), .Q(d_ff_38_q), .reset(not_35_out));  // open: Qn, preset
  D_Flip_Flop d_ff_39 (.D(multiplexer_18_out), .clk(or_12_out), .Q(d_ff_39_q), .reset(not_35_out));  // open: Qn, preset
  D_Flip_Flop d_ff_40 (.D(multiplexer_19_out), .clk(or_12_out), .Q(d_ff_40_q), .reset(not_35_out));  // open: Qn, preset
  D_Flip_Flop d_ff_41 (.D(multiplexer_20_out), .clk(or_12_out), .Q(d_ff_41_q), .reset(not_35_out));  // open: Qn, preset
  D_Flip_Flop d_ff_42 (.D(multiplexer_21_out), .clk(or_12_out), .Q(d_ff_42_q), .reset(not_35_out));  // open: Qn, preset
  D_Flip_Flop d_ff_43 (.D(multiplexer_22_out), .clk(or_12_out), .Q(d_ff_43_q), .reset(not_35_out));  // open: Qn, preset
  D_Flip_Flop d_ff_44 (.D(multiplexer_23_out), .clk(or_12_out), .Q(d_ff_44_q), .reset(not_35_out));  // open: Qn, preset
  buf or_12 (or_12_out, or_14_out);  // OR_Gate
  or or_13 (or_13_out, and_8_out, and_9_out, and_10_out, and_11_out);
  or or_14 (or_14_out, and_12_out, and_13_out, and_14_out, and_15_out);
  buf buffer_17 (C0d, not_27_out);
  buf buffer_18 (out_35, not_28_out);
  buf buffer_19 (out_36, not_29_out);
  buf buffer_20 (out_37, not_30_out);
  buf buffer_21 (out_38, and_19_out);
  buf buffer_22 (out_39, or_9_out);
  buf buffer_23 (out_40, not_31_out);
  or or_15 (or_15_out, and_16_out, nor_10_out);
  Multiplexer #(.width(8)) multiplexer_25 (.out(multiplexer_25_out), .sel(and_18_out));  // open: in0, in1
  not not_32 (not_32_out, d_ff_35_q);
  not not_33 (not_33_out, d_ff_36_q);
  Multiplexer multiplexer_26 (.in0(ZA_in[0]), .in1(ZA_in[1]), .out(multiplexer_26_out[0]), .sel(nM3));
  Multiplexer multiplexer_27 (.in0(ZA_in[1]), .in1(ZA_in[2]), .out(multiplexer_26_out[1]), .sel(nM3));
  Multiplexer multiplexer_28 (.in0(ZA_in[2]), .in1(ZA_in[3]), .out(multiplexer_26_out[2]), .sel(nM3));
  Multiplexer multiplexer_29 (.in0(ZA_in[3]), .in1(ZA_in[4]), .out(multiplexer_26_out[3]), .sel(nM3));
  Multiplexer multiplexer_30 (.in0(ZA_in[4]), .in1(ZA_in[5]), .out(multiplexer_26_out[4]), .sel(nM3));
  Multiplexer multiplexer_31 (.in0(ZA_in[5]), .in1(ZA_in[6]), .out(multiplexer_26_out[5]), .sel(nM3));
  Multiplexer multiplexer_32 (.in0(ZA_in[6]), .in1(ZA_in[7]), .out(multiplexer_26_out[6]), .sel(nM3));
  and and_20 (and_20_out, or_10_out, or_11_out);
  or or_16 (or_16_out, or_10_out, multiplexer_5_out[0]);
  or or_17 (or_17_out, or_10_out, not_24_out);
  not not_34 (not_34_out, d_ff_1_q);
  not not_35 (not_35_out, d_ff_3_q);
  not not_36 (not_36_out, d_ff_37_q);
  D_Flip_Flop d_ff_45 (
    .D(nand_43_out), .clk(or_14_out), .Q(d_ff_45_q), .Qn(d_ff_45_qn), .reset(not_37_out));  // open: preset
  not not_37 (not_37_out, d_ff_1_q);
  or or_18 (or_18_out, d_ff_56_q, nor_17_out);
  or or_19 (or_19_out, nor_17_out, d_ff_50_qn);
  D_Flip_Flop d_ff_46 (
    .D(d_ff_46_qn), .clk(not_32_out), .Q(d_ff_46_q), .Qn(d_ff_46_qn), .reset(not_1_out));  // open: preset
  D_Flip_Flop d_ff_47 (
    .D(d_ff_47_qn), .clk(not_33_out), .Q(d_ff_47_q), .Qn(d_ff_47_qn), .reset(not_1_out));  // open: preset
  and and_21 (and_21_out, nand_3_out, and_20_out);
  D_Flip_Flop d_ff_48 (.D(VD_in[4]), .clk(or_16_out), .reset(not_38_out));  // open: Q, Qn, preset
  not not_38 (not_38_out, d_ff_1_q);
  D_Flip_Flop d_ff_49 (.D(multiplexer_14_out[7]), .clk(or_17_out), .preset(not_34_out));  // open: Q, Qn, reset
  Multiplexer #(.width(8)) multiplexer_33 (
    .in0(multiplexer_15_out), .in1(multiplexer_25_out), .out(multiplexer_33_out), .sel(nor_1_out));
  Multiplexer #(.width(8)) multiplexer_34 (
    .in0(ZD_in), .in1(multiplexer_25_out), .out(multiplexer_34_out), .sel(nor_1_out));
  nand nand_4 (nand_4_out, d_ff_66_q, 1'b1, d_ff_59_qn, d_ff_52_qn, d_ff_55_qn, d_ff_45_qn);
  nand nand_5 (nand_5_out, d_ff_59_q, d_ff_45_qn);
  nand nand_6 (nand_6_out, d_ff_59_qn, d_ff_66_q, d_ff_45_qn);
  nand nand_7 (nand_7_out, d_ff_59_q, d_ff_52_q, d_ff_45_q);
  nand nand_8 (nand_8_out, d_ff_45_q, d_ff_52_q);
  nand nand_9 (nand_9_out, d_ff_52_q, d_ff_59_q, d_ff_55_q);
  nand nand_10 (nand_10_out, d_ff_59_q, d_ff_55_q, d_ff_45_q);
  nand nand_11 (nand_11_out, d_ff_59_q, d_ff_45_q);
  nand nand_12 (nand_12_out, d_ff_59_q, d_ff_52_q);
  D_Flip_Flop d_ff_50 (.D(nand_13_out), .clk(or_13_out), .Qn(d_ff_50_qn), .reset(not_45_out));  // open: Q, preset
  nand nand_13 (nand_13_out, or_18_out, or_19_out);
  not not_39 (not_39_out, undriven);
  D_Flip_Flop d_ff_51 (.D(multiplexer_14_out[6]), .clk(or_17_out), .preset(not_34_out));  // open: Q, Qn, reset
  not not_40 (not_40_out, nand_4_out);
  and and_22 (and_22_out, not_36_out, nand_4_out);
  D_Flip_Flop d_ff_52 (
    .D(nand_44_out), .clk(or_14_out), .Q(d_ff_52_q), .Qn(d_ff_52_qn), .reset(not_37_out));  // open: preset
  nand nand_14 (nand_14_out, d_ff_52_qn, d_ff_45_qn, d_ff_55_q, d_ff_59_q);
  not not_41 (not_41_out, d_ff_56_q);
  assign VA_out = not_39_out ? multiplexer_26_out : 7'bz;  // Controlled_Buffer controlled_buffer_1
  not not_42 (not_42_out, multiplexer_5_out[0]);
  not not_43 (not_43_out, multiplexer_5_out[1]);
  not not_44 (not_44_out, multiplexer_5_out[2]);
  and and_23 (and_23_out, not_40_out, d_ff_58_q);
  nor nor_14 (nor_14_out, d_ff_58_q, 1'b0);
  D_Flip_Flop d_ff_53 (.D(and_22_out), .clk(or_14_out), .Q(d_ff_53_q), .preset(not_35_out));  // open: Qn, reset
  not not_45 (not_45_out, d_ff_1_q);
  not not_46 (not_46_out, and_27_out);
  nor nor_15 (nor_15_out, and_28_out, nor_8_out);
  D_Flip_Flop d_ff_54 (.D(multiplexer_14_out[5]), .clk(or_17_out), .preset(not_34_out));  // open: Q, Qn, reset
  nor nor_16 (nor_16_out, and_23_out, nor_14_out);
  not not_47 (not_47_out, d_ff_3_q);
  D_Flip_Flop d_ff_55 (
    .D(nand_45_out), .clk(or_14_out), .Q(d_ff_55_q), .Qn(d_ff_55_qn), .reset(not_37_out));  // open: preset
  D_Flip_Flop d_ff_56 (
    .D(nand_56_out), .clk(or_13_out), .Q(d_ff_56_q), .Qn(d_ff_56_qn), .preset(not_45_out));  // open: reset
  nor nor_17 (nor_17_out, d_ff_50_qn, not_46_out, d_ff_71_q);
  nand nand_15 (nand_15_out, d_ff_60_q, d_ff_64_q);
  // NAND_Gate nand_16 has open pins: in0=nor_13_out, in1=not_42_out, in2=not_43_out, in3=not_44_out, out=open
  nand nand_17 (nand_17_out, nor_13_out, multiplexer_5_out[0], not_43_out, not_44_out);
  nand nand_18 (nand_18_out, nor_13_out, not_42_out, multiplexer_5_out[1], not_44_out);
  nand nand_19 (nand_19_out, nor_13_out, multiplexer_5_out[0], multiplexer_5_out[1], not_44_out);
  nand nand_20 (nand_20_out, nor_13_out, not_42_out, not_43_out, multiplexer_5_out[2]);
  nand nand_21 (nand_21_out, nor_13_out, multiplexer_5_out[0], not_43_out, multiplexer_5_out[2]);
  nand nand_22 (nand_22_out, nor_13_out, not_42_out, multiplexer_5_out[1], multiplexer_5_out[2]);
  nand nand_23 (nand_23_out, nor_13_out, multiplexer_5_out[0], multiplexer_5_out[1], multiplexer_5_out[2]);
  nand nand_24 (nand_24_out, nor_11_out, not_42_out, not_43_out, not_44_out);
  // NAND_Gate nand_25 has open pins: in0=nor_11_out, in1=multiplexer_5_out[0], in2=not_43_out, in3=not_44_out, out=open
  // NAND_Gate nand_26 has open pins: in0=nor_11_out, in1=not_42_out, in2=multiplexer_5_out[1], in3=not_44_out, out=open
  nand nand_27 (nand_27_out, nor_11_out, multiplexer_5_out[0], multiplexer_5_out[1], not_44_out);
  // NAND_Gate nand_28 has open pins: in0=nor_11_out, in1=not_42_out, in2=not_43_out, in3=multiplexer_5_out[2], out=open
  // NAND_Gate nand_29 has open pins: in0=nor_11_out, in1=multiplexer_5_out[0], in2=not_43_out, in3=multiplexer_5_out[2], out=open
  nand nand_30 (nand_30_out, nor_11_out, not_42_out, multiplexer_5_out[1], multiplexer_5_out[2]);
  // NAND_Gate nand_31 has open pins: in0=nor_11_out, in1=multiplexer_5_out[0], in2=multiplexer_5_out[1], in3=multiplexer_5_out[2], out=open
  // NAND_Gate nand_32 has open pins: in0=nor_12_out, in1=not_42_out, in2=not_43_out, in3=not_44_out, out=open
  nand nand_33 (nand_33_out, nor_12_out, multiplexer_5_out[0], not_43_out, not_44_out);
  nand nand_34 (nand_34_out, nor_12_out, not_42_out, multiplexer_5_out[1], not_44_out);
  // NAND_Gate nand_35 has open pins: in0=nor_12_out, in1=multiplexer_5_out[0], in2=multiplexer_5_out[1], in3=not_44_out, out=open
  nand nand_36 (nand_36_out, nor_12_out, not_42_out, not_43_out, multiplexer_5_out[2]);
  nand nand_37 (nand_37_out, nor_12_out, multiplexer_5_out[0], not_43_out, multiplexer_5_out[2]);
  // NAND_Gate nand_38 has open pins: in0=nor_12_out, in1=not_42_out, in2=multiplexer_5_out[1], in3=multiplexer_5_out[2], out=open
  nand nand_39 (nand_39_out, nor_12_out, multiplexer_5_out[0], multiplexer_5_out[1], multiplexer_5_out[2]);
  not not_48 (not_48_out, or_14_out);
  and and_24 (and_24_out, d_ff_53_q, d_ff_3_q);
  and and_25 (and_25_out, not_47_out, d_ff_19_q);
  not not_49 (not_49_out, nor_17_out);
  nand nand_40 (nand_40_out, d_ff_60_q, d_ff_67_qn);
  nand nand_41 (nand_41_out, d_ff_67_qn, d_ff_64_q);
  nand nand_42 (nand_42_out, d_ff_64_qn, d_ff_67_q, d_ff_60_qn);
  D_Flip_Flop d_ff_57 (.D(multiplexer_14_out[4]), .clk(or_17_out), .preset(not_34_out));  // open: Q, Qn, reset
  not not_50 (not_50_out, nand_37_out);
  D_Flip_Flop d_ff_58 (
    .D(nor_16_out), .clk(not_51_out), .Q(d_ff_58_q), .Qn(d_ff_58_qn), .preset(not_50_out), .reset(not_52_out));
  not not_51 (not_51_out, not_48_out);
  not not_52 (not_52_out, d_ff_1_q);
  or or_20 (or_20_out, and_24_out, and_25_out);
  D_Flip_Flop d_ff_59 (
    .D(nand_46_out), .clk(or_14_out), .Q(d_ff_59_q), .Qn(d_ff_59_qn), .reset(not_37_out));  // open: preset
  nand nand_43 (nand_43_out, nand_5_out, nand_6_out, nand_7_out);
  nand nand_44 (nand_44_out, nand_6_out, nand_8_out, nand_14_out);
  nand nand_45 (nand_45_out, nand_6_out, nand_7_out, nand_9_out, nand_10_out);
  nand nand_46 (nand_46_out, nand_8_out, nand_14_out, nand_11_out, nand_12_out);
  nand nand_47 (nand_47_out, d_ff_59_q, d_ff_55_qn, d_ff_52_qn, d_ff_45_qn);
  D_Flip_Flop d_ff_60 (
    .D(nand_48_out), .clk(or_13_out), .Q(d_ff_60_q), .Qn(d_ff_60_qn), .preset(not_45_out));  // open: reset
  nand nand_48 (nand_48_out, not_49_out, nand_15_out, nand_42_out, nand_40_out);
  nand nand_49 (nand_49_out, nand_41_out, not_49_out, nand_51_out);
  nand nand_50 (nand_50_out, d_ff_67_q, nor_17_out);
  nand nand_51 (nand_51_out, d_ff_67_q, d_ff_64_qn);
  nand nand_52 (nand_52_out, d_ff_64_qn, d_ff_67_q, d_ff_60_qn, not_41_out);
  nand nand_53 (nand_53_out, d_ff_56_q, d_ff_60_q);
  nand nand_54 (nand_54_out, d_ff_56_q, d_ff_67_qn);
  nand nand_55 (nand_55_out, d_ff_56_q, d_ff_64_q);
  D_Flip_Flop d_ff_61 (.D(multiplexer_14_out[3]), .clk(or_17_out), .preset(not_34_out));  // open: Q, Qn, reset
  not not_53 (not_53_out, d_ff_58_qn);
  D_Flip_Flop d_ff_62 (.D(1'b0), .clk(d_ff_63_q), .Q(d_ff_62_q), .preset(not_53_out), .reset(not_52_out));  // open: Qn
  buf buffer_24 (C4o, or_20_out);
  D_Flip_Flop d_ff_63 (.D(nand_47_out), .clk(or_14_out), .Q(d_ff_63_q), .preset(not_37_out));  // open: Qn, reset
  D_Flip_Flop d_ff_64 (
    .D(nand_50_out), .clk(or_13_out), .Q(d_ff_64_q), .Qn(d_ff_64_qn), .preset(not_45_out));  // open: reset
  nand nand_56 (nand_56_out, nand_52_out, 1'b1, not_49_out, nand_53_out, nand_54_out, nand_55_out);
  D_Flip_Flop d_ff_65 (.D(multiplexer_14_out[2]), .clk(or_17_out), .preset(not_34_out));  // open: Q, Qn, reset
  D_Flip_Flop d_ff_66 (.D(d_ff_62_q), .clk(or_13_out), .Q(d_ff_66_q));  // open: Qn, preset, reset
  D_Flip_Flop d_ff_67 (
    .D(nand_49_out), .clk(or_13_out), .Q(d_ff_67_q), .Qn(d_ff_67_qn), .reset(not_45_out));  // open: preset
  D_Flip_Flop d_ff_68 (.D(multiplexer_14_out[1]), .clk(or_17_out), .preset(not_34_out));  // open: Q, Qn, reset
  not not_54 (not_54_out, d_ff_4_q);
  not not_55 (not_55_out, and_29_out);
  not not_56 (not_56_out, 1'b1);
  and and_26 (and_26_out, d_ff_71_q, 1'b1);
  D_Flip_Flop d_ff_69 (.D(and_26_out), .clk(d_ff_56_qn), .Q(d_ff_69_q), .reset(not_57_out));  // open: Qn, preset
  D_Flip_Flop d_ff_70 (.D(multiplexer_14_out[0]), .clk(or_17_out), .preset(not_34_out));  // open: Q, Qn, reset
  D_Flip_Flop d_ff_71 (
    .D(buffer_1_out[5]), .clk(or_13_out), .Q(d_ff_71_q), .Qn(d_ff_71_qn), .preset(not_54_out));  // open: reset
  D_Flip_Flop d_ff_72 (.D(1'b1), .clk(or_21_out), .Q(d_ff_72_q), .reset(not_55_out));  // open: Qn, preset
  D_Flip_Flop d_ff_73 (
    .D(xor_delay_6x_1_out_2), .clk(or_21_out), .Q(d_ff_92_q[7]), .reset(not_56_out));  // open: Qn, preset
  D_Flip_Flop d_ff_74 (.D(d_ff_69_q), .clk(d_ff_56_qn), .Q(d_ff_74_q), .reset(not_57_out));  // open: Qn, preset
  not not_57 (not_57_out, d_ff_4_q);
  nand nand_57 (nand_57_out, d_ff_80_q, d_ff_91_q);
  D_Flip_Flop d_ff_75 (.D(d_ff_71_qn), .clk(or_21_out), .reset(not_55_out));  // open: Q, Qn, preset
  xor_delay_6x xor_delay_6x_1 (.in_1(d_ff_69_q), .out_2(xor_delay_6x_1_out_2));
  nand nand_58 (nand_58_out, d_ff_80_qn, d_ff_91_qn, d_ff_50_qn, not_58_out);
  nand nand_59 (nand_59_out, d_ff_80_q, d_ff_83_q, d_ff_88_qn, d_ff_91_qn);
  not not_58 (not_58_out, d_ff_71_q);
  D_Flip_Flop d_ff_76 (
    .D(xor_delay_6x_2_out_2), .clk(or_21_out), .Q(d_ff_92_q[6]), .reset(not_56_out));  // open: Qn, preset
  xor_delay_6x xor_delay_6x_2 (.in_1(d_ff_74_q), .out_2(xor_delay_6x_2_out_2));
  D_Flip_Flop d_ff_77 (.D(d_ff_74_q), .clk(d_ff_56_qn), .Q(d_ff_77_q), .reset(not_57_out));  // open: Qn, preset
  not not_59 (not_59_out, d_ff_1_q);
  nand nand_60 (nand_60_out, nand_58_out, nand_59_out, nand_61_out, nand_57_out);
  and and_27 (and_27_out, d_ff_80_qn, d_ff_91_qn);
  nand nand_61 (nand_61_out, d_ff_88_q, d_ff_91_qn, d_ff_80_q);
  nand nand_62 (nand_62_out, d_ff_80_q, d_ff_91_qn, d_ff_83_qn);
  nand nand_63 (nand_63_out, d_ff_80_q, d_ff_88_q, d_ff_91_q);
  nand nand_64 (nand_64_out, d_ff_88_q, d_ff_80_q, d_ff_83_q);
  nand nand_65 (nand_65_out, d_ff_91_q, d_ff_80_q, d_ff_83_q);
  and and_28 (and_28_out, d_ff_72_q, d_ff_2_q);
  D_Flip_Flop d_ff_78 (
    .D(xor_delay_6x_3_out_2), .clk(or_21_out), .Q(d_ff_92_q[5]), .reset(not_56_out));  // open: Qn, preset
  xor_delay_6x xor_delay_6x_3 (.in_1(d_ff_77_q), .out_2(xor_delay_6x_3_out_2));
  D_Flip_Flop d_ff_79 (.D(d_ff_77_q), .clk(d_ff_56_qn), .Q(d_ff_79_q), .reset(not_57_out));  // open: Qn, preset
  D_Flip_Flop d_ff_80 (
    .D(nand_60_out), .clk(d_ff_56_qn), .Q(d_ff_80_q), .Qn(d_ff_80_qn), .reset(not_59_out));  // open: preset
  nand nand_66 (nand_66_out, nand_59_out, nand_58_out, nand_61_out, nand_62_out);
  nand nand_67 (nand_67_out, nand_62_out, nand_58_out, nand_59_out, nand_63_out);
  nand nand_68 (nand_68_out, nand_62_out, nand_58_out, nand_64_out, nand_65_out);
  D_Flip_Flop d_ff_81 (
    .D(xor_delay_6x_4_out_2), .clk(or_21_out), .Q(d_ff_92_q[4]), .reset(not_56_out));  // open: Qn, preset
  xor_delay_6x xor_delay_6x_4 (.in_1(d_ff_79_q), .out_2(xor_delay_6x_4_out_2));
  D_Flip_Flop d_ff_82 (.D(d_ff_79_q), .clk(d_ff_56_qn), .Q(d_ff_82_q), .reset(not_60_out));  // open: Qn, preset
  D_Flip_Flop d_ff_83 (
    .D(nand_68_out), .clk(d_ff_56_qn), .Q(d_ff_83_q), .Qn(d_ff_83_qn), .reset(not_59_out));  // open: preset
  D_Flip_Flop d_ff_84 (
    .D(xor_delay_6x_5_out_2), .clk(or_21_out), .Q(d_ff_92_q[3]), .reset(not_56_out));  // open: Qn, preset
  D_Flip_Flop d_ff_85 (.D(d_ff_82_q), .clk(d_ff_56_qn), .Q(d_ff_85_q), .reset(not_60_out));  // open: Qn, preset
  not not_60 (not_60_out, d_ff_4_q);
  D_Flip_Flop d_ff_86 (
    .D(xor_delay_6x_6_out_2), .clk(or_21_out), .Q(d_ff_92_q[2]), .reset(not_56_out));  // open: Qn, preset
  xor_delay_6x xor_delay_6x_5 (.in_1(d_ff_82_q), .out_2(xor_delay_6x_5_out_2));
  D_Flip_Flop d_ff_87 (.D(d_ff_85_q), .clk(d_ff_56_qn), .Q(d_ff_87_q), .reset(not_60_out));  // open: Qn, preset
  D_Flip_Flop d_ff_88 (
    .D(nand_67_out), .clk(d_ff_56_qn), .Q(d_ff_88_q), .Qn(d_ff_88_qn), .reset(not_59_out));  // open: preset
  xor_delay_6x xor_delay_6x_6 (.in_1(d_ff_85_q), .out_2(xor_delay_6x_6_out_2));
  D_Flip_Flop d_ff_89 (
    .D(xor_delay_6x_7_out_2), .clk(or_21_out), .Q(d_ff_92_q[1]), .reset(not_56_out));  // open: Qn, preset
  xor_delay_6x xor_delay_6x_7 (.in_1(d_ff_87_q), .out_2(xor_delay_6x_7_out_2));
  D_Flip_Flop d_ff_90 (.D(d_ff_87_q), .clk(d_ff_56_qn), .Q(d_ff_90_q), .reset(not_60_out));  // open: Qn, preset
  D_Flip_Flop d_ff_91 (
    .D(nand_66_out), .clk(d_ff_56_qn), .Q(d_ff_91_q), .Qn(d_ff_91_qn), .reset(not_59_out));  // open: preset
  D_Flip_Flop d_ff_92 (
    .D(xor_delay_6x_8_out_2), .clk(or_21_out), .Q(d_ff_92_q[0]), .reset(not_56_out));  // open: Qn, preset
  xor_delay_6x xor_delay_6x_8 (.in_1(d_ff_90_q), .out_2(xor_delay_6x_8_out_2));
  and and_29 (and_29_out, nand_30_out, d_ff_1_q);
  D_Flip_Flop d_ff_93 (.D(nand_62_out), .clk(d_ff_56_qn), .Q(d_ff_93_q), .preset(not_59_out));  // open: Qn, reset
  or or_21 (or_21_out, d_ff_93_q, d_ff_56_qn);

  // Notes on the sheet:
  //   w5
endmodule

module cnt_bit (
  input  cin,
  input  val,
  input  load,
  input  clk,
  input  res,
  output cout,
  output q,
  output nq
);

  wire multiplexer_1_out, not_1_out, xor_1_out;

  and and_1 (cout, cin, q);
  xor xor_1 (xor_1_out, cin, q);
  not not_1 (not_1_out, res);
  Multiplexer multiplexer_1 (.in0(val), .in1(xor_1_out), .out(multiplexer_1_out), .sel(load));
  D_Flip_Flop d_ff_1 (.D(multiplexer_1_out), .clk(clk), .Q(q), .Qn(nq), .reset(not_1_out));  // open: preset
endmodule

module clk_div (
  input  VCLK,
  input  Reset,
  input  PAL,
  output out_4
);

  wire and_1_out, and_2_out, and_3_out, and_4_out, cnt_bit_1_cout, cnt_bit_1_nq, cnt_bit_2_cout,
       cnt_bit_2_nq, cnt_bit_3_cout, cnt_bit_3_nq, cnt_bit_4_cout, cnt_bit_4_nq, cnt_bit_5_cout,
       cnt_bit_5_nq, cnt_bit_6_cout, cnt_bit_6_nq, cnt_bit_7_nq, cnt_bit_8_nq, nor_1_out, nor_2_out,
       nor_3_out;

  and and_1 (and_1_out, nor_3_out, 1'b1, and_4_out);
  and and_2 (and_2_out, nor_3_out, 1'b1, 1'b1);
  cnt_bit cnt_bit_1 (
    .cin(and_1_out), .val(1'b1), .load(nor_3_out), .clk(VCLK), .res(1'b1), .cout(cnt_bit_1_cout),
    .nq(cnt_bit_1_nq));  // open: q
  cnt_bit cnt_bit_2 (
    .cin(and_2_out), .val(PAL), .load(nor_3_out), .clk(VCLK), .res(1'b1), .cout(cnt_bit_2_cout),
    .nq(cnt_bit_2_nq));  // open: q
  nor nor_1 (nor_1_out, cnt_bit_1_nq, cnt_bit_3_nq, cnt_bit_5_nq, cnt_bit_7_nq);
  nor nor_2 (nor_2_out, cnt_bit_2_nq, cnt_bit_8_nq, cnt_bit_6_nq, cnt_bit_4_nq);
  cnt_bit cnt_bit_3 (
    .cin(cnt_bit_1_cout), .val(1'b0), .load(nor_3_out), .clk(VCLK), .res(1'b1), .cout(cnt_bit_3_cout),
    .nq(cnt_bit_3_nq));  // open: q
  and and_3 (and_3_out, nor_1_out, and_4_out);
  cnt_bit cnt_bit_4 (
    .cin(cnt_bit_2_cout), .val(1'b0), .load(nor_3_out), .clk(VCLK), .res(1'b1), .cout(cnt_bit_4_cout),
    .nq(cnt_bit_4_nq));  // open: q
  and and_4 (and_4_out, nor_2_out, 1'b1);
  nor nor_3 (nor_3_out, Reset, and_3_out);
  cnt_bit cnt_bit_5 (
    .cin(cnt_bit_3_cout), .val(1'b0), .load(nor_3_out), .clk(VCLK), .res(1'b1), .cout(cnt_bit_5_cout),
    .q(out_4), .nq(cnt_bit_5_nq));
  cnt_bit cnt_bit_6 (
    .cin(cnt_bit_4_cout), .val(1'b1), .load(nor_3_out), .clk(VCLK), .res(1'b1), .cout(cnt_bit_6_cout),
    .nq(cnt_bit_6_nq));  // open: q
  cnt_bit cnt_bit_7 (
    .cin(cnt_bit_5_cout), .val(1'b1), .load(nor_3_out), .clk(VCLK), .res(1'b1), .nq(cnt_bit_7_nq));  // open: cout, q
  cnt_bit cnt_bit_8 (
    .cin(cnt_bit_6_cout), .val(1'b1), .load(nor_3_out), .clk(VCLK), .res(1'b1), .nq(cnt_bit_8_nq));  // open: cout, q
endmodule

module xor_delay_6x (
  input  in_1,
  output out_2
);

  wire xor_1_out, xor_2_out, xor_3_out, xor_4_out, xor_5_out;

  xor xor_1 (xor_1_out, in_1, 1'b0);
  xor xor_2 (xor_2_out, xor_1_out, 1'b0);
  xor xor_3 (xor_3_out, xor_2_out, 1'b0);
  xor xor_4 (xor_4_out, xor_3_out, 1'b0);
  xor xor_5 (xor_5_out, xor_4_out, 1'b0);
  xor xor_6 (out_2, xor_5_out, 1'b0);
endmodule
