// Logisim project YM3438.circ as structural Verilog: 20 circuits, main circuit main
module main (
  input  M,
  input  in_2,
  input  in_3,
  input  in_4,
  input  in_5,
  input  in_6,
  input  in_7,
  input  in_8,
  input  in_9,
  input  in_10,
  input  in_11,
  input  in_12,
  input  in_13,
  input  in_14,
  input  in_15,
  input  in_16,
  input  in_17,
  input  in_18,
  input  in_19,
  input  in_20,
  input  in_21,
  input  in_22,
  input  in_23,
  input  in_24,
  input  in_25,
  input  in_26,
  input  in_27,
  input  in_28,
  input  in_29,
  input  in_30,
  input  in_31,
  input  in_32,
  input  in_33,
  input  in_34,
  input  in_35,
  input  in_36,
  input  in_37,
  input  in_38,
  input  in_39,
  input  in_40,
  input  in_41,
  input  in_42,
  input  in_43,
  input  in_44,
  input  in_45,
  input  in_46,
  input  in_47,
  input  in_48,
  input  in_49,
  input  in_50
);

  wire C1, C2, clock_1_out, clock_2_g_15, envelope_1_env0, envelope_1_env1, envelope_1_env2, envelope_1_env3,
       envelope_1_env4, envelope_1_env5, envelope_1_env6, envelope_1_env7, envelope_1_env8, envelope_1_env9,
       FCLK1, FCLK2, fsm_1_g_66, fsm_1_g_67, fsm_1_g_68, fsm_1_g_69, fsm_1_g_70, fsm_1_g_74, fsm_1_g_75,
       fsm_1_g_77, fsm_1_g_79, fsm_1_g_100, fsm_1_g_109, fsm_1_g_114, fsm_1_g_118, fsm_1_g_122, fsm_1_g_123,
       fsm_1_g_124, fsm_1_g_125, fsm_1_g_127, lfo_1_lfo0, lfo_1_lfo1, lfo_1_lfo2, lfo_1_lfo2_1, lfo_1_lfo3,
       lfo_1_lfo3_1, lfo_1_lfo4, lfo_1_lfo4_1, lfo_1_lfo5, lfo_1_lfo5_1, lfo_1_lfo6, nFCLK1, nFCLK2,
       op_1_op0, op_1_op1, op_1_op2, op_1_op3, op_1_op4, op_1_op5, op_1_op6, op_1_op7, op_1_op8, op_1_op9,
       op_1_op10, op_1_op11, op_1_op12, op_1_op13, out_1_dac0, out_1_dac1, out_1_dac2, out_1_dac3,
       out_1_dac4, out_1_dac5, out_1_dac6, out_1_dac7, out_1_dac8, out_1_mol_sel, out_1_mor_sel,
       phase_gen_1_g_3652, phase_gen_1_g_3654, phase_gen_1_g_3656_2, phase_gen_1_g_3658, phase_gen_1_g_3660,
       phase_gen_1_pg0, phase_gen_1_pg1, phase_gen_1_pg2, phase_gen_1_pg3, phase_gen_1_pg4, phase_gen_1_pg5,
       phase_gen_1_pg6, phase_gen_1_pg7, phase_gen_1_pg8, phase_gen_1_pg9;

  Clock clock_1 (.out(clock_1_out));
  CLOCK clock_2 (
    .M(clock_1_out), .g_932(in_4), .g_15(clock_2_g_15), .FCLK1(FCLK1), .nFCLK1(nFCLK1), .FCLK2(FCLK2),
    .nFCLK2(nFCLK2), .C2(C2), .C1(C1));
  FSM fsm_1 (
    .C2(C2), .C1(C1), .FCLK2(FCLK2), .FCLK1(FCLK1), .g_15(clock_2_g_15), .g_77(fsm_1_g_77),
    .g_118(fsm_1_g_118), .g_123(fsm_1_g_123), .g_114(fsm_1_g_114), .g_127(fsm_1_g_127), .g_122(fsm_1_g_122),
    .g_124(fsm_1_g_124), .g_75(fsm_1_g_75), .g_79(fsm_1_g_79), .g_109(fsm_1_g_109), .g_74(fsm_1_g_74),
    .g_3080(in_37), .g_3079(in_39), .g_3078(in_41), .g_345(in_43), .g_125(fsm_1_g_125), .g_69(fsm_1_g_69),
    .g_66(fsm_1_g_66), .g_67(fsm_1_g_67), .g_68(fsm_1_g_68), .g_100(fsm_1_g_100), .g_70(fsm_1_g_70));
  LFO lfo_1 (
    .FCLK2(FCLK2), .FCLK1(FCLK1), .g_77(fsm_1_g_77), .g_366(in_27), .g_1932(in_29), .g_655(in_30),
    .g_764(in_31), .g_763(in_32), .g_654(in_34), .LFO0(lfo_1_lfo0), .LFO1(lfo_1_lfo1), .LFO2(lfo_1_lfo2),
    .LFO3(lfo_1_lfo3), .LFO4(lfo_1_lfo4), .LFO5(lfo_1_lfo5), .LFO6(lfo_1_lfo6), .LFO5_1(lfo_1_lfo5_1),
    .LFO2_1(lfo_1_lfo2_1), .LFO3_1(lfo_1_lfo3_1), .LFO4_1(lfo_1_lfo4_1));
  PHASE_GEN phase_gen_1 (
    .FCLK2(FCLK2), .FCLK1(FCLK1), .g_69(fsm_1_g_69), .g_370(in_5), .g_1875(in_6), .g_2944(in_7),
    .g_2934(in_8), .g_2223(in_9), .g_2231(in_10), .g_2227(in_11), .g_2969(in_12), .g_2949(in_13),
    .g_2940(in_14), .g_2469(in_15), .g_2471(in_16), .g_2475(in_17), .g_2473(in_18), .g_3067(in_20),
    .g_3068(in_22), .g_3069(in_24), .LFO2_1(lfo_1_lfo2_1), .LFO3_1(lfo_1_lfo3_1), .LFO4_1(lfo_1_lfo4_1),
    .LFO5_1(lfo_1_lfo5_1), .LFO6(lfo_1_lfo6), .g_2974(in_33), .g_2966(in_35), .g_2958(in_36), .g_2952(in_38),
    .g_2945(in_40), .g_2941(in_42), .g_2939(in_44), .g_2937(in_45), .g_2963(in_46), .g_2955(in_47),
    .g_2951(in_48), .g_3656_2(phase_gen_1_g_3656_2), .g_3654(phase_gen_1_g_3654), .PG0(phase_gen_1_pg0),
    .PG1(phase_gen_1_pg1), .PG2(phase_gen_1_pg2), .PG3(phase_gen_1_pg3), .PG4(phase_gen_1_pg4),
    .PG5(phase_gen_1_pg5), .PG6(phase_gen_1_pg6), .PG7(phase_gen_1_pg7), .PG8(phase_gen_1_pg8),
    .PG9(phase_gen_1_pg9), .g_3660(phase_gen_1_g_3660), .g_3652(phase_gen_1_g_3652),
    .g_3658(phase_gen_1_g_3658));  // open: g_3170, g_3656
  ENVELOPE envelope_1 (
    .FCLK2(FCLK2), .FCLK1(FCLK1), .g_74(fsm_1_g_74), .TEST_i(in_49), .g_347(in_49), .g_374(in_50),
    .g_67(fsm_1_g_67), .g_1932(in_4), .LFO0(lfo_1_lfo0), .LFO1(lfo_1_lfo1), .LFO2(lfo_1_lfo2),
    .LFO3(lfo_1_lfo3), .LFO4(lfo_1_lfo4), .LFO5(lfo_1_lfo5), .g_3652(phase_gen_1_g_3652),
    .g_3654(phase_gen_1_g_3654), .g_3656(phase_gen_1_g_3656_2), .g_3658(phase_gen_1_g_3658),
    .g_3660(phase_gen_1_g_3660), .g_69(fsm_1_g_69), .ENV0(envelope_1_env0), .ENV1(envelope_1_env1),
    .ENV2(envelope_1_env2), .ENV3(envelope_1_env3), .ENV4(envelope_1_env4), .ENV5(envelope_1_env5),
    .ENV6(envelope_1_env6), .ENV7(envelope_1_env7), .ENV8(envelope_1_env8), .ENV9(envelope_1_env9));  // open: g_3065, g_3066, g_767, g_772, g_2463, g_2479, g_2462, g_2460, g_1878, g_1877, g_2461, KEY_ON, g_2252, g_2253, g_2251, g_2250, g_1883, g_2249, g_2248, g_2303, g_2301, g_2299, g_2297, g_2295, g_2270, g_2269, g_2268, g_2267, g_2266, g_2265, g_2264, g_1698, g_3100, g_1795, g_1796, g_1613
  OP op_1 (
    .FCLK2(FCLK2), .FCLK1(FCLK1), .g_124(fsm_1_g_124), .g_122(fsm_1_g_122), .g_125(fsm_1_g_125),
    .g_123(fsm_1_g_123), .g_114(fsm_1_g_114), .g_79(fsm_1_g_79), .ENV0(envelope_1_env0),
    .ENV1(envelope_1_env1), .ENV2(envelope_1_env2), .ENV3(envelope_1_env3), .ENV4(envelope_1_env4),
    .ENV5(envelope_1_env5), .ENV6(envelope_1_env6), .ENV7(envelope_1_env7), .ENV8(envelope_1_env8),
    .ENV9(envelope_1_env9), .PG0(phase_gen_1_pg0), .PG1(phase_gen_1_pg1), .PG2(phase_gen_1_pg2),
    .PG3(phase_gen_1_pg3), .PG4(phase_gen_1_pg4), .PG5(phase_gen_1_pg5), .PG6(phase_gen_1_pg6),
    .PG7(phase_gen_1_pg7), .PG8(phase_gen_1_pg8), .PG9(phase_gen_1_pg9), .g_127(fsm_1_g_127), .g_3077(in_19),
    .g_3076(in_21), .g_3075(in_23), .g_372(in_25), .OP13(op_1_op13), .OP12(op_1_op12), .OP11(op_1_op11),
    .OP10(op_1_op10), .OP9(op_1_op9), .OP8(op_1_op8), .OP7(op_1_op7), .OP6(op_1_op6), .OP5(op_1_op5),
    .OP4(op_1_op4), .OP3(op_1_op3), .OP2(op_1_op2), .OP1(op_1_op1), .OP0(op_1_op0));
  OUT out_1 (
    .FCLK2(FCLK2), .FCLK1(FCLK1), .g_118(fsm_1_g_118), .g_70(fsm_1_g_70), .g_378(in_2), .g_100(fsm_1_g_100),
    .g_79(fsm_1_g_79), .g_345(in_3), .g_109(fsm_1_g_109), .OP8(op_1_op8), .OP7(op_1_op7), .OP6(op_1_op6),
    .OP5(op_1_op5), .OP4(op_1_op4), .OP3(op_1_op3), .OP2(op_1_op2), .OP1(op_1_op1), .OP0(op_1_op0),
    .DAC0(out_1_dac0), .DAC1(out_1_dac1), .DAC2(out_1_dac2), .DAC3(out_1_dac3), .DAC4(out_1_dac4),
    .DAC5(out_1_dac5), .DAC6(out_1_dac6), .DAC7(out_1_dac7), .DAC8(out_1_dac8), .MOR_SEL(out_1_mor_sel),
    .MOL_SEL(out_1_mol_sel), .g_75(fsm_1_g_75), .g_3088(in_26), .g_3087(in_28));  // open: g_343, g_350, g_352, g_354, g_356, g_358, g_360, g_362, g_383, g_171, g_189, g_207, g_225, g_243, g_261, g_279, g_297, g_300
endmodule

module CLOCK (
  input  M,
  input  g_932,
  output C2,
  output C1,
  output g_15,
  output FCLK1,
  output nFCLK1,
  output FCLK2,
  output nFCLK2
);

  wire _1_out, _3_out, _7A_out, _7B_out, _10_q, _14_out, _16_out, _17_q, _18_q, _19_q, _20_out, _21_q, _22_q,
       _23_q, _24_out, _25_out, _26_q, _27_q, _29_out, _30_2_out, _30_out, _31_out, _34_out, _35_2_out,
       _35_out, _37_out, _38_out, not_1_out, not_2_out, not_3_out, not_4_out, not_5_out, not_6_out,
       not_7_out, not_8_out, not_9_out;

  not _38 (_38_out, M);
  not not_1 (not_1_out, g_932);
  SR_BIT _17 (.C2(C2), .C1(C1), .D(_16_out), .Q(_17_q));  // open: nQ
  nor _1 (_1_out, _38_out, not_8_out);
  nor _3 (_3_out, not_7_out, M);
  not _7A (_7A_out, _1_out);
  not not_2 (not_2_out, _1_out);
  not not_3 (not_3_out, not_2_out);
  not not_4 (not_4_out, _3_out);
  not not_5 (not_5_out, not_4_out);
  not _7B (_7B_out, _3_out);
  not _7A_2 (C2, _7A_out);
  not not_6 (not_6_out, not_3_out);
  not not_7 (not_7_out, not_6_out);
  not not_8 (not_8_out, not_9_out);
  not not_9 (not_9_out, not_5_out);
  not _7B_2 (C1, _7B_out);
  SDELAY12 _10 (.C2(C2), .C1(C1), .D(not_1_out), .Q(_10_q));  // open: Q22
  SR_BIT _18 (.C2(C2), .C1(C1), .D(_17_q), .Q(_18_q));  // open: nQ
  SR_BIT _19 (.C2(C2), .C1(C1), .D(_18_q), .Q(_19_q));  // open: nQ
  not _14 (_14_out, _10_q);
  and _15 (g_15, _14_out, not_1_out);
  SR_BIT _21 (.C2(C2), .C1(C1), .D(_19_q), .Q(_21_q));  // open: nQ
  SR_BIT _22 (.C2(C2), .C1(C1), .D(_21_q), .Q(_22_q));  // open: nQ
  or _25 (_25_out, _23_q, _17_q);
  or _24 (_24_out, _21_q, _19_q);
  or _20 (_20_out, _17_q, _18_q, _19_q, _21_q, _22_q);
  SR_BIT _23 (.C2(C2), .C1(C1), .D(_22_q), .Q(_23_q));  // open: nQ
  SR_BIT _27 (.C2(C2), .C1(C1), .D(_25_out), .Q(_27_q));  // open: nQ
  SR_BIT _26 (.C2(C2), .C1(C1), .D(_24_out), .Q(_26_q));  // open: nQ
  nor _16 (_16_out, g_15, _20_out);
  not _35 (_35_out, _27_q);
  not _30 (_30_out, _26_q);
  not _35_2 (_35_2_out, _35_out);
  not _30_2 (_30_2_out, _30_out);
  not _34 (_34_out, _35_2_out);
  not _33 (FCLK1, _34_out);
  not _36 (nFCLK1, _37_out);
  not _37 (_37_out, _35_out);
  not _29 (_29_out, _30_2_out);
  not _28 (FCLK2, _29_out);
  not _31 (_31_out, _30_out);
  not _32 (nFCLK2, _31_out);

  // Notes on the sheet:
  //   9
  //   2
  //   39
  //   /C2
  //   C2
  //   /C1
  //   C1
endmodule

module D_LATCH (
  input  EN,
  input  D,
  output Q,
  output nQ
);

  D_Flip_Flop #(.trigger("high")) d_ff_1 (.clk(EN), .D(D), .Q(Q), .Qn(nQ));  // open: preset, en, reset
endmodule

// SR BIT
module SR_BIT (
  input  C2,
  input  C1,
  input  D,
  output Q,
  output nQ
);

  wire d_latch_1_q;

  D_LATCH d_latch_1 (.EN(C1), .D(D), .Q(d_latch_1_q));  // open: nQ
  D_LATCH d_latch_2 (.EN(C2), .D(d_latch_1_q), .Q(Q), .nQ(nQ));
endmodule

module SDELAY12 (
  input  C2,
  input  C1,
  input  D,
  output Q,
  output Q22
);

  wire d_ff_1_q, d_ff_2_q, d_ff_3_q, d_ff_4_q, d_ff_5_q, d_ff_6_q, d_ff_7_q, d_ff_8_q, d_ff_9_q, d_ff_10_q,
       d_ff_11_q, d_ff_12_q, d_ff_13_q, d_ff_14_q, d_ff_15_q, d_ff_16_q, d_ff_17_q, d_ff_19_q, d_ff_20_q,
       d_ff_21_q, d_ff_22_q, d_ff_23_q;

  D_Flip_Flop #(.trigger("high")) d_ff_1 (.clk(C1), .D(D), .Q(d_ff_1_q));  // open: Qn, preset, en, reset
  D_Flip_Flop #(.trigger("high")) d_ff_2 (.clk(C1), .D(d_ff_22_q), .Q(d_ff_2_q));  // open: Qn, preset, en, reset
  D_Flip_Flop #(.trigger("high")) d_ff_3 (.clk(C1), .D(d_ff_23_q), .Q(d_ff_3_q));  // open: Qn, preset, en, reset
  D_Flip_Flop #(.trigger("high")) d_ff_4 (.clk(C2), .D(d_ff_1_q), .Q(d_ff_4_q));  // open: Qn, preset, en, reset
  D_Flip_Flop #(.trigger("high")) d_ff_5 (.clk(C2), .D(d_ff_2_q), .Q(d_ff_5_q));  // open: Qn, preset, en, reset
  D_Flip_Flop #(.trigger("high")) d_ff_6 (.clk(C2), .D(d_ff_3_q), .Q(d_ff_6_q));  // open: Qn, preset, en, reset
  D_Flip_Flop #(.trigger("high")) d_ff_7 (.clk(C1), .D(d_ff_4_q), .Q(d_ff_7_q));  // open: Qn, preset, en, reset
  D_Flip_Flop #(.trigger("high")) d_ff_8 (.clk(C1), .D(d_ff_5_q), .Q(d_ff_8_q));  // open: Qn, preset, en, reset
  D_Flip_Flop #(.trigger("high")) d_ff_9 (.clk(C1), .D(d_ff_6_q), .Q(d_ff_9_q));  // open: Qn, preset, en, reset
  D_Flip_Flop #(.trigger("high")) d_ff_10 (.clk(C2), .D(d_ff_7_q), .Q(d_ff_10_q));  // open: Qn, preset, en, reset
  D_Flip_Flop #(.trigger("high")) d_ff_11 (.clk(C2), .D(d_ff_8_q), .Q(d_ff_11_q));  // open: Qn, preset, en, reset
  D_Flip_Flop #(.trigger("high")) d_ff_12 (.clk(C2), .D(d_ff_9_q), .Q(d_ff_12_q));  // open: Qn, preset, en, reset
  D_Flip_Flop #(.trigger("high")) d_ff_13 (.clk(C1), .D(d_ff_10_q), .Q(d_ff_13_q));  // open: Qn, preset, en, reset
  D_Flip_Flop #(.trigger("high")) d_ff_14 (.clk(C1), .D(d_ff_11_q), .Q(d_ff_14_q));  // open: Qn, preset, en, reset
  D_Flip_Flop #(.trigger("high")) d_ff_15 (.clk(C1), .D(d_ff_12_q), .Q(d_ff_15_q));  // open: Qn, preset, en, reset
  D_Flip_Flop #(.trigger("high")) d_ff_16 (.clk(C2), .D(d_ff_13_q), .Q(d_ff_16_q));  // open: Qn, preset, en, reset
  D_Flip_Flop #(.trigger("high")) d_ff_17 (.clk(C2), .D(d_ff_14_q), .Q(d_ff_17_q));  // open: Qn, preset, en, reset
  D_Flip_Flop #(.trigger("high")) d_ff_18 (.clk(C2), .D(d_ff_15_q), .Q(Q22));  // open: Qn, preset, en, reset
  D_Flip_Flop #(.trigger("high")) d_ff_19 (.clk(C1), .D(d_ff_16_q), .Q(d_ff_19_q));  // open: Qn, preset, en, reset
  D_Flip_Flop #(.trigger("high")) d_ff_20 (.clk(C1), .D(d_ff_17_q), .Q(d_ff_20_q));  // open: Qn, preset, en, reset
  D_Flip_Flop #(.trigger("high")) d_ff_21 (.clk(C1), .D(Q22), .Q(d_ff_21_q));  // open: Qn, preset, en, reset
  D_Flip_Flop #(.trigger("high")) d_ff_22 (.clk(C2), .D(d_ff_19_q), .Q(d_ff_22_q));  // open: Qn, preset, en, reset
  D_Flip_Flop #(.trigger("high")) d_ff_23 (.clk(C2), .D(d_ff_20_q), .Q(d_ff_23_q));  // open: Qn, preset, en, reset
  D_Flip_Flop #(.trigger("high")) d_ff_24 (.clk(C2), .D(d_ff_21_q), .Q(Q));  // open: Qn, preset, en, reset
endmodule

// CNT BIT
module CNT_BIT (
  input  C2,
  input  C1,
  input  CIN,
  input  RES,
  output Q,
  output nQ,
  output CO
);

  wire and_1_out, d_ff_1_q, not_1_out, xor_1_out;

  not not_1 (not_1_out, RES);
  and and_1 (and_1_out, not_1_out, xor_1_out);
  xor xor_1 (xor_1_out, Q, CIN);
  and and_2 (CO, Q, CIN);
  D_Flip_Flop #(.trigger("high")) d_ff_1 (.clk(C1), .D(and_1_out), .Q(d_ff_1_q));  // open: Qn, preset, en, reset
  D_Flip_Flop #(.trigger("high")) d_ff_2 (.clk(C2), .D(d_ff_1_q), .Q(Q), .Qn(nQ));  // open: preset, en, reset
endmodule

module FSM (
  input  C2,
  input  C1,
  input  FCLK2,
  input  FCLK1,
  input  g_345,
  input  g_3080,
  input  g_3079,
  input  g_3078,
  input  g_15,
  output g_125,
  output g_122,
  output g_123,
  output g_114,
  output g_109,
  output g_77,
  output g_127,
  output g_124,
  output g_118,
  output g_74,
  output g_79,
  output g_70,
  output g_100,
  output g_75,
  output g_66,
  output g_69,
  output g_67,
  output g_68
);

  wire _4_co, _4_q, _5_q, _6_out, _8_q, _11_q, _12_q, _13_q, _40_co, _40_q, _41_2_out, _41_out, _42_q,
       _43_co, _43_q, _44_2_out, _44_out, _47_out, _48_out, _49_out, _50_out, _51_out, _52_out, _53_out,
       _54_out, _55_out, _56_out, _57_out, _58_out, _59_out, _60_out, _61_out, _62_out, _63_out, _64_out,
       _71_out, _72_out, _73_out, _76_out, _78_out, _80_out, _81_out, _82_out, _83_out, _84_out, _85_out,
       _86_out, _87_out, _88_out, _89_out, _90_out, _97_2_out, _97_out, _98_2_out, _98_out, _99_2_out,
       _99_out, _110_out, _112_out, _113_2_out, _113_3_out, _113_4_out, _113_5_out, _113_out, _115_out,
       _116_out, _117_out, _119_out, _120_out, _121_2_out, _121_3_out, _121_out, _126_2_out, _126_3_out,
       _126_out, _128_q, _134_out, _135_out, _136_out, _137_out, _138_out, _139_out, _151_out, d_latch_1_nq,
       d_latch_2_nq, decoder_1_out0, decoder_1_out1, decoder_1_out2, decoder_1_out3, decoder_1_out4,
       decoder_1_out5, decoder_1_out6, decoder_1_out7, nor_2_out, not_1_out, not_2_out, not_3_out;

  not not_1 (not_1_out, g_345);
  or _6 (_6_out, _11_q, _42_q);
  SR_BIT _11 (.C2(C2), .C1(C1), .D(_8_q), .Q(_11_q));  // open: nQ
  SR_BIT _8 (.C2(C2), .C1(C1), .D(_13_q), .Q(_8_q));  // open: nQ
  SR_BIT _13 (.C2(C2), .C1(C1), .D(_12_q), .Q(_13_q));  // open: nQ
  SR_BIT _12 (.C2(C2), .C1(C1), .D(g_15), .Q(_12_q));  // open: nQ
  CNT_BIT _43 (.C2(FCLK2), .C1(FCLK1), .CIN(1'b1), .RES(_6_out), .Q(_43_q), .CO(_43_co));  // open: nQ
  CNT_BIT _42 (.C2(FCLK2), .C1(FCLK1), .CIN(_43_co), .RES(_6_out), .Q(_42_q));  // open: nQ, CO
  CNT_BIT _40 (.C2(FCLK2), .C1(FCLK1), .CIN(_42_q), .RES(_11_q), .Q(_40_q), .CO(_40_co));  // open: nQ
  CNT_BIT _4 (.C2(FCLK2), .C1(FCLK1), .CIN(_40_co), .RES(_11_q), .Q(_4_q), .CO(_4_co));  // open: nQ
  CNT_BIT _5 (.C2(FCLK2), .C1(FCLK1), .CIN(_4_co), .RES(_11_q), .Q(_5_q));  // open: nQ, CO
  not _97 (_97_out, _43_q);
  not _98 (_98_out, _42_q);
  not _99 (_99_out, _40_q);
  not _41 (_41_out, _4_q);
  not _44 (_44_out, _5_q);
  not _97_2 (_97_2_out, _97_out);
  not _98_2 (_98_2_out, _98_out);
  not _99_2 (_99_2_out, _99_out);
  not _41_2 (_41_2_out, _41_out);
  not _44_2 (_44_2_out, _44_out);
  and _88 (_88_out, _97_out, _98_2_out, _44_2_out, _99_2_out, _41_2_out);
  and _87 (_87_out, _97_2_out, _98_out, _44_2_out, _99_2_out, _41_2_out);
  and _86 (_86_out, _97_out, _98_out, _44_2_out, _41_2_out, _99_2_out);
  and _85 (_85_out, _97_out, _98_2_out, _44_2_out, _99_out, _41_2_out);
  and _84 (_84_out, _97_2_out, _98_out, _44_2_out, _99_out, _41_2_out);
  and _83 (_83_out, _97_out, _98_out, _44_2_out, _99_out, _41_2_out);
  and _47 (_47_out, _97_out, _98_2_out, _99_2_out, _41_out, _44_2_out);
  and _48 (_48_out, _97_2_out, _98_out, _99_2_out, _41_out, _44_2_out);
  and _49 (_49_out, _97_out, _98_out, _99_2_out, _41_out, _44_2_out);
  and _50 (_50_out, _97_out, _98_2_out, _99_out, _41_out, _44_2_out);
  and _51 (_51_out, _97_2_out, _98_out, _99_out, _41_out, _44_2_out);
  and _52 (_52_out, _97_out, _98_out, _99_out, _41_out, _44_2_out);
  and _53 (_53_out, _97_out, _98_2_out, _99_2_out, _41_2_out, _44_out);
  and _54 (_54_out, _97_2_out, _98_out, _99_2_out, _41_2_out, _44_out);
  and _55 (_55_out, _97_out, _98_out, _99_2_out, _41_2_out, _44_out);
  and _56 (_56_out, _97_out, _98_2_out, _99_out, _41_2_out, _44_out);
  and _57 (_57_out, _97_2_out, _98_out, _99_out, _41_2_out, _44_out);
  and _58 (_58_out, _97_out, _98_out, _99_out, _41_2_out, _44_out);
  and _59 (_59_out, _97_out, _98_2_out, _99_2_out, _41_out, _44_out);
  and _60 (_60_out, _97_2_out, _98_out, _99_2_out, _41_out, _44_out);
  and _61 (_61_out, _97_out, _98_out, _99_2_out, _41_out, _44_out);
  and _62 (_62_out, _97_out, _98_2_out, _99_out, _41_out, _44_out);
  and _63 (_63_out, _97_2_out, _98_out, _99_out, _41_out, _44_out);
  and _64 (_64_out, _97_out, _98_out, _99_out, _41_out, _44_out);
  Decoder #(.select(3), .disabled(0), .enable("false")) decoder_1 (
    .out0(decoder_1_out0), .out1(decoder_1_out1), .out2(decoder_1_out2), .out3(decoder_1_out3),
    .out4(decoder_1_out4), .out5(decoder_1_out5), .out6(decoder_1_out6), .out7(decoder_1_out7),
    .sel({g_3078, g_3079, g_3080}));
  or _89 (_89_out, _88_out, _87_out, _86_out, _85_out, _84_out, _83_out);
  nor _90 (_90_out, _88_out, _87_out, _86_out, _85_out, _84_out, _83_out);
  or _82 (_82_out, _47_out, _48_out, _49_out, _50_out, _51_out, _52_out);
  nor _81 (_81_out, _47_out, _48_out, _49_out, _50_out, _51_out, _52_out);
  nor _80 (_80_out, _53_out, _54_out, _55_out, _56_out, _57_out, _58_out);
  not _70 (g_70, _71_out);
  nor _71 (_71_out, _58_out, _57_out, _59_out, _60_out);
  or _72 (_72_out, _59_out, _60_out, _61_out, _62_out, _63_out, _64_out);
  nor _76 (_76_out, _59_out, _60_out, _61_out, _62_out, _63_out, _64_out);
  not _79 (g_79, _80_out);
  not _75 (g_75, _76_out);
  or _134 (_134_out, decoder_1_out0, decoder_1_out1, decoder_1_out2);
  or _135 (_135_out, decoder_1_out0, decoder_1_out1, decoder_1_out3, decoder_1_out4);
  or _138 (_138_out, decoder_1_out2, decoder_1_out5);
  or _139 (_139_out, decoder_1_out1, decoder_1_out5);
  or _136 (_136_out, decoder_1_out0, decoder_1_out1, decoder_1_out4, decoder_1_out5, decoder_1_out6);
  or _151 (_151_out, decoder_1_out5, decoder_1_out6, decoder_1_out7);
  or _137 (_137_out, decoder_1_out7, decoder_1_out4, decoder_1_out5, decoder_1_out6);
  nor _73 (_73_out, _85_out, _50_out, _56_out, _62_out);
  D_LATCH d_latch_1 (.EN(FCLK1), .D(g_75), .nQ(d_latch_1_nq));  // open: Q
  D_LATCH d_latch_2 (.EN(FCLK1), .D(_62_out), .nQ(d_latch_2_nq));  // open: Q
  not not_2 (not_2_out, g_75);
  not not_3 (not_3_out, _62_out);
  and _126 (_126_out, decoder_1_out3, _82_out);
  and _126_2 (_126_2_out, _134_out, _72_out);
  nand _120 (_120_out, decoder_1_out2, _82_out);
  and _121 (_121_out, _82_out, _135_out);
  and _121_2 (_121_2_out, _136_out, g_79);
  and _116 (_116_out, _138_out, _82_out);
  and _117 (_117_out, _139_out, _72_out);
  and _113 (_113_out, _151_out, _82_out);
  and _113_2 (_113_2_out, decoder_1_out7, g_79);
  and _113_3 (_113_3_out, 1'b1, _72_out);
  and _113_4 (_113_4_out, _137_out, _89_out);
  and _119 (_119_out, _90_out, _81_out);
  nor nor_1 (g_100, d_latch_1_nq, not_2_out);
  nor nor_2 (nor_2_out, d_latch_2_nq, not_3_out);
  nor _126_3 (_126_3_out, _126_out, _126_2_out);
  nor _121_3 (_121_3_out, _121_out, _121_2_out);
  nor _115 (_115_out, _116_out, _117_out, _89_out);
  not _118 (g_118, _119_out);
  not _74 (g_74, _73_out);
  buf _66 (g_66, nor_2_out);
  buf _69 (g_69, _62_out);
  buf _67 (g_67, _64_out);
  buf _68 (g_68, _63_out);
  not _112 (_112_out, _113_5_out);
  nor _113_5 (_113_5_out, _113_out, _113_2_out, _113_3_out, _113_4_out);
  SR_BIT _128 (.C2(FCLK2), .C1(FCLK1), .D(_89_out), .Q(_128_q));  // open: nQ
  nand _110 (_110_out, not_1_out, _112_out);
  not _125 (g_125, _126_3_out);
  not _122 (g_122, _120_out);
  not _123 (g_123, _121_3_out);
  not _114 (g_114, _115_out);
  not _109 (g_109, _110_out);
  not _78 (_78_out, _88_out);
  not _77 (g_77, _78_out);
  not _127 (g_127, _128_q);
  buf _124 (g_124, _89_out);

  // Notes on the sheet:
  //   111
  //   140 - 150
  //   100
  //   65
endmodule

module SDELAY24 (
  input  C2,
  input  C1,
  input  D,
  output Q40,
  output Q,
  output Q44
);

  wire d_ff_1_q, d_ff_2_q, d_ff_3_q, d_ff_4_q, d_ff_5_q, d_ff_6_q, d_ff_7_q, d_ff_8_q, d_ff_9_q, d_ff_10_q,
       d_ff_11_q, d_ff_12_q, d_ff_13_q, d_ff_14_q, d_ff_15_q, d_ff_16_q, d_ff_17_q, d_ff_18_q, d_ff_19_q,
       d_ff_20_q, d_ff_21_q, d_ff_22_q, d_ff_23_q, d_ff_25_q, d_ff_26_q, d_ff_27_q, d_ff_28_q, d_ff_29_q,
       d_ff_30_q, d_ff_31_q, d_ff_32_q, d_ff_33_q, d_ff_34_q, d_ff_35_q, d_ff_36_q, d_ff_37_q, d_ff_38_q,
       d_ff_39_q, d_ff_40_q, d_ff_41_q, d_ff_42_q, d_ff_43_q, d_ff_44_q, d_ff_45_q, d_ff_46_q;

  D_Flip_Flop #(.trigger("high")) d_ff_1 (.clk(C1), .D(D), .Q(d_ff_1_q));  // open: Qn, preset, en, reset
  D_Flip_Flop #(.trigger("high")) d_ff_2 (.clk(C1), .D(d_ff_43_q), .Q(d_ff_2_q));  // open: Qn, preset, en, reset
  D_Flip_Flop #(.trigger("high")) d_ff_3 (.clk(C1), .D(d_ff_44_q), .Q(d_ff_3_q));  // open: Qn, preset, en, reset
  D_Flip_Flop #(.trigger("high")) d_ff_4 (.clk(C1), .D(d_ff_45_q), .Q(d_ff_4_q));  // open: Qn, preset, en, reset
  D_Flip_Flop #(.trigger("high")) d_ff_5 (.clk(C1), .D(d_ff_46_q), .Q(d_ff_5_q));  // open: Qn, preset, en, reset
  D_Flip_Flop #(.trigger("high")) d_ff_6 (.clk(C1), .D(Q40), .Q(d_ff_6_q));  // open: Qn, preset, en, reset
  D_Flip_Flop #(.trigger("high")) d_ff_7 (.clk(C2), .D(d_ff_1_q), .Q(d_ff_7_q));  // open: Qn, preset, en, reset
  D_Flip_Flop #(.trigger("high")) d_ff_8 (.clk(C2), .D(d_ff_2_q), .Q(d_ff_8_q));  // open: Qn, preset, en, reset
  D_Flip_Flop #(.trigger("high")) d_ff_9 (.clk(C2), .D(d_ff_3_q), .Q(d_ff_9_q));  // open: Qn, preset, en, reset
  D_Flip_Flop #(.trigger("high")) d_ff_10 (.clk(C2), .D(d_ff_4_q), .Q(d_ff_10_q));  // open: Qn, preset, en, reset
  D_Flip_Flop #(.trigger("high")) d_ff_11 (.clk(C2), .D(d_ff_5_q), .Q(d_ff_11_q));  // open: Qn, preset, en, reset
  D_Flip_Flop #(.trigger("high")) d_ff_12 (.clk(C2), .D(d_ff_6_q), .Q(d_ff_12_q));  // open: Qn, preset, en, reset
  D_Flip_Flop #(.trigger("high")) d_ff_13 (.clk(C1), .D(d_ff_7_q), .Q(d_ff_13_q));  // open: Qn, preset, en, reset
  D_Flip_Flop #(.trigger("high")) d_ff_14 (.clk(C1), .D(d_ff_8_q), .Q(d_ff_14_q));  // open: Qn, preset, en, reset
  D_Flip_Flop #(.trigger("high")) d_ff_15 (.clk(C1), .D(d_ff_9_q), .Q(d_ff_15_q));  // open: Qn, preset, en, reset
  D_Flip_Flop #(.trigger("high")) d_ff_16 (.clk(C1), .D(d_ff_10_q), .Q(d_ff_16_q));  // open: Qn, preset, en, reset
  D_Flip_Flop #(.trigger("high")) d_ff_17 (.clk(C1), .D(d_ff_11_q), .Q(d_ff_17_q));  // open: Qn, preset, en, reset
  D_Flip_Flop #(.trigger("high")) d_ff_18 (.clk(C1), .D(d_ff_12_q), .Q(d_ff_18_q));  // open: Qn, preset, en, reset
  D_Flip_Flop #(.trigger("high")) d_ff_19 (.clk(C2), .D(d_ff_13_q), .Q(d_ff_19_q));  // open: Qn, preset, en, reset
  D_Flip_Flop #(.trigger("high")) d_ff_20 (.clk(C2), .D(d_ff_14_q), .Q(d_ff_20_q));  // open: Qn, preset, en, reset
  D_Flip_Flop #(.trigger("high")) d_ff_21 (.clk(C2), .D(d_ff_15_q), .Q(d_ff_21_q));  // open: Qn, preset, en, reset
  D_Flip_Flop #(.trigger("high")) d_ff_22 (.clk(C2), .D(d_ff_16_q), .Q(d_ff_22_q));  // open: Qn, preset, en, reset
  D_Flip_Flop #(.trigger("high")) d_ff_23 (.clk(C2), .D(d_ff_17_q), .Q(d_ff_23_q));  // open: Qn, preset, en, reset
  D_Flip_Flop #(.trigger("high")) d_ff_24 (.clk(C2), .D(d_ff_18_q), .Q(Q44));  // open: Qn, preset, en, reset
  D_Flip_Flop #(.trigger("high")) d_ff_25 (.clk(C1), .D(d_ff_19_q), .Q(d_ff_25_q));  // open: Qn, preset, en, reset
  D_Flip_Flop #(.trigger("high")) d_ff_26 (.clk(C1), .D(d_ff_20_q), .Q(d_ff_26_q));  // open: Qn, preset, en, reset
  D_Flip_Flop #(.trigger("high")) d_ff_27 (.clk(C1), .D(d_ff_21_q), .Q(d_ff_27_q));  // open: Qn, preset, en, reset
  D_Flip_Flop #(.trigger("high")) d_ff_28 (.clk(C1), .D(d_ff_22_q), .Q(d_ff_28_q));  // open: Qn, preset, en, reset
  D_Flip_Flop #(.trigger("high")) d_ff_29 (.clk(C1), .D(d_ff_23_q), .Q(d_ff_29_q));  // open: Qn, preset, en, reset
  D_Flip_Flop #(.trigger("high")) d_ff_30 (.clk(C1), .D(Q44), .Q(d_ff_30_q));  // open: Qn, preset, en, reset
  D_Flip_Flop #(.trigger("high")) d_ff_31 (.clk(C2), .D(d_ff_25_q), .Q(d_ff_31_q));  // open: Qn, preset, en, reset
  D_Flip_Flop #(.trigger("high")) d_ff_32 (.clk(C2), .D(d_ff_26_q), .Q(d_ff_32_q));  // open: Qn, preset, en, reset
  D_Flip_Flop #(.trigger("high")) d_ff_33 (.clk(C2), .D(d_ff_27_q), .Q(d_ff_33_q));  // open: Qn, preset, en, reset
  D_Flip_Flop #(.trigger("high")) d_ff_34 (.clk(C2), .D(d_ff_28_q), .Q(d_ff_34_q));  // open: Qn, preset, en, reset
  D_Flip_Flop #(.trigger("high")) d_ff_35 (.clk(C2), .D(d_ff_29_q), .Q(d_ff_35_q));  // open: Qn, preset, en, reset
  D_Flip_Flop #(.trigger("high")) d_ff_36 (.clk(C2), .D(d_ff_30_q), .Q(d_ff_36_q));  // open: Qn, preset, en, reset
  D_Flip_Flop #(.trigger("high")) d_ff_37 (.clk(C1), .D(d_ff_31_q), .Q(d_ff_37_q));  // open: Qn, preset, en, reset
  D_Flip_Flop #(.trigger("high")) d_ff_38 (.clk(C1), .D(d_ff_32_q), .Q(d_ff_38_q));  // open: Qn, preset, en, reset
  D_Flip_Flop #(.trigger("high")) d_ff_39 (.clk(C1), .D(d_ff_33_q), .Q(d_ff_39_q));  // open: Qn, preset, en, reset
  D_Flip_Flop #(.trigger("high")) d_ff_40 (.clk(C1), .D(d_ff_34_q), .Q(d_ff_40_q));  // open: Qn, preset, en, reset
  D_Flip_Flop #(.trigger("high")) d_ff_41 (.clk(C1), .D(d_ff_35_q), .Q(d_ff_41_q));  // open: Qn, preset, en, reset
  D_Flip_Flop #(.trigger("high")) d_ff_42 (.clk(C1), .D(d_ff_36_q), .Q(d_ff_42_q));  // open: Qn, preset, en, reset
  D_Flip_Flop #(.trigger("high")) d_ff_43 (.clk(C2), .D(d_ff_37_q), .Q(d_ff_43_q));  // open: Qn, preset, en, reset
  D_Flip_Flop #(.trigger("high")) d_ff_44 (.clk(C2), .D(d_ff_38_q), .Q(d_ff_44_q));  // open: Qn, preset, en, reset
  D_Flip_Flop #(.trigger("high")) d_ff_45 (.clk(C2), .D(d_ff_39_q), .Q(d_ff_45_q));  // open: Qn, preset, en, reset
  D_Flip_Flop #(.trigger("high")) d_ff_46 (.clk(C2), .D(d_ff_40_q), .Q(d_ff_46_q));  // open: Qn, preset, en, reset
  D_Flip_Flop #(.trigger("high")) d_ff_47 (.clk(C2), .D(d_ff_41_q), .Q(Q40));  // open: Qn, preset, en, reset
  D_Flip_Flop #(.trigger("high")) d_ff_48 (.clk(C2), .D(d_ff_42_q), .Q(Q));  // open: Qn, preset, en, reset
endmodule
// PHASE GEN
module PHASE_GEN (
  input  FCLK2,
  input  FCLK1,
  input  g_69,
  input  g_370,
  input  g_1875,
  input  g_2223,
  input  g_2231,
  input  g_2227,
  input  g_2934,
  input  g_2969,
  input  g_2949,
  input  g_2944,
  input  g_2940,
  input  g_2469,
  input  g_2471,
  input  g_2475,
  input  g_2473,
  input  g_3067,
  input  g_3068,
  input  g_3069,
  input  LFO2_1,
  input  LFO3_1,
  input  LFO4_1,
  input  LFO5_1,
  input  LFO6,
  input  g_2974,
  input  g_2966,
  input  g_2958,
  input  g_2952,
  input  g_2945,
  input  g_2941,
  input  g_2939,
  input  g_2937,
  input  g_2963,
  input  g_2955,
  input  g_2951,
  output g_3652,
  output g_3656,
  output g_3660,
  output g_3658,
  output g_3654,
  output g_3656_2,
  output g_3170,
  output PG0,
  output PG1,
  output PG2,
  output PG3,
  output PG4,
  output PG5,
  output PG6,
  output PG7,
  output PG8,
  output PG9
);

  wire _2DEC1, _2DEC2, _2DEC3, _2DEC4, _2DEC5, _2DEC6, _2DEC7, _3DEC2, _3DEC3, _3DEC4, _3DEC5, _3DEC6,
       _3DEC7, _4DEC1, _4DEC2, _4DEC3, _4DEC4, _4DEC5, _4DEC6, _4DEC7, _2337_nq, _2338_q, _2350_nq, _2351_q,
       _2366_out, _2367_nq, _2369_nq, _2370_2_out, _2370_3_out, _2370_out, _2371_out, _2372_nq, _2374_nq,
       _2375_2_out, _2375_3_out, _2375_out, _2376_out, _2377_nq, _2379_nq, _2380_2_out, _2380_3_out,
       _2380_out, _2381_2_out, _2381_3_out, _2381_4_out, _2381_5_out, _2381_out, _2382_out, _2383_nq,
       _2385_nq, _2386_2_out, _2386_3_out, _2386_out, _2387_2_out, _2387_3_out, _2387_4_out, _2387_5_out,
       _2387_6_nq, _2387_out, _2388_out, _2391_nq, _2392_2_out, _2392_3_out, _2392_out, _2393_2_out,
       _2393_3_out, _2393_4_out, _2393_5_out, _2393_out, _2394_out, _2395_nq, _2397_nq, _2398_2_out,
       _2398_3_out, _2398_out, _2399_2_out, _2399_3_out, _2399_4_out, _2399_5_out, _2399_out, _2400_out,
       _2401_nq, _2403_nq, _2404_2_out, _2404_3_out, _2404_out, _2405_2_out, _2405_3_out, _2405_4_out,
       _2405_5_out, _2405_out, _2406_out, _2407_nq, _2409_nq, _2410_2_out, _2410_3_out, _2410_out,
       _2411_2_out, _2411_3_out, _2411_4_out, _2411_5_out, _2411_out, _2412_out, _2413_nq, _2415_nq,
       _2416_2_out, _2416_3_out, _2416_out, _2417_2_out, _2417_3_out, _2417_4_out, _2417_5_out, _2417_out,
       _2418_out, _2419_nq, _2421_nq, _2422_2_out, _2422_3_out, _2422_out, _2423_2_out, _2423_3_out,
       _2423_4_out, _2423_5_out, _2423_out, _2424_out, _2425_nq, _2427_nq, _2428_2_out, _2428_3_out,
       _2428_out, _2429_2_out, _2429_3_out, _2429_4_out, _2429_5_out, _2429_out, _2430_out, _2431_nq,
       _2433_nq, _2434_2_out, _2434_3_out, _2434_out, _2435_2_out, _2435_3_out, _2435_4_out, _2435_5_out,
       _2435_out, _2436_out, _2437_nq, _2439_nq, _2440_2_out, _2440_3_out, _2440_out, _2441_2_out,
       _2441_3_out, _2441_4_out, _2441_5_out, _2441_out, _2442_out, _2443_nq, _2445_nq, _2446_2_out,
       _2446_3_out, _2446_out, _2447_2_out, _2447_3_out, _2447_out, _2448_2_out, _2448_3_out, _2448_out,
       _2449_q, _2450_nq, _2451_2_out, _2451_3_out, _2451_4_out, _2451_5_out, _2451_6_out, _2451_7_out,
       _2451_out, _2452_2_out, _2452_3_out, _2452_4_out, _2452_5_out, _2452_out, _2453_2_out, _2453_3_out,
       _2453_4_out, _2453_out, _2454_out, _2455_out, _2456_out, _2457_q, _2458_q, _3091_out, _3092_out,
       _3093_out, _3094_out, _3095_out, _3096_q, _3097_out, _3098_out, _3099_out, _3100_out, _3101_q,
       _3102_nq, _3103_out, _3104_out, _3105_nq, _3106_out, _3107_out, _3108_out, _3109_nq, _3110_nq,
       _3111_out, _3112_nq, _3113_out, _3114_out, _3115_nq, _3116_out, _3117_out, _3118_nq, _3119_out,
       _3120_out, _3121_nq, _3122_out, _3123_out, _3124_nq, _3150_out, _3151_out, _3152_out, _3153_nq,
       _3154_nq, _3155_out, _3156_out, _3157_out, _3168_nq, _3171_q, _3172_out, _3174_out, _3175_nq,
       _3177_nq, _3178_out, _3179_nq, _3180_out, _3181_q, _3182_nq, _3183_out, _3185_nq, _3187_q, _3188_out,
       _3190_out, _3191_nq, _3193_nq, _3194_nq, _3195_out, _3196_out, _3197_q, _3198_nq, _3199_out, _3202_q,
       _3203_out, _3205_out, _3206_nq, _3208_nq, _3209_out, _3210_nq, _3211_out, _3212_q, _3213_nq,
       _3214_out, _3217_q, _3218_out, _3220_out, _3221_nq, _3223_nq, _3224_out, _3225_nq, _3226_out, _3227_q,
       _3228_nq, _3229_out, _3232_q, _3233_out, _3235_out, _3236_nq, _3238_out, _3239_nq, _3240_nq,
       _3241_out, _3242_q, _3243_nq, _3244_out, _3246_q, _3248_out, _3250_out, _3251_nq, _3253_nq, _3254_nq,
       _3255_out, _3256_out, _3257_q, _3258_nq, _3259_out, _3262_q, _3263_out, _3265_out, _3266_nq, _3268_nq,
       _3269_out, _3270_nq, _3271_out, _3272_q, _3273_out, _3274_nq, _3277_q, _3278_out, _3280_out, _3281_nq,
       _3283_nq, _3284_out, _3285_nq, _3286_out, _3287_q, _3288_nq, _3289_out, _3292_q, _3293_out, _3295_out,
       _3296_nq, _3298_nq, _3299_out, _3300_nq, _3301_out, _3302_q, _3303_nq, _3304_out, _3307_q, _3308_out,
       _3310_out, _3311_nq, _3313_nq, _3314_out, _3315_nq, _3316_out, _3317_q, _3318_nq, _3319_out, _3321_q,
       _3321_q40, _3322_out, _3324_out, _3325_nq, _3327_nq, _3328_out, _3329_nq, _3330_out, _3331_q,
       _3332_nq, _3333_out, _3335_q, _3335_q40, _3336_out, _3338_out, _3339_nq, _3341_nq, _3342_out,
       _3343_nq, _3344_out, _3345_q, _3346_nq, _3347_out, _3349_q, _3349_q40, _3350_out, _3352_out, _3353_nq,
       _3355_nq, _3356_out, _3357_nq, _3358_out, _3359_q, _3360_nq, _3361_out, _3363_q, _3363_q40, _3364_out,
       _3369_nq, _3370_out, _3371_nq, _3372_out, _3373_q, _3374_nq, _3375_out, _3377_q, _3377_q40, _3378_out,
       _3380_2_out, _3380_out, _3381_2_nq, _3381_nq, _3383_nq, _3384_out, _3385_nq, _3386_out, _3387_2_out,
       _3387_3_out, _3387_4_q, _3387_out, _3388_nq, _3389_out, _3396_q, _3396_q40, _3397_out, _3399_out,
       _3400_nq, _3402_nq, _3403_out, _3404_nq, _3405_out, _3406_q, _3407_nq, _3408_out, _3411_q, _3411_q40,
       _3412_out, _3414_out, _3415_nq, _3417_nq, _3418_out, _3419_nq, _3420_out, _3421_q, _3422_nq,
       _3423_out, _3426_q, _3426_q40, _3427_out, _3429_out, _3430_nq, _3432_nq, _3433_out, _3434_nq,
       _3435_out, _3436_q, _3439_q, _3439_q40, _3440_out, _3442_out, _3443_nq, _3445_nq, _3446_out, _3447_nq,
       _3448_out, _3449_q, _3452_q, _3452_q40, _3453_out, _3455_out, _3456_nq, _3458_nq, _3459_out, _3460_nq,
       _3461_out, _3462_q, _3465_2_out, _3465_3_out, _3465_4_out, _3465_5_out, _3465_6_out, _3465_7_out,
       _3465_out, _3493_out, _3494_out, _3495_out, _3496_out, _3497_out, _3498_out, _3499_out, _3500_out,
       _3501_out, _3502_out, _3503_out, _3527_nq, _3528_2_out, _3528_3_out, _3528_4_out, _3528_5_out,
       _3528_6_out, _3528_7_out, _3528_out, _3529_2_out, _3529_3_out, _3529_4_out, _3529_5_out, _3529_6_out,
       _3529_7_out, _3529_out, _3530_out, _3531_out, _3532_2_out, _3532_3_out, _3532_4_out, _3532_out,
       _3533_nq, _3534_nq, _3535_2_out, _3535_3_out, _3535_4_out, _3535_5_out, _3535_6_out, _3535_7_out,
       _3535_out, _3536_out, _3537_2_out, _3537_3_out, _3537_4_out, _3537_out, _3538_nq, _3539_nq,
       _3540_2_out, _3540_3_out, _3540_4_out, _3540_5_out, _3540_6_out, _3540_7_out, _3540_out, _3541_out,
       _3542_2_out, _3542_3_out, _3542_4_out, _3542_out, _3543_nq, _3544_nq, _3545_2_out, _3545_3_out,
       _3545_4_out, _3545_5_out, _3545_6_out, _3545_7_out, _3545_out, _3546_out, _3547_2_out, _3547_3_out,
       _3547_4_out, _3547_out, _3548_nq, _3549_nq, _3550_2_out, _3550_3_out, _3550_4_out, _3550_5_out,
       _3550_6_out, _3550_7_out, _3550_out, _3551_out, _3552_2_out, _3552_3_out, _3552_4_out, _3552_out,
       _3553_nq, _3554_nq, _3555_2_out, _3555_3_out, _3555_4_out, _3555_5_out, _3555_6_out, _3555_7_out,
       _3555_out, _3556_out, _3557_2_out, _3557_3_out, _3557_4_out, _3557_out, _3558_nq, _3559_nq,
       _3560_2_out, _3560_3_out, _3560_4_out, _3560_5_out, _3560_6_out, _3560_7_out, _3560_out, _3561_out,
       _3562_2_out, _3562_3_out, _3562_4_out, _3562_out, _3563_nq, _3564_nq, _3565_2_out, _3565_3_out,
       _3565_4_out, _3565_5_out, _3565_6_out, _3565_7_out, _3565_out, _3566_out, _3567_2_out, _3567_3_out,
       _3567_4_out, _3567_out, _3568_nq, _3569_nq, _3570_2_out, _3570_3_out, _3570_4_out, _3570_5_out,
       _3570_6_out, _3570_7_out, _3570_out, _3571_out, _3572_2_out, _3572_3_out, _3572_4_out, _3572_out,
       _3573_nq, _3574_nq, _3575_2_out, _3575_3_out, _3575_4_out, _3575_5_out, _3575_6_out, _3575_7_out,
       _3575_out, _3576_out, _3577_2_out, _3577_3_out, _3577_4_out, _3577_out, _3578_nq, _3579_nq,
       _3580_2_out, _3580_3_out, _3580_4_out, _3580_5_out, _3580_6_out, _3580_7_out, _3580_out, _3581_out,
       _3582_2_out, _3582_3_out, _3582_4_out, _3582_out, _3583_nq, _3584_nq, _3585_2_out, _3585_3_out,
       _3585_4_out, _3585_5_out, _3585_6_out, _3585_7_out, _3585_out, _3586_out, _3587_2_out, _3587_3_out,
       _3587_4_out, _3587_out, _3588_nq, _3589_nq, _3590_2_out, _3590_3_out, _3590_4_out, _3590_5_out,
       _3590_6_out, _3590_7_out, _3590_out, _3591_out, _3592_2_out, _3592_3_out, _3592_4_out, _3592_out,
       _3593_nq, _3594_nq, _3595_2_out, _3595_3_out, _3595_4_out, _3595_5_out, _3595_6_out, _3595_7_out,
       _3595_out, _3596_out, _3597_2_out, _3597_3_out, _3597_4_out, _3597_out, _3598_nq, _3599_nq,
       _3600_2_out, _3600_3_out, _3600_4_out, _3600_5_out, _3600_6_out, _3600_7_out, _3600_out, _3601_out,
       _3602_2_out, _3602_3_out, _3602_4_out, _3602_out, _3603_nq, _3604_nq, _3605_nq, _3606_nq, _3607_nq,
       _3608_nq, _3609_nq, _3610_nq, _3611_2_out, _3611_3_out, _3611_4_out, _3611_5_out, _3611_out,
       _3612_2_out, _3612_3_out, _3612_4_out, _3612_out, _3613_2_out, _3613_3_out, _3613_out, _3614_2_out,
       _3614_3_out, _3614_4_out, _3614_out, _3615_2_out, _3615_3_out, _3615_4_out, _3615_out, _3616_2_out,
       _3616_3_out, _3616_4_out, _3616_out, _3617_out, _3619_out, _3620_out, _3621_out, _3622_out, _3623_out,
       _3625_q, _3626_out, _3627_out, _3628_q, _3630_out, _3632_out, _3637_out, _3640_out, _3643_nq,
       _3650_out, _3651_q, _3653_q, _3655_q, _3657_q, _3659_q, _3663_out, _3664_q, _3665_nq, _3666_out,
       _3667_2_out, _3667_3_out, _3667_4_out, _3667_out, _3668_2_out, _3668_3_out, _3668_4_out, _3668_out,
       _3669_nq, _3670_nq, _3671_2_out, _3671_3_out, _3671_out, _3672_2_out, _3672_3_out, _3672_out,
       _3673_out, _3675_q, _3677_out, _3678_q, _3679_nq, _3680_out, _3681_2_out, _3681_3_out, _3681_4_out,
       _3681_out, _3683_nq, _3684_nq, _3685_2_out, _3685_3_out, _3685_out, _3686_2_out, _3686_3_out,
       _3686_out, _3687_out, _3688_nq, _3689_q, _3691_out, _3692_q, _3693_nq, _3694_out, _3697_nq, _3698_nq,
       _3699_2_out, _3699_3_out, _3699_out, _3700_2_out, _3700_3_out, _3700_out, _3701_out, _3702_nq,
       _3703_q, _3704_nq, _3705_nq, _3706_nq, _3711_out, _3712_nq, _3713_out, _3714_q, _3715_nq, _3716_out,
       _3717_2_out, _3717_3_out, _3717_4_out, _3717_out, _3719_nq, _3720_nq, _3721_2_out, _3721_3_out,
       _3721_out, _3722_2_out, _3722_3_out, _3722_out, _3723_nq, _3725_out, _3726_q, _3727_nq, _3728_out,
       _3729_2_out, _3729_3_out, _3729_4_out, _3729_out, _3731_nq, _3732_nq, _3733_2_out, _3733_3_out,
       _3733_out, _3734_2_out, _3734_3_out, _3734_out, _3735_nq, _3737_out, _3738_q, _3739_nq, _3740_out,
       _3741_2_out, _3741_3_out, _3741_4_out, _3741_out, _3744_nq, _3745_2_out, _3745_3_out, _3745_out,
       _3746_2_out, _3746_3_out, _3746_out, _3747_nq, _3749_out, _3750_nq, _3751_out, _3752_2_out,
       _3752_3_out, _3752_4_out, _3752_out, _3754_nq, _3755_nq, _3756_2_out, _3756_3_out, _3756_out,
       _3757_2_out, _3757_3_out, _3757_out, _3758_nq, _3760_q, _3761_nq, _3762_nq, _3763_out, _3764_2_nq,
       _3764_out, _3765_q, _3766_nq, _3767_out, _3787_out, _3788_q, _3790_out, _3791_2_out, _3791_3_out,
       _3791_4_out, _3791_out, _3792_out, _3793_nq, _3795_2_out, _3795_3_out, _3795_4_out, _3795_5_nq,
       _3795_out, _3796_2_out, _3796_3_out, _3796_out, _3797_out, _3798_nq, _3800_nq, _3801_2_out,
       _3801_3_out, _3801_out, _3802_out, _3803_nq, _3805_nq, _3806_q, _3808_out, _3824_out, _3825_out,
       _3826_2_out, _3826_3_out, _3826_out, _3827_out, _3829_2_out, _3829_out, _3842_q, _3843_q, _3844_q,
       _3845_nq, _3846_nq, _3847_nq, _3850_out, _3851_out, _3852_out, _3853_out, _3854_out, _3855_out,
       _3856_out, _3857_out, _3870_out, _3871_out, _3872_2_out, _3872_3_out, _3872_out, _3873_2_out,
       _3873_3_out, _3873_4_out, _3873_5_out, _3873_out, _3874_2_out, _3874_3_out, _3874_4_out, _3874_5_out,
       _3874_6_out, _3874_7_out, _3874_out, adder_1_cout, adder_1_out, adder_2_cout, adder_2_out,
       adder_3_cout, adder_3_out, adder_4_cout, adder_4_out, adder_5_cout, adder_5_out, adder_6_cout,
       adder_6_out, adder_7_cout, adder_7_out, adder_8_cout, adder_9_cout, adder_10_cout, adder_12_cout,
       adder_12_out, adder_13_cout, adder_13_out, adder_14_cout, adder_14_out, adder_15_cout, adder_15_out,
       adder_16_cout, adder_16_out, adder_17_cout, adder_17_out, adder_18_cout, adder_18_out, adder_19_cout,
       adder_19_out, adder_20_cout, adder_20_out, adder_21_cout, adder_21_out, adder_22_cout, adder_22_out,
       adder_23_out, adder_24_cout, adder_24_out, adder_25_cout, adder_25_out, adder_26_cout, adder_26_out,
       adder_27_cout, adder_27_out, adder_28_cout, adder_28_out, adder_29_cout, adder_29_out, adder_30_cout,
       adder_30_out, adder_31_cout, adder_31_out, adder_32_cout, adder_32_out, adder_33_cout, adder_33_out,
       adder_34_cout, adder_34_out, adder_35_cout, adder_35_out, adder_36_cout, adder_36_out, adder_37_cout,
       adder_37_out, adder_38_cout, adder_38_out, adder_39_cout, adder_39_out, adder_40_out, adder_41_cout,
       adder_41_out, adder_42_cout, adder_42_out, adder_43_cout, adder_43_out, adder_44_cout, adder_44_out,
       adder_45_cout, adder_45_out, adder_46_cout, adder_46_out, adder_47_cout, adder_47_out, adder_48_cout,
       adder_48_out, adder_49_cout, adder_49_out, adder_50_cout, adder_50_out, adder_51_cout, adder_51_out,
       adder_52_cout, adder_52_out, adder_53_cout, adder_53_out, adder_54_cout, adder_54_out, adder_55_cout,
       adder_55_out, adder_56_cout, adder_56_out, adder_57_cout, adder_57_out, adder_58_cout, adder_58_out,
       adder_59_cout, adder_59_out, adder_60_out, adder_61_cout, adder_61_out, adder_62_cout, adder_62_out,
       adder_63_cout, adder_63_out, adder_64_cout, adder_64_out, adder_65_cout, adder_65_out, adder_66_cout,
       adder_66_out, adder_67_cout, adder_67_out, adder_68_cout, adder_68_out, adder_69_cout, adder_69_out,
       adder_70_cout, adder_70_out, adder_71_cout, adder_71_out, adder_72_cout, adder_72_out, adder_73_cout,
       adder_73_out, adder_74_cout, adder_74_out, adder_75_cout, adder_75_out, adder_76_cout, adder_76_out,
       adder_77_cout, adder_77_out, adder_78_cout, adder_78_out, adder_79_cout, adder_79_out, adder_80_out,
       adder_81_cout, adder_81_out, adder_82_cout, adder_82_out, adder_83_cout, adder_83_out, adder_84_cout,
       adder_84_out, adder_85_cout, adder_85_out, adder_86_cout, adder_86_out, adder_87_cout, adder_87_out,
       adder_88_cout, adder_88_out, adder_89_cout, adder_89_out, adder_90_cout, adder_90_out, adder_91_cout,
       adder_91_out, adder_92_cout, adder_92_out, adder_93_cout, adder_93_out, adder_94_cout, adder_94_out,
       adder_95_cout, adder_95_out, adder_96_cout, adder_96_out, adder_97_cout, adder_97_out, adder_98_cout,
       adder_98_out, adder_99_cout, adder_99_out, adder_100_out, and_1_out, and_2_out, and_3_out, and_4_out,
       and_5_out, and_6_out, and_7_out, and_8_out, and_9_out, and_10_out, and_11_out, and_12_out, and_13_out,
       and_14_out, and_15_out, DEC0, DEC1, DEC2, DEC3, DEC4, DEC5, DEC6, DEC7, DEC8, DEC9, DEC10, DEC11,
       DEC12, DEC13, DEC14, DEC15, decoder_5_out5, decoder_5_out6, decoder_5_out7, decoder_5_out8,
       decoder_5_out9, decoder_6_out0, decoder_6_out1, decoder_6_out2, decoder_6_out3, not_1_out, or_1_out,
       or_2_out, or_3_out, or_4_out, or_5_out, or_6_out, or_7_out, or_8_out, or_9_out, or_10_out, sr_bit_1_q,
       sr_bit_2_q, sr_bit_3_q, sr_bit_4_q, sr_bit_5_q, sr_bit_6_q, sr_bit_7_q, sr_bit_8_q, sr_bit_9_q,
       sr_bit_10_q, sr_bit_11_q, sr_bit_12_q, sr_bit_13_q, sr_bit_14_q, sr_bit_15_q, sr_bit_16_q,
       sr_bit_17_q, sr_bit_18_q, sr_bit_19_q, sr_bit_20_q, sr_bit_22_q, sr_bit_23_q, sr_bit_24_q,
       sr_bit_25_q, sr_bit_26_q, sr_bit_27_q, sr_bit_28_q, sr_bit_29_q, sr_bit_30_q;
  wire [1:0] _2349_out;
  wire [2:0] _3505_out, _3642_out;
  wire [3:0] adder_9_out;

  not _3092 (_3092_out, g_69);
  not _3095 (_3095_out, g_370);
  not _3100 (_3100_out, g_1875);
  SR_BIT _3625 (.C2(FCLK2), .C1(FCLK1), .D(g_2223), .Q(_3625_q));  // open: nQ
  SR_BIT _2457 (.C2(FCLK2), .C1(FCLK1), .D(g_2231), .Q(_2457_q));  // open: nQ
  SR_BIT _2458 (.D(g_2227), .Q(_2458_q));  // open: C2, C1, nQ
  SR_BIT _3654 (.C2(FCLK2), .C1(FCLK1), .D(g_2934), .Q(g_3654));  // open: nQ
  SR_BIT _3658 (.C2(FCLK2), .C1(FCLK1), .D(g_2969), .Q(g_3658));  // open: nQ
  SR_BIT _3660 (.C2(FCLK2), .C1(FCLK1), .D(g_2949), .Q(g_3660));  // open: nQ
  SR_BIT _3656 (.C2(FCLK2), .C1(FCLK1), .D(g_2944), .Q(g_3656));  // open: nQ
  SR_BIT _3652 (.C2(FCLK2), .C1(FCLK1), .D(g_2940), .Q(g_3652));  // open: nQ
  xor _3505 (_3505_out[0], LFO2_1, LFO5_1);
  xor _3506 (_3505_out[1], LFO3_1, LFO5_1);
  xor _3504 (_3505_out[2], LFO4_1, LFO5_1);
  not _3091 (_3091_out, _3092_out);
  not _3099 (_3099_out, _3100_out);
  Decoder #(.select(4), .disabled(0), .enable("false")) decoder_1 (
    .out0(DEC0), .out1(DEC1), .out2(DEC2), .out3(DEC3), .out4(DEC4), .out5(DEC5), .out6(DEC6), .out7(DEC7),
    .out8(DEC8), .out9(DEC9), .out10(DEC10), .out11(DEC11), .out12(DEC12), .out13(DEC13), .out14(DEC14),
    .out15(DEC15), .sel({g_2473, g_2475, g_2471, g_2469}));
  Decoder #(.select(3), .disabled(0), .enable("false")) decoder_2 (
    .out1(_2DEC1), .out2(_2DEC2), .out3(_2DEC3), .out4(_2DEC4), .out5(_2DEC5), .out6(_2DEC6), .out7(_2DEC7),
    .sel({g_3067, g_3068, g_3069}));  // open: out0
  Decoder #(.select(3), .disabled(0), .enable("false")) decoder_3 (
    .out2(_3DEC2), .out3(_3DEC3), .out4(_3DEC4), .out5(_3DEC5), .out6(_3DEC6), .out7(_3DEC7), .sel(_3505_out));  // open: out0, out1
  buf _3626 (_3626_out, _3625_q);
  SR_BIT _3653 (.C2(FCLK2), .C1(FCLK1), .D(g_3654), .Q(_3653_q));  // open: nQ
  SR_BIT _3657 (.C2(FCLK2), .C1(FCLK1), .D(g_3658), .Q(_3657_q));  // open: nQ
  SR_BIT _3659 (.C2(FCLK2), .C1(FCLK1), .D(g_3660), .Q(_3659_q));  // open: nQ
  SR_BIT _3655 (.C2(FCLK2), .C1(FCLK1), .D(g_3656), .Q(_3655_q));  // open: nQ
  SR_BIT _3651 (.C2(FCLK2), .C1(FCLK1), .D(g_3652), .Q(_3651_q));  // open: nQ
  or _3829 (_3829_out, _2DEC6, _2DEC7);
  buf _3496 (_3496_out, _3DEC7);
  or _3870 (_3870_out, _3829_out, _2DEC5);
  or _3495 (_3495_out, _3DEC6, _3DEC7);
  or _3494 (_3494_out, _3DEC4, _3DEC5, _3DEC6, _3DEC7);
  or _3497 (_3497_out, _3DEC3, _3DEC4, _3DEC5, _3DEC6);
  or _3498 (_3498_out, _3DEC3, _3DEC2);
  or _3493 (_3493_out, _3DEC7, _3DEC6, _3DEC5, _3DEC4);
  or _3503 (_3503_out, _3DEC6, _3DEC3);
  or _3502 (_3502_out, _3DEC2, _3DEC6);
  or _3501 (_3501_out, _3DEC2, _3DEC3, _3DEC6, _3DEC7);
  or _3500 (_3500_out, _3DEC3, _3DEC4, _3DEC5);
  or _3499 (_3499_out, _3DEC5, _3DEC4, _3DEC6, _3DEC7);
  and _3756 (_3756_out, _3854_out, g_2945);
  and _3756_2 (_3756_2_out, g_2941, _3855_out);
  and _3757 (_3757_out, _3853_out, g_2939);
  and _3757_2 (_3757_2_out, g_2941, _3852_out);
  and _3745 (_3745_out, _3854_out, g_2941);
  and _3745_2 (_3745_2_out, g_2939, _3855_out);
  and _3746 (_3746_out, _3853_out, g_2937);
  and _3746_2 (_3746_2_out, g_2939, _3852_out);
  and _3733 (_3733_out, _3854_out, g_2939);
  and _3733_2 (_3733_2_out, g_2937, _3855_out);
  and _3734 (_3734_out, _3853_out, g_2963);
  and _3734_2 (_3734_2_out, g_2937, _3852_out);
  and _3721 (_3721_out, _3854_out, g_2937);
  and _3721_2 (_3721_2_out, g_2963, _3855_out);
  and _3722 (_3722_out, _3853_out, g_2955);
  and _3722_2 (_3722_2_out, g_2963, _3852_out);
  and _3699 (_3699_out, _3854_out, g_2963);
  and _3699_2 (_3699_2_out, g_2955, _3855_out);
  and _3700 (_3700_out, _3853_out, g_2951);
  and _3700_2 (_3700_2_out, g_2955, _3852_out);
  and _3685 (_3685_out, _3854_out, g_2955);
  and _3685_2 (_3685_2_out, g_2951, _3855_out);
  and _3686 (_3686_out, _3853_out, 1'b0);
  and _3686_2 (_3686_2_out, g_2951, _3852_out);
  and _3671 (_3671_out, _3854_out, g_2951);
  and _3671_2 (_3671_2_out, 1'b0, _3855_out);
  and _3672 (_3672_out, _3853_out, 1'b0);
  and _3672_2 (_3672_2_out, 1'b0, _3852_out);
  nand _3650 (_3650_out, _3653_q, _3651_q, _3655_q);
  D_LATCH _3846 (.EN(FCLK1), .D(_3851_out), .nQ(_3846_nq));  // open: Q
  not _3851 (_3851_out, _2DEC7);
  D_LATCH _3845 (.EN(FCLK1), .D(_3850_out), .nQ(_3845_nq));  // open: Q
  not _3850 (_3850_out, _2DEC6);
  D_LATCH _3847 (.EN(FCLK1), .D(_3829_2_out), .nQ(_3847_nq));  // open: Q
  or _3829_2 (_3829_2_out, _2DEC6, _2DEC7);
  D_LATCH _3754 (.EN(FCLK1), .D(_3756_3_out), .nQ(_3754_nq));  // open: Q
  nor _3756_3 (_3756_3_out, _3756_out, _3756_2_out);
  D_LATCH _3755 (.EN(FCLK1), .D(_3757_3_out), .nQ(_3755_nq));  // open: Q
  nor _3757_3 (_3757_3_out, _3757_out, _3757_2_out);
  D_LATCH _3643 (.EN(FCLK1), .D(_3745_3_out), .nQ(_3643_nq));  // open: Q
  nor _3745_3 (_3745_3_out, _3745_out, _3745_2_out);
  D_LATCH _3744 (.EN(FCLK1), .D(_3746_3_out), .nQ(_3744_nq));  // open: Q
  nor _3746_3 (_3746_3_out, _3746_out, _3746_2_out);
  D_LATCH _3731 (.EN(FCLK1), .D(_3733_3_out), .nQ(_3731_nq));  // open: Q
  nor _3733_3 (_3733_3_out, _3733_out, _3733_2_out);
  D_LATCH _3732 (.EN(FCLK1), .D(_3734_3_out), .nQ(_3732_nq));  // open: Q
  nor _3734_3 (_3734_3_out, _3734_out, _3734_2_out);
  D_LATCH _3719 (.EN(FCLK1), .D(_3721_3_out), .nQ(_3719_nq));  // open: Q
  nor _3721_3 (_3721_3_out, _3721_out, _3721_2_out);
  D_LATCH _3720 (.EN(FCLK1), .D(_3722_3_out), .nQ(_3720_nq));  // open: Q
  nor _3722_3 (_3722_3_out, _3722_out, _3722_2_out);
  D_LATCH _3697 (.EN(FCLK1), .D(_3699_3_out), .nQ(_3697_nq));  // open: Q
  nor _3699_3 (_3699_3_out, _3699_out, _3699_2_out);
  D_LATCH _3698 (.EN(FCLK1), .D(_3700_3_out), .nQ(_3698_nq));  // open: Q
  nor _3700_3 (_3700_3_out, _3700_out, _3700_2_out);
  D_LATCH _3683 (.EN(FCLK1), .D(_3685_3_out), .nQ(_3683_nq));  // open: Q
  nor _3685_3 (_3685_3_out, _3685_out, _3685_2_out);
  D_LATCH _3684 (.EN(FCLK1), .D(_3686_3_out), .nQ(_3684_nq));  // open: Q
  nor _3686_3 (_3686_3_out, _3686_out, _3686_2_out);
  D_LATCH _3669 (.EN(FCLK1), .D(_3671_3_out), .nQ(_3669_nq));  // open: Q
  nor _3671_3 (_3671_3_out, _3671_out, _3671_2_out);
  D_LATCH _3670 (.EN(FCLK1), .D(_3672_3_out), .nQ(_3670_nq));  // open: Q
  nor _3672_3 (_3672_3_out, _3672_out, _3672_2_out);
  and _3642 (_3642_out[0], _3657_q, _3650_out);
  and _3641 (_3642_out[1], _3650_out, _3659_q);
  nand _3871 (_3871_out, _3496_out, _3870_out);
  and _3873 (_3873_out, _3495_out, _2DEC2);
  and _3873_2 (_3873_2_out, _3494_out, _2DEC3);
  and _3873_3 (_3873_3_out, _2DEC4, _3497_out);
  and _3873_4 (_3873_4_out, _3498_out, _3870_out);
  and _3872 (_3872_out, _3496_out, _2DEC4);
  nor _3872_2 (_3872_2_out, _3872_out, _3872_3_out);
  and _3872_3 (_3872_3_out, _3493_out, _3870_out);
  and _3874 (_3874_out, _3870_out, _3503_out);
  and _3874_2 (_3874_2_out, _2DEC4, _3502_out);
  and _3874_3 (_3874_3_out, _2DEC3, _3501_out);
  and _3874_4 (_3874_4_out, _2DEC2, _3500_out);
  and _3874_5 (_3874_5_out, _2DEC1, _3499_out);
  and _3874_6 (_3874_6_out, 1'b0, 1'b0);
  Adder #(.width(1)) adder_1 (.a(_3754_nq), .b(_3755_nq), .out(adder_1_out), .cin(1'b0), .cout(adder_1_cout));
  Adder #(.width(1)) adder_2 (.a(_3643_nq), .b(_3744_nq), .out(adder_2_out), .cin(adder_1_cout), .cout(adder_2_cout));
  Adder #(.width(1)) adder_3 (.a(_3731_nq), .b(_3732_nq), .out(adder_3_out), .cin(adder_2_cout), .cout(adder_3_cout));
  Adder #(.width(1)) adder_4 (.a(_3719_nq), .b(_3720_nq), .out(adder_4_out), .cin(adder_3_cout), .cout(adder_4_cout));
  Adder #(.width(1)) adder_5 (.a(_3697_nq), .b(_3698_nq), .out(adder_5_out), .cin(adder_4_cout), .cout(adder_5_cout));
  Adder #(.width(1)) adder_6 (.a(_3683_nq), .b(_3684_nq), .out(adder_6_out), .cin(adder_5_cout), .cout(adder_6_cout));
  Adder #(.width(1)) adder_7 (.a(_3669_nq), .b(_3670_nq), .out(adder_7_out), .cin(adder_6_cout), .cout(adder_7_cout));
  or _3873_5 (_3873_5_out, _3873_out, _3873_2_out, _3873_3_out, _3873_4_out);
  nor _3874_7 (_3874_7_out, _3874_out, _3874_2_out, _3874_3_out, _3874_4_out, _3874_5_out, _3874_6_out);
  Decoder #(.select(3), .disabled(0), .enable("false")) decoder_4 (
    .out1(_4DEC1), .out2(_4DEC2), .out3(_4DEC3), .out4(_4DEC4), .out5(_4DEC5), .out6(_4DEC6), .out7(_4DEC7),
    .sel(_3642_out));  // open: out0
  not _3852 (_3852_out, _3871_out);
  not _3855 (_3855_out, _3873_5_out);
  not _3854 (_3854_out, _3872_2_out);
  not _3853 (_3853_out, _3874_7_out);
  and _3752 (_3752_out, adder_1_out, _3846_nq);
  and _3752_2 (_3752_2_out, adder_2_out, _3845_nq);
  and _3752_3 (_3752_3_out, _3847_nq, adder_3_out);
  and _3741 (_3741_out, adder_2_out, _3846_nq);
  and _3741_2 (_3741_2_out, adder_3_out, _3845_nq);
  and _3741_3 (_3741_3_out, _3847_nq, adder_4_out);
  and _3729 (_3729_out, adder_3_out, _3846_nq);
  and _3729_2 (_3729_2_out, adder_4_out, _3845_nq);
  and _3729_3 (_3729_3_out, _3847_nq, adder_5_out);
  and _3717 (_3717_out, adder_4_out, _3846_nq);
  and _3717_2 (_3717_2_out, adder_5_out, _3845_nq);
  and _3717_3 (_3717_3_out, _3847_nq, adder_6_out);
  and _3795 (_3795_out, adder_5_out, _3846_nq);
  and _3795_2 (_3795_2_out, adder_6_out, _3845_nq);
  and _3795_3 (_3795_3_out, _3847_nq, adder_7_out);
  and _3681 (_3681_out, adder_6_out, _3846_nq);
  and _3681_2 (_3681_2_out, adder_7_out, _3845_nq);
  and _3681_3 (_3681_3_out, _3847_nq, adder_7_cout);
  and _3667 (_3667_out, adder_7_out, _3846_nq);
  and _3667_2 (_3667_2_out, adder_7_cout, _3845_nq);
  and _3667_3 (_3667_3_out, _3847_nq, 1'b0);
  and _3668 (_3668_out, adder_7_cout, _3846_nq);
  and _3668_2 (_3668_2_out, 1'b0, _3845_nq);
  and _3668_3 (_3668_3_out, _3847_nq, 1'b0);
  or _3752_4 (_3752_4_out, _3752_out, _3752_2_out, _3752_3_out);
  or _3741_4 (_3741_4_out, _3741_out, _3741_2_out, _3741_3_out);
  or _3729_4 (_3729_4_out, _3729_out, _3729_2_out, _3729_3_out);
  or _3717_4 (_3717_4_out, _3717_out, _3717_2_out, _3717_3_out);
  or _3795_4 (_3795_4_out, _3795_out, _3795_2_out, _3795_3_out);
  or _3681_4 (_3681_4_out, _3681_out, _3681_2_out, _3681_3_out);
  or _3667_4 (_3667_4_out, _3667_out, _3667_2_out, _3667_3_out);
  or _3668_4 (_3668_4_out, _3668_out, _3668_2_out, _3668_3_out);
  xnor _3751 (_3751_out, LFO6, _3752_4_out);
  xnor _3740 (_3740_out, LFO6, _3741_4_out);
  xnor _3728 (_3728_out, LFO6, _3729_4_out);
  xnor _3716 (_3716_out, LFO6, _3717_4_out);
  xnor _3694 (_3694_out, LFO6, _3795_4_out);
  xnor _3680 (_3680_out, LFO6, _3681_4_out);
  xnor _3666 (_3666_out, LFO6, _3667_4_out);
  xnor _3767 (_3767_out, LFO6, _3668_4_out);
  not _3764 (_3764_out, LFO6);
  SR_BIT _2338 (.C2(FCLK2), .C1(FCLK1), .D(g_3654), .Q(_2338_q));  // open: nQ
  SR_BIT _2351 (.C2(FCLK2), .C1(FCLK1), .D(g_3656), .Q(_2351_q));  // open: nQ
  SR_BIT _2449 (.C2(FCLK2), .C1(FCLK1), .D(g_3652), .Q(_2449_q));  // open: nQ
  D_LATCH _3750 (.EN(FCLK2), .D(_3751_out), .nQ(_3750_nq));  // open: Q
  D_LATCH _3739 (.EN(FCLK2), .D(_3740_out), .nQ(_3739_nq));  // open: Q
  SR_BIT _3738 (.C2(FCLK2), .C1(FCLK1), .D(g_2974), .Q(_3738_q));  // open: nQ
  D_LATCH _3727 (.EN(FCLK2), .D(_3728_out), .nQ(_3727_nq));  // open: Q
  SR_BIT _3726 (.C2(FCLK2), .C1(FCLK1), .D(g_2966), .Q(_3726_q));  // open: nQ
  D_LATCH _3715 (.EN(FCLK2), .D(_3716_out), .nQ(_3715_nq));  // open: Q
  SR_BIT _3714 (.C2(FCLK2), .C1(FCLK1), .D(g_2958), .Q(_3714_q));  // open: nQ
  D_LATCH _3693 (.EN(FCLK2), .D(_3694_out), .nQ(_3693_nq));  // open: Q
  SR_BIT _3692 (.C2(FCLK2), .C1(FCLK1), .D(g_2952), .Q(_3692_q));  // open: nQ
  D_LATCH _3679 (.EN(FCLK2), .D(_3680_out), .nQ(_3679_nq));  // open: Q
  SR_BIT _3678 (.C2(FCLK2), .C1(FCLK1), .D(g_2945), .Q(_3678_q));  // open: nQ
  D_LATCH _3665 (.EN(FCLK2), .D(_3666_out), .nQ(_3665_nq));  // open: Q
  SR_BIT _3664 (.C2(FCLK2), .C1(FCLK1), .D(g_2941), .Q(_3664_q));  // open: nQ
  D_LATCH _3766 (.EN(FCLK2), .D(_3767_out), .nQ(_3766_nq));  // open: Q
  SR_BIT _3765 (.C2(FCLK2), .C1(FCLK1), .D(g_2939), .Q(_3765_q));  // open: nQ
  D_LATCH _3762 (.EN(FCLK2), .D(_3764_out), .nQ(_3762_nq));  // open: Q
  SR_BIT _3760 (.C2(FCLK2), .C1(FCLK1), .D(g_2937), .Q(_3760_q));  // open: nQ
  SR_BIT _3675 (.C2(FCLK2), .C1(FCLK1), .D(g_2963), .Q(_3675_q));  // open: nQ
  SR_BIT _3689 (.C2(FCLK2), .C1(FCLK1), .D(g_2955), .Q(_3689_q));  // open: nQ
  SR_BIT _3703 (.C2(FCLK2), .C1(FCLK1), .D(g_2951), .Q(_3703_q));  // open: nQ
  or _3623 (_3623_out, _2458_q, _2457_q);
  or _3622 (_3622_out, _2457_q, _2458_q);
  not _2456 (_2456_out, _2455_out);
  not _2455 (_2455_out, _3623_out);
  Adder #(.width(1)) adder_8 (.a(_3622_out), .b(_3655_q), .out(_3642_out[2]), .cin(1'b1), .cout(adder_8_cout));
  Adder #(.width(1)) adder_9 (.a(_2458_q), .b(_3651_q), .out(adder_9_out[0]), .cin(adder_8_cout), .cout(adder_9_cout));
  Adder #(.width(1)) adder_10 (.a(1'b0), .b(_3653_q), .out(adder_9_out[1]), .cin(adder_9_cout), .cout(adder_10_cout));
  Adder #(.width(1)) adder_11 (
    .a(_3623_out), .b(1'b0), .out(adder_9_out[2]), .cin(adder_10_cout), .cout(adder_9_out[3]));
  D_LATCH _2337 (.EN(FCLK1), .D(_2338_q), .nQ(_2337_nq));  // open: Q
  D_LATCH _2350 (.EN(FCLK1), .D(_2351_q), .nQ(_2350_nq));  // open: Q
  D_LATCH _2450 (.EN(FCLK1), .D(_2449_q), .nQ(_2450_nq));  // open: Q
  not _3790 (_3790_out, LFO6);
  not _3621 (_3621_out, _2337_nq);
  not _2349 (_2349_out[0], _2350_nq);
  not _3624 (_2349_out[1], _2450_nq);
  Adder #(.width(1)) adder_12 (.a(_3750_nq), .b(1'b0), .out(adder_12_out), .cin(_3790_out), .cout(adder_12_cout));
  Adder #(.width(1)) adder_13 (
    .a(_3739_nq), .b(_3738_q), .out(adder_13_out), .cin(adder_12_cout), .cout(adder_13_cout));
  Adder #(.width(1)) adder_14 (
    .a(_3727_nq), .b(_3726_q), .out(adder_14_out), .cin(adder_13_cout), .cout(adder_14_cout));
  Adder #(.width(1)) adder_15 (
    .a(_3715_nq), .b(_3714_q), .out(adder_15_out), .cin(adder_14_cout), .cout(adder_15_cout));
  Adder #(.width(1)) adder_16 (
    .a(_3693_nq), .b(_3692_q), .out(adder_16_out), .cin(adder_15_cout), .cout(adder_16_cout));
  Adder #(.width(1)) adder_17 (
    .a(_3679_nq), .b(_3678_q), .out(adder_17_out), .cin(adder_16_cout), .cout(adder_17_cout));
  Adder #(.width(1)) adder_18 (
    .a(_3665_nq), .b(_3664_q), .out(adder_18_out), .cin(adder_17_cout), .cout(adder_18_cout));
  Adder #(.width(1)) adder_19 (
    .a(_3766_nq), .b(_3765_q), .out(adder_19_out), .cin(adder_18_cout), .cout(adder_19_cout));
  Adder #(.width(1)) adder_20 (
    .a(_3762_nq), .b(_3760_q), .out(adder_20_out), .cin(adder_19_cout), .cout(adder_20_cout));
  Adder #(.width(1)) adder_21 (
    .a(_3762_nq), .b(_3675_q), .out(adder_21_out), .cin(adder_20_cout), .cout(adder_21_cout));
  Adder #(.width(1)) adder_22 (
    .a(_3762_nq), .b(_3689_q), .out(adder_22_out), .cin(adder_21_cout), .cout(adder_22_cout));
  Adder #(.width(1)) adder_23 (.a(_3762_nq), .b(_3703_q), .out(adder_23_out), .cin(adder_22_cout));  // open: cout
  Decoder #(.select(4), .disabled(0), .enable("false")) decoder_5 (
    .out5(decoder_5_out5), .out6(decoder_5_out6), .out7(decoder_5_out7), .out8(decoder_5_out8),
    .out9(decoder_5_out9), .sel(adder_9_out));  // open: out0, out1, out2, out3, out4, out10, out11, out12, out13, out14, out15
  D_LATCH _3758 (.EN(FCLK1), .D(adder_12_out), .nQ(_3758_nq));  // open: Q
  D_LATCH _3747 (.EN(FCLK1), .D(adder_13_out), .nQ(_3747_nq));  // open: Q
  D_LATCH _3735 (.EN(FCLK1), .D(adder_14_out), .nQ(_3735_nq));  // open: Q
  D_LATCH _3723 (.EN(FCLK1), .D(adder_15_out), .nQ(_3723_nq));  // open: Q
  D_LATCH _3704 (.EN(FCLK1), .D(adder_16_out), .nQ(_3704_nq));  // open: Q
  D_LATCH _3705 (.EN(FCLK1), .D(adder_17_out), .nQ(_3705_nq));  // open: Q
  D_LATCH _3706 (.EN(FCLK1), .D(adder_18_out), .nQ(_3706_nq));  // open: Q
  D_LATCH _3712 (.EN(FCLK1), .D(adder_19_out), .nQ(_3712_nq));  // open: Q
  D_LATCH _3761 (.EN(FCLK1), .D(adder_20_out), .nQ(_3761_nq));  // open: Q
  D_LATCH _3764_2 (.EN(FCLK1), .D(adder_21_out), .nQ(_3764_2_nq));  // open: Q
  D_LATCH _3688 (.EN(FCLK1), .D(adder_22_out), .nQ(_3688_nq));  // open: Q
  D_LATCH _3702 (.EN(FCLK1), .D(adder_23_out), .nQ(_3702_nq));  // open: Q
  Decoder #(.select(2), .disabled(0), .enable("false")) decoder_6 (
    .out0(decoder_6_out0), .out1(decoder_6_out1), .out2(decoder_6_out2), .out3(decoder_6_out3),
    .sel(_2349_out));
  not _3749 (_3749_out, _3758_nq);
  not _3737 (_3737_out, _3747_nq);
  not _3725 (_3725_out, _3735_nq);
  not _3713 (_3713_out, _3723_nq);
  not _3691 (_3691_out, _3704_nq);
  not _3677 (_3677_out, _3705_nq);
  not _3663 (_3663_out, _3706_nq);
  not _3711 (_3711_out, _3712_nq);
  not _3763 (_3763_out, _3761_nq);
  not _3673 (_3673_out, _3764_2_nq);
  not _3687 (_3687_out, _3688_nq);
  not _3701 (_3701_out, _3702_nq);
  and and_1 (and_1_out, _2456_out, decoder_5_out5);
  and and_2 (and_2_out, _2456_out, decoder_5_out6);
  and and_3 (and_3_out, _2456_out, decoder_5_out7);
  and and_4 (and_4_out, _2456_out, decoder_5_out8);
  and and_5 (and_5_out, _2456_out, decoder_5_out9);
  or _3632 (_3632_out, _4DEC1, _4DEC2, _4DEC6, _4DEC7);
  or _3640 (_3640_out, _4DEC7, _4DEC4, _4DEC3);
  or _3630 (_3630_out, _4DEC2, _4DEC4, _4DEC6);
  or _3637 (_3637_out, _4DEC7, _4DEC6, _4DEC5);
  D_LATCH _3168 (.EN(FCLK1), .D(_3150_out), .nQ(_3168_nq));  // open: Q
  or _3150 (_3150_out, DEC4, DEC5, DEC6, DEC7);
  D_LATCH _3153 (.EN(FCLK1), .D(_3151_out), .nQ(_3153_nq));  // open: Q
  or _3151 (_3151_out, DEC8, DEC9, DEC10, DEC11, DEC12, DEC13);
  D_LATCH _3154 (.EN(FCLK1), .D(_3152_out), .nQ(_3154_nq));  // open: Q
  or _3152 (_3152_out, DEC14, DEC15);
  and _2454 (_2454_out, and_5_out, and_5_out);
  not _3157 (_3157_out, _3168_nq);
  not _3155 (_3155_out, _3153_nq);
  not _3156 (_3156_out, _3154_nq);
  and _3825 (_3825_out, 1'b1, decoder_6_out0);
  and _3826 (_3826_out, _3749_out, decoder_6_out0);
  and _3826_2 (_3826_2_out, 1'b1, decoder_6_out1);
  and _3791 (_3791_out, _3737_out, decoder_6_out0);
  and _3791_2 (_3791_2_out, _3749_out, decoder_6_out1);
  and _3791_3 (_3791_3_out, 1'b0, decoder_6_out2);
  and _2441 (_2441_out, decoder_6_out0, _3725_out);
  and _2441_2 (_2441_2_out, decoder_6_out1, _3737_out);
  and _2441_3 (_2441_3_out, _3749_out, decoder_6_out2);
  and _2441_4 (_2441_4_out, 1'b0, decoder_6_out3);
  and _2435 (_2435_out, decoder_6_out0, _3713_out);
  and _2435_2 (_2435_2_out, decoder_6_out1, _3725_out);
  and _2435_3 (_2435_3_out, _3737_out, decoder_6_out2);
  and _2435_4 (_2435_4_out, _3749_out, decoder_6_out3);
  and _2429 (_2429_out, decoder_6_out0, _3691_out);
  and _2429_2 (_2429_2_out, decoder_6_out1, _3713_out);
  and _2429_3 (_2429_3_out, _3725_out, decoder_6_out2);
  and _2429_4 (_2429_4_out, _3737_out, decoder_6_out3);
  and _2423 (_2423_out, decoder_6_out0, _3677_out);
  and _2423_2 (_2423_2_out, decoder_6_out1, _3691_out);
  and _2423_3 (_2423_3_out, _3713_out, decoder_6_out2);
  and _2423_4 (_2423_4_out, _3725_out, decoder_6_out3);
  and _2417 (_2417_out, decoder_6_out0, _3663_out);
  and _2417_2 (_2417_2_out, decoder_6_out1, _3677_out);
  and _2417_3 (_2417_3_out, _3691_out, decoder_6_out2);
  and _2417_4 (_2417_4_out, _3713_out, decoder_6_out3);
  and _2411 (_2411_out, decoder_6_out0, _3711_out);
  and _2411_2 (_2411_2_out, decoder_6_out1, _3663_out);
  and _2411_3 (_2411_3_out, _3677_out, decoder_6_out2);
  and _2411_4 (_2411_4_out, _3691_out, decoder_6_out3);
  and _2405 (_2405_out, decoder_6_out0, _3763_out);
  and _2405_2 (_2405_2_out, decoder_6_out1, _3711_out);
  and _2405_3 (_2405_3_out, _3663_out, decoder_6_out2);
  and _2405_4 (_2405_4_out, _3677_out, decoder_6_out3);
  and _2399 (_2399_out, decoder_6_out0, _3673_out);
  and _2399_2 (_2399_2_out, decoder_6_out1, _3763_out);
  and _2399_3 (_2399_3_out, _3711_out, decoder_6_out2);
  and _2399_4 (_2399_4_out, _3663_out, decoder_6_out3);
  and _2393 (_2393_out, decoder_6_out0, _3687_out);
  and _2393_2 (_2393_2_out, decoder_6_out1, _3673_out);
  and _2393_3 (_2393_3_out, _3763_out, decoder_6_out2);
  and _2393_4 (_2393_4_out, _3711_out, decoder_6_out3);
  and _2387 (_2387_out, decoder_6_out0, _3701_out);
  and _2387_2 (_2387_2_out, decoder_6_out1, _3687_out);
  and _2387_3 (_2387_3_out, _3673_out, decoder_6_out2);
  and _2387_4 (_2387_4_out, _3763_out, decoder_6_out3);
  and _2381 (_2381_out, decoder_6_out0, 1'b0);
  and _2381_2 (_2381_2_out, decoder_6_out1, _3701_out);
  and _2381_3 (_2381_3_out, _3687_out, decoder_6_out2);
  and _2381_4 (_2381_4_out, _3673_out, decoder_6_out3);
  and _2447 (_2447_out, _3701_out, decoder_6_out2);
  and _2447_2 (_2447_2_out, _3687_out, decoder_6_out3);
  and _2448 (_2448_out, 1'b0, decoder_6_out2);
  and _2448_2 (_2448_2_out, _3701_out, decoder_6_out3);
  and _3387 (_3387_out, and_4_out, and_4_out);
  or _3826_3 (_3826_3_out, _3826_out, _3826_2_out);
  or _3791_4 (_3791_4_out, _3791_out, _3791_2_out, _3791_3_out);
  or _2441_5 (_2441_5_out, _2441_out, _2441_2_out, _2441_3_out, _2441_4_out);
  or _2435_5 (_2435_5_out, _2435_out, _2435_2_out, _2435_3_out, _2435_4_out);
  or _2429_5 (_2429_5_out, _2429_out, _2429_2_out, _2429_3_out, _2429_4_out);
  or _2423_5 (_2423_5_out, _2423_out, _2423_2_out, _2423_3_out, _2423_4_out);
  or _2417_5 (_2417_5_out, _2417_out, _2417_2_out, _2417_3_out, _2417_4_out);
  or _2411_5 (_2411_5_out, _2411_out, _2411_2_out, _2411_3_out, _2411_4_out);
  or _2405_5 (_2405_5_out, _2405_out, _2405_2_out, _2405_3_out, _2405_4_out);
  or _2399_5 (_2399_5_out, _2399_out, _2399_2_out, _2399_3_out, _2399_4_out);
  or _2393_5 (_2393_5_out, _2393_out, _2393_2_out, _2393_3_out, _2393_4_out);
  or _2387_5 (_2387_5_out, _2387_out, _2387_2_out, _2387_3_out, _2387_4_out);
  or _2381_5 (_2381_5_out, _2381_out, _2381_2_out, _2381_3_out, _2381_4_out);
  or _2447_3 (_2447_3_out, _2447_out, _2447_2_out);
  or _2448_3 (_2448_3_out, _2448_out, _2448_2_out);
  and _3387_2 (_3387_2_out, and_5_out, _3637_out);
  or _3387_3 (_3387_3_out, _3387_out, _3387_2_out);
  and _2453 (_2453_out, and_3_out, and_3_out);
  and _2453_2 (_2453_2_out, and_4_out, _3637_out);
  or _2453_3 (_2453_3_out, _2453_out, _2453_2_out, _2453_4_out);
  and _2453_4 (_2453_4_out, and_5_out, _3640_out);
  not _3620 (_3620_out, _3621_out);
  and _2452 (_2452_out, _3630_out, and_5_out);
  not not_1 (not_1_out, _3621_out);
  not _3619 (_3619_out, _3620_out);
  and _2452_2 (_2452_2_out, _3637_out, and_3_out);
  and _2452_3 (_2452_3_out, _3640_out, and_4_out);
  or _2452_4 (_2452_4_out, _2452_out, _2452_3_out, _2452_2_out, _2452_5_out);
  nand _3824 (_3824_out, _2441_5_out, not_1_out);
  and _3801 (_3801_out, _3825_out, _3619_out);
  and _3801_2 (_3801_2_out, _2435_5_out, not_1_out);
  and _3796 (_3796_out, _3826_3_out, _3619_out);
  and _3796_2 (_3796_2_out, _2429_5_out, not_1_out);
  and _2446 (_2446_out, _3791_4_out, _3619_out);
  and _2446_2 (_2446_2_out, _2423_5_out, not_1_out);
  and _2440 (_2440_out, _2441_5_out, _3619_out);
  and _2440_2 (_2440_2_out, _2417_5_out, not_1_out);
  and _2434 (_2434_out, _2435_5_out, _3619_out);
  and _2434_2 (_2434_2_out, _2411_5_out, not_1_out);
  and _2428 (_2428_out, _2429_5_out, _3619_out);
  and _2428_2 (_2428_2_out, _2405_5_out, not_1_out);
  and _2422 (_2422_out, _2423_5_out, _3619_out);
  and _2422_2 (_2422_2_out, _2399_5_out, not_1_out);
  and _2416 (_2416_out, _2417_5_out, _3619_out);
  and _2416_2 (_2416_2_out, _2393_5_out, not_1_out);
  and _2410 (_2410_out, _2411_5_out, _3619_out);
  and _2410_2 (_2410_2_out, _2387_5_out, not_1_out);
  and _2404 (_2404_out, _2405_5_out, _3619_out);
  and _2404_2 (_2404_2_out, _2381_5_out, not_1_out);
  and _2398 (_2398_out, _2399_5_out, _3619_out);
  and _2398_2 (_2398_2_out, _2447_3_out, not_1_out);
  and _2392 (_2392_out, _2393_5_out, _3619_out);
  and _2392_2 (_2392_2_out, _2448_3_out, not_1_out);
  and _2386 (_2386_out, _2387_5_out, _3619_out);
  and _2386_2 (_2386_2_out, 1'b0, not_1_out);
  and _2380 (_2380_out, _2381_5_out, _3619_out);
  and _2380_2 (_2380_2_out, 1'b0, not_1_out);
  and _2375 (_2375_out, _2447_3_out, _3619_out);
  and _2375_2 (_2375_2_out, 1'b0, not_1_out);
  and _2370 (_2370_out, _2448_3_out, _3619_out);
  and _2370_2 (_2370_2_out, 1'b0, not_1_out);
  and _2452_5 (_2452_5_out, and_2_out, and_2_out);
  nor _3801_3 (_3801_3_out, _3801_out, _3801_2_out);
  nor _3796_3 (_3796_3_out, _3796_out, _3796_2_out);
  nor _2446_3 (_2446_3_out, _2446_out, _2446_2_out);
  nor _2440_3 (_2440_3_out, _2440_out, _2440_2_out);
  nor _2434_3 (_2434_3_out, _2434_out, _2434_2_out);
  nor _2428_3 (_2428_3_out, _2428_out, _2428_2_out);
  nor _2422_3 (_2422_3_out, _2422_out, _2422_2_out);
  nor _2416_3 (_2416_3_out, _2416_out, _2416_2_out);
  nor _2410_3 (_2410_3_out, _2410_out, _2410_2_out);
  nor _2404_3 (_2404_3_out, _2404_out, _2404_2_out);
  nor _2398_3 (_2398_3_out, _2398_out, _2398_2_out);
  nor _2392_3 (_2392_3_out, _2392_out, _2392_2_out);
  nor _2386_3 (_2386_3_out, _2386_out, _2386_2_out);
  nor _2380_3 (_2380_3_out, _2380_out, _2380_2_out);
  nor _2375_3 (_2375_3_out, _2375_out, _2375_2_out);
  nor _2370_3 (_2370_3_out, _2370_out, _2370_2_out);
  and _2451 (_2451_out, and_1_out, and_1_out);
  and _2451_2 (_2451_2_out, and_2_out, _3637_out);
  and _2451_3 (_2451_3_out, and_3_out, _3640_out);
  or _2451_4 (_2451_4_out, _2451_2_out, _2451_out, _2451_3_out, _2451_6_out, _2451_5_out, _2451_7_out);
  and _3532 (_3532_out, _3802_out, _3157_out);
  and _3532_2 (_3532_2_out, 1'b0, _3155_out);
  and _3532_3 (_3532_3_out, 1'b0, _3156_out);
  and _3537 (_3537_out, _3797_out, _3157_out);
  and _3537_2 (_3537_2_out, _3802_out, _3155_out);
  and _3537_3 (_3537_3_out, 1'b0, _3156_out);
  and _3542 (_3542_out, _3792_out, _3157_out);
  and _3542_2 (_3542_2_out, _3797_out, _3155_out);
  and _3542_3 (_3542_3_out, _3802_out, _3156_out);
  and _3547 (_3547_out, _2442_out, _3157_out);
  and _3547_2 (_3547_2_out, _3792_out, _3155_out);
  and _3547_3 (_3547_3_out, _3797_out, _3156_out);
  and _3552 (_3552_out, _2436_out, _3157_out);
  and _3552_2 (_3552_2_out, _2442_out, _3155_out);
  and _3552_3 (_3552_3_out, _3792_out, _3156_out);
  and _3557 (_3557_out, _2430_out, _3157_out);
  and _3557_2 (_3557_2_out, _2436_out, _3155_out);
  and _3557_3 (_3557_3_out, _2442_out, _3156_out);
  and _3562 (_3562_out, _2424_out, _3157_out);
  and _3562_2 (_3562_2_out, _2430_out, _3155_out);
  and _3562_3 (_3562_3_out, _2436_out, _3156_out);
  and _3567 (_3567_out, _2418_out, _3157_out);
  and _3567_2 (_3567_2_out, _2424_out, _3155_out);
  and _3567_3 (_3567_3_out, _2430_out, _3156_out);
  and _3572 (_3572_out, _2412_out, _3157_out);
  and _3572_2 (_3572_2_out, _2418_out, _3155_out);
  and _3572_3 (_3572_3_out, _2424_out, _3156_out);
  and _3577 (_3577_out, _2406_out, _3157_out);
  and _3577_2 (_3577_2_out, _2412_out, _3155_out);
  and _3577_3 (_3577_3_out, _2418_out, _3156_out);
  and _3582 (_3582_out, _2400_out, _3157_out);
  and _3582_2 (_3582_2_out, _2406_out, _3155_out);
  and _3582_3 (_3582_3_out, _2412_out, _3156_out);
  and _3587 (_3587_out, _2394_out, _3157_out);
  and _3587_2 (_3587_2_out, _2400_out, _3155_out);
  and _3587_3 (_3587_3_out, _2406_out, _3156_out);
  and _3592 (_3592_out, _2388_out, _3157_out);
  and _3592_2 (_3592_2_out, _2394_out, _3155_out);
  and _3592_3 (_3592_3_out, _2400_out, _3156_out);
  and _3597 (_3597_out, _2382_out, _3157_out);
  and _3597_2 (_3597_2_out, _2388_out, _3155_out);
  and _3597_3 (_3597_3_out, _2394_out, _3156_out);
  and _3602 (_3602_out, _2376_out, _3157_out);
  and _3602_2 (_3602_2_out, _2382_out, _3155_out);
  and _3602_3 (_3602_3_out, _2388_out, _3156_out);
  and _3616 (_3616_out, _2371_out, _3157_out);
  and _3616_2 (_3616_2_out, _2376_out, _3155_out);
  and _3616_3 (_3616_3_out, _2382_out, _3156_out);
  and _3615 (_3615_out, _2366_out, _3157_out);
  and _3615_2 (_3615_2_out, _2371_out, _3155_out);
  and _3615_3 (_3615_3_out, _2376_out, _3156_out);
  and _3614 (_3614_out, 1'b0, _3157_out);
  and _3614_2 (_3614_2_out, _2366_out, _3155_out);
  and _3614_3 (_3614_3_out, _2371_out, _3156_out);
  and _2451_5 (_2451_5_out, and_5_out, _3632_out);
  and _2451_6 (_2451_6_out, and_4_out, _3630_out);
  nor _3532_4 (_3532_4_out, _3532_out, _3532_2_out, _3532_3_out);
  nor _3537_4 (_3537_4_out, _3537_out, _3537_2_out, _3537_3_out);
  nor _3542_4 (_3542_4_out, _3542_out, _3542_2_out, _3542_3_out);
  nor _3547_4 (_3547_4_out, _3547_out, _3547_2_out, _3547_3_out);
  nor _3552_4 (_3552_4_out, _3552_out, _3552_2_out, _3552_3_out);
  nor _3557_4 (_3557_4_out, _3557_out, _3557_2_out, _3557_3_out);
  nor _3562_4 (_3562_4_out, _3562_out, _3562_2_out, _3562_3_out);
  nor _3567_4 (_3567_4_out, _3567_out, _3567_2_out, _3567_3_out);
  nor _3572_4 (_3572_4_out, _3572_out, _3572_2_out, _3572_3_out);
  nor _3577_4 (_3577_4_out, _3577_out, _3577_2_out, _3577_3_out);
  nor _3582_4 (_3582_4_out, _3582_out, _3582_2_out, _3582_3_out);
  nor _3587_4 (_3587_4_out, _3587_out, _3587_2_out, _3587_3_out);
  nor _3592_4 (_3592_4_out, _3592_out, _3592_2_out, _3592_3_out);
  nor _3597_4 (_3597_4_out, _3597_out, _3597_2_out, _3597_3_out);
  nor _3602_4 (_3602_4_out, _3602_out, _3602_2_out, _3602_3_out);
  nor _3616_4 (_3616_4_out, _3616_out, _3616_2_out, _3616_3_out);
  nor _3615_4 (_3615_4_out, _3615_out, _3615_2_out, _3615_3_out);
  nor _3614_4 (_3614_4_out, _3614_out, _3614_2_out, _3614_3_out);
  and _2451_7 (_2451_7_out, 1'b0, 1'b0);
  SR_BIT _3628 (.C2(FCLK2), .C1(FCLK1), .D(_3626_out), .Q(_3628_q));  // open: nQ
  SR_BIT _3844 (.C2(FCLK2), .C1(FCLK1), .D(_3856_out), .Q(_3844_q));  // open: nQ
  xor _3856 (_3856_out, _3626_out, _2451_4_out);
  SR_BIT _3843 (.C2(FCLK2), .C1(FCLK1), .D(_3857_out), .Q(_3843_q));  // open: nQ
  xor _3857 (_3857_out, _3626_out, _2452_4_out);
  SR_BIT _3842 (.C2(FCLK2), .C1(FCLK1), .D(_3827_out), .Q(_3842_q));  // open: nQ
  xor _3827 (_3827_out, _3626_out, _2453_3_out);
  SR_BIT _3806 (.C2(FCLK2), .C1(FCLK1), .D(_3808_out), .Q(_3806_q));  // open: nQ
  xor _3808 (_3808_out, _3626_out, _3387_3_out);
  SR_BIT _3788 (.C2(FCLK2), .C1(FCLK1), .D(_3787_out), .Q(_3788_q));  // open: nQ
  xor _3787 (_3787_out, _3626_out, _2454_out);
  D_LATCH _3805 (.EN(FCLK2), .D(_3824_out), .nQ(_3805_nq));  // open: Q
  D_LATCH _3800 (.EN(FCLK2), .D(_3801_3_out), .nQ(_3800_nq));  // open: Q
  D_LATCH _3795_5 (.EN(FCLK2), .D(_3796_3_out), .nQ(_3795_5_nq));  // open: Q
  D_LATCH _2445 (.EN(FCLK2), .D(_2446_3_out), .nQ(_2445_nq));  // open: Q
  D_LATCH _2439 (.EN(FCLK2), .D(_2440_3_out), .nQ(_2439_nq));  // open: Q
  D_LATCH _2433 (.EN(FCLK2), .D(_2434_3_out), .nQ(_2433_nq));  // open: Q
  D_LATCH _2427 (.EN(FCLK2), .D(_2428_3_out), .nQ(_2427_nq));  // open: Q
  D_LATCH _2421 (.EN(FCLK2), .D(_2422_3_out), .nQ(_2421_nq));  // open: Q
  D_LATCH _2415 (.EN(FCLK2), .D(_2416_3_out), .nQ(_2415_nq));  // open: Q
  D_LATCH _2409 (.EN(FCLK2), .D(_2410_3_out), .nQ(_2409_nq));  // open: Q
  D_LATCH _2403 (.EN(FCLK2), .D(_2404_3_out), .nQ(_2403_nq));  // open: Q
  D_LATCH _2397 (.EN(FCLK2), .D(_2398_3_out), .nQ(_2397_nq));  // open: Q
  D_LATCH _2391 (.EN(FCLK2), .D(_2392_3_out), .nQ(_2391_nq));  // open: Q
  D_LATCH _2385 (.EN(FCLK2), .D(_2386_3_out), .nQ(_2385_nq));  // open: Q
  D_LATCH _2379 (.EN(FCLK2), .D(_2380_3_out), .nQ(_2379_nq));  // open: Q
  D_LATCH _2374 (.EN(FCLK2), .D(_2375_3_out), .nQ(_2374_nq));  // open: Q
  D_LATCH _2369 (.EN(FCLK2), .D(_2370_3_out), .nQ(_2369_nq));  // open: Q
  buf _3627 (_3627_out, _3628_q);
  D_LATCH _3115 (.EN(FCLK1), .D(_3116_out), .nQ(_3115_nq));  // open: Q
  or _3116 (_3116_out, DEC14, DEC14);
  D_LATCH _3109 (.EN(FCLK1), .D(_3107_out), .nQ(_3109_nq));  // open: Q
  or _3107 (_3107_out, DEC15, DEC15);
  D_LATCH _3105 (.EN(FCLK1), .D(_3106_out), .nQ(_3105_nq));  // open: Q
  or _3106 (_3106_out, DEC0, DEC0);
  D_LATCH _3112 (.EN(FCLK1), .D(_3113_out), .nQ(_3112_nq));  // open: Q
  or _3113 (_3113_out, DEC2, DEC3, DEC6, DEC7, DEC10, DEC11);
  D_LATCH _3118 (.EN(FCLK1), .D(_3119_out), .nQ(_3118_nq));  // open: Q
  or _3119 (_3119_out, DEC12, DEC13);
  D_LATCH _3803 (.EN(FCLK1), .D(adder_24_out), .nQ(_3803_nq));  // open: Q
  Adder #(.width(1)) adder_24 (.a(_3844_q), .b(_3805_nq), .out(adder_24_out), .cin(_3627_out), .cout(adder_24_cout));
  D_LATCH _3798 (.EN(FCLK1), .D(adder_25_out), .nQ(_3798_nq));  // open: Q
  Adder #(.width(1)) adder_25 (
    .a(_3843_q), .b(_3800_nq), .out(adder_25_out), .cin(adder_24_cout), .cout(adder_25_cout));
  D_LATCH _3793 (.EN(FCLK1), .D(adder_26_out), .nQ(_3793_nq));  // open: Q
  Adder #(.width(1)) adder_26 (
    .a(_3842_q), .b(_3795_5_nq), .out(adder_26_out), .cin(adder_25_cout), .cout(adder_26_cout));
  D_LATCH _2443 (.EN(FCLK1), .D(adder_27_out), .nQ(_2443_nq));  // open: Q
  Adder #(.width(1)) adder_27 (
    .a(_3806_q), .b(_2445_nq), .out(adder_27_out), .cin(adder_26_cout), .cout(adder_27_cout));
  D_LATCH _2437 (.EN(FCLK1), .D(adder_28_out), .nQ(_2437_nq));  // open: Q
  Adder #(.width(1)) adder_28 (
    .a(_3788_q), .b(_2439_nq), .out(adder_28_out), .cin(adder_27_cout), .cout(adder_28_cout));
  D_LATCH _2431 (.EN(FCLK1), .D(adder_29_out), .nQ(_2431_nq));  // open: Q
  Adder #(.width(1)) adder_29 (
    .a(_3627_out), .b(_2433_nq), .out(adder_29_out), .cin(adder_28_cout), .cout(adder_29_cout));
  D_LATCH _2425 (.EN(FCLK1), .D(adder_30_out), .nQ(_2425_nq));  // open: Q
  Adder #(.width(1)) adder_30 (
    .a(_3627_out), .b(_2427_nq), .out(adder_30_out), .cin(adder_29_cout), .cout(adder_30_cout));
  D_LATCH _2419 (.EN(FCLK1), .D(adder_31_out), .nQ(_2419_nq));  // open: Q
  Adder #(.width(1)) adder_31 (
    .a(_3627_out), .b(_2421_nq), .out(adder_31_out), .cin(adder_30_cout), .cout(adder_31_cout));
  D_LATCH _2413 (.EN(FCLK1), .D(adder_32_out), .nQ(_2413_nq));  // open: Q
  Adder #(.width(1)) adder_32 (
    .a(_3627_out), .b(_2415_nq), .out(adder_32_out), .cin(adder_31_cout), .cout(adder_32_cout));
  D_LATCH _2407 (.EN(FCLK1), .D(adder_33_out), .nQ(_2407_nq));  // open: Q
  Adder #(.width(1)) adder_33 (
    .a(_3627_out), .b(_2409_nq), .out(adder_33_out), .cin(adder_32_cout), .cout(adder_33_cout));
  D_LATCH _2401 (.EN(FCLK1), .D(adder_34_out), .nQ(_2401_nq));  // open: Q
  Adder #(.width(1)) adder_34 (
    .a(_3627_out), .b(_2403_nq), .out(adder_34_out), .cin(adder_33_cout), .cout(adder_34_cout));
  D_LATCH _2395 (.EN(FCLK1), .D(adder_35_out), .nQ(_2395_nq));  // open: Q
  Adder #(.width(1)) adder_35 (
    .a(_3627_out), .b(_2397_nq), .out(adder_35_out), .cin(adder_34_cout), .cout(adder_35_cout));
  D_LATCH _2387_6 (.EN(FCLK1), .D(adder_36_out), .nQ(_2387_6_nq));  // open: Q
  Adder #(.width(1)) adder_36 (
    .a(_3627_out), .b(_2391_nq), .out(adder_36_out), .cin(adder_35_cout), .cout(adder_36_cout));
  D_LATCH _2383 (.EN(FCLK1), .D(adder_37_out), .nQ(_2383_nq));  // open: Q
  Adder #(.width(1)) adder_37 (
    .a(_3627_out), .b(_2385_nq), .out(adder_37_out), .cin(adder_36_cout), .cout(adder_37_cout));
  D_LATCH _2377 (.EN(FCLK1), .D(adder_38_out), .nQ(_2377_nq));  // open: Q
  Adder #(.width(1)) adder_38 (
    .a(_3627_out), .b(_2379_nq), .out(adder_38_out), .cin(adder_37_cout), .cout(adder_38_cout));
  D_LATCH _2372 (.EN(FCLK1), .D(adder_39_out), .nQ(_2372_nq));  // open: Q
  Adder #(.width(1)) adder_39 (
    .a(_3627_out), .b(_2374_nq), .out(adder_39_out), .cin(adder_38_cout), .cout(adder_39_cout));
  D_LATCH _2367 (.EN(FCLK1), .D(adder_40_out), .nQ(_2367_nq));  // open: Q
  Adder #(.width(1)) adder_40 (.a(_3627_out), .b(_2369_nq), .out(adder_40_out), .cin(adder_39_cout));  // open: cout
  not _3114 (_3114_out, _3115_nq);
  not _3108 (_3108_out, _3109_nq);
  not _3104 (_3104_out, _3105_nq);
  not _3111 (_3111_out, _3112_nq);
  not _3117 (_3117_out, _3118_nq);
  not _3802 (_3802_out, _3803_nq);
  not _3797 (_3797_out, _3798_nq);
  not _3792 (_3792_out, _3793_nq);
  not _2442 (_2442_out, _2443_nq);
  not _2436 (_2436_out, _2437_nq);
  not _2430 (_2430_out, _2431_nq);
  not _2424 (_2424_out, _2425_nq);
  not _2418 (_2418_out, _2419_nq);
  not _2412 (_2412_out, _2413_nq);
  not _2406 (_2406_out, _2407_nq);
  not _2400 (_2400_out, _2401_nq);
  not _2394 (_2394_out, _2395_nq);
  not _2388 (_2388_out, _2387_6_nq);
  not _2382 (_2382_out, _2383_nq);
  not _2376 (_2376_out, _2377_nq);
  not _2371 (_2371_out, _2372_nq);
  not _2366 (_2366_out, _2367_nq);
  not _3530 (_3530_out, _3802_out);
  not _3531 (_3531_out, _3797_out);
  not _3536 (_3536_out, _3792_out);
  not _3541 (_3541_out, _2442_out);
  not _3546 (_3546_out, _2436_out);
  not _3551 (_3551_out, _2430_out);
  not _3556 (_3556_out, _2424_out);
  not _3561 (_3561_out, _2418_out);
  not _3566 (_3566_out, _2412_out);
  not _3571 (_3571_out, _2406_out);
  not _3576 (_3576_out, _2400_out);
  not _3581 (_3581_out, _2394_out);
  not _3586 (_3586_out, _2388_out);
  not _3591 (_3591_out, _2382_out);
  not _3596 (_3596_out, _2376_out);
  not _3601 (_3601_out, _2371_out);
  not _3617 (_3617_out, _2366_out);
  or _3122 (_3122_out, DEC1, DEC3, DEC5, DEC7, DEC9, DEC11, DEC13);
  D_LATCH _3121 (.EN(FCLK1), .D(_3122_out), .nQ(_3121_nq));  // open: Q
  nor _3123 (_3123_out, _3114_out, _3108_out);
  and _3465 (_3465_out, 1'b0, 1'b0);
  and _3465_2 (_3465_2_out, _3797_out, _3104_out);
  and _3465_3 (_3465_3_out, _3530_out, _3108_out);
  and _3465_4 (_3465_4_out, 1'b0, _3111_out);
  and _3465_5 (_3465_5_out, 1'b1, _3114_out);
  and _3465_6 (_3465_6_out, 1'b0, _3117_out);
  and _3528 (_3528_out, 1'b0, 1'b0);
  and _3528_2 (_3528_2_out, _3792_out, _3104_out);
  and _3528_3 (_3528_3_out, _3531_out, _3108_out);
  and _3528_4 (_3528_4_out, _3802_out, _3111_out);
  and _3528_5 (_3528_5_out, _3530_out, _3114_out);
  and _3528_6 (_3528_6_out, 1'b0, _3117_out);
  and _3529 (_3529_out, 1'b0, 1'b0);
  and _3529_2 (_3529_2_out, _2442_out, _3104_out);
  and _3529_3 (_3529_3_out, _3536_out, _3108_out);
  and _3529_4 (_3529_4_out, _3797_out, _3111_out);
  and _3529_5 (_3529_5_out, _3531_out, _3114_out);
  and _3529_6 (_3529_6_out, _3802_out, _3117_out);
  and _3535 (_3535_out, 1'b0, 1'b0);
  and _3535_2 (_3535_2_out, _2436_out, _3104_out);
  and _3535_3 (_3535_3_out, _3541_out, _3108_out);
  and _3535_4 (_3535_4_out, _3792_out, _3111_out);
  and _3535_5 (_3535_5_out, _3536_out, _3114_out);
  and _3535_6 (_3535_6_out, _3797_out, _3117_out);
  and _3540 (_3540_out, 1'b0, 1'b0);
  and _3540_2 (_3540_2_out, _2430_out, _3104_out);
  and _3540_3 (_3540_3_out, _3546_out, _3108_out);
  and _3540_4 (_3540_4_out, _2442_out, _3111_out);
  and _3540_5 (_3540_5_out, _3541_out, _3114_out);
  and _3540_6 (_3540_6_out, _3792_out, _3117_out);
  and _3545 (_3545_out, 1'b0, 1'b0);
  and _3545_2 (_3545_2_out, _2424_out, _3104_out);
  and _3545_3 (_3545_3_out, _3551_out, _3108_out);
  and _3545_4 (_3545_4_out, _2436_out, _3111_out);
  and _3545_5 (_3545_5_out, _3546_out, _3114_out);
  and _3545_6 (_3545_6_out, _2442_out, _3117_out);
  and _3550 (_3550_out, 1'b0, 1'b0);
  and _3550_2 (_3550_2_out, _2418_out, _3104_out);
  and _3550_3 (_3550_3_out, _3556_out, _3108_out);
  and _3550_4 (_3550_4_out, _2430_out, _3111_out);
  and _3550_5 (_3550_5_out, _3551_out, _3114_out);
  and _3550_6 (_3550_6_out, _2436_out, _3117_out);
  and _3555 (_3555_out, 1'b0, 1'b0);
  and _3555_2 (_3555_2_out, _2412_out, _3104_out);
  and _3555_3 (_3555_3_out, _3561_out, _3108_out);
  and _3555_4 (_3555_4_out, _2424_out, _3111_out);
  and _3555_5 (_3555_5_out, _3556_out, _3114_out);
  and _3555_6 (_3555_6_out, _2430_out, _3117_out);
  and _3560 (_3560_out, 1'b0, 1'b0);
  and _3560_2 (_3560_2_out, _2406_out, _3104_out);
  and _3560_3 (_3560_3_out, _3566_out, _3108_out);
  and _3560_4 (_3560_4_out, _2418_out, _3111_out);
  and _3560_5 (_3560_5_out, _3561_out, _3114_out);
  and _3560_6 (_3560_6_out, _2424_out, _3117_out);
  and _3565 (_3565_out, 1'b0, 1'b0);
  and _3565_2 (_3565_2_out, _2400_out, _3104_out);
  and _3565_3 (_3565_3_out, _3571_out, _3108_out);
  and _3565_4 (_3565_4_out, _2412_out, _3111_out);
  and _3565_5 (_3565_5_out, _3566_out, _3114_out);
  and _3565_6 (_3565_6_out, _2418_out, _3117_out);
  and _3570 (_3570_out, 1'b0, 1'b0);
  and _3570_2 (_3570_2_out, _2394_out, _3104_out);
  and _3570_3 (_3570_3_out, _3576_out, _3108_out);
  and _3570_4 (_3570_4_out, _2406_out, _3111_out);
  and _3570_5 (_3570_5_out, _3571_out, _3114_out);
  and _3570_6 (_3570_6_out, _2412_out, _3117_out);
  and _3575 (_3575_out, 1'b0, 1'b0);
  and _3575_2 (_3575_2_out, _2388_out, _3104_out);
  and _3575_3 (_3575_3_out, _3581_out, _3108_out);
  and _3575_4 (_3575_4_out, _2400_out, _3111_out);
  and _3575_5 (_3575_5_out, _3576_out, _3114_out);
  and _3575_6 (_3575_6_out, _2406_out, _3117_out);
  and _3580 (_3580_out, 1'b0, 1'b0);
  and _3580_2 (_3580_2_out, _2382_out, _3104_out);
  and _3580_3 (_3580_3_out, _3586_out, _3108_out);
  and _3580_4 (_3580_4_out, _2394_out, _3111_out);
  and _3580_5 (_3580_5_out, _3581_out, _3114_out);
  and _3580_6 (_3580_6_out, _2400_out, _3117_out);
  and _3585 (_3585_out, 1'b0, 1'b0);
  and _3585_2 (_3585_2_out, _2376_out, _3104_out);
  and _3585_3 (_3585_3_out, _3591_out, _3108_out);
  and _3585_4 (_3585_4_out, _2388_out, _3111_out);
  and _3585_5 (_3585_5_out, _3586_out, _3114_out);
  and _3585_6 (_3585_6_out, _2394_out, _3117_out);
  and _3590 (_3590_out, 1'b0, 1'b0);
  and _3590_2 (_3590_2_out, _2371_out, _3104_out);
  and _3590_3 (_3590_3_out, _3596_out, _3108_out);
  and _3590_4 (_3590_4_out, _2382_out, _3111_out);
  and _3590_5 (_3590_5_out, _3591_out, _3114_out);
  and _3590_6 (_3590_6_out, _2388_out, _3117_out);
  and _3595 (_3595_out, 1'b0, 1'b0);
  and _3595_2 (_3595_2_out, _2366_out, _3104_out);
  and _3595_3 (_3595_3_out, _3601_out, _3108_out);
  and _3595_4 (_3595_4_out, _2376_out, _3111_out);
  and _3595_5 (_3595_5_out, _3596_out, _3114_out);
  and _3595_6 (_3595_6_out, _2382_out, _3117_out);
  and _3600 (_3600_out, 1'b0, 1'b0);
  and _3600_2 (_3600_2_out, 1'b0, _3104_out);
  and _3600_3 (_3600_3_out, _3617_out, _3108_out);
  and _3600_4 (_3600_4_out, _2371_out, _3111_out);
  and _3600_5 (_3600_5_out, _3601_out, _3114_out);
  and _3600_6 (_3600_6_out, _2376_out, _3117_out);
  and _3611 (_3611_out, 1'b1, _3108_out);
  and _3611_2 (_3611_2_out, _2366_out, _3111_out);
  and _3611_3 (_3611_3_out, _3617_out, _3114_out);
  and _3611_4 (_3611_4_out, _2371_out, _3117_out);
  and _3612 (_3612_out, 1'b1, _3108_out);
  and _3612_2 (_3612_2_out, 1'b1, _3114_out);
  and _3612_3 (_3612_3_out, _2366_out, _3117_out);
  and _3613 (_3613_out, _3114_out, 1'b1);
  and _3613_2 (_3613_2_out, _3108_out, 1'b1);
  D_LATCH _3102 (.EN(FCLK2), .D(_3120_out), .nQ(_3102_nq));  // open: Q
  not _3120 (_3120_out, _3121_nq);
  nor _3465_7 (_3465_7_out, _3465_out, _3465_2_out, _3465_3_out, _3465_4_out, _3465_5_out, _3465_6_out);
  nor _3528_7 (_3528_7_out, _3528_out, _3528_2_out, _3528_3_out, _3528_4_out, _3528_5_out, _3528_6_out);
  nor _3529_7 (_3529_7_out, _3529_out, _3529_2_out, _3529_3_out, _3529_4_out, _3529_5_out, _3529_6_out);
  nor _3535_7 (_3535_7_out, _3535_out, _3535_2_out, _3535_3_out, _3535_4_out, _3535_5_out, _3535_6_out);
  nor _3540_7 (_3540_7_out, _3540_out, _3540_2_out, _3540_3_out, _3540_4_out, _3540_5_out, _3540_6_out);
  nor _3545_7 (_3545_7_out, _3545_out, _3545_2_out, _3545_3_out, _3545_4_out, _3545_5_out, _3545_6_out);
  nor _3550_7 (_3550_7_out, _3550_out, _3550_2_out, _3550_3_out, _3550_4_out, _3550_5_out, _3550_6_out);
  nor _3555_7 (_3555_7_out, _3555_out, _3555_2_out, _3555_3_out, _3555_4_out, _3555_5_out, _3555_6_out);
  nor _3560_7 (_3560_7_out, _3560_out, _3560_2_out, _3560_3_out, _3560_4_out, _3560_5_out, _3560_6_out);
  nor _3565_7 (_3565_7_out, _3565_out, _3565_2_out, _3565_3_out, _3565_4_out, _3565_5_out, _3565_6_out);
  nor _3570_7 (_3570_7_out, _3570_out, _3570_2_out, _3570_3_out, _3570_4_out, _3570_5_out, _3570_6_out);
  nor _3575_7 (_3575_7_out, _3575_out, _3575_2_out, _3575_3_out, _3575_4_out, _3575_5_out, _3575_6_out);
  nor _3580_7 (_3580_7_out, _3580_out, _3580_2_out, _3580_3_out, _3580_4_out, _3580_5_out, _3580_6_out);
  nor _3585_7 (_3585_7_out, _3585_out, _3585_2_out, _3585_3_out, _3585_4_out, _3585_5_out, _3585_6_out);
  nor _3590_7 (_3590_7_out, _3590_out, _3590_2_out, _3590_3_out, _3590_4_out, _3590_5_out, _3590_6_out);
  nor _3595_7 (_3595_7_out, _3595_out, _3595_2_out, _3595_3_out, _3595_4_out, _3595_5_out, _3595_6_out);
  nor _3600_7 (_3600_7_out, _3600_out, _3600_2_out, _3600_3_out, _3600_4_out, _3600_5_out, _3600_6_out);
  nor _3611_5 (_3611_5_out, _3611_out, _3611_2_out, _3611_3_out, _3611_4_out);
  nor _3612_4 (_3612_4_out, _3612_out, _3612_2_out, _3612_3_out);
  nor _3613_3 (_3613_3_out, _3613_out, _3613_2_out);
  not _3103 (_3103_out, _3102_nq);
  D_LATCH _3124 (.EN(FCLK2), .D(_3123_out), .nQ(_3124_nq));  // open: Q
  D_LATCH _3185 (.EN(FCLK2), .D(_3465_7_out), .nQ(_3185_nq));  // open: Q
  D_LATCH _3182 (.EN(FCLK2), .D(_3802_out), .nQ(_3182_nq));  // open: Q
  D_LATCH _3527 (.EN(FCLK2), .D(_3528_7_out), .nQ(_3527_nq));  // open: Q
  D_LATCH _3198 (.EN(FCLK2), .D(_3797_out), .nQ(_3198_nq));  // open: Q
  D_LATCH _3533 (.EN(FCLK2), .D(_3532_4_out), .nQ(_3533_nq));  // open: Q
  D_LATCH _3534 (.EN(FCLK2), .D(_3529_7_out), .nQ(_3534_nq));  // open: Q
  D_LATCH _3213 (.EN(FCLK2), .D(_3792_out), .nQ(_3213_nq));  // open: Q
  D_LATCH _3538 (.EN(FCLK2), .D(_3537_4_out), .nQ(_3538_nq));  // open: Q
  D_LATCH _3539 (.EN(FCLK2), .D(_3535_7_out), .nQ(_3539_nq));  // open: Q
  D_LATCH _3228 (.EN(FCLK2), .D(_2442_out), .nQ(_3228_nq));  // open: Q
  D_LATCH _3543 (.EN(FCLK2), .D(_3542_4_out), .nQ(_3543_nq));  // open: Q
  D_LATCH _3544 (.EN(FCLK2), .D(_3540_7_out), .nQ(_3544_nq));  // open: Q
  D_LATCH _3243 (.EN(FCLK2), .D(_2436_out), .nQ(_3243_nq));  // open: Q
  D_LATCH _3548 (.EN(FCLK2), .D(_3547_4_out), .nQ(_3548_nq));  // open: Q
  D_LATCH _3549 (.EN(FCLK2), .D(_3545_7_out), .nQ(_3549_nq));  // open: Q
  D_LATCH _3258 (.EN(FCLK2), .D(_2430_out), .nQ(_3258_nq));  // open: Q
  D_LATCH _3553 (.EN(FCLK2), .D(_3552_4_out), .nQ(_3553_nq));  // open: Q
  D_LATCH _3554 (.EN(FCLK2), .D(_3550_7_out), .nQ(_3554_nq));  // open: Q
  D_LATCH _3274 (.EN(FCLK2), .D(_2424_out), .nQ(_3274_nq));  // open: Q
  D_LATCH _3558 (.EN(FCLK2), .D(_3557_4_out), .nQ(_3558_nq));  // open: Q
  D_LATCH _3559 (.EN(FCLK2), .D(_3555_7_out), .nQ(_3559_nq));  // open: Q
  D_LATCH _3288 (.EN(FCLK2), .D(_2418_out), .nQ(_3288_nq));  // open: Q
  D_LATCH _3563 (.EN(FCLK2), .D(_3562_4_out), .nQ(_3563_nq));  // open: Q
  D_LATCH _3564 (.EN(FCLK2), .D(_3560_7_out), .nQ(_3564_nq));  // open: Q
  D_LATCH _3303 (.EN(FCLK2), .D(_2412_out), .nQ(_3303_nq));  // open: Q
  D_LATCH _3568 (.EN(FCLK2), .D(_3567_4_out), .nQ(_3568_nq));  // open: Q
  D_LATCH _3569 (.EN(FCLK2), .D(_3565_7_out), .nQ(_3569_nq));  // open: Q
  D_LATCH _3318 (.EN(FCLK2), .D(_2406_out), .nQ(_3318_nq));  // open: Q
  D_LATCH _3573 (.EN(FCLK2), .D(_3572_4_out), .nQ(_3573_nq));  // open: Q
  D_LATCH _3574 (.EN(FCLK2), .D(_3570_7_out), .nQ(_3574_nq));  // open: Q
  D_LATCH _3332 (.EN(FCLK2), .D(_2400_out), .nQ(_3332_nq));  // open: Q
  D_LATCH _3578 (.EN(FCLK2), .D(_3577_4_out), .nQ(_3578_nq));  // open: Q
  D_LATCH _3579 (.EN(FCLK2), .D(_3575_7_out), .nQ(_3579_nq));  // open: Q
  D_LATCH _3346 (.EN(FCLK2), .D(_2394_out), .nQ(_3346_nq));  // open: Q
  D_LATCH _3583 (.EN(FCLK2), .D(_3582_4_out), .nQ(_3583_nq));  // open: Q
  D_LATCH _3584 (.EN(FCLK2), .D(_3580_7_out), .nQ(_3584_nq));  // open: Q
  D_LATCH _3360 (.EN(FCLK2), .D(_2388_out), .nQ(_3360_nq));  // open: Q
  D_LATCH _3588 (.EN(FCLK2), .D(_3587_4_out), .nQ(_3588_nq));  // open: Q
  D_LATCH _3589 (.EN(FCLK2), .D(_3585_7_out), .nQ(_3589_nq));  // open: Q
  D_LATCH _3374 (.EN(FCLK2), .D(_2382_out), .nQ(_3374_nq));  // open: Q
  D_LATCH _3593 (.EN(FCLK2), .D(_3592_4_out), .nQ(_3593_nq));  // open: Q
  D_LATCH _3594 (.EN(FCLK2), .D(_3590_7_out), .nQ(_3594_nq));  // open: Q
  D_LATCH _3388 (.EN(FCLK2), .D(_2376_out), .nQ(_3388_nq));  // open: Q
  D_LATCH _3598 (.EN(FCLK2), .D(_3597_4_out), .nQ(_3598_nq));  // open: Q
  D_LATCH _3599 (.EN(FCLK2), .D(_3595_7_out), .nQ(_3599_nq));  // open: Q
  D_LATCH _3407 (.EN(FCLK2), .D(_2371_out), .nQ(_3407_nq));  // open: Q
  D_LATCH _3603 (.EN(FCLK2), .D(_3602_4_out), .nQ(_3603_nq));  // open: Q
  D_LATCH _3604 (.EN(FCLK2), .D(_3600_7_out), .nQ(_3604_nq));  // open: Q
  D_LATCH _3422 (.EN(FCLK2), .D(_2366_out), .nQ(_3422_nq));  // open: Q
  D_LATCH _3605 (.EN(FCLK2), .D(_3616_4_out), .nQ(_3605_nq));  // open: Q
  D_LATCH _3606 (.EN(FCLK2), .D(_3611_5_out), .nQ(_3606_nq));  // open: Q
  D_LATCH _3607 (.EN(FCLK2), .D(_3615_4_out), .nQ(_3607_nq));  // open: Q
  D_LATCH _3608 (.EN(FCLK2), .D(_3612_4_out), .nQ(_3608_nq));  // open: Q
  D_LATCH _3609 (.EN(FCLK2), .D(_3614_4_out), .nQ(_3609_nq));  // open: Q
  D_LATCH _3610 (.EN(FCLK2), .D(_3613_3_out), .nQ(_3610_nq));  // open: Q
  SR_BIT _3096 (.C2(FCLK2), .C1(FCLK1), .D(_3099_out), .Q(_3096_q));  // open: nQ
  SR_BIT _3101 (.C2(FCLK2), .C1(FCLK1), .D(_3103_out), .Q(_3101_q));  // open: nQ
  not _3183 (_3183_out, _3182_nq);
  not _3199 (_3199_out, _3198_nq);
  not _3214 (_3214_out, _3213_nq);
  not _3229 (_3229_out, _3228_nq);
  not _3244 (_3244_out, _3243_nq);
  not _3259 (_3259_out, _3258_nq);
  not _3273 (_3273_out, _3274_nq);
  not _3289 (_3289_out, _3288_nq);
  not _3304 (_3304_out, _3303_nq);
  not _3319 (_3319_out, _3318_nq);
  not _3333 (_3333_out, _3332_nq);
  not _3347 (_3347_out, _3346_nq);
  not _3361 (_3361_out, _3360_nq);
  not _3375 (_3375_out, _3374_nq);
  not _3389 (_3389_out, _3388_nq);
  not _3408 (_3408_out, _3407_nq);
  not _3423 (_3423_out, _3422_nq);
  Adder #(.width(1)) adder_41 (.a(1'b0), .b(_3185_nq), .out(adder_41_out), .cin(_3124_nq), .cout(adder_41_cout));
  Adder #(.width(1)) adder_42 (.a(1'b0), .b(_3527_nq), .out(adder_42_out), .cin(adder_41_cout), .cout(adder_42_cout));
  Adder #(.width(1)) adder_43 (
    .a(_3533_nq), .b(_3534_nq), .out(adder_43_out), .cin(adder_42_cout), .cout(adder_43_cout));
  Adder #(.width(1)) adder_44 (
    .a(_3538_nq), .b(_3539_nq), .out(adder_44_out), .cin(adder_43_cout), .cout(adder_44_cout));
  Adder #(.width(1)) adder_45 (
    .a(_3543_nq), .b(_3544_nq), .out(adder_45_out), .cin(adder_44_cout), .cout(adder_45_cout));
  Adder #(.width(1)) adder_46 (
    .a(_3548_nq), .b(_3549_nq), .out(adder_46_out), .cin(adder_45_cout), .cout(adder_46_cout));
  Adder #(.width(1)) adder_47 (
    .a(_3553_nq), .b(_3554_nq), .out(adder_47_out), .cin(adder_46_cout), .cout(adder_47_cout));
  Adder #(.width(1)) adder_48 (
    .a(_3558_nq), .b(_3559_nq), .out(adder_48_out), .cin(adder_47_cout), .cout(adder_48_cout));
  Adder #(.width(1)) adder_49 (
    .a(_3563_nq), .b(_3564_nq), .out(adder_49_out), .cin(adder_48_cout), .cout(adder_49_cout));
  Adder #(.width(1)) adder_50 (
    .a(_3568_nq), .b(_3569_nq), .out(adder_50_out), .cin(adder_49_cout), .cout(adder_50_cout));
  Adder #(.width(1)) adder_51 (
    .a(_3573_nq), .b(_3574_nq), .out(adder_51_out), .cin(adder_50_cout), .cout(adder_51_cout));
  Adder #(.width(1)) adder_52 (
    .a(_3578_nq), .b(_3579_nq), .out(adder_52_out), .cin(adder_51_cout), .cout(adder_52_cout));
  Adder #(.width(1)) adder_53 (
    .a(_3583_nq), .b(_3584_nq), .out(adder_53_out), .cin(adder_52_cout), .cout(adder_53_cout));
  Adder #(.width(1)) adder_54 (
    .a(_3588_nq), .b(_3589_nq), .out(adder_54_out), .cin(adder_53_cout), .cout(adder_54_cout));
  Adder #(.width(1)) adder_55 (
    .a(_3593_nq), .b(_3594_nq), .out(adder_55_out), .cin(adder_54_cout), .cout(adder_55_cout));
  Adder #(.width(1)) adder_56 (
    .a(_3598_nq), .b(_3599_nq), .out(adder_56_out), .cin(adder_55_cout), .cout(adder_56_cout));
  Adder #(.width(1)) adder_57 (
    .a(_3603_nq), .b(_3604_nq), .out(adder_57_out), .cin(adder_56_cout), .cout(adder_57_cout));
  Adder #(.width(1)) adder_58 (
    .a(_3605_nq), .b(_3606_nq), .out(adder_58_out), .cin(adder_57_cout), .cout(adder_58_cout));
  Adder #(.width(1)) adder_59 (
    .a(_3607_nq), .b(_3608_nq), .out(adder_59_out), .cin(adder_58_cout), .cout(adder_59_cout));
  Adder #(.width(1)) adder_60 (.a(_3609_nq), .b(_3610_nq), .out(adder_60_out), .cin(adder_59_cout));  // open: cout
  nand _3094 (_3094_out, _3095_out, _3096_q);
  nand _3098 (_3098_out, _3101_q, _3099_out);
  SR_BIT sr_bit_1 (.C2(FCLK2), .C1(FCLK1), .D(adder_41_out), .Q(sr_bit_1_q));  // open: nQ
  SR_BIT _3181 (.C2(FCLK2), .C1(FCLK1), .D(_3183_out), .Q(_3181_q));  // open: nQ
  SR_BIT sr_bit_2 (.C2(FCLK2), .C1(FCLK1), .D(adder_42_out), .Q(sr_bit_2_q));  // open: nQ
  SR_BIT _3197 (.C2(FCLK2), .C1(FCLK1), .D(_3199_out), .Q(_3197_q));  // open: nQ
  SR_BIT sr_bit_3 (.C2(FCLK2), .C1(FCLK1), .D(adder_43_out), .Q(sr_bit_3_q));  // open: nQ
  SR_BIT _3212 (.C2(FCLK2), .C1(FCLK1), .D(_3214_out), .Q(_3212_q));  // open: nQ
  SR_BIT sr_bit_4 (.C2(FCLK2), .C1(FCLK1), .D(adder_44_out), .Q(sr_bit_4_q));  // open: nQ
  SR_BIT _3227 (.C2(FCLK2), .C1(FCLK1), .D(_3229_out), .Q(_3227_q));  // open: nQ
  SR_BIT sr_bit_5 (.C2(FCLK2), .C1(FCLK1), .D(adder_45_out), .Q(sr_bit_5_q));  // open: nQ
  SR_BIT _3242 (.C2(FCLK2), .C1(FCLK1), .D(_3244_out), .Q(_3242_q));  // open: nQ
  SR_BIT sr_bit_6 (.C2(FCLK2), .C1(FCLK1), .D(adder_46_out), .Q(sr_bit_6_q));  // open: nQ
  SR_BIT _3257 (.C2(FCLK2), .C1(FCLK1), .D(_3259_out), .Q(_3257_q));  // open: nQ
  SR_BIT sr_bit_7 (.C2(FCLK2), .C1(FCLK1), .D(adder_47_out), .Q(sr_bit_7_q));  // open: nQ
  SR_BIT _3272 (.C2(FCLK2), .C1(FCLK1), .D(_3273_out), .Q(_3272_q));  // open: nQ
  SR_BIT sr_bit_8 (.C2(FCLK2), .C1(FCLK1), .D(adder_48_out), .Q(sr_bit_8_q));  // open: nQ
  SR_BIT _3287 (.C2(FCLK2), .C1(FCLK1), .D(_3289_out), .Q(_3287_q));  // open: nQ
  SR_BIT sr_bit_9 (.C2(FCLK2), .C1(FCLK1), .D(adder_49_out), .Q(sr_bit_9_q));  // open: nQ
  SR_BIT _3302 (.C2(FCLK2), .C1(FCLK1), .D(_3304_out), .Q(_3302_q));  // open: nQ
  SR_BIT sr_bit_10 (.C2(FCLK2), .C1(FCLK1), .D(adder_50_out), .Q(sr_bit_10_q));  // open: nQ
  SR_BIT _3317 (.C2(FCLK2), .C1(FCLK1), .D(_3319_out), .Q(_3317_q));  // open: nQ
  SR_BIT sr_bit_11 (.C2(FCLK2), .C1(FCLK1), .D(adder_51_out), .Q(sr_bit_11_q));  // open: nQ
  SR_BIT _3331 (.C2(FCLK2), .C1(FCLK1), .D(_3333_out), .Q(_3331_q));  // open: nQ
  SR_BIT sr_bit_12 (.C2(FCLK2), .C1(FCLK1), .D(adder_52_out), .Q(sr_bit_12_q));  // open: nQ
  SR_BIT _3345 (.C2(FCLK2), .C1(FCLK1), .D(_3347_out), .Q(_3345_q));  // open: nQ
  SR_BIT sr_bit_13 (.C2(FCLK2), .C1(FCLK1), .D(adder_53_out), .Q(sr_bit_13_q));  // open: nQ
  SR_BIT _3359 (.C2(FCLK2), .C1(FCLK1), .D(_3361_out), .Q(_3359_q));  // open: nQ
  SR_BIT sr_bit_14 (.C2(FCLK2), .C1(FCLK1), .D(adder_54_out), .Q(sr_bit_14_q));  // open: nQ
  SR_BIT _3373 (.C2(FCLK2), .C1(FCLK1), .D(_3375_out), .Q(_3373_q));  // open: nQ
  SR_BIT sr_bit_15 (.C2(FCLK2), .C1(FCLK1), .D(adder_55_out), .Q(sr_bit_15_q));  // open: nQ
  SR_BIT _3387_4 (.C2(FCLK2), .C1(FCLK1), .D(_3389_out), .Q(_3387_4_q));  // open: nQ
  SR_BIT sr_bit_16 (.C2(FCLK2), .C1(FCLK1), .D(adder_56_out), .Q(sr_bit_16_q));  // open: nQ
  SR_BIT _3406 (.C2(FCLK2), .C1(FCLK1), .D(_3408_out), .Q(_3406_q));  // open: nQ
  SR_BIT sr_bit_17 (.C2(FCLK2), .C1(FCLK1), .D(adder_57_out), .Q(sr_bit_17_q));  // open: nQ
  SR_BIT _3421 (.C2(FCLK2), .C1(FCLK1), .D(_3423_out), .Q(_3421_q));  // open: nQ
  SR_BIT sr_bit_18 (.C2(FCLK2), .C1(FCLK1), .D(adder_58_out), .Q(sr_bit_18_q));  // open: nQ
  SR_BIT _3436 (.C2(FCLK2), .C1(FCLK1), .D(1'b0), .Q(_3436_q));  // open: nQ
  SR_BIT sr_bit_19 (.C2(FCLK2), .C1(FCLK1), .D(adder_59_out), .Q(sr_bit_19_q));  // open: nQ
  SR_BIT _3449 (.C2(FCLK2), .C1(FCLK1), .D(1'b0), .Q(_3449_q));  // open: nQ
  SR_BIT sr_bit_20 (.C2(FCLK2), .C1(FCLK1), .D(adder_60_out), .Q(sr_bit_20_q));  // open: nQ
  SR_BIT _3462 (.C2(FCLK2), .C1(FCLK1), .D(1'b0), .Q(_3462_q));  // open: nQ
  not _3093 (_3093_out, _3094_out);
  not _3097 (_3097_out, _3098_out);
  D_LATCH _3177 (.EN(FCLK2), .D(_3178_out), .nQ(_3177_nq));  // open: Q
  nand _3178 (_3178_out, sr_bit_1_q, _3099_out);
  D_LATCH _3179 (.EN(FCLK2), .D(_3180_out), .nQ(_3179_nq));  // open: Q
  nand _3180 (_3180_out, _3181_q, _3097_out);
  D_LATCH _3193 (.EN(FCLK2), .D(_3195_out), .nQ(_3193_nq));  // open: Q
  nand _3195 (_3195_out, sr_bit_2_q, _3099_out);
  D_LATCH _3194 (.EN(FCLK2), .D(_3196_out), .nQ(_3194_nq));  // open: Q
  nand _3196 (_3196_out, _3197_q, _3097_out);
  D_LATCH _3208 (.EN(FCLK2), .D(_3209_out), .nQ(_3208_nq));  // open: Q
  nand _3209 (_3209_out, sr_bit_3_q, _3099_out);
  D_LATCH _3210 (.EN(FCLK2), .D(_3211_out), .nQ(_3210_nq));  // open: Q
  nand _3211 (_3211_out, _3212_q, _3097_out);
  D_LATCH _3223 (.EN(FCLK2), .D(_3224_out), .nQ(_3223_nq));  // open: Q
  nand _3224 (_3224_out, sr_bit_4_q, _3099_out);
  D_LATCH _3225 (.EN(FCLK2), .D(_3226_out), .nQ(_3225_nq));  // open: Q
  nand _3226 (_3226_out, _3227_q, _3097_out);
  D_LATCH _3239 (.EN(FCLK2), .D(_3238_out), .nQ(_3239_nq));  // open: Q
  nand _3238 (_3238_out, sr_bit_5_q, _3099_out);
  D_LATCH _3240 (.EN(FCLK2), .D(_3241_out), .nQ(_3240_nq));  // open: Q
  nand _3241 (_3241_out, _3242_q, _3097_out);
  D_LATCH _3253 (.EN(FCLK2), .D(_3255_out), .nQ(_3253_nq));  // open: Q
  nand _3255 (_3255_out, sr_bit_6_q, _3099_out);
  D_LATCH _3254 (.EN(FCLK2), .D(_3256_out), .nQ(_3254_nq));  // open: Q
  nand _3256 (_3256_out, _3257_q, _3097_out);
  D_LATCH _3268 (.EN(FCLK2), .D(_3269_out), .nQ(_3268_nq));  // open: Q
  nand _3269 (_3269_out, sr_bit_7_q, _3099_out);
  D_LATCH _3270 (.EN(FCLK2), .D(_3271_out), .nQ(_3270_nq));  // open: Q
  nand _3271 (_3271_out, _3272_q, _3097_out);
  D_LATCH _3283 (.EN(FCLK2), .D(_3284_out), .nQ(_3283_nq));  // open: Q
  nand _3284 (_3284_out, sr_bit_8_q, _3099_out);
  D_LATCH _3285 (.EN(FCLK2), .D(_3286_out), .nQ(_3285_nq));  // open: Q
  nand _3286 (_3286_out, _3287_q, _3097_out);
  D_LATCH _3298 (.EN(FCLK2), .D(_3299_out), .nQ(_3298_nq));  // open: Q
  nand _3299 (_3299_out, sr_bit_9_q, _3099_out);
  D_LATCH _3300 (.EN(FCLK2), .D(_3301_out), .nQ(_3300_nq));  // open: Q
  nand _3301 (_3301_out, _3302_q, _3097_out);
  D_LATCH _3313 (.EN(FCLK2), .D(_3314_out), .nQ(_3313_nq));  // open: Q
  nand _3314 (_3314_out, sr_bit_10_q, _3099_out);
  D_LATCH _3315 (.EN(FCLK2), .D(_3316_out), .nQ(_3315_nq));  // open: Q
  nand _3316 (_3316_out, _3317_q, _3097_out);
  D_LATCH _3327 (.EN(FCLK2), .D(_3328_out), .nQ(_3327_nq));  // open: Q
  nand _3328 (_3328_out, sr_bit_11_q, _3099_out);
  D_LATCH _3329 (.EN(FCLK2), .D(_3330_out), .nQ(_3329_nq));  // open: Q
  nand _3330 (_3330_out, _3331_q, _3097_out);
  D_LATCH _3341 (.EN(FCLK2), .D(_3342_out), .nQ(_3341_nq));  // open: Q
  nand _3342 (_3342_out, sr_bit_12_q, _3099_out);
  D_LATCH _3343 (.EN(FCLK2), .D(_3344_out), .nQ(_3343_nq));  // open: Q
  nand _3344 (_3344_out, _3345_q, _3097_out);
  D_LATCH _3355 (.EN(FCLK2), .D(_3356_out), .nQ(_3355_nq));  // open: Q
  nand _3356 (_3356_out, sr_bit_13_q, _3099_out);
  D_LATCH _3357 (.EN(FCLK2), .D(_3358_out), .nQ(_3357_nq));  // open: Q
  nand _3358 (_3358_out, _3359_q, _3097_out);
  D_LATCH _3369 (.EN(FCLK2), .D(_3370_out), .nQ(_3369_nq));  // open: Q
  nand _3370 (_3370_out, sr_bit_14_q, _3099_out);
  D_LATCH _3371 (.EN(FCLK2), .D(_3372_out), .nQ(_3371_nq));  // open: Q
  nand _3372 (_3372_out, _3373_q, _3097_out);
  D_LATCH _3383 (.EN(FCLK2), .D(_3384_out), .nQ(_3383_nq));  // open: Q
  nand _3384 (_3384_out, sr_bit_15_q, _3099_out);
  D_LATCH _3385 (.EN(FCLK2), .D(_3386_out), .nQ(_3385_nq));  // open: Q
  nand _3386 (_3386_out, _3387_4_q, _3097_out);
  D_LATCH _3402 (.EN(FCLK2), .D(_3403_out), .nQ(_3402_nq));  // open: Q
  nand _3403 (_3403_out, sr_bit_16_q, _3099_out);
  D_LATCH _3404 (.EN(FCLK2), .D(_3405_out), .nQ(_3404_nq));  // open: Q
  nand _3405 (_3405_out, _3406_q, _3097_out);
  D_LATCH _3417 (.EN(FCLK2), .D(_3418_out), .nQ(_3417_nq));  // open: Q
  nand _3418 (_3418_out, sr_bit_17_q, _3099_out);
  D_LATCH _3419 (.EN(FCLK2), .D(_3420_out), .nQ(_3419_nq));  // open: Q
  nand _3420 (_3420_out, _3421_q, _3097_out);
  D_LATCH _3432 (.EN(FCLK2), .D(_3433_out), .nQ(_3432_nq));  // open: Q
  nand _3433 (_3433_out, sr_bit_18_q, _3099_out);
  D_LATCH _3434 (.EN(FCLK2), .D(_3435_out), .nQ(_3434_nq));  // open: Q
  nand _3435 (_3435_out, _3436_q, _3097_out);
  D_LATCH _3445 (.EN(FCLK2), .D(_3446_out), .nQ(_3445_nq));  // open: Q
  nand _3446 (_3446_out, sr_bit_19_q, _3099_out);
  D_LATCH _3447 (.EN(FCLK2), .D(_3448_out), .nQ(_3447_nq));  // open: Q
  nand _3448 (_3448_out, _3449_q, _3097_out);
  D_LATCH _3458 (.EN(FCLK2), .D(_3459_out), .nQ(_3458_nq));  // open: Q
  nand _3459 (_3459_out, sr_bit_20_q, _3099_out);
  D_LATCH _3460 (.EN(FCLK2), .D(_3461_out), .nQ(_3460_nq));  // open: Q
  nand _3461 (_3461_out, _3462_q, _3097_out);
  Adder #(.width(1)) adder_61 (.a(_3177_nq), .b(_3179_nq), .out(adder_61_out), .cin(1'b0), .cout(adder_61_cout));
  Adder #(.width(1)) adder_62 (
    .a(_3193_nq), .b(_3194_nq), .out(adder_62_out), .cin(adder_61_cout), .cout(adder_62_cout));
  Adder #(.width(1)) adder_63 (
    .a(_3208_nq), .b(_3210_nq), .out(adder_63_out), .cin(adder_62_cout), .cout(adder_63_cout));
  Adder #(.width(1)) adder_64 (
    .a(_3223_nq), .b(_3225_nq), .out(adder_64_out), .cin(adder_63_cout), .cout(adder_64_cout));
  Adder #(.width(1)) adder_65 (
    .a(_3239_nq), .b(_3240_nq), .out(adder_65_out), .cin(adder_64_cout), .cout(adder_65_cout));
  Adder #(.width(1)) adder_66 (
    .a(_3253_nq), .b(_3254_nq), .out(adder_66_out), .cin(adder_65_cout), .cout(adder_66_cout));
  Adder #(.width(1)) adder_67 (
    .a(_3268_nq), .b(_3270_nq), .out(adder_67_out), .cin(adder_66_cout), .cout(adder_67_cout));
  Adder #(.width(1)) adder_68 (
    .a(_3283_nq), .b(_3285_nq), .out(adder_68_out), .cin(adder_67_cout), .cout(adder_68_cout));
  Adder #(.width(1)) adder_69 (
    .a(_3298_nq), .b(_3300_nq), .out(adder_69_out), .cin(adder_68_cout), .cout(adder_69_cout));
  Adder #(.width(1)) adder_70 (
    .a(_3313_nq), .b(_3315_nq), .out(adder_70_out), .cin(adder_69_cout), .cout(adder_70_cout));
  Adder #(.width(1)) adder_71 (
    .a(_3327_nq), .b(_3329_nq), .out(adder_71_out), .cin(adder_70_cout), .cout(adder_71_cout));
  Adder #(.width(1)) adder_72 (
    .a(_3341_nq), .b(_3343_nq), .out(adder_72_out), .cin(adder_71_cout), .cout(adder_72_cout));
  Adder #(.width(1)) adder_73 (
    .a(_3355_nq), .b(_3357_nq), .out(adder_73_out), .cin(adder_72_cout), .cout(adder_73_cout));
  Adder #(.width(1)) adder_74 (
    .a(_3369_nq), .b(_3371_nq), .out(adder_74_out), .cin(adder_73_cout), .cout(adder_74_cout));
  Adder #(.width(1)) adder_75 (
    .a(_3383_nq), .b(_3385_nq), .out(adder_75_out), .cin(adder_74_cout), .cout(adder_75_cout));
  Adder #(.width(1)) adder_76 (
    .a(_3402_nq), .b(_3404_nq), .out(adder_76_out), .cin(adder_75_cout), .cout(adder_76_cout));
  Adder #(.width(1)) adder_77 (
    .a(_3417_nq), .b(_3419_nq), .out(adder_77_out), .cin(adder_76_cout), .cout(adder_77_cout));
  Adder #(.width(1)) adder_78 (
    .a(_3432_nq), .b(_3434_nq), .out(adder_78_out), .cin(adder_77_cout), .cout(adder_78_cout));
  Adder #(.width(1)) adder_79 (
    .a(_3445_nq), .b(_3447_nq), .out(adder_79_out), .cin(adder_78_cout), .cout(adder_79_cout));
  Adder #(.width(1)) adder_80 (.a(_3458_nq), .b(_3460_nq), .out(adder_80_out), .cin(adder_79_cout));  // open: cout
  SDELAY24 _3171 (.C2(FCLK2), .C1(FCLK1), .D(adder_81_out), .Q(_3171_q));  // open: Q40, Q44
  D_LATCH _3175 (.EN(FCLK2), .D(adder_61_out), .nQ(_3175_nq));  // open: Q
  SDELAY24 _3187 (.C2(FCLK2), .C1(FCLK1), .D(adder_82_out), .Q(_3187_q));  // open: Q40, Q44
  D_LATCH _3191 (.EN(FCLK2), .D(adder_62_out), .nQ(_3191_nq));  // open: Q
  SDELAY24 _3202 (.C2(FCLK2), .C1(FCLK1), .D(adder_83_out), .Q(_3202_q));  // open: Q40, Q44
  D_LATCH _3206 (.EN(FCLK2), .D(adder_63_out), .nQ(_3206_nq));  // open: Q
  SDELAY24 _3217 (.C2(FCLK2), .C1(FCLK1), .D(adder_84_out), .Q(_3217_q));  // open: Q40, Q44
  D_LATCH _3221 (.EN(FCLK2), .D(adder_64_out), .nQ(_3221_nq));  // open: Q
  SDELAY24 _3232 (.C2(FCLK2), .C1(FCLK1), .D(adder_85_out), .Q(_3232_q));  // open: Q40, Q44
  D_LATCH _3236 (.EN(FCLK2), .D(adder_65_out), .nQ(_3236_nq));  // open: Q
  SDELAY24 _3246 (.C2(FCLK2), .C1(FCLK1), .D(adder_86_out), .Q(_3246_q));  // open: Q40, Q44
  D_LATCH _3251 (.EN(FCLK2), .D(adder_66_out), .nQ(_3251_nq));  // open: Q
  SDELAY24 _3262 (.C2(FCLK2), .C1(FCLK1), .D(adder_87_out), .Q(_3262_q));  // open: Q40, Q44
  D_LATCH _3266 (.EN(FCLK2), .D(adder_67_out), .nQ(_3266_nq));  // open: Q
  SDELAY24 _3277 (.C2(FCLK2), .C1(FCLK1), .D(adder_88_out), .Q(_3277_q));  // open: Q40, Q44
  D_LATCH _3281 (.EN(FCLK2), .D(adder_68_out), .nQ(_3281_nq));  // open: Q
  SDELAY24 _3292 (.C2(FCLK2), .C1(FCLK1), .D(adder_89_out), .Q(_3292_q));  // open: Q40, Q44
  D_LATCH _3296 (.EN(FCLK2), .D(adder_69_out), .nQ(_3296_nq));  // open: Q
  SDELAY24 _3307 (.C2(FCLK2), .C1(FCLK1), .D(adder_90_out), .Q(_3307_q));  // open: Q40, Q44
  D_LATCH _3311 (.EN(FCLK2), .D(adder_70_out), .nQ(_3311_nq));  // open: Q
  SDELAY24 _3321 (.C2(FCLK2), .C1(FCLK1), .D(adder_91_out), .Q(_3321_q), .Q40(_3321_q40));  // open: Q44
  D_LATCH _3325 (.EN(FCLK2), .D(adder_71_out), .nQ(_3325_nq));  // open: Q
  SDELAY24 _3335 (.C2(FCLK2), .C1(FCLK1), .D(adder_92_out), .Q(_3335_q), .Q40(_3335_q40));  // open: Q44
  D_LATCH _3339 (.EN(FCLK2), .D(adder_72_out), .nQ(_3339_nq));  // open: Q
  SDELAY24 _3349 (.C2(FCLK2), .C1(FCLK1), .D(adder_93_out), .Q(_3349_q), .Q40(_3349_q40));  // open: Q44
  D_LATCH _3353 (.EN(FCLK2), .D(adder_73_out), .nQ(_3353_nq));  // open: Q
  SDELAY24 _3363 (.C2(FCLK2), .C1(FCLK1), .D(adder_94_out), .Q(_3363_q), .Q40(_3363_q40));  // open: Q44
  D_LATCH _3381 (.EN(FCLK2), .D(adder_74_out), .nQ(_3381_nq));  // open: Q
  SDELAY24 _3377 (.C2(FCLK2), .C1(FCLK1), .D(adder_95_out), .Q(_3377_q), .Q40(_3377_q40));  // open: Q44
  D_LATCH _3381_2 (.EN(FCLK2), .D(adder_75_out), .nQ(_3381_2_nq));  // open: Q
  SDELAY24 _3396 (.C2(FCLK2), .C1(FCLK1), .D(adder_96_out), .Q(_3396_q), .Q40(_3396_q40));  // open: Q44
  D_LATCH _3400 (.EN(FCLK2), .D(adder_76_out), .nQ(_3400_nq));  // open: Q
  SDELAY24 _3411 (.C2(FCLK2), .C1(FCLK1), .D(adder_97_out), .Q(_3411_q), .Q40(_3411_q40));  // open: Q44
  D_LATCH _3415 (.EN(FCLK2), .D(adder_77_out), .nQ(_3415_nq));  // open: Q
  SDELAY24 _3426 (.C2(FCLK2), .C1(FCLK1), .D(adder_98_out), .Q(_3426_q), .Q40(_3426_q40));  // open: Q44
  D_LATCH _3430 (.EN(FCLK2), .D(adder_78_out), .nQ(_3430_nq));  // open: Q
  SDELAY24 _3439 (.C2(FCLK2), .C1(FCLK1), .D(adder_99_out), .Q(_3439_q), .Q40(_3439_q40));  // open: Q44
  D_LATCH _3443 (.EN(FCLK2), .D(adder_79_out), .nQ(_3443_nq));  // open: Q
  SDELAY24 _3452 (.C2(FCLK2), .C1(FCLK1), .D(adder_100_out), .Q(_3452_q), .Q40(_3452_q40));  // open: Q44
  D_LATCH _3456 (.EN(FCLK2), .D(adder_80_out), .nQ(_3456_nq));  // open: Q
  not _3174 (_3174_out, _3175_nq);
  not _3190 (_3190_out, _3191_nq);
  not _3205 (_3205_out, _3206_nq);
  not _3220 (_3220_out, _3221_nq);
  not _3235 (_3235_out, _3236_nq);
  not _3250 (_3250_out, _3251_nq);
  not _3265 (_3265_out, _3266_nq);
  not _3280 (_3280_out, _3281_nq);
  not _3295 (_3295_out, _3296_nq);
  not _3310 (_3310_out, _3311_nq);
  not _3324 (_3324_out, _3325_nq);
  not _3338 (_3338_out, _3339_nq);
  not _3352 (_3352_out, _3353_nq);
  not _3380 (_3380_out, _3381_nq);
  not _3380_2 (_3380_2_out, _3381_2_nq);
  not _3399 (_3399_out, _3400_nq);
  not _3414 (_3414_out, _3415_nq);
  not _3429 (_3429_out, _3430_nq);
  not _3442 (_3442_out, _3443_nq);
  not _3455 (_3455_out, _3456_nq);
  and _3172 (_3172_out, _3171_q, _3093_out);
  and _3188 (_3188_out, _3187_q, _3093_out);
  and _3203 (_3203_out, _3202_q, _3093_out);
  and _3218 (_3218_out, _3217_q, _3093_out);
  and _3233 (_3233_out, _3232_q, _3093_out);
  and _3248 (_3248_out, _3246_q, _3093_out);
  and _3263 (_3263_out, _3262_q, _3093_out);
  and _3278 (_3278_out, _3277_q, _3093_out);
  and _3293 (_3293_out, _3292_q, _3093_out);
  and _3308 (_3308_out, _3307_q, _3093_out);
  not _3391 (PG0, _3321_q40);
  and _3322 (_3322_out, _3321_q, _3093_out);
  not _3392 (PG1, _3335_q40);
  and _3336 (_3336_out, _3335_q, _3093_out);
  not _3393 (PG2, _3349_q40);
  and _3350 (_3350_out, _3349_q, _3093_out);
  not _3394 (PG3, _3363_q40);
  and _3364 (_3364_out, _3363_q, _3093_out);
  not _3395 (PG4, _3377_q40);
  and _3378 (_3378_out, _3377_q, _3093_out);
  not _3410 (PG5, _3396_q40);
  and _3397 (_3397_out, _3396_q, _3093_out);
  not _3425 (PG6, _3411_q40);
  and _3412 (_3412_out, _3411_q, _3093_out);
  not _3438 (PG7, _3426_q40);
  and _3427 (_3427_out, _3426_q, _3093_out);
  not _3451 (PG8, _3439_q40);
  and _3440 (_3440_out, _3439_q, _3093_out);
  not _3464 (PG9, _3452_q40);
  and _3453 (_3453_out, _3452_q, _3093_out);
  Adder #(.width(1)) adder_81 (.a(_3172_out), .b(_3174_out), .out(adder_81_out), .cin(1'b0), .cout(adder_81_cout));
  Adder #(.width(1)) adder_82 (
    .a(_3188_out), .b(_3190_out), .out(adder_82_out), .cin(adder_81_cout), .cout(adder_82_cout));
  Adder #(.width(1)) adder_83 (
    .a(_3203_out), .b(_3205_out), .out(adder_83_out), .cin(adder_82_cout), .cout(adder_83_cout));
  Adder #(.width(1)) adder_84 (
    .a(_3218_out), .b(_3220_out), .out(adder_84_out), .cin(adder_83_cout), .cout(adder_84_cout));
  Adder #(.width(1)) adder_85 (
    .a(_3233_out), .b(_3235_out), .out(adder_85_out), .cin(adder_84_cout), .cout(adder_85_cout));
  Adder #(.width(1)) adder_86 (
    .a(_3248_out), .b(_3250_out), .out(adder_86_out), .cin(adder_85_cout), .cout(adder_86_cout));
  Adder #(.width(1)) adder_87 (
    .a(_3263_out), .b(_3265_out), .out(adder_87_out), .cin(adder_86_cout), .cout(adder_87_cout));
  Adder #(.width(1)) adder_88 (
    .a(_3278_out), .b(_3280_out), .out(adder_88_out), .cin(adder_87_cout), .cout(adder_88_cout));
  Adder #(.width(1)) adder_89 (
    .a(_3293_out), .b(_3295_out), .out(adder_89_out), .cin(adder_88_cout), .cout(adder_89_cout));
  Adder #(.width(1)) adder_90 (
    .a(_3308_out), .b(_3310_out), .out(adder_90_out), .cin(adder_89_cout), .cout(adder_90_cout));
  Adder #(.width(1)) adder_91 (
    .a(_3322_out), .b(_3324_out), .out(adder_91_out), .cin(adder_90_cout), .cout(adder_91_cout));
  Adder #(.width(1)) adder_92 (
    .a(_3336_out), .b(_3338_out), .out(adder_92_out), .cin(adder_91_cout), .cout(adder_92_cout));
  Adder #(.width(1)) adder_93 (
    .a(_3350_out), .b(_3352_out), .out(adder_93_out), .cin(adder_92_cout), .cout(adder_93_cout));
  Adder #(.width(1)) adder_94 (
    .a(_3364_out), .b(_3380_out), .out(adder_94_out), .cin(adder_93_cout), .cout(adder_94_cout));
  Adder #(.width(1)) adder_95 (
    .a(_3378_out), .b(_3380_2_out), .out(adder_95_out), .cin(adder_94_cout), .cout(adder_95_cout));
  Adder #(.width(1)) adder_96 (
    .a(_3397_out), .b(_3399_out), .out(adder_96_out), .cin(adder_95_cout), .cout(adder_96_cout));
  Adder #(.width(1)) adder_97 (
    .a(_3412_out), .b(_3414_out), .out(adder_97_out), .cin(adder_96_cout), .cout(adder_97_cout));
  Adder #(.width(1)) adder_98 (
    .a(_3427_out), .b(_3429_out), .out(adder_98_out), .cin(adder_97_cout), .cout(adder_98_cout));
  Adder #(.width(1)) adder_99 (
    .a(_3440_out), .b(_3442_out), .out(adder_99_out), .cin(adder_98_cout), .cout(adder_99_cout));
  Adder #(.width(1)) adder_100 (.a(_3453_out), .b(_3455_out), .out(adder_100_out), .cin(adder_99_cout));  // open: cout
  and and_6 (and_6_out, _3091_out, _3171_q);
  and and_7 (and_7_out, _3091_out, _3187_q);
  and and_8 (and_8_out, _3091_out, _3202_q);
  and and_9 (and_9_out, _3091_out, _3217_q);
  and and_10 (and_10_out, _3091_out, _3232_q);
  and and_11 (and_11_out, _3091_out, _3246_q);
  and and_12 (and_12_out, _3091_out, _3262_q);
  and and_13 (and_13_out, _3091_out, _3277_q);
  and and_14 (and_14_out, _3091_out, _3292_q);
  and and_15 (and_15_out, _3091_out, _3307_q);
  or or_1 (or_1_out, and_6_out, sr_bit_22_q);
  or or_2 (or_2_out, and_7_out, sr_bit_23_q);
  or or_3 (or_3_out, and_8_out, sr_bit_24_q);
  or or_4 (or_4_out, and_9_out, sr_bit_25_q);
  or or_5 (or_5_out, and_10_out, sr_bit_26_q);
  or or_6 (or_6_out, and_11_out, sr_bit_27_q);
  or or_7 (or_7_out, and_12_out, sr_bit_28_q);
  or or_8 (or_8_out, and_13_out, sr_bit_29_q);
  or or_9 (or_9_out, and_14_out, sr_bit_30_q);
  or or_10 (or_10_out, and_15_out, _3110_nq);
  SR_BIT sr_bit_21 (.C2(FCLK2), .C1(FCLK1), .D(or_1_out), .Q(g_3170));  // open: nQ
  SR_BIT sr_bit_22 (.C2(FCLK2), .C1(FCLK1), .D(or_2_out), .Q(sr_bit_22_q));  // open: nQ
  SR_BIT sr_bit_23 (.C2(FCLK2), .C1(FCLK1), .D(or_3_out), .Q(sr_bit_23_q));  // open: nQ
  SR_BIT sr_bit_24 (.C2(FCLK2), .C1(FCLK1), .D(or_4_out), .Q(sr_bit_24_q));  // open: nQ
  SR_BIT sr_bit_25 (.C2(FCLK2), .C1(FCLK1), .D(or_5_out), .Q(sr_bit_25_q));  // open: nQ
  SR_BIT sr_bit_26 (.C2(FCLK2), .C1(FCLK1), .D(or_6_out), .Q(sr_bit_26_q));  // open: nQ
  SR_BIT sr_bit_27 (.C2(FCLK2), .C1(FCLK1), .D(or_7_out), .Q(sr_bit_27_q));  // open: nQ
  SR_BIT sr_bit_28 (.C2(FCLK2), .C1(FCLK1), .D(or_8_out), .Q(sr_bit_28_q));  // open: nQ
  SR_BIT sr_bit_29 (.C2(FCLK2), .C1(FCLK1), .D(or_9_out), .Q(sr_bit_29_q));  // open: nQ
  SR_BIT sr_bit_30 (.C2(FCLK2), .C1(FCLK1), .D(or_10_out), .Q(sr_bit_30_q));  // open: nQ
  D_LATCH _3110 (.EN(FCLK2), .D(1'b1), .nQ(_3110_nq));  // open: Q

  assign g_3656_2 = g_3656;

  // Notes on the sheet:
  //   3882 - 3884
  //   3828, 3830 - 3833
  //   3848, 3849
  //   3484 - 3492
  //   3129 - 3149
  //   3158 - 3167, 3169
  //   3753
  //   3742
  //   3730
  //   3718
  //   3696
  //   3682
  //   3668
  //   3643 - 3645
  //   3634 - 3636
  //   3638, 3639
  //   3633, 3631, 3629
  //   3649
  //   3648
  //   3647
  //   3646
  //   3759
  //   3748
  //   3736
  //   3724
  //   3707
  //   3708
  //   3709
  //   3710
  //   3661
  //   3662
  //   3676
  //   3690
  //   2352 - 2365
  //   2339 - 2348
  //   5
  //   6
  //   7
  //   8
  //   9
  //   3618
  //   3804
  //   3799
  //   3794
  //   2444
  //   2438
  //   2432
  //   2426
  //   2420
  //   2414
  //   2408
  //   2402
  //   2396
  //   2390
  //   2384
  //   2378
  //   2373
  //   2368
  //   3598
  //   3184
  //   3200
  //   3215
  //   3230
  //   3245
  //   3260
  //   3275
  //   3290
  //   3305
  //   3320
  //   3334
  //   3348
  //   3362
  //   3376
  //   3390
  //   3409
  //   3424
  //   3437
  //   3450
  //   3463
  //   FA_SEQ
  //   FA_SEQ
  //   FA_SEQ
  //   FA_SEQ
  //   FA_SEQ
  //   FA_SEQ
  //   FA_SEQ
  //   FA_SEQ
  //   FA_SEQ
  //   FA_SEQ
  //   FA_SEQ
  //   FA_SEQ
  //   FA_SEQ
  //   FA_SEQ
  //   FA_SEQ
  //   FA_SEQ
  //   FA_SEQ
  //   FA_SEQ
  //   FA_SEQ
  //   FA_SEQ
  //   3176
  //   3192
  //   3207
  //   3222
  //   3237
  //   3252
  //   3267
  //   3282
  //   3297
  //   3312
  //   3326
  //   3340
  //   3354
  //   3368
  //   3382
  //   3401
  //   3416
  //   3431
  //   3444
  //   3457
  //   3173
  //   3189
  //   3204
  //   3219
  //   3234
  //   3249
  //   3264
  //   3279
  //   3294
  //   3309
  //   3323
  //   3337
  //   3351
  //   3365
  //   3379
  //   3398
  //   3413
  //   3428
  //   3441
  //   3454
  //   3170
  //   A2
  //   A1
  //   3186
  //   A2
  //   A1
  //   3201
  //   A2
  //   A1
  //   3216
  //   A2
  //   A1
  //   3231
  //   A2
  //   A1
  //   3247
  //   A2
  //   A1
  //   3261
  //   A2
  //   A1
  //   3276
  //   A2
  //   A1
  //   3291
  //   A2
  //   A1
  //   3306
  //   A2
  //   A1
  //   B
  //   B
  //   B
  //   B
  //   B
  //   B
  //   B
  //   B
  //   B
  //   B
  //   AON21SR
  //   AON21SR
  //   AON21SR
  //   AON21SR
  //   AON21SR
  //   AON21SR
  //   AON21SR
  //   AON21SR
  //   AON21SR
  //   AON21SR
endmodule

module LFO (
  input  FCLK2,
  input  FCLK1,
  input  g_77,
  input  g_366,
  input  g_1932,
  input  g_655,
  input  g_764,
  input  g_763,
  input  g_654,
  output LFO0,
  output LFO1,
  output LFO2,
  output LFO3,
  output LFO4,
  output LFO5,
  output LFO6,
  output LFO2_1,
  output LFO3_1,
  output LFO4_1,
  output LFO5_1
);

  wire _3466_q, _3467_out, _3468_out, _3469_q, _3471_out, _3473_out, _3475_out, _3477_out, _3478_q, _3479_nq,
       _3481_2_out, _3481_out, _3507_out, _3508_out, _3509_out, _3510_out, _3511_out, _3512_out, _3513_out,
       _3514_q, _3515_q, _3516_q, _3517_q, _3518_q, _3519_q, _3777_q, _3779_out, _3807_q, _3809_out,
       _3810_out, _3811_out, _3812_out, _3813_out, _3814_out, _3815_out, _3816_out, _3817_out, _3818_q,
       _3819_q, _3820_q, _3821_q, _3822_q, _3823_q, _3834_out, _3835_out, _3836_out, _3837_out, _3838_out,
       _3839_out, _3840_out, _3841_out, _3862_out, and_1_out, and_2_out, and_3_out, and_4_out, and_5_out,
       and_6_out, and_7_out, and_8_out, and_9_out, and_10_out, and_11_out, and_12_out, and_13_out,
       and_14_out, d_latch_1_nq, decoder_1_out0, decoder_1_out1, decoder_1_out2, decoder_1_out3,
       decoder_1_out4, decoder_1_out5, decoder_1_out6, decoder_1_out7, nor_1_out, not_1_out, sr_bit_1_q,
       xor_1_out, xor_2_out, xor_3_out, xor_4_out, xor_5_out, xor_6_out, xor_7_out, xor_8_out, xor_9_out,
       xor_10_out, xor_11_out, xor_12_out, xor_13_out, xor_14_out;

  or _3779 (_3779_out, g_77, g_366);
  not _3817 (_3817_out, g_1932);
  xor xor_1 (xor_1_out, _3779_out, _3819_q);
  and and_1 (and_1_out, _3779_out, _3819_q);
  xor xor_2 (xor_2_out, and_1_out, _3818_q);
  and and_2 (and_2_out, and_1_out, _3818_q);
  xor xor_3 (xor_3_out, and_2_out, _3820_q);
  and and_3 (and_3_out, and_2_out, _3820_q);
  xor xor_4 (xor_4_out, and_3_out, _3821_q);
  and and_4 (and_4_out, and_3_out, _3821_q);
  xor xor_5 (xor_5_out, and_4_out, _3823_q);
  and and_5 (and_5_out, and_4_out, _3823_q);
  xor xor_6 (xor_6_out, and_5_out, _3822_q);
  and and_6 (and_6_out, and_5_out, _3822_q);
  xor xor_7 (xor_7_out, and_6_out, _3807_q);
  and and_7 (and_7_out, and_6_out, _3807_q);
  nor _3816 (_3816_out, _3817_out, _3862_out);
  SR_BIT _3777 (.C2(FCLK2), .C1(FCLK1), .D(g_77), .Q(_3777_q));  // open: nQ
  SR_BIT _3819 (.C2(FCLK2), .C1(FCLK1), .D(_3815_out), .Q(_3819_q));  // open: nQ
  and _3815 (_3815_out, xor_1_out, _3816_out);
  SR_BIT _3818 (.C2(FCLK2), .C1(FCLK1), .D(_3814_out), .Q(_3818_q));  // open: nQ
  and _3814 (_3814_out, xor_2_out, _3816_out);
  SR_BIT _3820 (.C2(FCLK2), .C1(FCLK1), .D(_3813_out), .Q(_3820_q));  // open: nQ
  and _3813 (_3813_out, xor_3_out, _3816_out);
  SR_BIT _3821 (.C2(FCLK2), .C1(FCLK1), .D(_3812_out), .Q(_3821_q));  // open: nQ
  and _3812 (_3812_out, xor_4_out, _3816_out);
  SR_BIT _3823 (.C2(FCLK2), .C1(FCLK1), .D(_3811_out), .Q(_3823_q));  // open: nQ
  and _3811 (_3811_out, xor_5_out, _3816_out);
  SR_BIT _3822 (.C2(FCLK2), .C1(FCLK1), .D(_3810_out), .Q(_3822_q));  // open: nQ
  and _3810 (_3810_out, xor_6_out, _3816_out);
  SR_BIT _3807 (.C2(FCLK2), .C1(FCLK1), .D(_3809_out), .Q(_3807_q));  // open: nQ
  and _3809 (_3809_out, xor_7_out, _3816_out);
  Decoder #(.select(3), .disabled(0), .enable("false")) decoder_1 (
    .out0(decoder_1_out0), .out1(decoder_1_out1), .out2(decoder_1_out2), .out3(decoder_1_out3),
    .out4(decoder_1_out4), .out5(decoder_1_out5), .out6(decoder_1_out6), .out7(decoder_1_out7),
    .sel({g_654, g_763, g_764}));
  and _3841 (_3841_out, _3820_q, _3821_q, _3822_q, _3807_q, decoder_1_out0);
  and _3840 (_3840_out, _3819_q, _3820_q, _3821_q, _3807_q, decoder_1_out1);
  and _3839 (_3839_out, _3819_q, _3818_q, _3820_q, _3807_q, decoder_1_out2);
  and _3838 (_3838_out, _3807_q, _3818_q, _3819_q, decoder_1_out3);
  and _3837 (_3837_out, _3821_q, _3820_q, _3818_q, _3823_q, _3822_q, decoder_1_out4);
  and _3836 (_3836_out, _3821_q, _3822_q, _3820_q, decoder_1_out5);
  and _3835 (_3835_out, _3821_q, decoder_1_out6);
  and _3834 (_3834_out, _3819_q, _3820_q, decoder_1_out7);
  or _3862 (_3862_out, _3841_out, _3840_out, _3839_out, _3838_out, _3837_out, _3836_out, _3835_out, _3834_out);
  D_LATCH d_latch_1 (.EN(FCLK1), .D(_3777_q), .nQ(d_latch_1_nq));  // open: Q
  not not_1 (not_1_out, _3777_q);
  and and_8 (and_8_out, _3862_out, _3514_q);
  and and_9 (and_9_out, and_8_out, _3515_q);
  and and_10 (and_10_out, and_9_out, _3516_q);
  and and_11 (and_11_out, and_10_out, _3517_q);
  and and_12 (and_12_out, and_11_out, _3518_q);
  and and_13 (and_13_out, and_12_out, _3519_q);
  and and_14 (and_14_out, and_13_out, sr_bit_1_q);
  nor nor_1 (nor_1_out, d_latch_1_nq, not_1_out);
  xor xor_8 (xor_8_out, _3862_out, _3514_q);
  xor xor_9 (xor_9_out, and_8_out, _3515_q);
  xor xor_10 (xor_10_out, and_9_out, _3516_q);
  xor xor_11 (xor_11_out, and_10_out, _3517_q);
  xor xor_12 (xor_12_out, and_11_out, _3518_q);
  xor xor_13 (xor_13_out, and_12_out, _3519_q);
  xor xor_14 (xor_14_out, and_13_out, sr_bit_1_q);
  and _3510 (_3510_out, xor_8_out, g_655);
  and _3511 (_3511_out, xor_9_out, g_655);
  and _3512 (_3512_out, xor_10_out, g_655);
  and _3513 (_3513_out, xor_11_out, g_655);
  and _3509 (_3509_out, xor_12_out, g_655);
  and _3508 (_3508_out, xor_13_out, g_655);
  and _3507 (_3507_out, xor_14_out, g_655);
  not _3481 (_3481_out, nor_1_out);
  SR_BIT _3514 (.C2(FCLK2), .C1(FCLK1), .D(_3510_out), .Q(_3514_q));  // open: nQ
  SR_BIT _3515 (.C2(FCLK2), .C1(FCLK1), .D(_3511_out), .Q(_3515_q));  // open: nQ
  SR_BIT _3516 (.C2(FCLK2), .C1(FCLK1), .D(_3512_out), .Q(_3516_q));  // open: nQ
  SR_BIT _3517 (.C2(FCLK2), .C1(FCLK1), .D(_3513_out), .Q(_3517_q));  // open: nQ
  SR_BIT _3518 (.C2(FCLK2), .C1(FCLK1), .D(_3509_out), .Q(_3518_q));  // open: nQ
  SR_BIT _3519 (.C2(FCLK2), .C1(FCLK1), .D(_3508_out), .Q(_3519_q));  // open: nQ
  SR_BIT sr_bit_1 (.C2(FCLK2), .C1(FCLK1), .D(_3507_out), .Q(sr_bit_1_q));  // open: nQ
  not _3481_2 (_3481_2_out, _3481_out);
  D_Flip_Flop #(.trigger("high")) _3466 (.clk(_3481_2_out), .D(_3514_q), .Q(_3466_q));  // open: Qn, preset, en, reset
  D_Flip_Flop #(.trigger("high")) _3469 (.clk(_3481_2_out), .D(_3515_q), .Q(_3469_q));  // open: Qn, preset, en, reset
  D_Flip_Flop #(.trigger("high")) _3470 (.clk(_3481_2_out), .D(_3516_q), .Q(LFO2_1));  // open: Qn, preset, en, reset
  D_Flip_Flop #(.trigger("high")) _3472 (.clk(_3481_2_out), .D(_3517_q), .Q(LFO3_1));  // open: Qn, preset, en, reset
  D_Flip_Flop #(.trigger("high")) _3474 (.clk(_3481_2_out), .D(_3518_q), .Q(LFO4_1));  // open: Qn, preset, en, reset
  D_Flip_Flop #(.trigger("high")) _3476 (.clk(_3481_2_out), .D(_3519_q), .Q(LFO5_1));  // open: Qn, preset, en, reset
  D_Flip_Flop #(.trigger("high")) _3478 (
    .clk(_3481_2_out), .D(sr_bit_1_q), .Q(_3478_q));  // open: Qn, preset, en, reset
  xor _3467 (_3467_out, _3466_q, _3478_q);
  xor _3468 (_3468_out, _3469_q, _3478_q);
  xor _3471 (_3471_out, LFO2_1, _3478_q);
  xor _3473 (_3473_out, LFO3_1, _3478_q);
  xor _3475 (_3475_out, LFO4_1, _3478_q);
  xor _3477 (_3477_out, LFO5_1, _3478_q);
  D_LATCH _3479 (.EN(FCLK1), .D(_3478_q), .nQ(_3479_nq));  // open: Q
  not not_2 (LFO0, _3467_out);
  not not_3 (LFO1, _3468_out);
  not _3523 (LFO2, _3471_out);
  not _3524 (LFO3, _3473_out);
  not _3525 (LFO4, _3475_out);
  not _3526 (LFO5, _3477_out);
  not _3480 (LFO6, _3479_nq);

  // Notes on the sheet:
  //   B
  //   A
  //   HA
  //   B
  //   A
  //   HA
  //   B
  //   A
  //   HA
  //   B
  //   A
  //   HA
  //   B
  //   A
  //   HA
  //   B
  //   A
  //   HA
  //   B
  //   A
  //   HA
  //   3780
  //   S
  //   CO
  //   3781
  //   S
  //   CO
  //   3786
  //   S
  //   CO
  //   3785
  //   S
  //   CO
  //   3784
  //   S
  //   CO
  //   3783
  //   S
  //   CO
  //   3782
  //   S
  //   CO
  //   3858 - 3861
  //   3863 - 3869
  //   B
  //   A
  //   HA
  //   B
  //   A
  //   HA
  //   B
  //   A
  //   HA
  //   B
  //   A
  //   HA
  //   B
  //   A
  //   HA
  //   B
  //   A
  //   HA
  //   B
  //   A
  //   HA
  //   3878
  //   3879
  //   3880
  //   3881
  //   3877
  //   3876
  //   3875
  //   3778
  //   S
  //   CO
  //   S
  //   CO
  //   S
  //   CO
  //   S
  //   CO
  //   S
  //   CO
  //   S
  //   CO
  //   S
  //   CO
  //   3520
  //   SLATCH
  //   SLATCH
  //   SLATCH
  //   SLATCH
  //   SLATCH
  //   SLATCH
  //   SLATCH
  //   3521
  //   3522
endmodule
module OP (
  input  FCLK2,
  input  FCLK1,
  input  g_124,
  input  g_122,
  input  g_125,
  input  g_123,
  input  g_114,
  input  g_79,
  input  ENV0,
  input  ENV1,
  input  ENV2,
  input  ENV3,
  input  ENV4,
  input  ENV5,
  input  ENV6,
  input  ENV7,
  input  ENV8,
  input  ENV9,
  input  PG0,
  input  PG1,
  input  PG2,
  input  PG3,
  input  PG4,
  input  PG5,
  input  PG6,
  input  PG7,
  input  PG8,
  input  PG9,
  input  g_127,
  input  g_3077,
  input  g_3076,
  input  g_3075,
  input  g_372,
  output OP13,
  output OP12,
  output OP11,
  output OP10,
  output OP9,
  output OP8,
  output OP7,
  output OP6,
  output OP5,
  output OP4,
  output OP3,
  output OP2,
  output OP1,
  output OP0
);

  wire _826_out, _827_2_out, _827_3_out, _827_out, _828_2_out, _828_3_out, _828_4_out, _828_out, _829_2_out,
       _829_3_out, _829_4_out, _829_5_out, _829_out, _830_2_out, _830_3_out, _830_4_out, _830_5_out,
       _830_out, _831_2_out, _831_3_out, _831_4_out, _831_5_out, _831_out, _832_2_out, _832_3_out,
       _832_4_out, _832_5_out, _832_out, _833_2_out, _833_3_out, _833_4_out, _833_5_out, _833_out,
       _834_2_out, _834_3_out, _834_4_out, _834_5_out, _834_out, _835_2_out, _835_3_out, _835_4_out,
       _835_5_out, _835_out, _836_2_out, _836_3_out, _836_4_out, _836_5_out, _836_out, _837_2_out,
       _837_3_out, _837_4_out, _837_out, _838_2_out, _838_3_out, _838_out, _855_2_out, _855_3_out,
       _855_4_out, _855_5_out, _855_out, _856_2_out, _856_3_out, _856_4_out, _856_out, _857_2_out,
       _857_3_out, _857_4_out, _857_out, _858_2_out, _858_3_out, _858_4_out, _858_out, _859_2_out,
       _859_3_out, _859_4_out, _859_out, _860_2_out, _860_3_out, _860_out, _861_2_out, _861_3_out, _861_out,
       _862_2_out, _862_3_out, _862_out, _863_out, _864_out, _865_out, _866_out, _867_2_out, _867_3_out,
       _867_out, _868_out, _869_2_out, _869_out, _870_2_out, _870_out, _871_2_out, _871_out, _877_out,
       _880_2_out, _880_3_out, _880_out, _882_2_out, _882_3_out, _882_out, _884_2_out, _884_3_out, _884_out,
       _886_2_out, _886_3_out, _886_4_out, _886_out, _887_2_out, _887_3_out, _887_out, _889_out, _892_2_out,
       _892_3_out, _892_out, _894_2_out, _894_3_out, _894_out, _896_2_out, _896_3_out, _896_out, _898_2_out,
       _898_3_out, _898_4_out, _898_out, _899_2_out, _899_3_out, _899_out, _901_out, _904_2_out, _904_3_out,
       _904_out, _906_2_out, _906_3_out, _906_out, _908_2_out, _908_3_out, _908_out, _910_2_out, _910_3_out,
       _910_4_out, _910_out, _911_2_out, _911_3_out, _911_out, _913_out, _916_2_out, _916_3_out, _916_out,
       _918_2_out, _918_3_out, _918_out, _920_2_out, _920_3_out, _920_out, _922_2_out, _922_3_out,
       _922_4_out, _922_out, _923_2_out, _923_3_out, _923_out, _925_out, _928_2_out, _928_3_out, _928_out,
       _930_2_out, _930_3_out, _930_out, _932_2_out, _932_3_out, _932_out, _934_2_out, _934_3_out,
       _934_4_out, _934_out, _935_2_out, _935_3_out, _935_out, _937_out, _940_2_out, _940_3_out, _940_out,
       _942_2_out, _942_3_out, _942_out, _944_2_out, _944_3_out, _944_out, _946_2_out, _946_3_out,
       _946_4_out, _946_out, _947_2_out, _947_3_out, _947_out, _949_out, _952_2_out, _952_3_out, _952_out,
       _954_2_out, _954_3_out, _954_out, _956_2_out, _956_3_out, _956_out, _958_2_out, _958_3_out,
       _958_4_out, _958_out, _959_2_out, _959_3_out, _959_out, _961_out, _964_2_out, _964_3_out, _964_out,
       _966_2_out, _966_3_out, _966_out, _968_2_out, _968_3_out, _968_out, _970_2_out, _970_3_out,
       _970_4_out, _970_out, _971_2_out, _971_3_out, _971_out, _973_out, _976_2_out, _976_3_out, _976_out,
       _978_2_out, _978_3_out, _978_out, _980_2_out, _980_3_out, _980_out, _982_2_out, _982_3_out,
       _982_4_out, _982_out, _983_2_out, _983_3_out, _983_out, _985_out, _988_2_out, _988_3_out, _988_out,
       _990_2_out, _990_3_out, _990_out, _992_2_out, _992_3_out, _992_out, _994_2_out, _994_3_out,
       _994_4_out, _994_out, _995_2_out, _995_3_out, _995_out, _997_out, _1000_2_out, _1000_3_out, _1000_out,
       _1002_2_out, _1002_3_out, _1002_out, _1004_2_out, _1004_3_out, _1004_out, _1006_2_out, _1006_3_out,
       _1006_4_out, _1006_out, _1007_2_out, _1007_3_out, _1007_out, _1009_out, _1012_2_out, _1012_3_out,
       _1012_out, _1014_2_out, _1014_3_out, _1014_out, _1016_2_out, _1016_3_out, _1016_out, _1018_2_out,
       _1018_3_out, _1018_4_out, _1018_out, _1019_2_out, _1019_3_out, _1019_out, _1021_out, _1024_2_out,
       _1024_3_out, _1024_out, _1026_2_out, _1026_3_out, _1026_out, _1028_2_out, _1028_3_out, _1028_out,
       _1030_2_out, _1030_3_out, _1030_4_out, _1030_out, _1031_2_out, _1031_3_out, _1031_out, _1033_out,
       _1036_2_out, _1036_3_out, _1036_out, _1038_2_out, _1038_3_out, _1038_out, _1040_2_out, _1040_3_out,
       _1040_out, _1042_2_out, _1042_3_out, _1042_4_out, _1042_out, _1043_2_out, _1043_3_out, _1043_out,
       _1045_out, _1046_out, _1047_out, _1048_out, _1049_out, _1184_out, _1185_out, _1186_out, _1206_out,
       _1223_out, _1260_out, _1261_out, _1264_out, _1265_out, _1266_out, _1267_out, _1272_out, _1273_out,
       _1274_out, _1299_2_out, _1299_out, _1300_out, _1301_out, _1302_out, _1303_out, adder_1_cout,
       adder_1_out, adder_2_cout, adder_2_out, adder_3_cout, adder_3_out, adder_4_cout, adder_4_out,
       adder_5_cout, adder_5_out, adder_6_cout, adder_6_out, adder_7_cout, adder_7_out, adder_8_cout,
       adder_8_out, adder_9_cout, adder_9_out, adder_10_out, adder_11_cout, adder_11_out, adder_12_cout,
       adder_12_out, adder_13_cout, adder_13_out, adder_14_cout, adder_14_out, adder_15_cout, adder_15_out,
       adder_16_cout, adder_16_out, adder_17_cout, adder_17_out, adder_18_cout, adder_18_out, adder_19_cout,
       adder_19_out, adder_20_cout, adder_20_out, adder_21_cout, adder_21_out, adder_22_cout, adder_22_out,
       adder_23_cout, adder_23_out, adder_24_cout, adder_24_out, adder_25_cout, adder_25_out, adder_26_cout,
       adder_26_out, adder_27_cout, adder_27_out, adder_28_cout, adder_28_out, adder_29_cout, adder_29_out,
       adder_30_cout, adder_30_out, adder_31_cout, adder_31_out, adder_32_cout, adder_32_out, adder_33_cout,
       adder_33_out, adder_34_cout, adder_34_out, adder_35_cout, adder_35_out, adder_36_cout, adder_36_out,
       adder_37_cout, adder_37_out, adder_38_cout, adder_38_out, adder_39_cout, adder_39_out, adder_40_cout,
       adder_40_out, adder_41_cout, adder_41_out, adder_42_cout, adder_42_out, adder_43_cout, adder_43_out,
       adder_44_cout, adder_44_out, adder_45_cout, adder_45_out, adder_46_cout, adder_46_out, adder_47_out,
       and_1_out, and_2_out, and_3_out, and_4_out, and_5_out, and_6_out, and_7_out, and_8_out, and_10_out,
       and_11_out, and_12_out, and_13_out, and_14_out, and_15_out, and_16_out, and_17_out, and_18_out,
       and_19_out, and_20_out, and_21_out, and_22_out, and_23_out, decoder_1_out0, decoder_1_out1,
       decoder_1_out2, decoder_1_out3, decoder_2_out0, decoder_2_out1, decoder_2_out2, decoder_2_out3,
       decoder_3_out0, decoder_3_out1, decoder_3_out2, decoder_3_out3, decoder_4_out0, decoder_4_out1,
       decoder_4_out2, decoder_4_out3, sdelay6_1_q, sdelay6_2_q, sdelay6_3_q, sdelay6_4_q, sdelay6_5_q,
       sdelay6_6_q, sdelay6_7_q, sdelay6_8_q, sdelay6_9_q, sdelay6_10_q, sdelay6_11_q, sdelay6_12_q,
       sdelay6_13_q, sdelay6_14_q, sdelay6_15_q, sdelay6_16_q, sdelay6_17_q, sdelay6_18_q, sdelay6_19_q,
       sdelay6_20_q, sdelay6_21_q, sdelay6_22_q, sdelay6_23_q, sdelay6_24_q, sdelay6_25_q, sdelay6_26_q,
       sdelay6_27_q, sdelay6_28_q, sdelay6_29_q, sdelay6_30_q, sdelay6_31_q, sdelay6_32_q, sdelay6_33_q,
       sdelay6_34_q, sdelay6_35_q, sdelay6_36_q, sdelay6_37_q, sdelay6_38_q, sdelay6_39_q, sdelay6_40_q,
       sdelay6_41_q, sdelay6_42_q, sr_bit_1_q, sr_bit_2_q, sr_bit_3_q, sr_bit_4_q, sr_bit_5_q, sr_bit_6_q,
       sr_bit_7_q, sr_bit_8_q, sr_bit_9_q, sr_bit_10_q, sr_bit_11_q, sr_bit_12_q, sr_bit_13_q, sr_bit_14_q,
       sr_bit_15_q, sr_bit_16_q, sr_bit_17_q, sr_bit_18_q, sr_bit_19_q, sr_bit_20_q, sr_bit_21_q,
       sr_bit_22_q, sr_bit_23_q, sr_bit_24_q, sr_bit_25_q, sr_bit_26_q, sr_bit_27_q, sr_bit_28_q,
       sr_bit_29_q, sr_bit_30_q, sr_bit_31_q, sr_bit_32_q, sr_bit_33_q, sr_bit_34_q, sr_bit_35_q,
       sr_bit_40_q, sr_bit_41_q, sr_bit_42_q, sr_bit_43_q, sr_bit_44_q, sr_bit_45_q, sr_bit_46_q,
       sr_bit_47_q, sr_bit_48_q, sr_bit_49_q, sr_bit_50_q, sr_bit_51_q, sr_bit_52_q, sr_bit_53_q,
       sr_bit_54_q, sr_bit_55_q, sr_bit_56_q, sr_bit_70_q, xor_1_out, xor_2_out, xor_3_out, xor_4_out,
       xor_5_out, xor_6_out, xor_7_out, xor_8_out, xor_9_out, xor_10_out, xor_11_out, xor_12_out, xor_13_out,
       xor_14_out, xor_15_out, xor_16_out, xor_17_out, xor_18_out, xor_19_out, xor_20_out, xor_21_out,
       xor_22_out, xor_23_out;
  wire [1:0] _1213_out, _1296_out, sr_bit_37_q, sr_bit_39_q;
  wire [3:0] _1207_out;
  wire [4:0] _1219_out;
  wire [9:0] op_feedback_1_fb, register_1_q, register_2_q, register_3_q, register_4_q, register_5_q,
       register_6_q, register_7_q, register_8_q, register_9_q, register_10_q, register_11_q, register_13_q;
  wire [12:0] exp_table_1_d0, not_2_out, register_15_q, register_16_q;
  wire [13:0] sr_bit_57_q;
  wire [18:0] not_1_out, register_12_q, register_14_q, sine_table_1_d0;

  Adder #(.width(1)) adder_1 (.a(PG0), .b(register_13_q[0]), .out(adder_1_out), .cin(1'b0), .cout(adder_1_cout));
  Adder #(.width(1)) adder_2 (
    .a(PG1), .b(register_13_q[1]), .out(adder_2_out), .cin(adder_1_cout), .cout(adder_2_cout));
  Adder #(.width(1)) adder_3 (
    .a(PG2), .b(register_13_q[2]), .out(adder_3_out), .cin(adder_2_cout), .cout(adder_3_cout));
  Adder #(.width(1)) adder_4 (
    .a(PG3), .b(register_13_q[3]), .out(adder_4_out), .cin(adder_3_cout), .cout(adder_4_cout));
  Adder #(.width(1)) adder_5 (
    .a(PG4), .b(register_13_q[4]), .out(adder_5_out), .cin(adder_4_cout), .cout(adder_5_cout));
  Adder #(.width(1)) adder_6 (
    .a(PG5), .b(register_13_q[5]), .out(adder_6_out), .cin(adder_5_cout), .cout(adder_6_cout));
  Adder #(.width(1)) adder_7 (
    .a(PG6), .b(register_13_q[6]), .out(adder_7_out), .cin(adder_6_cout), .cout(adder_7_cout));
  Adder #(.width(1)) adder_8 (
    .a(PG7), .b(register_13_q[7]), .out(adder_8_out), .cin(adder_7_cout), .cout(adder_8_cout));
  Adder #(.width(1)) adder_9 (
    .a(PG8), .b(register_13_q[8]), .out(adder_9_out), .cin(adder_8_cout), .cout(adder_9_cout));
  Adder #(.width(1)) adder_10 (.a(PG9), .b(register_13_q[9]), .out(adder_10_out), .cin(adder_9_cout));  // open: cout
  SR_BIT sr_bit_1 (.C2(FCLK2), .C1(FCLK1), .D(ENV0), .Q(sr_bit_1_q));  // open: nQ
  SR_BIT sr_bit_2 (.C2(FCLK2), .C1(FCLK1), .D(ENV1), .Q(sr_bit_2_q));  // open: nQ
  SR_BIT sr_bit_3 (.C2(FCLK2), .C1(FCLK1), .D(ENV2), .Q(sr_bit_3_q));  // open: nQ
  SR_BIT sr_bit_4 (.C2(FCLK2), .C1(FCLK1), .D(ENV3), .Q(sr_bit_4_q));  // open: nQ
  SR_BIT sr_bit_5 (.C2(FCLK2), .C1(FCLK1), .D(ENV4), .Q(sr_bit_5_q));  // open: nQ
  SR_BIT sr_bit_6 (.C2(FCLK2), .C1(FCLK1), .D(ENV5), .Q(sr_bit_6_q));  // open: nQ
  SR_BIT sr_bit_7 (.C2(FCLK2), .C1(FCLK1), .D(ENV6), .Q(sr_bit_7_q));  // open: nQ
  SR_BIT sr_bit_8 (.C2(FCLK2), .C1(FCLK1), .D(ENV7), .Q(sr_bit_8_q));  // open: nQ
  SR_BIT sr_bit_9 (.C2(FCLK2), .C1(FCLK1), .D(ENV8), .Q(sr_bit_9_q));  // open: nQ
  SR_BIT sr_bit_10 (.C2(FCLK2), .C1(FCLK1), .D(ENV9), .Q(sr_bit_10_q));  // open: nQ
  SR_BIT sr_bit_11 (.C2(FCLK2), .C1(FCLK1), .D(_1303_out), .Q(sr_bit_11_q));  // open: nQ
  SR_BIT sr_bit_12 (.C2(FCLK2), .C1(FCLK1), .D(adder_1_out), .Q(sr_bit_12_q));  // open: nQ
  SR_BIT sr_bit_13 (.C2(FCLK2), .C1(FCLK1), .D(adder_2_out), .Q(sr_bit_13_q));  // open: nQ
  SR_BIT sr_bit_14 (.C2(FCLK2), .C1(FCLK1), .D(adder_3_out), .Q(sr_bit_14_q));  // open: nQ
  SR_BIT sr_bit_15 (.C2(FCLK2), .C1(FCLK1), .D(adder_4_out), .Q(sr_bit_15_q));  // open: nQ
  SR_BIT sr_bit_16 (.C2(FCLK2), .C1(FCLK1), .D(adder_5_out), .Q(sr_bit_16_q));  // open: nQ
  SR_BIT sr_bit_17 (.C2(FCLK2), .C1(FCLK1), .D(adder_6_out), .Q(sr_bit_17_q));  // open: nQ
  SR_BIT sr_bit_18 (.C2(FCLK2), .C1(FCLK1), .D(adder_7_out), .Q(sr_bit_18_q));  // open: nQ
  SR_BIT sr_bit_19 (.C2(FCLK2), .C1(FCLK1), .D(adder_8_out), .Q(sr_bit_19_q));  // open: nQ
  SR_BIT sr_bit_20 (.C2(FCLK2), .C1(FCLK1), .D(adder_9_out), .Q(sr_bit_20_q));  // open: nQ
  SR_BIT sr_bit_21 (.C2(FCLK2), .C1(FCLK1), .D(adder_10_out), .Q(sr_bit_21_q));  // open: nQ
  Register #(.width(10), .trigger("high")) register_1 (
    .D(op_feedback_1_fb), .Q(register_1_q), .clk(FCLK1));  // open: en, clr
  Register #(.width(10), .trigger("high")) register_2 (
    .D(register_1_q), .Q(register_2_q), .clk(FCLK2));  // open: en, clr
  OP_FEEDBACK op_feedback_1 (
    .OP(sr_bit_57_q), .g_127(g_127), .g_3077(g_3077), .g_3076(g_3076), .g_3075(g_3075), .FB(op_feedback_1_fb));
  not _1274 (_1274_out, sr_bit_11_q);
  xor _1303 (_1303_out, sr_bit_12_q, sr_bit_20_q);
  xor _1302 (_1302_out, sr_bit_13_q, sr_bit_20_q);
  xor _1301 (_1301_out, sr_bit_14_q, sr_bit_20_q);
  xor _1300 (_1300_out, sr_bit_15_q, sr_bit_20_q);
  xor _1299 (_1299_out, sr_bit_16_q, sr_bit_20_q);
  xor _1299_2 (_1299_2_out, sr_bit_17_q, sr_bit_20_q);
  xor _1296 (_1296_out[0], sr_bit_18_q, sr_bit_20_q);
  xor _1294 (_1296_out[1], sr_bit_19_q, sr_bit_20_q);
  Register #(.width(10), .trigger("high")) register_3 (
    .D(register_4_q), .Q(register_3_q), .clk(FCLK2));  // open: en, clr
  Register #(.width(10), .trigger("high")) register_4 (
    .D(register_2_q), .Q(register_4_q), .clk(FCLK1));  // open: en, clr
  and _1273 (_1273_out, not_1_out[0], _1274_out);
  and _1272 (_1272_out, not_1_out[2], _1274_out);
  and _1266 (_1266_out, not_1_out[4], _1274_out);
  and _1267 (_1267_out, not_1_out[6], _1274_out);
  and _1265 (_1265_out, not_1_out[8], _1274_out);
  and _1264 (_1264_out, not_1_out[10], _1274_out);
  and _1261 (_1261_out, not_1_out[12], _1274_out);
  and _1260 (_1260_out, _1274_out, not_1_out[14]);
  Register #(.width(10), .trigger("high")) register_5 (
    .D(register_3_q), .Q(register_5_q), .clk(FCLK1));  // open: en, clr
  Adder #(.width(1)) adder_11 (.a(not_1_out[1]), .b(_1273_out), .out(adder_11_out), .cin(1'b0), .cout(adder_11_cout));
  Adder #(.width(1)) adder_12 (
    .a(not_1_out[3]), .b(_1272_out), .out(adder_12_out), .cin(adder_11_cout), .cout(adder_12_cout));
  Adder #(.width(1)) adder_13 (
    .a(not_1_out[5]), .b(_1266_out), .out(adder_13_out), .cin(adder_12_cout), .cout(adder_13_cout));
  Adder #(.width(1)) adder_14 (
    .a(not_1_out[7]), .b(_1267_out), .out(adder_14_out), .cin(adder_13_cout), .cout(adder_14_cout));
  Adder #(.width(1)) adder_15 (
    .a(not_1_out[9]), .b(_1265_out), .out(adder_15_out), .cin(adder_14_cout), .cout(adder_15_cout));
  Adder #(.width(1)) adder_16 (
    .a(not_1_out[11]), .b(_1264_out), .out(adder_16_out), .cin(adder_15_cout), .cout(adder_16_cout));
  Adder #(.width(1)) adder_17 (
    .a(not_1_out[13]), .b(_1261_out), .out(adder_17_out), .cin(adder_16_cout), .cout(adder_17_cout));
  Adder #(.width(1)) adder_18 (
    .a(not_1_out[15]), .b(_1260_out), .out(adder_18_out), .cin(adder_17_cout), .cout(adder_18_cout));
  Adder #(.width(1)) adder_19 (
    .a(not_1_out[16]), .b(_1260_out), .out(adder_19_out), .cin(adder_18_cout), .cout(adder_19_cout));
  SINE_TABLE sine_table_1 (
    .CA0(decoder_1_out0), .CA1(decoder_1_out1), .CA2(decoder_1_out2), .CA3(decoder_1_out3), .RA0(_1302_out),
    .RA1(_1301_out), .RA2(_1300_out), .RA3(_1299_out), .RA4(_1299_2_out), .D0(sine_table_1_d0[0]),
    .D1(sine_table_1_d0[1]), .D2(sine_table_1_d0[2]), .D3(sine_table_1_d0[3]), .D4(sine_table_1_d0[4]),
    .D5(sine_table_1_d0[5]), .D6(sine_table_1_d0[6]), .D7(sine_table_1_d0[7]), .D8(sine_table_1_d0[8]),
    .D9(sine_table_1_d0[9]), .D10(sine_table_1_d0[10]), .D11(sine_table_1_d0[11]), .D12(sine_table_1_d0[12]),
    .D13(sine_table_1_d0[13]), .D14(sine_table_1_d0[14]), .D15(sine_table_1_d0[15]),
    .D16(sine_table_1_d0[16]), .D17(sine_table_1_d0[17]), .D18(sine_table_1_d0[18]));
  Decoder #(.select(2), .disabled(0), .enable("false")) decoder_1 (
    .out0(decoder_1_out0), .out1(decoder_1_out1), .out2(decoder_1_out2), .out3(decoder_1_out3),
    .sel(_1296_out));
  Register #(.width(10), .trigger("high")) register_6 (
    .D(register_7_q), .Q(register_6_q), .clk(FCLK1));  // open: en, clr
  Register #(.width(10), .trigger("high")) register_7 (
    .D(register_5_q), .Q(register_7_q), .clk(FCLK2));  // open: en, clr
  xor xor_1 (xor_1_out, adder_19_cout, not_1_out[17]);
  and and_1 (and_1_out, adder_19_cout, not_1_out[17]);
  xor xor_2 (xor_2_out, and_1_out, not_1_out[18]);
  and and_2 (and_2_out, and_1_out, not_1_out[18]);
  Register #(.width(10), .trigger("high")) register_8 (
    .D(register_6_q), .Q(register_8_q), .clk(FCLK2));  // open: en, clr
  Register #(.width(10), .trigger("high")) register_9 (
    .D(register_8_q), .Q(register_9_q), .clk(FCLK1));  // open: en, clr
  Adder #(.width(1)) adder_20 (.a(adder_13_out), .b(sr_bit_1_q), .out(adder_20_out), .cin(1'b0), .cout(adder_20_cout));
  Adder #(.width(1)) adder_21 (
    .a(adder_14_out), .b(sr_bit_2_q), .out(adder_21_out), .cin(adder_20_cout), .cout(adder_21_cout));
  Adder #(.width(1)) adder_22 (
    .a(adder_15_out), .b(sr_bit_3_q), .out(adder_22_out), .cin(adder_21_cout), .cout(adder_22_cout));
  Adder #(.width(1)) adder_23 (
    .a(adder_16_out), .b(sr_bit_4_q), .out(adder_23_out), .cin(adder_22_cout), .cout(adder_23_cout));
  Adder #(.width(1)) adder_24 (
    .a(adder_17_out), .b(sr_bit_5_q), .out(adder_24_out), .cin(adder_23_cout), .cout(adder_24_cout));
  Adder #(.width(1)) adder_25 (
    .a(adder_18_out), .b(sr_bit_6_q), .out(adder_25_out), .cin(adder_24_cout), .cout(adder_25_cout));
  Adder #(.width(1)) adder_26 (
    .a(adder_19_out), .b(sr_bit_7_q), .out(adder_26_out), .cin(adder_25_cout), .cout(adder_26_cout));
  Adder #(.width(1)) adder_27 (
    .a(xor_1_out), .b(sr_bit_8_q), .out(adder_27_out), .cin(adder_26_cout), .cout(adder_27_cout));
  Adder #(.width(1)) adder_28 (
    .a(xor_2_out), .b(sr_bit_9_q), .out(adder_28_out), .cin(adder_27_cout), .cout(adder_28_cout));
  Adder #(.width(1)) adder_29 (
    .a(and_2_out), .b(sr_bit_10_q), .out(adder_29_out), .cin(adder_28_cout), .cout(adder_29_cout));
  Register #(.width(10), .trigger("high")) register_10 (
    .D(register_9_q), .Q(register_10_q), .clk(FCLK2));  // open: en, clr
  SR_BIT sr_bit_22 (.C2(FCLK2), .C1(FCLK1), .D(adder_11_out), .Q(sr_bit_22_q));  // open: nQ
  SR_BIT sr_bit_23 (.C2(FCLK2), .C1(FCLK1), .D(adder_12_out), .Q(sr_bit_23_q));  // open: nQ
  SR_BIT sr_bit_24 (.C2(FCLK2), .C1(FCLK1), .D(adder_20_out), .Q(sr_bit_24_q));  // open: nQ
  SR_BIT sr_bit_25 (.C2(FCLK2), .C1(FCLK1), .D(adder_21_out), .Q(sr_bit_25_q));  // open: nQ
  SR_BIT sr_bit_26 (.C2(FCLK2), .C1(FCLK1), .D(adder_22_out), .Q(sr_bit_26_q));  // open: nQ
  SR_BIT sr_bit_27 (.C2(FCLK2), .C1(FCLK1), .D(adder_23_out), .Q(sr_bit_27_q));  // open: nQ
  SR_BIT sr_bit_28 (.C2(FCLK2), .C1(FCLK1), .D(adder_24_out), .Q(sr_bit_28_q));  // open: nQ
  SR_BIT sr_bit_29 (.C2(FCLK2), .C1(FCLK1), .D(adder_25_out), .Q(sr_bit_29_q));  // open: nQ
  SR_BIT sr_bit_30 (.C2(FCLK2), .C1(FCLK1), .D(adder_26_out), .Q(sr_bit_30_q));  // open: nQ
  SR_BIT sr_bit_31 (.C2(FCLK2), .C1(FCLK1), .D(adder_27_out), .Q(sr_bit_31_q));  // open: nQ
  SR_BIT sr_bit_32 (.C2(FCLK2), .C1(FCLK1), .D(adder_28_out), .Q(sr_bit_32_q));  // open: nQ
  SR_BIT sr_bit_33 (.C2(FCLK2), .C1(FCLK1), .D(adder_29_out), .Q(sr_bit_33_q));  // open: nQ
  SR_BIT sr_bit_34 (.C2(FCLK2), .C1(FCLK1), .D(adder_29_cout), .Q(sr_bit_34_q));  // open: nQ
  Register #(.width(10), .trigger("high")) register_11 (
    .D(register_10_q), .Q(register_11_q), .clk(FCLK1));  // open: en, clr
  Register #(.width(19), .trigger("high")) register_12 (
    .D(sine_table_1_d0), .Q(register_12_q), .clk(FCLK1));  // open: en, clr
  Register #(.width(10), .trigger("high")) register_13 (
    .D(register_11_q), .Q(register_13_q), .clk(FCLK2));  // open: en, clr
  buf _1206 (_1206_out, sr_bit_34_q);
  Register #(.width(19), .trigger("high")) register_14 (
    .D(register_12_q), .Q(register_14_q), .clk(FCLK2));  // open: en, clr
  assign not_1_out = ~register_14_q;  // NOT_Gate not_1, 19 bits wide
  nor _1223 (_1223_out, _1206_out, sr_bit_22_q);
  nor _1219 (_1219_out[0], _1206_out, sr_bit_23_q);
  nor _1220 (_1219_out[1], _1206_out, sr_bit_24_q);
  nor _1221 (_1219_out[2], _1206_out, sr_bit_25_q);
  nor _1222 (_1219_out[3], _1206_out, sr_bit_26_q);
  nor _1212 (_1219_out[4], _1206_out, sr_bit_27_q);
  nor _1213 (_1213_out[0], _1206_out, sr_bit_28_q);
  nor _1211 (_1213_out[1], _1206_out, sr_bit_29_q);
  nor _1210 (_1207_out[3], _1206_out, sr_bit_30_q);
  nor _1209 (_1207_out[2], _1206_out, sr_bit_31_q);
  nor _1208 (_1207_out[1], _1206_out, sr_bit_32_q);
  nor _1207 (_1207_out[0], _1206_out, sr_bit_33_q);
  EXP_TABLE exp_table_1 (
    .CA0(decoder_2_out0), .CA1(decoder_2_out1), .CA2(decoder_2_out2), .CA3(decoder_2_out3),
    .RA0(_1219_out[0]), .RA1(_1219_out[1]), .RA2(_1219_out[2]), .RA3(_1219_out[3]), .RA4(_1219_out[4]),
    .D0(exp_table_1_d0[0]), .D1(exp_table_1_d0[1]), .D2(exp_table_1_d0[2]), .D3(exp_table_1_d0[3]),
    .D4(exp_table_1_d0[4]), .D5(exp_table_1_d0[5]), .D6(exp_table_1_d0[6]), .D7(exp_table_1_d0[7]),
    .D8(exp_table_1_d0[8]), .D9(exp_table_1_d0[9]), .D10(exp_table_1_d0[10]), .D11(exp_table_1_d0[11]),
    .D12(exp_table_1_d0[12]));
  Decoder #(.select(2), .disabled(0), .enable("false")) decoder_2 (
    .out0(decoder_2_out0), .out1(decoder_2_out1), .out2(decoder_2_out2), .out3(decoder_2_out3),
    .sel(_1213_out));
  Register #(.width(13), .trigger("high")) register_15 (
    .D(exp_table_1_d0), .Q(register_15_q), .clk(FCLK1));  // open: en, clr
  assign not_2_out = ~register_16_q;  // NOT_Gate not_2, 13 bits wide
  Register #(.width(13), .trigger("high")) register_16 (
    .D(register_15_q), .Q(register_16_q), .clk(FCLK2));  // open: en, clr
  SR_BIT sr_bit_35 (.C2(FCLK2), .C1(FCLK1), .D(sr_bit_21_q), .Q(sr_bit_35_q));  // open: nQ
  SR_BIT sr_bit_36 (.C2(FCLK2), .C1(FCLK1), .D(_1207_out[0]), .Q(sr_bit_37_q[1]));  // open: nQ
  SR_BIT sr_bit_37 (.C2(FCLK2), .C1(FCLK1), .D(_1207_out[1]), .Q(sr_bit_37_q[0]));  // open: nQ
  SR_BIT sr_bit_38 (.C2(FCLK2), .C1(FCLK1), .D(_1207_out[2]), .Q(sr_bit_39_q[1]));  // open: nQ
  SR_BIT sr_bit_39 (.C2(FCLK2), .C1(FCLK1), .D(_1207_out[3]), .Q(sr_bit_39_q[0]));  // open: nQ
  SR_BIT sr_bit_40 (.C2(FCLK2), .C1(FCLK1), .D(_1223_out), .Q(sr_bit_40_q));  // open: nQ
  SR_BIT sr_bit_41 (.C2(FCLK2), .C1(FCLK1), .D(sr_bit_35_q), .Q(sr_bit_41_q));  // open: nQ
  and _1185 (_1185_out, sr_bit_40_q, not_2_out[1]);
  and _1186 (_1186_out, sr_bit_40_q, not_2_out[3]);
  and _1184 (_1184_out, sr_bit_40_q, not_2_out[5]);
  Adder #(.width(1)) adder_30 (.a(not_2_out[0]), .b(_1185_out), .out(adder_30_out), .cin(1'b0), .cout(adder_30_cout));
  Adder #(.width(1)) adder_31 (
    .a(not_2_out[2]), .b(_1186_out), .out(adder_31_out), .cin(adder_30_cout), .cout(adder_31_cout));
  Adder #(.width(1)) adder_32 (
    .a(not_2_out[4]), .b(_1184_out), .out(adder_32_out), .cin(adder_31_cout), .cout(adder_32_cout));
  xor xor_3 (xor_3_out, adder_32_cout, not_2_out[6]);
  and and_3 (and_3_out, adder_32_cout, not_2_out[6]);
  xor xor_4 (xor_4_out, and_3_out, not_2_out[7]);
  and and_4 (and_4_out, and_3_out, not_2_out[7]);
  xor xor_5 (xor_5_out, and_4_out, not_2_out[8]);
  and and_5 (and_5_out, and_4_out, not_2_out[8]);
  xor xor_6 (xor_6_out, and_5_out, not_2_out[9]);
  and and_6 (and_6_out, and_5_out, not_2_out[9]);
  xor xor_7 (xor_7_out, and_6_out, not_2_out[10]);
  and and_7 (and_7_out, and_6_out, not_2_out[10]);
  xor xor_8 (xor_8_out, and_7_out, not_2_out[11]);
  and and_8 (and_8_out, and_7_out, not_2_out[11]);
  xor xor_9 (xor_9_out, and_8_out, not_2_out[12]);
  // AND_Gate and_9 has open pins: in0=and_8_out, in1=not_2_out[12], out=open
  Decoder #(.select(2), .disabled(0), .enable("false")) decoder_3 (
    .out0(decoder_3_out0), .out1(decoder_3_out1), .out2(decoder_3_out2), .out3(decoder_3_out3),
    .sel(sr_bit_37_q));
  Decoder #(.select(2), .disabled(0), .enable("false")) decoder_4 (
    .out0(decoder_4_out0), .out1(decoder_4_out1), .out2(decoder_4_out2), .out3(decoder_4_out3),
    .sel(sr_bit_39_q));
  SR_BIT sr_bit_42 (.C2(FCLK2), .C1(FCLK1), .D(sr_bit_41_q), .Q(sr_bit_42_q));  // open: nQ
  buf _868 (_868_out, sr_bit_42_q);
  and _838 (_838_out, decoder_4_out1, adder_30_out);
  and _838_2 (_838_2_out, decoder_4_out0, adder_31_out);
  and _837 (_837_out, decoder_4_out2, adder_30_out);
  and _837_2 (_837_2_out, decoder_4_out1, adder_31_out);
  and _837_3 (_837_3_out, decoder_4_out0, adder_32_out);
  and _836 (_836_out, decoder_4_out3, adder_30_out);
  and _836_2 (_836_2_out, decoder_4_out2, adder_31_out);
  and _836_3 (_836_3_out, decoder_4_out1, adder_32_out);
  and _836_4 (_836_4_out, decoder_4_out0, xor_3_out);
  and _835 (_835_out, decoder_4_out3, adder_31_out);
  and _835_2 (_835_2_out, decoder_4_out2, adder_32_out);
  and _835_3 (_835_3_out, decoder_4_out1, xor_3_out);
  and _835_4 (_835_4_out, decoder_4_out0, xor_4_out);
  and _834 (_834_out, decoder_4_out3, adder_32_out);
  and _834_2 (_834_2_out, decoder_4_out2, xor_3_out);
  and _834_3 (_834_3_out, decoder_4_out1, xor_4_out);
  and _834_4 (_834_4_out, decoder_4_out0, xor_5_out);
  and _833 (_833_out, decoder_4_out3, xor_3_out);
  and _833_2 (_833_2_out, decoder_4_out2, xor_4_out);
  and _833_3 (_833_3_out, decoder_4_out1, xor_5_out);
  and _833_4 (_833_4_out, decoder_4_out0, xor_6_out);
  and _832 (_832_out, decoder_4_out3, xor_4_out);
  and _832_2 (_832_2_out, decoder_4_out2, xor_5_out);
  and _832_3 (_832_3_out, decoder_4_out1, xor_6_out);
  and _832_4 (_832_4_out, decoder_4_out0, xor_7_out);
  and _831 (_831_out, decoder_4_out3, xor_5_out);
  and _831_2 (_831_2_out, decoder_4_out2, xor_6_out);
  and _831_3 (_831_3_out, decoder_4_out1, xor_7_out);
  and _831_4 (_831_4_out, decoder_4_out0, xor_8_out);
  and _830 (_830_out, decoder_4_out3, xor_6_out);
  and _830_2 (_830_2_out, decoder_4_out2, xor_7_out);
  and _830_3 (_830_3_out, decoder_4_out1, xor_8_out);
  and _830_4 (_830_4_out, decoder_4_out0, xor_9_out);
  and _829 (_829_out, decoder_4_out3, xor_7_out);
  and _829_2 (_829_2_out, decoder_4_out2, xor_8_out);
  and _829_3 (_829_3_out, decoder_4_out1, xor_9_out);
  and _829_4 (_829_4_out, decoder_4_out0, 1'b1);
  and _828 (_828_out, decoder_4_out3, xor_8_out);
  and _828_2 (_828_2_out, decoder_4_out2, xor_9_out);
  and _828_3 (_828_3_out, decoder_4_out1, 1'b1);
  and _827 (_827_out, decoder_4_out3, xor_9_out);
  and _827_2 (_827_2_out, decoder_4_out2, 1'b1);
  and _826 (_826_out, 1'b1, decoder_4_out3);
  or _838_3 (_838_3_out, _838_out, _838_2_out);
  or _837_4 (_837_4_out, _837_out, _837_2_out, _837_3_out);
  or _828_4 (_828_4_out, _828_out, _828_2_out, _828_3_out);
  or _827_3 (_827_3_out, _827_out, _827_2_out);
  or _836_5 (_836_5_out, _836_out, _836_2_out, _836_3_out, _836_4_out);
  or _835_5 (_835_5_out, _835_out, _835_2_out, _835_3_out, _835_4_out);
  or _834_5 (_834_5_out, _834_out, _834_2_out, _834_3_out, _834_4_out);
  or _833_5 (_833_5_out, _833_out, _833_2_out, _833_3_out, _833_4_out);
  or _832_5 (_832_5_out, _832_out, _832_2_out, _832_3_out, _832_4_out);
  or _831_5 (_831_5_out, _831_out, _831_2_out, _831_3_out, _831_4_out);
  or _830_5 (_830_5_out, _830_out, _830_2_out, _830_3_out, _830_4_out);
  or _829_5 (_829_5_out, _829_out, _829_2_out, _829_3_out, _829_4_out);
  and _855 (_855_out, decoder_3_out3, _838_3_out);
  and _855_2 (_855_2_out, decoder_3_out2, _834_5_out);
  and _855_3 (_855_3_out, decoder_3_out1, _830_5_out);
  and _855_4 (_855_4_out, decoder_3_out0, _826_out);
  and _856 (_856_out, decoder_3_out3, _837_4_out);
  and _856_2 (_856_2_out, decoder_3_out2, _833_5_out);
  and _856_3 (_856_3_out, decoder_3_out1, _829_5_out);
  and _857 (_857_out, decoder_3_out3, _836_5_out);
  and _857_2 (_857_2_out, decoder_3_out2, _832_5_out);
  and _857_3 (_857_3_out, decoder_3_out1, _828_4_out);
  and _858 (_858_out, decoder_3_out3, _835_5_out);
  and _858_2 (_858_2_out, decoder_3_out2, _831_5_out);
  and _858_3 (_858_3_out, decoder_3_out1, _827_3_out);
  and _859 (_859_out, decoder_3_out3, _834_5_out);
  and _859_2 (_859_2_out, decoder_3_out2, _830_5_out);
  and _859_3 (_859_3_out, decoder_3_out1, _826_out);
  and _860 (_860_out, decoder_3_out3, _833_5_out);
  and _860_2 (_860_2_out, decoder_3_out2, _829_5_out);
  and _861 (_861_out, decoder_3_out3, _832_5_out);
  and _861_2 (_861_2_out, decoder_3_out2, _828_4_out);
  and _862 (_862_out, decoder_3_out3, _831_5_out);
  and _862_2 (_862_2_out, decoder_3_out2, _827_3_out);
  and _867 (_867_out, decoder_3_out3, _830_5_out);
  and _867_2 (_867_2_out, decoder_3_out2, _826_out);
  and _866 (_866_out, decoder_3_out3, _829_5_out);
  and _865 (_865_out, decoder_3_out3, _828_4_out);
  and _864 (_864_out, decoder_3_out3, _827_3_out);
  and _863 (_863_out, decoder_3_out3, _826_out);
  or _855_5 (_855_5_out, _855_out, _855_2_out, _855_3_out, _855_4_out);
  or _856_4 (_856_4_out, _856_out, _856_2_out, _856_3_out);
  or _857_4 (_857_4_out, _857_out, _857_2_out, _857_3_out);
  or _858_4 (_858_4_out, _858_out, _858_2_out, _858_3_out);
  or _859_4 (_859_4_out, _859_out, _859_2_out, _859_3_out);
  or _860_3 (_860_3_out, _860_out, _860_2_out);
  or _861_3 (_861_3_out, _861_out, _861_2_out);
  or _862_3 (_862_3_out, _862_out, _862_2_out);
  or _867_3 (_867_3_out, _867_out, _867_2_out);
  xor _877 (_877_out, _868_out, _855_5_out);
  xor _889 (_889_out, _868_out, _856_4_out);
  xor _901 (_901_out, _868_out, _857_4_out);
  xor _913 (_913_out, _868_out, _858_4_out);
  xor _925 (_925_out, _868_out, _859_4_out);
  xor _937 (_937_out, _868_out, _860_3_out);
  xor _949 (_949_out, _868_out, _861_3_out);
  xor _961 (_961_out, _868_out, _862_3_out);
  xor _973 (_973_out, _868_out, _867_3_out);
  xor _985 (_985_out, _868_out, _866_out);
  xor _1033 (_1033_out, _868_out, _865_out);
  xor _1021 (_1021_out, _868_out, _864_out);
  xor _1009 (_1009_out, _868_out, _863_out);
  xor _997 (_997_out, _868_out, g_372);
  xor xor_10 (xor_10_out, _877_out, _868_out);
  and and_10 (and_10_out, _877_out, _868_out);
  xor xor_11 (xor_11_out, _889_out, and_10_out);
  and and_11 (and_11_out, _889_out, and_10_out);
  xor xor_12 (xor_12_out, _901_out, and_11_out);
  and and_12 (and_12_out, _901_out, and_11_out);
  xor xor_13 (xor_13_out, _913_out, and_12_out);
  and and_13 (and_13_out, _913_out, and_12_out);
  xor xor_14 (xor_14_out, _925_out, and_13_out);
  and and_14 (and_14_out, _925_out, and_13_out);
  xor xor_15 (xor_15_out, _937_out, and_14_out);
  and and_15 (and_15_out, _937_out, and_14_out);
  xor xor_16 (xor_16_out, _949_out, and_15_out);
  and and_16 (and_16_out, _949_out, and_15_out);
  xor xor_17 (xor_17_out, _961_out, and_16_out);
  and and_17 (and_17_out, _961_out, and_16_out);
  xor xor_18 (xor_18_out, _973_out, and_17_out);
  and and_18 (and_18_out, _973_out, and_17_out);
  xor xor_19 (xor_19_out, _985_out, and_18_out);
  and and_19 (and_19_out, _985_out, and_18_out);
  xor xor_20 (xor_20_out, _1033_out, and_19_out);
  and and_20 (and_20_out, _1033_out, and_19_out);
  xor xor_21 (xor_21_out, _1021_out, and_20_out);
  and and_21 (and_21_out, _1021_out, and_20_out);
  xor xor_22 (xor_22_out, _1009_out, and_21_out);
  and and_22 (and_22_out, _1009_out, and_21_out);
  xor xor_23 (xor_23_out, _997_out, and_22_out);
  and and_23 (and_23_out, _997_out, and_22_out);
  not _869 (_869_out, g_79);
  SR_BIT sr_bit_43 (.C2(FCLK2), .C1(FCLK1), .D(xor_10_out), .Q(sr_bit_43_q));  // open: nQ
  SR_BIT sr_bit_44 (.C2(FCLK2), .C1(FCLK1), .D(xor_11_out), .Q(sr_bit_44_q));  // open: nQ
  SR_BIT sr_bit_45 (.C2(FCLK2), .C1(FCLK1), .D(xor_12_out), .Q(sr_bit_45_q));  // open: nQ
  SR_BIT sr_bit_46 (.C2(FCLK2), .C1(FCLK1), .D(xor_13_out), .Q(sr_bit_46_q));  // open: nQ
  SR_BIT sr_bit_47 (.C2(FCLK2), .C1(FCLK1), .D(xor_14_out), .Q(sr_bit_47_q));  // open: nQ
  SR_BIT sr_bit_48 (.C2(FCLK2), .C1(FCLK1), .D(xor_15_out), .Q(sr_bit_48_q));  // open: nQ
  SR_BIT sr_bit_49 (.C2(FCLK2), .C1(FCLK1), .D(xor_16_out), .Q(sr_bit_49_q));  // open: nQ
  SR_BIT sr_bit_50 (.C2(FCLK2), .C1(FCLK1), .D(xor_17_out), .Q(sr_bit_50_q));  // open: nQ
  SR_BIT sr_bit_51 (.C2(FCLK2), .C1(FCLK1), .D(xor_18_out), .Q(sr_bit_51_q));  // open: nQ
  SR_BIT sr_bit_52 (.C2(FCLK2), .C1(FCLK1), .D(xor_19_out), .Q(sr_bit_52_q));  // open: nQ
  SR_BIT sr_bit_53 (.C2(FCLK2), .C1(FCLK1), .D(xor_20_out), .Q(sr_bit_53_q));  // open: nQ
  SR_BIT sr_bit_54 (.C2(FCLK2), .C1(FCLK1), .D(xor_21_out), .Q(sr_bit_54_q));  // open: nQ
  SR_BIT sr_bit_55 (.C2(FCLK2), .C1(FCLK1), .D(xor_22_out), .Q(sr_bit_55_q));  // open: nQ
  SR_BIT sr_bit_56 (.C2(FCLK2), .C1(FCLK1), .D(xor_23_out), .Q(sr_bit_56_q));  // open: nQ
  not _869_2 (_869_2_out, _869_out);
  and _880 (_880_out, sdelay6_1_q, _869_out);
  and _880_2 (_880_2_out, _869_2_out, sr_bit_43_q);
  and _892 (_892_out, sdelay6_2_q, _869_out);
  and _892_2 (_892_2_out, _869_2_out, sr_bit_44_q);
  and _904 (_904_out, sdelay6_3_q, _869_out);
  and _904_2 (_904_2_out, _869_2_out, sr_bit_45_q);
  and _916 (_916_out, sdelay6_4_q, _869_out);
  and _916_2 (_916_2_out, _869_2_out, sr_bit_46_q);
  and _928 (_928_out, sdelay6_5_q, _869_out);
  and _928_2 (_928_2_out, _869_2_out, sr_bit_47_q);
  and _940 (_940_out, sdelay6_6_q, _869_out);
  and _940_2 (_940_2_out, _869_2_out, sr_bit_48_q);
  and _952 (_952_out, sdelay6_7_q, _869_out);
  and _952_2 (_952_2_out, _869_2_out, sr_bit_49_q);
  and _964 (_964_out, sdelay6_8_q, _869_out);
  and _964_2 (_964_2_out, _869_2_out, sr_bit_50_q);
  and _976 (_976_out, sdelay6_9_q, _869_out);
  and _976_2 (_976_2_out, _869_2_out, sr_bit_51_q);
  and _988 (_988_out, sdelay6_10_q, _869_out);
  and _988_2 (_988_2_out, _869_2_out, sr_bit_52_q);
  and _1036 (_1036_out, sdelay6_11_q, _869_out);
  and _1036_2 (_1036_2_out, _869_2_out, sr_bit_53_q);
  and _1024 (_1024_out, sdelay6_12_q, _869_out);
  and _1024_2 (_1024_2_out, _869_2_out, sr_bit_54_q);
  and _1012 (_1012_out, sdelay6_13_q, _869_out);
  and _1012_2 (_1012_2_out, _869_2_out, sr_bit_55_q);
  and _1000 (_1000_out, sdelay6_14_q, _869_out);
  and _1000_2 (_1000_2_out, _869_2_out, sr_bit_56_q);
  SDELAY6 sdelay6_1 (.C2(FCLK2), .C1(FCLK1), .D(_880_3_out), .Q(sdelay6_1_q));
  or _880_3 (_880_3_out, _880_out, _880_2_out);
  SDELAY6 sdelay6_2 (.C2(FCLK2), .C1(FCLK1), .D(_892_3_out), .Q(sdelay6_2_q));
  or _892_3 (_892_3_out, _892_out, _892_2_out);
  SDELAY6 sdelay6_3 (.C2(FCLK2), .C1(FCLK1), .D(_904_3_out), .Q(sdelay6_3_q));
  or _904_3 (_904_3_out, _904_out, _904_2_out);
  SDELAY6 sdelay6_4 (.C2(FCLK2), .C1(FCLK1), .D(_916_3_out), .Q(sdelay6_4_q));
  or _916_3 (_916_3_out, _916_out, _916_2_out);
  SDELAY6 sdelay6_5 (.C2(FCLK2), .C1(FCLK1), .D(_928_3_out), .Q(sdelay6_5_q));
  or _928_3 (_928_3_out, _928_out, _928_2_out);
  SDELAY6 sdelay6_6 (.C2(FCLK2), .C1(FCLK1), .D(_940_3_out), .Q(sdelay6_6_q));
  or _940_3 (_940_3_out, _940_out, _940_2_out);
  SDELAY6 sdelay6_7 (.C2(FCLK2), .C1(FCLK1), .D(_952_3_out), .Q(sdelay6_7_q));
  or _952_3 (_952_3_out, _952_out, _952_2_out);
  SDELAY6 sdelay6_8 (.C2(FCLK2), .C1(FCLK1), .D(_964_3_out), .Q(sdelay6_8_q));
  or _964_3 (_964_3_out, _964_out, _964_2_out);
  SDELAY6 sdelay6_9 (.C2(FCLK2), .C1(FCLK1), .D(_976_3_out), .Q(sdelay6_9_q));
  or _976_3 (_976_3_out, _976_out, _976_2_out);
  SDELAY6 sdelay6_10 (.C2(FCLK2), .C1(FCLK1), .D(_988_3_out), .Q(sdelay6_10_q));
  or _988_3 (_988_3_out, _988_out, _988_2_out);
  SDELAY6 sdelay6_11 (.C2(FCLK2), .C1(FCLK1), .D(_1036_3_out), .Q(sdelay6_11_q));
  or _1036_3 (_1036_3_out, _1036_out, _1036_2_out);
  SDELAY6 sdelay6_12 (.C2(FCLK2), .C1(FCLK1), .D(_1024_3_out), .Q(sdelay6_12_q));
  or _1024_3 (_1024_3_out, _1024_out, _1024_2_out);
  SDELAY6 sdelay6_13 (.C2(FCLK2), .C1(FCLK1), .D(_1012_3_out), .Q(sdelay6_13_q));
  or _1012_3 (_1012_3_out, _1012_out, _1012_2_out);
  SDELAY6 sdelay6_14 (.C2(FCLK2), .C1(FCLK1), .D(_1000_3_out), .Q(sdelay6_14_q));
  or _1000_3 (_1000_3_out, _1000_out, _1000_2_out);
  not _871 (_871_out, _871_2_out);
  not _871_2 (_871_2_out, g_79);
  and _882 (_882_out, sdelay6_15_q, _871_2_out);
  and _882_2 (_882_2_out, _871_out, sdelay6_1_q);
  and _894 (_894_out, sdelay6_16_q, _871_2_out);
  and _894_2 (_894_2_out, _871_out, sdelay6_2_q);
  and _906 (_906_out, sdelay6_17_q, _871_2_out);
  and _906_2 (_906_2_out, _871_out, sdelay6_3_q);
  and _918 (_918_out, sdelay6_18_q, _871_2_out);
  and _918_2 (_918_2_out, _871_out, sdelay6_4_q);
  and _930 (_930_out, sdelay6_19_q, _871_2_out);
  and _930_2 (_930_2_out, _871_out, sdelay6_5_q);
  and _942 (_942_out, sdelay6_20_q, _871_2_out);
  and _942_2 (_942_2_out, _871_out, sdelay6_6_q);
  and _954 (_954_out, sdelay6_21_q, _871_2_out);
  and _954_2 (_954_2_out, _871_out, sdelay6_7_q);
  and _966 (_966_out, sdelay6_22_q, _871_2_out);
  and _966_2 (_966_2_out, _871_out, sdelay6_8_q);
  and _978 (_978_out, sdelay6_23_q, _871_2_out);
  and _978_2 (_978_2_out, _871_out, sdelay6_9_q);
  and _990 (_990_out, sdelay6_24_q, _871_2_out);
  and _990_2 (_990_2_out, _871_out, sdelay6_10_q);
  and _1038 (_1038_out, sdelay6_25_q, _871_2_out);
  and _1038_2 (_1038_2_out, _871_out, sdelay6_11_q);
  and _1026 (_1026_out, sdelay6_26_q, _871_2_out);
  and _1026_2 (_1026_2_out, _871_out, sdelay6_12_q);
  and _1014 (_1014_out, sdelay6_27_q, _871_2_out);
  and _1014_2 (_1014_2_out, _871_out, sdelay6_13_q);
  and _1002 (_1002_out, sdelay6_28_q, _871_2_out);
  and _1002_2 (_1002_2_out, _871_out, sdelay6_14_q);
  or _882_3 (_882_3_out, _882_out, _882_2_out);
  or _894_3 (_894_3_out, _894_out, _894_2_out);
  or _906_3 (_906_3_out, _906_out, _906_2_out);
  or _918_3 (_918_3_out, _918_out, _918_2_out);
  or _930_3 (_930_3_out, _930_out, _930_2_out);
  or _942_3 (_942_3_out, _942_out, _942_2_out);
  or _954_3 (_954_3_out, _954_out, _954_2_out);
  or _966_3 (_966_3_out, _966_out, _966_2_out);
  or _978_3 (_978_3_out, _978_out, _978_2_out);
  or _990_3 (_990_3_out, _990_out, _990_2_out);
  or _1038_3 (_1038_3_out, _1038_out, _1038_2_out);
  or _1026_3 (_1026_3_out, _1026_out, _1026_2_out);
  or _1014_3 (_1014_3_out, _1014_out, _1014_2_out);
  or _1002_3 (_1002_3_out, _1002_out, _1002_2_out);
  SDELAY6 sdelay6_15 (.C2(FCLK2), .C1(FCLK1), .D(_882_3_out), .Q(sdelay6_15_q));
  SDELAY6 sdelay6_16 (.C2(FCLK2), .C1(FCLK1), .D(_894_3_out), .Q(sdelay6_16_q));
  SDELAY6 sdelay6_17 (.C2(FCLK2), .C1(FCLK1), .D(_906_3_out), .Q(sdelay6_17_q));
  SDELAY6 sdelay6_18 (.C2(FCLK2), .C1(FCLK1), .D(_918_3_out), .Q(sdelay6_18_q));
  SDELAY6 sdelay6_19 (.C2(FCLK2), .C1(FCLK1), .D(_930_3_out), .Q(sdelay6_19_q));
  SDELAY6 sdelay6_20 (.C2(FCLK2), .C1(FCLK1), .D(_942_3_out), .Q(sdelay6_20_q));
  SDELAY6 sdelay6_21 (.C2(FCLK2), .C1(FCLK1), .D(_954_3_out), .Q(sdelay6_21_q));
  SDELAY6 sdelay6_22 (.C2(FCLK2), .C1(FCLK1), .D(_966_3_out), .Q(sdelay6_22_q));
  SDELAY6 sdelay6_23 (.C2(FCLK2), .C1(FCLK1), .D(_978_3_out), .Q(sdelay6_23_q));
  SDELAY6 sdelay6_24 (.C2(FCLK2), .C1(FCLK1), .D(_990_3_out), .Q(sdelay6_24_q));
  SDELAY6 sdelay6_25 (.C2(FCLK2), .C1(FCLK1), .D(_1038_3_out), .Q(sdelay6_25_q));
  SDELAY6 sdelay6_26 (.C2(FCLK2), .C1(FCLK1), .D(_1026_3_out), .Q(sdelay6_26_q));
  SDELAY6 sdelay6_27 (.C2(FCLK2), .C1(FCLK1), .D(_1014_3_out), .Q(sdelay6_27_q));
  SDELAY6 sdelay6_28 (.C2(FCLK2), .C1(FCLK1), .D(_1002_3_out), .Q(sdelay6_28_q));
  not _870 (_870_out, g_124);
  not _870_2 (_870_2_out, _870_out);
  and _884 (_884_out, sdelay6_29_q, _870_out);
  and _884_2 (_884_2_out, _870_2_out, sr_bit_43_q);
  and _896 (_896_out, sdelay6_30_q, _870_out);
  and _896_2 (_896_2_out, _870_2_out, sr_bit_44_q);
  and _908 (_908_out, sdelay6_31_q, _870_out);
  and _908_2 (_908_2_out, _870_2_out, sr_bit_45_q);
  and _920 (_920_out, sdelay6_32_q, _870_out);
  and _920_2 (_920_2_out, _870_2_out, sr_bit_46_q);
  and _932 (_932_out, sdelay6_33_q, _870_out);
  and _932_2 (_932_2_out, _870_2_out, sr_bit_47_q);
  and _944 (_944_out, sdelay6_34_q, _870_out);
  and _944_2 (_944_2_out, _870_2_out, sr_bit_48_q);
  and _956 (_956_out, sdelay6_35_q, _870_out);
  and _956_2 (_956_2_out, _870_2_out, sr_bit_49_q);
  and _968 (_968_out, sdelay6_36_q, _870_out);
  and _968_2 (_968_2_out, _870_2_out, sr_bit_50_q);
  and _980 (_980_out, sdelay6_37_q, _870_out);
  and _980_2 (_980_2_out, _870_2_out, sr_bit_51_q);
  and _992 (_992_out, sdelay6_38_q, _870_out);
  and _992_2 (_992_2_out, _870_2_out, sr_bit_52_q);
  and _1040 (_1040_out, sdelay6_39_q, _870_out);
  and _1040_2 (_1040_2_out, _870_2_out, sr_bit_53_q);
  and _1028 (_1028_out, sdelay6_40_q, _870_out);
  and _1028_2 (_1028_2_out, _870_2_out, sr_bit_54_q);
  and _1016 (_1016_out, sdelay6_41_q, _870_out);
  and _1016_2 (_1016_2_out, _870_2_out, sr_bit_55_q);
  and _1004 (_1004_out, sdelay6_42_q, _870_out);
  and _1004_2 (_1004_2_out, _870_2_out, sr_bit_56_q);
  or _884_3 (_884_3_out, _884_out, _884_2_out);
  or _896_3 (_896_3_out, _896_out, _896_2_out);
  or _908_3 (_908_3_out, _908_out, _908_2_out);
  or _920_3 (_920_3_out, _920_out, _920_2_out);
  or _932_3 (_932_3_out, _932_out, _932_2_out);
  or _944_3 (_944_3_out, _944_out, _944_2_out);
  or _956_3 (_956_3_out, _956_out, _956_2_out);
  or _968_3 (_968_3_out, _968_out, _968_2_out);
  or _980_3 (_980_3_out, _980_out, _980_2_out);
  or _992_3 (_992_3_out, _992_out, _992_2_out);
  or _1040_3 (_1040_3_out, _1040_out, _1040_2_out);
  or _1028_3 (_1028_3_out, _1028_out, _1028_2_out);
  or _1016_3 (_1016_3_out, _1016_out, _1016_2_out);
  or _1004_3 (_1004_3_out, _1004_out, _1004_2_out);
  SDELAY6 sdelay6_29 (.C2(FCLK2), .C1(FCLK1), .D(_884_3_out), .Q(sdelay6_29_q));
  SDELAY6 sdelay6_30 (.C2(FCLK2), .C1(FCLK1), .D(_896_3_out), .Q(sdelay6_30_q));
  SDELAY6 sdelay6_31 (.C2(FCLK2), .C1(FCLK1), .D(_908_3_out), .Q(sdelay6_31_q));
  SDELAY6 sdelay6_32 (.C2(FCLK2), .C1(FCLK1), .D(_920_3_out), .Q(sdelay6_32_q));
  SDELAY6 sdelay6_33 (.C2(FCLK2), .C1(FCLK1), .D(_932_3_out), .Q(sdelay6_33_q));
  SDELAY6 sdelay6_34 (.C2(FCLK2), .C1(FCLK1), .D(_944_3_out), .Q(sdelay6_34_q));
  SDELAY6 sdelay6_35 (.C2(FCLK2), .C1(FCLK1), .D(_956_3_out), .Q(sdelay6_35_q));
  SDELAY6 sdelay6_36 (.C2(FCLK2), .C1(FCLK1), .D(_968_3_out), .Q(sdelay6_36_q));
  SDELAY6 sdelay6_37 (.C2(FCLK2), .C1(FCLK1), .D(_980_3_out), .Q(sdelay6_37_q));
  SDELAY6 sdelay6_38 (.C2(FCLK2), .C1(FCLK1), .D(_992_3_out), .Q(sdelay6_38_q));
  SDELAY6 sdelay6_39 (.C2(FCLK2), .C1(FCLK1), .D(_1040_3_out), .Q(sdelay6_39_q));
  SDELAY6 sdelay6_40 (.C2(FCLK2), .C1(FCLK1), .D(_1028_3_out), .Q(sdelay6_40_q));
  SDELAY6 sdelay6_41 (.C2(FCLK2), .C1(FCLK1), .D(_1016_3_out), .Q(sdelay6_41_q));
  SDELAY6 sdelay6_42 (.C2(FCLK2), .C1(FCLK1), .D(_1004_3_out), .Q(sdelay6_42_q));
  buf _1048 (_1048_out, g_124);
  buf _1047 (_1047_out, g_122);
  buf _1049 (_1049_out, g_125);
  buf _1046 (_1046_out, g_123);
  buf _1045 (_1045_out, g_114);
  and _887 (_887_out, sdelay6_1_q, _1045_out);
  and _887_2 (_887_2_out, _1046_out, sr_bit_43_q);
  and _886 (_886_out, sr_bit_43_q, _1047_out);
  and _886_2 (_886_2_out, _1049_out, sdelay6_29_q);
  and _886_3 (_886_3_out, _1048_out, sdelay6_15_q);
  and _899 (_899_out, sdelay6_2_q, _1045_out);
  and _899_2 (_899_2_out, _1046_out, sr_bit_44_q);
  and _898 (_898_out, sr_bit_44_q, _1047_out);
  and _898_2 (_898_2_out, _1049_out, sdelay6_30_q);
  and _898_3 (_898_3_out, _1048_out, sdelay6_16_q);
  and _911 (_911_out, sdelay6_3_q, _1045_out);
  and _911_2 (_911_2_out, _1046_out, sr_bit_45_q);
  and _910 (_910_out, sr_bit_45_q, _1047_out);
  and _910_2 (_910_2_out, _1049_out, sdelay6_31_q);
  and _910_3 (_910_3_out, _1048_out, sdelay6_17_q);
  and _923 (_923_out, sdelay6_4_q, _1045_out);
  and _923_2 (_923_2_out, _1046_out, sr_bit_46_q);
  and _922 (_922_out, sr_bit_46_q, _1047_out);
  and _922_2 (_922_2_out, _1049_out, sdelay6_32_q);
  and _922_3 (_922_3_out, _1048_out, sdelay6_18_q);
  and _935 (_935_out, sdelay6_5_q, _1045_out);
  and _935_2 (_935_2_out, _1046_out, sr_bit_47_q);
  and _934 (_934_out, sr_bit_47_q, _1047_out);
  and _934_2 (_934_2_out, _1049_out, sdelay6_33_q);
  and _934_3 (_934_3_out, _1048_out, sdelay6_19_q);
  and _947 (_947_out, sdelay6_6_q, _1045_out);
  and _947_2 (_947_2_out, _1046_out, sr_bit_48_q);
  and _946 (_946_out, sr_bit_48_q, _1047_out);
  and _946_2 (_946_2_out, _1049_out, sdelay6_34_q);
  and _946_3 (_946_3_out, _1048_out, sdelay6_20_q);
  and _959 (_959_out, sdelay6_7_q, _1045_out);
  and _959_2 (_959_2_out, _1046_out, sr_bit_49_q);
  and _958 (_958_out, sr_bit_49_q, _1047_out);
  and _958_2 (_958_2_out, _1049_out, sdelay6_35_q);
  and _958_3 (_958_3_out, _1048_out, sdelay6_21_q);
  and _971 (_971_out, sdelay6_8_q, _1045_out);
  and _971_2 (_971_2_out, _1046_out, sr_bit_50_q);
  and _970 (_970_out, sr_bit_50_q, _1047_out);
  and _970_2 (_970_2_out, _1049_out, sdelay6_36_q);
  and _970_3 (_970_3_out, _1048_out, sdelay6_22_q);
  and _983 (_983_out, sdelay6_9_q, _1045_out);
  and _983_2 (_983_2_out, _1046_out, sr_bit_51_q);
  and _982 (_982_out, sr_bit_51_q, _1047_out);
  and _982_2 (_982_2_out, _1049_out, sdelay6_37_q);
  and _982_3 (_982_3_out, _1048_out, sdelay6_23_q);
  and _995 (_995_out, sdelay6_10_q, _1045_out);
  and _995_2 (_995_2_out, _1046_out, sr_bit_52_q);
  and _994 (_994_out, sr_bit_52_q, _1047_out);
  and _994_2 (_994_2_out, _1049_out, sdelay6_38_q);
  and _994_3 (_994_3_out, _1048_out, sdelay6_24_q);
  and _1043 (_1043_out, sdelay6_11_q, _1045_out);
  and _1043_2 (_1043_2_out, _1046_out, sr_bit_53_q);
  and _1042 (_1042_out, sr_bit_53_q, _1047_out);
  and _1042_2 (_1042_2_out, _1049_out, sdelay6_39_q);
  and _1042_3 (_1042_3_out, _1048_out, sdelay6_25_q);
  and _1031 (_1031_out, sdelay6_12_q, _1045_out);
  and _1031_2 (_1031_2_out, _1046_out, sr_bit_54_q);
  and _1030 (_1030_out, sr_bit_54_q, _1047_out);
  and _1030_2 (_1030_2_out, _1049_out, sdelay6_40_q);
  and _1030_3 (_1030_3_out, _1048_out, sdelay6_26_q);
  and _1019 (_1019_out, sdelay6_13_q, _1045_out);
  and _1019_2 (_1019_2_out, _1046_out, sr_bit_55_q);
  and _1018 (_1018_out, sr_bit_55_q, _1047_out);
  and _1018_2 (_1018_2_out, _1049_out, sdelay6_41_q);
  and _1018_3 (_1018_3_out, _1048_out, sdelay6_27_q);
  and _1007 (_1007_out, sdelay6_14_q, _1045_out);
  and _1007_2 (_1007_2_out, _1046_out, sr_bit_56_q);
  and _1006 (_1006_out, sr_bit_56_q, _1047_out);
  and _1006_2 (_1006_2_out, _1049_out, sdelay6_42_q);
  and _1006_3 (_1006_3_out, _1048_out, sdelay6_28_q);
  or _887_3 (_887_3_out, _887_out, _887_2_out);
  or _886_4 (_886_4_out, _886_out, _886_2_out, _886_3_out);
  or _899_3 (_899_3_out, _899_out, _899_2_out);
  or _898_4 (_898_4_out, _898_out, _898_2_out, _898_3_out);
  or _911_3 (_911_3_out, _911_out, _911_2_out);
  or _910_4 (_910_4_out, _910_out, _910_2_out, _910_3_out);
  or _923_3 (_923_3_out, _923_out, _923_2_out);
  or _922_4 (_922_4_out, _922_out, _922_2_out, _922_3_out);
  or _935_3 (_935_3_out, _935_out, _935_2_out);
  or _934_4 (_934_4_out, _934_out, _934_2_out, _934_3_out);
  or _947_3 (_947_3_out, _947_out, _947_2_out);
  or _946_4 (_946_4_out, _946_out, _946_2_out, _946_3_out);
  or _959_3 (_959_3_out, _959_out, _959_2_out);
  or _958_4 (_958_4_out, _958_out, _958_2_out, _958_3_out);
  or _971_3 (_971_3_out, _971_out, _971_2_out);
  or _970_4 (_970_4_out, _970_out, _970_2_out, _970_3_out);
  or _983_3 (_983_3_out, _983_out, _983_2_out);
  or _982_4 (_982_4_out, _982_out, _982_2_out, _982_3_out);
  or _995_3 (_995_3_out, _995_out, _995_2_out);
  or _994_4 (_994_4_out, _994_out, _994_2_out, _994_3_out);
  or _1043_3 (_1043_3_out, _1043_out, _1043_2_out);
  or _1042_4 (_1042_4_out, _1042_out, _1042_2_out, _1042_3_out);
  or _1031_3 (_1031_3_out, _1031_out, _1031_2_out);
  or _1030_4 (_1030_4_out, _1030_out, _1030_2_out, _1030_3_out);
  or _1019_3 (_1019_3_out, _1019_out, _1019_2_out);
  or _1018_4 (_1018_4_out, _1018_out, _1018_2_out, _1018_3_out);
  or _1007_3 (_1007_3_out, _1007_out, _1007_2_out);
  or _1006_4 (_1006_4_out, _1006_out, _1006_2_out, _1006_3_out);
  Adder #(.width(1)) adder_33 (.a(_887_3_out), .b(_886_4_out), .out(adder_33_out), .cin(1'b0), .cout(adder_33_cout));
  Adder #(.width(1)) adder_34 (
    .a(_899_3_out), .b(_898_4_out), .out(adder_34_out), .cin(adder_33_cout), .cout(adder_34_cout));
  Adder #(.width(1)) adder_35 (
    .a(_911_3_out), .b(_910_4_out), .out(adder_35_out), .cin(adder_34_cout), .cout(adder_35_cout));
  Adder #(.width(1)) adder_36 (
    .a(_923_3_out), .b(_922_4_out), .out(adder_36_out), .cin(adder_35_cout), .cout(adder_36_cout));
  Adder #(.width(1)) adder_37 (
    .a(_935_3_out), .b(_934_4_out), .out(adder_37_out), .cin(adder_36_cout), .cout(adder_37_cout));
  Adder #(.width(1)) adder_38 (
    .a(_947_3_out), .b(_946_4_out), .out(adder_38_out), .cin(adder_37_cout), .cout(adder_38_cout));
  Adder #(.width(1)) adder_39 (
    .a(_959_3_out), .b(_958_4_out), .out(adder_39_out), .cin(adder_38_cout), .cout(adder_39_cout));
  Adder #(.width(1)) adder_40 (
    .a(_971_3_out), .b(_970_4_out), .out(adder_40_out), .cin(adder_39_cout), .cout(adder_40_cout));
  Adder #(.width(1)) adder_41 (
    .a(_983_3_out), .b(_982_4_out), .out(adder_41_out), .cin(adder_40_cout), .cout(adder_41_cout));
  Adder #(.width(1)) adder_42 (
    .a(_995_3_out), .b(_994_4_out), .out(adder_42_out), .cin(adder_41_cout), .cout(adder_42_cout));
  Adder #(.width(1)) adder_43 (
    .a(_1043_3_out), .b(_1042_4_out), .out(adder_43_out), .cin(adder_42_cout), .cout(adder_43_cout));
  Adder #(.width(1)) adder_44 (
    .a(_1031_3_out), .b(_1030_4_out), .out(adder_44_out), .cin(adder_43_cout), .cout(adder_44_cout));
  Adder #(.width(1)) adder_45 (
    .a(_1019_3_out), .b(_1018_4_out), .out(adder_45_out), .cin(adder_44_cout), .cout(adder_45_cout));
  Adder #(.width(1)) adder_46 (
    .a(_1007_3_out), .b(_1006_4_out), .out(adder_46_out), .cin(adder_45_cout), .cout(adder_46_cout));
  Adder #(.width(1)) adder_47 (
    .a(_1007_3_out), .b(_1006_4_out), .out(adder_47_out), .cin(adder_46_cout));  // open: cout
  SR_BIT sr_bit_57 (.C2(FCLK2), .C1(FCLK1), .D(adder_34_out), .Q(sr_bit_57_q[0]));  // open: nQ
  SR_BIT sr_bit_58 (.C2(FCLK2), .C1(FCLK1), .D(adder_35_out), .Q(sr_bit_57_q[1]));  // open: nQ
  SR_BIT sr_bit_59 (.C2(FCLK2), .C1(FCLK1), .D(adder_36_out), .Q(sr_bit_57_q[2]));  // open: nQ
  SR_BIT sr_bit_60 (.C2(FCLK2), .C1(FCLK1), .D(adder_37_out), .Q(sr_bit_57_q[3]));  // open: nQ
  SR_BIT sr_bit_61 (.C2(FCLK2), .C1(FCLK1), .D(adder_38_out), .Q(sr_bit_57_q[4]));  // open: nQ
  SR_BIT sr_bit_62 (.C2(FCLK2), .C1(FCLK1), .D(adder_39_out), .Q(sr_bit_57_q[5]));  // open: nQ
  SR_BIT sr_bit_63 (.C2(FCLK2), .C1(FCLK1), .D(adder_40_out), .Q(sr_bit_57_q[6]));  // open: nQ
  SR_BIT sr_bit_64 (.C2(FCLK2), .C1(FCLK1), .D(adder_41_out), .Q(sr_bit_57_q[7]));  // open: nQ
  SR_BIT sr_bit_65 (.C2(FCLK2), .C1(FCLK1), .D(adder_42_out), .Q(sr_bit_57_q[8]));  // open: nQ
  SR_BIT sr_bit_66 (.C2(FCLK2), .C1(FCLK1), .D(adder_43_out), .Q(sr_bit_57_q[9]));  // open: nQ
  SR_BIT sr_bit_67 (.C2(FCLK2), .C1(FCLK1), .D(adder_44_out), .Q(sr_bit_57_q[10]));  // open: nQ
  SR_BIT sr_bit_68 (.C2(FCLK2), .C1(FCLK1), .D(adder_45_out), .Q(sr_bit_57_q[11]));  // open: nQ
  SR_BIT sr_bit_69 (.C2(FCLK2), .C1(FCLK1), .D(adder_46_out), .Q(sr_bit_57_q[12]));  // open: nQ
  SR_BIT sr_bit_70 (.C2(FCLK2), .C1(FCLK1), .D(adder_47_out), .Q(sr_bit_70_q));  // open: nQ
  buf _1063 (OP13, sr_bit_43_q);
  buf _1064 (OP12, sr_bit_44_q);
  buf _1065 (OP11, sr_bit_45_q);
  buf _1066 (OP10, sr_bit_46_q);
  buf _1067 (OP9, sr_bit_47_q);
  buf _1068 (OP8, sr_bit_48_q);
  buf _1069 (OP7, sr_bit_49_q);
  buf _1070 (OP6, sr_bit_50_q);
  buf _1071 (OP5, sr_bit_51_q);
  buf _1072 (OP4, sr_bit_52_q);
  buf _1073 (OP3, sr_bit_53_q);
  buf _1074 (OP2, sr_bit_54_q);
  buf _1075 (OP1, sr_bit_55_q);
  buf _1078 (OP0, sr_bit_56_q);
  buf _1142 (sr_bit_57_q[13], sr_bit_70_q);

  // Notes on the sheet:
  //   1319
  //   1318
  //   1317
  //   1316
  //   1315
  //   1314
  //   1310
  //   1311
  //   1312
  //   1313
  //   1235
  //   1233
  //   1231
  //   1228
  //   1225
  //   1234
  //   1232
  //   1230
  //   1229
  //   1226
  //   1275
  //   1304
  //   1305
  //   1306
  //   1307
  //   1308
  //   1309
  //   1297
  //   1295
  //   1293
  //   1292
  //   D
  //   C1
  //   C2
  //   C2
  //   C1
  //   1290, 1291
  //   1143 - 1152
  //   SDELAY5  10 BIT
  //   C2
  //   C1
  //   1271
  //   1270
  //   1268
  //   1269
  //   1263
  //   1262
  //   1258
  //   1259
  //   1257
  //   1256
  //   A
  //   B
  //   HA
  //   1255
  //   A
  //   B
  //   HA
  //   1286 - 1289
  //   C1
  //   S
  //   CO
  //   S
  //   CO
  //   C2
  //   C1
  //   1242
  //   1241
  //   1240
  //   1239
  //   1238
  //   1218
  //   1217
  //   1216
  //   1215
  //   1214
  //   C2
  //   D
  //   C1
  //   C2
  //   1132 - 1141
  //   SR BIT  10 BIT
  //   D
  //   C1
  //   1237
  //   1236
  //   1243
  //   1244
  //   1245
  //   1227
  //   1224
  //   1204
  //   1203
  //   1201
  //   1199
  //   1197
  //   1196
  //   1246 - 1254, 1276 - 1285
  //   C2
  //   SR BITi  19 BIT
  //   1190 - 1195
  //   D
  //   C1
  //   C2
  //   1171 - 1183
  //   SR BITi  13 BIT
  //   874
  //   1198
  //   1200
  //   1202
  //   1205
  //   1189
  //   1
  //   0
  //   1188
  //   1187
  //   1170
  //   A
  //   B
  //   HA
  //   A
  //   B
  //   HA
  //   A
  //   B
  //   HA
  //   A
  //   B
  //   HA
  //   A
  //   B
  //   HA
  //   A
  //   B
  //   HA
  //   A
  //   B
  //   HA
  //   873
  //   1169
  //   S
  //   CO
  //   1168
  //   S
  //   CO
  //   1167
  //   S
  //   CO
  //   1166
  //   S
  //   CO
  //   1165
  //   S
  //   CO
  //   1164
  //   S
  //   CO
  //   1163
  //   S
  //   CO
  //   872
  //   B
  //   A
  //   B
  //   A
  //   B
  //   A
  //   B
  //   A
  //   B
  //   A
  //   B
  //   A
  //   B
  //   A
  //   B
  //   A
  //   B
  //   A
  //   B
  //   A
  //   B
  //   A
  //   B
  //   A
  //   B
  //   A
  //   B
  //   A
  //   878
  //   HA
  //   890
  //   HA
  //   902
  //   HA
  //   914
  //   HA
  //   926
  //   HA
  //   938
  //   HA
  //   950
  //   HA
  //   962
  //   HA
  //   974
  //   HA
  //   986
  //   HA
  //   1034
  //   HA
  //   1022
  //   HA
  //   1010
  //   HA
  //   998
  //   HA
  //   S
  //   CO
  //   S
  //   CO
  //   S
  //   CO
  //   S
  //   CO
  //   S
  //   CO
  //   S
  //   CO
  //   S
  //   CO
  //   S
  //   CO
  //   S
  //   CO
  //   S
  //   CO
  //   S
  //   CO
  //   S
  //   CO
  //   S
  //   CO
  //   S
  //   CO
  //   879
  //   891
  //   903
  //   915
  //   927
  //   939
  //   951
  //   963
  //   975
  //   987
  //   1035
  //   1023
  //   1011
  //   999
  //   881
  //   893
  //   905
  //   917
  //   929
  //   941
  //   953
  //   965
  //   977
  //   989
  //   1037
  //   1025
  //   1013
  //   1001
  //   883
  //   895
  //   907
  //   919
  //   931
  //   943
  //   955
  //   967
  //   979
  //   991
  //   1039
  //   1027
  //   1015
  //   1003
  //   885
  //   897
  //   909
  //   921
  //   933
  //   945
  //   957
  //   969
  //   981
  //   993
  //   1041
  //   1029
  //   1017
  //   1005
  //   888
  //   900
  //   912
  //   924
  //   936
  //   948
  //   960
  //   972
  //   984
  //   996
  //   1044
  //   1032
  //   1020
  //   1008
  //   1076
  //   not used
  //   1062
  //   1061
  //   1060
  //   1059
  //   1058
  //   1057
  //   1056
  //   1055
  //   1054
  //   1053
  //   1052
  //   1051
  //   1050
  //   1077
endmodule

module SDELAY6 (
  input  C2,
  input  C1,
  input  D,
  output Q
);

  wire d_ff_1_q, d_ff_2_q, d_ff_3_q, d_ff_4_q, d_ff_5_q, d_ff_6_q, d_ff_7_q, d_ff_8_q, d_ff_9_q, d_ff_10_q,
       d_ff_11_q;

  D_Flip_Flop #(.trigger("high")) d_ff_1 (.clk(C1), .D(D), .Q(d_ff_1_q));  // open: Qn, preset, en, reset
  D_Flip_Flop #(.trigger("high")) d_ff_2 (.clk(C1), .D(d_ff_10_q), .Q(d_ff_2_q));  // open: Qn, preset, en, reset
  D_Flip_Flop #(.trigger("high")) d_ff_3 (.clk(C1), .D(d_ff_11_q), .Q(d_ff_3_q));  // open: Qn, preset, en, reset
  D_Flip_Flop #(.trigger("high")) d_ff_4 (.clk(C2), .D(d_ff_1_q), .Q(d_ff_4_q));  // open: Qn, preset, en, reset
  D_Flip_Flop #(.trigger("high")) d_ff_5 (.clk(C2), .D(d_ff_2_q), .Q(d_ff_5_q));  // open: Qn, preset, en, reset
  D_Flip_Flop #(.trigger("high")) d_ff_6 (.clk(C2), .D(d_ff_3_q), .Q(d_ff_6_q));  // open: Qn, preset, en, reset
  D_Flip_Flop #(.trigger("high")) d_ff_7 (.clk(C1), .D(d_ff_4_q), .Q(d_ff_7_q));  // open: Qn, preset, en, reset
  D_Flip_Flop #(.trigger("high")) d_ff_8 (.clk(C1), .D(d_ff_5_q), .Q(d_ff_8_q));  // open: Qn, preset, en, reset
  D_Flip_Flop #(.trigger("high")) d_ff_9 (.clk(C1), .D(d_ff_6_q), .Q(d_ff_9_q));  // open: Qn, preset, en, reset
  D_Flip_Flop #(.trigger("high")) d_ff_10 (.clk(C2), .D(d_ff_7_q), .Q(d_ff_10_q));  // open: Qn, preset, en, reset
  D_Flip_Flop #(.trigger("high")) d_ff_11 (.clk(C2), .D(d_ff_8_q), .Q(d_ff_11_q));  // open: Qn, preset, en, reset
  D_Flip_Flop #(.trigger("high")) d_ff_12 (.clk(C2), .D(d_ff_9_q), .Q(Q));  // open: Qn, preset, en, reset
endmodule

// EXP TABLE
module EXP_TABLE (
  input  CA0,
  input  CA1,
  input  CA2,
  input  CA3,
  input  RA0,
  input  RA1,
  input  RA2,
  input  RA3,
  input  RA4,
  output D0,
  output D1,
  output D2,
  output D3,
  output D4,
  output D5,
  output D6,
  output D7,
  output D8,
  output D9,
  output D10,
  output D11,
  output D12
);

  ROM #(.addrWidth(5), .dataWidth(13)) rom_1 (
    .addr({RA4, RA3, RA2, RA1, RA0}), .data({D12, D11, D10, D9, D8, D7, D6, D5, D4, D3, D2, D1, D0}),
    .sel(1'b1));

  // Notes on the sheet:
  //   contents of rom_1 (hex, n*v repeats v):
  //   1111 564 1547 1675 1675 678 967 1789 1800 890 1867 1456 1453 456 1345 354 534 1656 767 787 1797 989
  //   1676 989 676 898 665 999 0 333 222 22
endmodule

// SINE TABLE
module SINE_TABLE (
  input  CA0,
  input  CA1,
  input  CA2,
  input  CA3,
  input  RA0,
  input  RA1,
  input  RA2,
  input  RA3,
  input  RA4,
  output D0,
  output D1,
  output D2,
  output D3,
  output D4,
  output D5,
  output D6,
  output D7,
  output D8,
  output D9,
  output D10,
  output D11,
  output D12,
  output D13,
  output D14,
  output D15,
  output D16,
  output D17,
  output D18
);

  ROM #(.addrWidth(5), .dataWidth(19)) rom_1 (
    .addr({RA4, RA3, RA2, RA1, RA0}),
    .data({D18, D17, D16, D15, D14, D13, D12, D11, D10, D9, D8, D7, D6, D5, D4, D3, D2, D1, D0}), .sel(1'b1));

  // Notes on the sheet:
  //   contents of rom_1 (hex, n*v repeats v):
  //   13321 63463 7757 76564 45453 76767 7787 4545 343 232 454 343 232 545 6565 24 6565 75433 767 222 5455
  //   665 7676 8787 9898 10909 0 9098 78787 6554 3333 56
endmodule

// OP FEEDBACK
module OP_FEEDBACK (
  input  [13:0] OP,
  input  g_127,
  input  g_3077,
  input  g_3076,
  input  g_3075,
  output [9:0] FB
);

  wire _1093_out, _1097_2_out, _1097_3_out, _1097_4_out, _1097_5_out, _1097_6_out, _1097_7_out, _1097_8_out,
       _1097_out, _1098_2_out, _1098_3_out, _1098_4_out, _1098_5_out, _1098_6_out, _1098_7_out, _1098_8_out,
       _1098_out, _1099_2_out, _1099_3_out, _1099_4_out, _1099_5_out, _1099_6_out, _1099_7_out, _1099_8_out,
       _1099_out, _1100_2_out, _1100_3_out, _1100_4_out, _1100_5_out, _1100_out, _1101_2_out, _1101_3_out,
       _1101_out, _1102_2_out, _1102_3_out, _1102_4_out, _1102_5_out, _1102_out, _1103_2_out, _1103_3_out,
       _1103_4_out, _1103_5_out, _1103_6_out, _1103_7_out, _1103_out, _1108_2_out, _1108_3_out, _1108_4_out,
       _1108_5_out, _1108_6_out, _1108_7_out, _1108_8_out, _1108_9_out, _1109_2_out, _1109_3_out,
       _1109_4_out, _1109_5_out, _1109_6_out, _1109_7_out, _1109_8_out, _1109_9_out, _1110_2_out,
       _1110_3_out, _1110_4_out, _1110_5_out, _1110_6_out, _1110_7_out, _1110_8_out, _1110_9_out,
       _1112_2_out, _1112_3_out, _1112_4_out, _1112_5_out, _1112_6_out, _1112_7_out, _1112_out, _1114_2_out,
       _1114_3_out, _1114_4_out, _1114_5_out, _1114_out, decoder_1_out1, decoder_1_out2, decoder_1_out3,
       decoder_1_out4, decoder_1_out5, decoder_1_out6, decoder_1_out7;

  nor _1112 (_1112_out, _1112_2_out, _1112_3_out, _1112_4_out, _1112_5_out, _1112_6_out, _1112_7_out);
  or _1108 (FB[1], _1108_2_out, _1108_3_out, _1108_4_out, _1108_5_out, _1108_6_out, _1108_7_out, _1108_8_out, _1108_9_out);
  or _1109 (FB[3], _1109_2_out, _1109_3_out, _1109_4_out, _1109_5_out, _1109_6_out, _1109_7_out, _1109_8_out, _1109_9_out);
  or _1110 (FB[5], _1110_2_out, _1110_3_out, _1110_4_out, _1110_5_out, _1110_6_out, _1110_7_out, _1110_8_out, _1110_9_out);
  nor _1114 (_1114_out, _1114_2_out, _1114_3_out, _1114_4_out, _1114_5_out);
  and _1108_2 (_1108_2_out, decoder_1_out7, OP[3]);
  and _1108_3 (_1108_3_out, decoder_1_out6, OP[4]);
  and _1108_4 (_1108_4_out, decoder_1_out5, OP[5]);
  and _1108_5 (_1108_5_out, decoder_1_out4, OP[6]);
  and _1108_6 (_1108_6_out, decoder_1_out3, OP[7]);
  and _1108_7 (_1108_7_out, decoder_1_out2, OP[8]);
  and _1108_8 (_1108_8_out, decoder_1_out1, OP[9]);
  and _1108_9 (_1108_9_out, g_127, OP[1]);
  and _1109_2 (_1109_2_out, decoder_1_out7, OP[5]);
  and _1109_3 (_1109_3_out, decoder_1_out6, OP[6]);
  and _1109_4 (_1109_4_out, decoder_1_out5, OP[7]);
  and _1109_5 (_1109_5_out, decoder_1_out4, OP[8]);
  and _1109_6 (_1109_6_out, decoder_1_out3, OP[9]);
  and _1109_7 (_1109_7_out, decoder_1_out2, OP[10]);
  and _1109_8 (_1109_8_out, decoder_1_out1, OP[11]);
  and _1109_9 (_1109_9_out, g_127, OP[3]);
  and _1110_2 (_1110_2_out, decoder_1_out7, OP[7]);
  and _1110_3 (_1110_3_out, decoder_1_out6, OP[8]);
  and _1110_4 (_1110_4_out, decoder_1_out5, OP[9]);
  and _1110_5 (_1110_5_out, decoder_1_out4, OP[10]);
  and _1110_6 (_1110_6_out, decoder_1_out3, OP[11]);
  and _1110_7 (_1110_7_out, decoder_1_out2, OP[12]);
  and _1110_8 (_1110_8_out, decoder_1_out1, OP[13]);
  and _1110_9 (_1110_9_out, g_127, OP[5]);
  and _1112_2 (_1112_2_out, OP[7], g_127);
  and _1112_3 (_1112_3_out, OP[13], decoder_1_out3);
  and _1112_4 (_1112_4_out, OP[12], decoder_1_out4);
  and _1112_5 (_1112_5_out, OP[11], decoder_1_out5);
  and _1112_6 (_1112_6_out, OP[10], decoder_1_out6);
  and _1112_7 (_1112_7_out, OP[9], decoder_1_out7);
  and _1114_2 (_1114_2_out, decoder_1_out7, OP[11]);
  and _1114_3 (_1114_3_out, decoder_1_out6, OP[12]);
  and _1114_4 (_1114_4_out, decoder_1_out5, OP[13]);
  and _1114_5 (_1114_5_out, g_127, OP[9]);
  not _1093 (_1093_out, g_127);
  Decoder #(.select(3), .disabled(0)) decoder_1 (
    .out1(decoder_1_out1), .out2(decoder_1_out2), .out3(decoder_1_out3), .out4(decoder_1_out4),
    .out5(decoder_1_out5), .out6(decoder_1_out6), .out7(decoder_1_out7), .sel({g_3075, g_3076, g_3077}),
    .en(_1093_out));  // open: out0
  Pull_Resistor pull_resistor_1 (.node(decoder_1_out1));
  Pull_Resistor pull_resistor_2 (.node(decoder_1_out2));
  Pull_Resistor pull_resistor_3 (.node(decoder_1_out3));
  Pull_Resistor pull_resistor_4 (.node(decoder_1_out4));
  Pull_Resistor pull_resistor_5 (.node(decoder_1_out5));
  Pull_Resistor pull_resistor_6 (.node(decoder_1_out6));
  Pull_Resistor pull_resistor_7 (.node(decoder_1_out7));
  and _1097 (_1097_out, decoder_1_out7, OP[2]);
  and _1097_2 (_1097_2_out, decoder_1_out6, OP[3]);
  and _1097_3 (_1097_3_out, decoder_1_out5, OP[4]);
  and _1097_4 (_1097_4_out, decoder_1_out4, OP[5]);
  and _1097_5 (_1097_5_out, decoder_1_out3, OP[6]);
  and _1097_6 (_1097_6_out, decoder_1_out2, OP[7]);
  and _1097_7 (_1097_7_out, decoder_1_out1, OP[8]);
  and _1097_8 (_1097_8_out, g_127, OP[0]);
  and _1098 (_1098_out, decoder_1_out7, OP[4]);
  and _1098_2 (_1098_2_out, decoder_1_out6, OP[5]);
  and _1098_3 (_1098_3_out, decoder_1_out5, OP[6]);
  and _1098_4 (_1098_4_out, decoder_1_out4, OP[7]);
  and _1098_5 (_1098_5_out, decoder_1_out3, OP[8]);
  and _1098_6 (_1098_6_out, decoder_1_out2, OP[9]);
  and _1098_7 (_1098_7_out, decoder_1_out1, OP[10]);
  and _1098_8 (_1098_8_out, g_127, OP[2]);
  and _1099 (_1099_out, decoder_1_out7, OP[6]);
  and _1099_2 (_1099_2_out, decoder_1_out6, OP[7]);
  and _1099_3 (_1099_3_out, decoder_1_out5, OP[8]);
  and _1099_4 (_1099_4_out, decoder_1_out4, OP[9]);
  and _1099_5 (_1099_5_out, decoder_1_out3, OP[10]);
  and _1099_6 (_1099_6_out, decoder_1_out2, OP[11]);
  and _1099_7 (_1099_7_out, decoder_1_out1, OP[12]);
  and _1099_8 (_1099_8_out, g_127, OP[4]);
  and _1103 (_1103_out, OP[6], g_127);
  and _1103_2 (_1103_2_out, OP[12], decoder_1_out3);
  and _1103_3 (_1103_3_out, OP[11], decoder_1_out4);
  and _1103_4 (_1103_4_out, OP[10], decoder_1_out5);
  and _1103_5 (_1103_5_out, OP[9], decoder_1_out6);
  and _1103_6 (_1103_6_out, OP[8], decoder_1_out7);
  and _1100 (_1100_out, decoder_1_out7, OP[10]);
  and _1100_2 (_1100_2_out, decoder_1_out6, OP[11]);
  and _1100_3 (_1100_3_out, decoder_1_out5, OP[12]);
  and _1100_4 (_1100_4_out, g_127, OP[8]);
  and _1101 (_1101_out, decoder_1_out2, OP[13]);
  and _1101_2 (_1101_2_out, decoder_1_out1, OP[13]);
  and _1102 (_1102_out, decoder_1_out4, OP[13]);
  and _1102_2 (_1102_2_out, decoder_1_out3, OP[13]);
  and _1102_3 (_1102_3_out, decoder_1_out2, OP[13]);
  and _1102_4 (_1102_4_out, decoder_1_out1, OP[13]);
  nor _1101_3 (_1101_3_out, _1101_out, _1101_2_out);
  or _1097_9 (FB[0], _1097_out, _1097_2_out, _1097_3_out, _1097_4_out, _1097_5_out, _1097_6_out, _1097_7_out, _1097_8_out);
  or _1098_9 (FB[2], _1098_out, _1098_2_out, _1098_3_out, _1098_4_out, _1098_5_out, _1098_6_out, _1098_7_out, _1098_8_out);
  or _1099_9 (FB[4], _1099_out, _1099_2_out, _1099_3_out, _1099_4_out, _1099_5_out, _1099_6_out, _1099_7_out, _1099_8_out);
  nor _1103_7 (_1103_7_out, _1103_out, _1103_2_out, _1103_3_out, _1103_4_out, _1103_5_out, _1103_6_out);
  nor _1100_5 (_1100_5_out, _1100_out, _1100_2_out, _1100_3_out, _1100_4_out);
  nor _1102_5 (_1102_5_out, _1102_out, _1102_2_out, _1102_3_out, _1102_4_out);
  nand _1104 (FB[6], _1103_7_out, _1101_3_out);
  nand _1111 (FB[7], _1101_3_out, _1112_out);
  nand _1100A (FB[9], _1100_5_out, _1102_5_out);
  nand _1113 (FB[8], _1114_out, _1102_5_out);

  // Notes on the sheet:
  //   1079 - 1092
  //   1094 - 1096
endmodule

module OUT (
  input  FCLK2,
  input  FCLK1,
  input  g_3088,
  input  g_3087,
  input  g_75,
  input  g_118,
  input  g_70,
  input  g_378,
  input  g_100,
  input  g_79,
  input  g_345,
  input  g_109,
  input  OP8,
  input  g_343,
  input  OP7,
  input  g_350,
  input  OP6,
  input  g_352,
  input  OP5,
  input  g_354,
  input  OP4,
  input  g_356,
  input  OP3,
  input  g_358,
  input  OP2,
  input  g_360,
  input  OP1,
  input  g_362,
  input  OP0,
  input  g_383,
  output MOL_SEL,
  output MOR_SEL,
  output DAC0,
  output g_171,
  output DAC1,
  output g_189,
  output DAC2,
  output g_207,
  output DAC3,
  output g_225,
  output DAC4,
  output g_243,
  output DAC5,
  output g_261,
  output DAC6,
  output g_279,
  output DAC7,
  output g_297,
  output DAC8,
  output g_300
);

  wire _101_out, _102_out, _103_2_out, _103_out, _104_2_out, _104_out, _105_out, _106_out, _107_out,
       _129_out, _130_out, _131_out, _132_out, _133_2_out, _133_out, _152_2_out, _152_out, _153_2_out,
       _153_out, _154_out, _156_2_out, _156_out, _157_q, _158_out, _159_out, _160_2_out, _160_3_out,
       _160_out, _167_q, _167_qn, _168_2_out, _168_3_out, _168_out, _169_2_out, _169_3_out, _169_out,
       _172_out, _174_2_out, _174_out, _175_q, _176_out, _177_out, _178_2_out, _178_3_out, _178_out, _185_q,
       _185_qn, _186_2_out, _186_3_out, _186_out, _187_2_out, _187_3_out, _187_out, _190_out, _192_2_out,
       _192_out, _193_q, _194_out, _195_out, _196_2_out, _196_3_out, _196_out, _203_q, _203_qn, _204_2_out,
       _204_3_out, _204_out, _205_2_out, _205_3_out, _205_out, _208_out, _210_2_out, _210_out, _211_q,
       _212_out, _213_out, _214_2_out, _214_3_out, _214_out, _221_q, _221_qn, _222_2_out, _222_3_out,
       _222_out, _223_2_out, _223_3_out, _223_out, _226_out, _228_2_out, _228_out, _229_q, _230_out,
       _231_out, _232_2_out, _232_3_out, _232_out, _239_q, _239_qn, _240_2_out, _240_3_out, _240_out,
       _241_2_out, _241_3_out, _241_out, _244_out, _246_2_out, _246_out, _247_q, _248_out, _249_out,
       _250_2_out, _250_3_out, _250_out, _257_q, _257_qn, _258_2_out, _258_3_out, _258_out, _259_2_out,
       _259_3_out, _259_out, _262_out, _264_2_out, _264_out, _265_q, _266_out, _267_out, _268_2_out,
       _268_3_out, _268_out, _275_q, _275_qn, _276_2_out, _276_3_out, _276_out, _277_2_out, _277_3_out,
       _277_out, _280_out, _282_2_out, _282_out, _283_q, _284_out, _285_out, _286_2_out, _286_3_out,
       _286_out, _293_q, _293_qn, _294_2_out, _294_3_out, _294_out, _295_2_out, _295_3_out, _295_out,
       _298_out, _299_2_out, _299_3_out, _299_out, _301_q, _301_qn, _302_2_out, _302_3_out, _302_out,
       _309_2_out, _309_3_out, _309_out, _310_out, _311_out, _312_q, _313_2_out, _313_out, _316_out,
       _319_out, _320_out, adder_1_cout, adder_1_out, adder_2_cout, adder_2_out, adder_3_cout, adder_3_out,
       adder_4_cout, adder_4_out, adder_5_cout, adder_5_out, adder_6_cout, adder_6_out, adder_7_cout,
       adder_7_out, adder_8_cout, adder_8_out, adder_9_out, not_1_out, not_2_out, not_3_out, sr_bit_1_q,
       sr_bit_2_q, sr_bit_3_q, sr_bit_4_q, sr_bit_5_q, sr_bit_6_q, sr_bit_7_q, sr_bit_8_q, sr_bit_9_q,
       sr_bit_10_q, sr_bit_11_q, sr_bit_12_q, sr_bit_13_q, sr_bit_14_q, sr_bit_15_q, sr_bit_16_q,
       sr_bit_17_q, sr_bit_18_q, sr_bit_19_q, sr_bit_20_q, sr_bit_21_q, sr_bit_22_q, sr_bit_23_q,
       sr_bit_24_q, sr_bit_25_q, sr_bit_26_q, sr_bit_27_q, sr_bit_28_q, sr_bit_29_q, sr_bit_30_q,
       sr_bit_31_q, sr_bit_32_q, sr_bit_33_q, sr_bit_34_q, sr_bit_35_q, sr_bit_36_q, sr_bit_37_q,
       sr_bit_38_q, sr_bit_39_q, sr_bit_40_q, sr_bit_41_q, sr_bit_42_q, sr_bit_43_q, sr_bit_44_q,
       sr_bit_45_q, sr_bit_46_q, sr_bit_47_q, sr_bit_48_q, sr_bit_49_q, sr_bit_50_q, sr_bit_51_q,
       sr_bit_52_q, sr_bit_53_q, sr_bit_54_q;

  not _298 (_298_out, g_383);
  nor _105 (_105_out, g_79, g_345);
  not _320 (_320_out, g_75);
  not _107 (_107_out, _106_out);
  or _106 (_106_out, _105_out, g_345);
  and _154 (_154_out, g_109, OP8);
  nor _158 (_158_out, _107_out, _157_q);
  and _172 (_172_out, g_109, OP7);
  nor _176 (_176_out, _107_out, _175_q);
  and _190 (_190_out, g_109, OP6);
  nor _194 (_194_out, _107_out, _193_q);
  and _208 (_208_out, g_109, OP5);
  nor _212 (_212_out, _107_out, _211_q);
  and _226 (_226_out, g_109, OP4);
  nor _230 (_230_out, _107_out, _229_q);
  and _244 (_244_out, g_109, OP3);
  nor _248 (_248_out, _107_out, _247_q);
  and _262 (_262_out, g_109, OP2);
  nor _266 (_266_out, _107_out, _265_q);
  and _280 (_280_out, g_109, OP1);
  nor _284 (_284_out, _107_out, _283_q);
  and _316 (_316_out, g_109, OP0);
  nor _311 (_311_out, _107_out, _312_q);
  nor _101 (_101_out, g_100, g_345);
  Adder #(.width(1)) adder_1 (.a(_154_out), .b(_158_out), .out(adder_1_out), .cin(g_345), .cout(adder_1_cout));
  Adder #(.width(1)) adder_2 (.a(_172_out), .b(_176_out), .out(adder_2_out), .cin(adder_1_cout), .cout(adder_2_cout));
  Adder #(.width(1)) adder_3 (.a(_190_out), .b(_194_out), .out(adder_3_out), .cin(adder_2_cout), .cout(adder_3_cout));
  Adder #(.width(1)) adder_4 (.a(_208_out), .b(_212_out), .out(adder_4_out), .cin(adder_3_cout), .cout(adder_4_cout));
  Adder #(.width(1)) adder_5 (.a(_226_out), .b(_230_out), .out(adder_5_out), .cin(adder_4_cout), .cout(adder_5_cout));
  Adder #(.width(1)) adder_6 (.a(_244_out), .b(_248_out), .out(adder_6_out), .cin(adder_5_cout), .cout(adder_6_cout));
  Adder #(.width(1)) adder_7 (.a(_262_out), .b(_266_out), .out(adder_7_out), .cin(adder_6_cout), .cout(adder_7_cout));
  Adder #(.width(1)) adder_8 (.a(_280_out), .b(_284_out), .out(adder_8_out), .cin(adder_7_cout), .cout(adder_8_cout));
  Adder #(.width(1)) adder_9 (.a(_316_out), .b(_311_out), .out(adder_9_out), .cin(adder_8_cout));  // open: cout
  not _131 (_131_out, adder_9_out);
  and _104 (_104_out, g_70, g_378);
  and _156 (_156_out, adder_1_out, not_1_out);
  and _174 (_174_out, adder_2_out, not_1_out);
  and _192 (_192_out, adder_3_out, not_1_out);
  and _210 (_210_out, adder_4_out, not_1_out);
  and _228 (_228_out, adder_5_out, not_1_out);
  and _246 (_246_out, adder_6_out, not_1_out);
  and _264 (_264_out, adder_7_out, not_1_out);
  and _282 (_282_out, adder_8_out, not_1_out);
  not not_1 (not_1_out, _132_out);
  and _313 (_313_out, adder_9_out, _133_out);
  and _132 (_132_out, _131_out, _311_out, _316_out);
  nor _129 (_129_out, _311_out, _316_out);
  or _319 (_319_out, _320_out, g_345);
  nor _102 (_102_out, g_118, g_345);
  nor _104_2 (_104_2_out, g_345, _104_out);
  nor _156_2 (_156_2_out, _156_out, _133_2_out);
  nor _174_2 (_174_2_out, _174_out, _133_2_out);
  nor _192_2 (_192_2_out, _192_out, _133_2_out);
  nor _210_2 (_210_2_out, _210_out, _133_2_out);
  nor _228_2 (_228_2_out, _228_out, _133_2_out);
  nor _246_2 (_246_2_out, _246_out, _133_2_out);
  nor _264_2 (_264_2_out, _264_out, _133_2_out);
  nor _282_2 (_282_2_out, _282_out, _133_2_out);
  nor _313_2 (_313_2_out, _313_out, _132_out);
  not _133 (_133_out, _133_2_out);
  and _318 (MOL_SEL, g_3088, _319_out);
  and _317 (MOR_SEL, g_3087, _319_out);
  not _133_2 (_133_2_out, _130_out);
  nand _130 (_130_out, adder_9_out, _129_out);
  SDELAY6 _157 (.C2(FCLK2), .C1(FCLK1), .D(_156_2_out), .Q(_157_q));
  SDELAY6 _175 (.C2(FCLK2), .C1(FCLK1), .D(_174_2_out), .Q(_175_q));
  SDELAY6 _193 (.C2(FCLK2), .C1(FCLK1), .D(_192_2_out), .Q(_193_q));
  SDELAY6 _211 (.C2(FCLK2), .C1(FCLK1), .D(_210_2_out), .Q(_211_q));
  SDELAY6 _229 (.C2(FCLK2), .C1(FCLK1), .D(_228_2_out), .Q(_229_q));
  SDELAY6 _247 (.C2(FCLK2), .C1(FCLK1), .D(_246_2_out), .Q(_247_q));
  SDELAY6 _265 (.C2(FCLK2), .C1(FCLK1), .D(_264_2_out), .Q(_265_q));
  SDELAY6 _283 (.C2(FCLK2), .C1(FCLK1), .D(_282_2_out), .Q(_283_q));
  SDELAY6 _312 (.C2(FCLK2), .C1(FCLK1), .D(_313_2_out), .Q(_312_q));
  not not_2 (not_2_out, _105_out);
  not not_3 (not_3_out, not_2_out);
  not _159 (_159_out, _157_q);
  not _177 (_177_out, _175_q);
  not _195 (_195_out, _193_q);
  not _213 (_213_out, _211_q);
  not _231 (_231_out, _229_q);
  not _249 (_249_out, _247_q);
  not _267 (_267_out, _265_q);
  not _285 (_285_out, _283_q);
  not _310 (_310_out, _312_q);
  and _160 (_160_out, sr_bit_46_q, not_3_out);
  and _160_2 (_160_2_out, not_2_out, _159_out);
  and _178 (_178_out, sr_bit_47_q, not_3_out);
  and _178_2 (_178_2_out, not_2_out, _177_out);
  and _196 (_196_out, sr_bit_48_q, not_3_out);
  and _196_2 (_196_2_out, not_2_out, _195_out);
  and _214 (_214_out, sr_bit_49_q, not_3_out);
  and _214_2 (_214_2_out, not_2_out, _213_out);
  and _232 (_232_out, sr_bit_50_q, not_3_out);
  and _232_2 (_232_2_out, not_2_out, _231_out);
  and _250 (_250_out, sr_bit_51_q, not_3_out);
  and _250_2 (_250_2_out, not_2_out, _249_out);
  and _268 (_268_out, sr_bit_52_q, not_3_out);
  and _268_2 (_268_2_out, not_2_out, _267_out);
  and _286 (_286_out, sr_bit_53_q, not_3_out);
  and _286_2 (_286_2_out, not_2_out, _285_out);
  and _309 (_309_out, sr_bit_54_q, not_3_out);
  and _309_2 (_309_2_out, not_2_out, _310_out);
  SR_BIT sr_bit_1 (.C2(FCLK2), .C1(FCLK1), .D(_160_3_out), .Q(sr_bit_1_q));  // open: nQ
  or _160_3 (_160_3_out, _160_out, _160_2_out);
  SR_BIT sr_bit_2 (.C2(FCLK2), .C1(FCLK1), .D(_178_3_out), .Q(sr_bit_2_q));  // open: nQ
  or _178_3 (_178_3_out, _178_out, _178_2_out);
  SR_BIT sr_bit_3 (.C2(FCLK2), .C1(FCLK1), .D(_196_3_out), .Q(sr_bit_3_q));  // open: nQ
  or _196_3 (_196_3_out, _196_out, _196_2_out);
  SR_BIT sr_bit_4 (.C2(FCLK2), .C1(FCLK1), .D(_214_3_out), .Q(sr_bit_4_q));  // open: nQ
  or _214_3 (_214_3_out, _214_out, _214_2_out);
  SR_BIT sr_bit_5 (.C2(FCLK2), .C1(FCLK1), .D(_232_3_out), .Q(sr_bit_5_q));  // open: nQ
  or _232_3 (_232_3_out, _232_out, _232_2_out);
  SR_BIT sr_bit_6 (.C2(FCLK2), .C1(FCLK1), .D(_250_3_out), .Q(sr_bit_6_q));  // open: nQ
  or _250_3 (_250_3_out, _250_out, _250_2_out);
  SR_BIT sr_bit_7 (.C2(FCLK2), .C1(FCLK1), .D(_268_3_out), .Q(sr_bit_7_q));  // open: nQ
  or _268_3 (_268_3_out, _268_out, _268_2_out);
  SR_BIT sr_bit_8 (.C2(FCLK2), .C1(FCLK1), .D(_286_3_out), .Q(sr_bit_8_q));  // open: nQ
  or _286_3 (_286_3_out, _286_out, _286_2_out);
  SR_BIT sr_bit_9 (.C2(FCLK2), .C1(FCLK1), .D(_309_3_out), .Q(sr_bit_9_q));  // open: nQ
  or _309_3 (_309_3_out, _309_out, _309_2_out);
  SR_BIT sr_bit_10 (.C2(FCLK2), .C1(FCLK1), .D(sr_bit_1_q), .Q(sr_bit_10_q));  // open: nQ
  SR_BIT sr_bit_11 (.C2(FCLK2), .C1(FCLK1), .D(sr_bit_2_q), .Q(sr_bit_11_q));  // open: nQ
  SR_BIT sr_bit_12 (.C2(FCLK2), .C1(FCLK1), .D(sr_bit_3_q), .Q(sr_bit_12_q));  // open: nQ
  SR_BIT sr_bit_13 (.C2(FCLK2), .C1(FCLK1), .D(sr_bit_4_q), .Q(sr_bit_13_q));  // open: nQ
  SR_BIT sr_bit_14 (.C2(FCLK2), .C1(FCLK1), .D(sr_bit_5_q), .Q(sr_bit_14_q));  // open: nQ
  SR_BIT sr_bit_15 (.C2(FCLK2), .C1(FCLK1), .D(sr_bit_6_q), .Q(sr_bit_15_q));  // open: nQ
  SR_BIT sr_bit_16 (.C2(FCLK2), .C1(FCLK1), .D(sr_bit_7_q), .Q(sr_bit_16_q));  // open: nQ
  SR_BIT sr_bit_17 (.C2(FCLK2), .C1(FCLK1), .D(sr_bit_8_q), .Q(sr_bit_17_q));  // open: nQ
  SR_BIT sr_bit_18 (.C2(FCLK2), .C1(FCLK1), .D(sr_bit_9_q), .Q(sr_bit_18_q));  // open: nQ
  SR_BIT sr_bit_19 (.C2(FCLK2), .C1(FCLK1), .D(sr_bit_10_q), .Q(sr_bit_19_q));  // open: nQ
  SR_BIT sr_bit_20 (.C2(FCLK2), .C1(FCLK1), .D(sr_bit_11_q), .Q(sr_bit_20_q));  // open: nQ
  SR_BIT sr_bit_21 (.C2(FCLK2), .C1(FCLK1), .D(sr_bit_12_q), .Q(sr_bit_21_q));  // open: nQ
  SR_BIT sr_bit_22 (.C2(FCLK2), .C1(FCLK1), .D(sr_bit_13_q), .Q(sr_bit_22_q));  // open: nQ
  SR_BIT sr_bit_23 (.C2(FCLK2), .C1(FCLK1), .D(sr_bit_14_q), .Q(sr_bit_23_q));  // open: nQ
  SR_BIT sr_bit_24 (.C2(FCLK2), .C1(FCLK1), .D(sr_bit_15_q), .Q(sr_bit_24_q));  // open: nQ
  SR_BIT sr_bit_25 (.C2(FCLK2), .C1(FCLK1), .D(sr_bit_16_q), .Q(sr_bit_25_q));  // open: nQ
  SR_BIT sr_bit_26 (.C2(FCLK2), .C1(FCLK1), .D(sr_bit_17_q), .Q(sr_bit_26_q));  // open: nQ
  SR_BIT sr_bit_27 (.C2(FCLK2), .C1(FCLK1), .D(sr_bit_18_q), .Q(sr_bit_27_q));  // open: nQ
  SR_BIT sr_bit_28 (.C2(FCLK2), .C1(FCLK1), .D(sr_bit_19_q), .Q(sr_bit_28_q));  // open: nQ
  SR_BIT sr_bit_29 (.C2(FCLK2), .C1(FCLK1), .D(sr_bit_20_q), .Q(sr_bit_29_q));  // open: nQ
  SR_BIT sr_bit_30 (.C2(FCLK2), .C1(FCLK1), .D(sr_bit_21_q), .Q(sr_bit_30_q));  // open: nQ
  SR_BIT sr_bit_31 (.C2(FCLK2), .C1(FCLK1), .D(sr_bit_22_q), .Q(sr_bit_31_q));  // open: nQ
  SR_BIT sr_bit_32 (.C2(FCLK2), .C1(FCLK1), .D(sr_bit_23_q), .Q(sr_bit_32_q));  // open: nQ
  SR_BIT sr_bit_33 (.C2(FCLK2), .C1(FCLK1), .D(sr_bit_24_q), .Q(sr_bit_33_q));  // open: nQ
  SR_BIT sr_bit_34 (.C2(FCLK2), .C1(FCLK1), .D(sr_bit_25_q), .Q(sr_bit_34_q));  // open: nQ
  SR_BIT sr_bit_35 (.C2(FCLK2), .C1(FCLK1), .D(sr_bit_26_q), .Q(sr_bit_35_q));  // open: nQ
  SR_BIT sr_bit_36 (.C2(FCLK2), .C1(FCLK1), .D(sr_bit_27_q), .Q(sr_bit_36_q));  // open: nQ
  SR_BIT sr_bit_37 (.C2(FCLK2), .C1(FCLK1), .D(sr_bit_28_q), .Q(sr_bit_37_q));  // open: nQ
  SR_BIT sr_bit_38 (.C2(FCLK2), .C1(FCLK1), .D(sr_bit_29_q), .Q(sr_bit_38_q));  // open: nQ
  SR_BIT sr_bit_39 (.C2(FCLK2), .C1(FCLK1), .D(sr_bit_30_q), .Q(sr_bit_39_q));  // open: nQ
  SR_BIT sr_bit_40 (.C2(FCLK2), .C1(FCLK1), .D(sr_bit_31_q), .Q(sr_bit_40_q));  // open: nQ
  SR_BIT sr_bit_41 (.C2(FCLK2), .C1(FCLK1), .D(sr_bit_32_q), .Q(sr_bit_41_q));  // open: nQ
  SR_BIT sr_bit_42 (.C2(FCLK2), .C1(FCLK1), .D(sr_bit_33_q), .Q(sr_bit_42_q));  // open: nQ
  SR_BIT sr_bit_43 (.C2(FCLK2), .C1(FCLK1), .D(sr_bit_34_q), .Q(sr_bit_43_q));  // open: nQ
  SR_BIT sr_bit_44 (.C2(FCLK2), .C1(FCLK1), .D(sr_bit_35_q), .Q(sr_bit_44_q));  // open: nQ
  SR_BIT sr_bit_45 (.C2(FCLK2), .C1(FCLK1), .D(sr_bit_36_q), .Q(sr_bit_45_q));  // open: nQ
  not _103 (_103_out, _104_2_out);
  not _152 (_152_out, _101_out);
  not _153 (_153_out, _102_out);
  SR_BIT sr_bit_46 (.C2(FCLK2), .C1(FCLK1), .D(sr_bit_37_q), .Q(sr_bit_46_q));  // open: nQ
  SR_BIT sr_bit_47 (.C2(FCLK2), .C1(FCLK1), .D(sr_bit_38_q), .Q(sr_bit_47_q));  // open: nQ
  SR_BIT sr_bit_48 (.C2(FCLK2), .C1(FCLK1), .D(sr_bit_39_q), .Q(sr_bit_48_q));  // open: nQ
  SR_BIT sr_bit_49 (.C2(FCLK2), .C1(FCLK1), .D(sr_bit_40_q), .Q(sr_bit_49_q));  // open: nQ
  SR_BIT sr_bit_50 (.C2(FCLK2), .C1(FCLK1), .D(sr_bit_41_q), .Q(sr_bit_50_q));  // open: nQ
  SR_BIT sr_bit_51 (.C2(FCLK2), .C1(FCLK1), .D(sr_bit_42_q), .Q(sr_bit_51_q));  // open: nQ
  SR_BIT sr_bit_52 (.C2(FCLK2), .C1(FCLK1), .D(sr_bit_43_q), .Q(sr_bit_52_q));  // open: nQ
  SR_BIT sr_bit_53 (.C2(FCLK2), .C1(FCLK1), .D(sr_bit_44_q), .Q(sr_bit_53_q));  // open: nQ
  SR_BIT sr_bit_54 (.C2(FCLK2), .C1(FCLK1), .D(sr_bit_45_q), .Q(sr_bit_54_q));  // open: nQ
  not _103_2 (_103_2_out, _103_out);
  not _152_2 (_152_2_out, _152_out);
  not _153_2 (_153_2_out, _153_out);
  and _168 (_168_out, sr_bit_37_q, _153_2_out);
  or _168_2 (_168_2_out, _168_out, _168_3_out);
  and _168_3 (_168_3_out, _153_out, sr_bit_46_q);
  and _186 (_186_out, sr_bit_38_q, _153_2_out);
  or _186_2 (_186_2_out, _186_out, _186_3_out);
  and _186_3 (_186_3_out, _153_out, sr_bit_47_q);
  and _204 (_204_out, sr_bit_39_q, _153_2_out);
  or _204_2 (_204_2_out, _204_out, _204_3_out);
  and _204_3 (_204_3_out, _153_out, sr_bit_48_q);
  and _222 (_222_out, sr_bit_40_q, _153_2_out);
  or _222_2 (_222_2_out, _222_out, _222_3_out);
  and _222_3 (_222_3_out, _153_out, sr_bit_49_q);
  and _240 (_240_out, sr_bit_41_q, _153_2_out);
  or _240_2 (_240_2_out, _240_out, _240_3_out);
  and _240_3 (_240_3_out, _153_out, sr_bit_50_q);
  and _258 (_258_out, sr_bit_42_q, _153_2_out);
  or _258_2 (_258_2_out, _258_out, _258_3_out);
  and _258_3 (_258_3_out, _153_out, sr_bit_51_q);
  and _276 (_276_out, sr_bit_43_q, _153_2_out);
  or _276_2 (_276_2_out, _276_out, _276_3_out);
  and _276_3 (_276_3_out, _153_out, sr_bit_52_q);
  and _294 (_294_out, sr_bit_44_q, _153_2_out);
  or _294_2 (_294_2_out, _294_out, _294_3_out);
  and _294_3 (_294_3_out, _153_out, sr_bit_53_q);
  and _302 (_302_out, sr_bit_45_q, _153_2_out);
  or _302_2 (_302_2_out, _302_out, _302_3_out);
  and _302_3 (_302_3_out, _153_out, sr_bit_54_q);
  D_Flip_Flop #(.trigger("high")) _167 (
    .clk(_152_out), .D(_168_2_out), .Q(_167_q), .Qn(_167_qn));  // open: preset, en, reset
  D_Flip_Flop #(.trigger("high")) _185 (
    .clk(_152_out), .D(_186_2_out), .Q(_185_q), .Qn(_185_qn));  // open: preset, en, reset
  D_Flip_Flop #(.trigger("high")) _203 (
    .clk(_152_out), .D(_204_2_out), .Q(_203_q), .Qn(_203_qn));  // open: preset, en, reset
  D_Flip_Flop #(.trigger("high")) _221 (
    .clk(_152_out), .D(_222_2_out), .Q(_221_q), .Qn(_221_qn));  // open: preset, en, reset
  D_Flip_Flop #(.trigger("high")) _239 (
    .clk(_152_out), .D(_240_2_out), .Q(_239_q), .Qn(_239_qn));  // open: preset, en, reset
  D_Flip_Flop #(.trigger("high")) _257 (
    .clk(_152_out), .D(_258_2_out), .Q(_257_q), .Qn(_257_qn));  // open: preset, en, reset
  D_Flip_Flop #(.trigger("high")) _275 (
    .clk(_152_out), .D(_276_2_out), .Q(_275_q), .Qn(_275_qn));  // open: preset, en, reset
  D_Flip_Flop #(.trigger("high")) _293 (
    .clk(_152_out), .D(_294_2_out), .Q(_293_q), .Qn(_293_qn));  // open: preset, en, reset
  D_Flip_Flop #(.trigger("high")) _301 (
    .clk(_152_out), .D(_302_2_out), .Q(_301_q), .Qn(_301_qn));  // open: preset, en, reset
  and _169 (_169_out, _167_q, _103_2_out);
  and _169_2 (_169_2_out, _103_out, g_343);
  and _187 (_187_out, _185_q, _103_2_out);
  and _187_2 (_187_2_out, _103_out, g_350);
  and _205 (_205_out, _203_q, _103_2_out);
  and _205_2 (_205_2_out, _103_out, g_352);
  and _223 (_223_out, _221_q, _103_2_out);
  and _223_2 (_223_2_out, _103_out, g_354);
  and _241 (_241_out, _239_q, _103_2_out);
  and _241_2 (_241_2_out, _103_out, g_356);
  and _259 (_259_out, _257_q, _103_2_out);
  and _259_2 (_259_2_out, _103_out, g_358);
  and _277 (_277_out, _275_q, _103_2_out);
  and _277_2 (_277_2_out, _103_out, g_360);
  and _295 (_295_out, _293_q, _103_2_out);
  and _295_2 (_295_2_out, _103_out, g_362);
  and _299 (_299_out, _301_q, _103_2_out);
  and _299_2 (_299_2_out, _103_out, _298_out);
  nor _169_3 (_169_3_out, _169_out, _169_2_out);
  nor _187_3 (_187_3_out, _187_out, _187_2_out);
  nor _205_3 (_205_3_out, _205_out, _205_2_out);
  nor _223_3 (_223_3_out, _223_out, _223_2_out);
  nor _241_3 (_241_3_out, _241_out, _241_2_out);
  nor _259_3 (_259_3_out, _259_out, _259_2_out);
  nor _277_3 (_277_3_out, _277_out, _277_2_out);
  nor _295_3 (_295_3_out, _295_out, _295_2_out);
  or _299_3 (_299_3_out, _299_out, _299_2_out);
  not _170 (DAC0, _169_3_out);
  not _171 (g_171, _167_qn);
  not _188 (DAC1, _187_3_out);
  not _189 (g_189, _185_qn);
  not _206 (DAC2, _205_3_out);
  not _207 (g_207, _203_qn);
  not _224 (DAC3, _223_3_out);
  not _225 (g_225, _221_qn);
  not _242 (DAC4, _241_3_out);
  not _243 (g_243, _239_qn);
  not _260 (DAC5, _259_3_out);
  not _261 (g_261, _257_qn);
  not _278 (DAC6, _277_3_out);
  not _279 (g_279, _275_qn);
  not _296 (DAC7, _295_3_out);
  not _297 (g_297, _293_qn);
  not _321 (DAC8, _299_3_out);
  not _300 (g_300, _301_qn);

  // Notes on the sheet:
  //   155
  //   173
  //   191
  //   209
  //   227
  //   245
  //   263
  //   281
  //   315
  //   A1
  //   A2
  //   A1
  //   A2
  //   A1
  //   A2
  //   A1
  //   A2
  //   A1
  //   A2
  //   A1
  //   A2
  //   A1
  //   A2
  //   A1
  //   A2
  //   A1
  //   A2
  //   314
  //   A1
  //   A2
  //   AOI21
  //   B
  //   AOI21
  //   B
  //   AOI21
  //   B
  //   AOI21
  //   B
  //   AOI21
  //   B
  //   AOI21
  //   B
  //   AOI21
  //   B
  //   AOI21
  //   B
  //   AOI21
  //   B
  //   AOI21
  //   B
  //   108
  //   108
  //   161
  //   179
  //   197
  //   215
  //   233
  //   251
  //   269
  //   287
  //   308
  //   162
  //   180
  //   198
  //   216
  //   234
  //   252
  //   270
  //   288
  //   307
  //   163
  //   181
  //   199
  //   217
  //   235
  //   253
  //   271
  //   289
  //   306
  //   164
  //   182
  //   200
  //   218
  //   236
  //   254
  //   272
  //   290
  //   305
  //   165
  //   183
  //   201
  //   219
  //   237
  //   255
  //   273
  //   291
  //   304
  //   166
  //   184
  //   202
  //   220
  //   238
  //   256
  //   274
  //   292
  //   303
  //   SLATCH
  //   SLATCH
  //   SLATCH
  //   SLATCH
  //   SLATCH
  //   SLATCH
  //   SLATCH
  //   SLATCH
  //   SLATCH
endmodule
module ENVELOPE (
  input  FCLK2,
  input  FCLK1,
  input  g_3065,
  input  g_3066,
  input  g_74,
  input  g_767,
  input  g_772,
  input  g_2463,
  input  g_2479,
  input  TEST_i,
  input  g_347,
  input  g_374,
  input  g_67,
  input  g_1932,
  input  g_2462,
  input  g_2460,
  input  g_1878,
  input  g_1877,
  input  g_2461,
  input  KEY_ON,
  input  LFO0,
  input  LFO1,
  input  LFO2,
  input  LFO3,
  input  LFO4,
  input  LFO5,
  input  g_2252,
  input  g_2253,
  input  g_2251,
  input  g_2250,
  input  g_1883,
  input  g_2249,
  input  g_2248,
  input  g_3652,
  input  g_3654,
  input  g_3656,
  input  g_3658,
  input  g_3660,
  input  g_2303,
  input  g_2301,
  input  g_2299,
  input  g_2297,
  input  g_2295,
  input  g_69,
  input  g_2270,
  input  g_2269,
  input  g_2268,
  input  g_2267,
  input  g_2266,
  input  g_2265,
  input  g_2264,
  output g_1698,
  output g_3100,
  output g_1795,
  output g_1796,
  output ENV0,
  output ENV1,
  output ENV2,
  output ENV3,
  output ENV4,
  output ENV5,
  output ENV6,
  output ENV7,
  output ENV8,
  output ENV9,
  output g_1613
);

  wire _1SEL0, _1SEL1, _1SEL2, _1SEL3, _1SEL4, _1SEL5, _1321_2_out, _1321_out, _1327, _1327_3_out, _1327_out,
       _1332_2_out, _1332_3_out, _1332_out, _1334_out, _1335_2_out, _1335_3_out, _1335_4_out, _1335_5_out,
       _1335_out, _1337_2_out, _1337_out, _1343, _1343_3_out, _1343_out, _1348_2_out, _1348_3_out, _1348_out,
       _1350_out, _1351_2_out, _1351_3_out, _1351_4_out, _1351_5_out, _1351_out, _1353_2_out, _1353_out,
       _1359, _1359_3_out, _1359_out, _1364_2_out, _1364_3_out, _1364_out, _1366_out, _1367_2_out,
       _1367_3_out, _1367_4_out, _1367_5_out, _1367_out, _1373, _1373_3_out, _1373_out, _1378_2_out,
       _1378_3_out, _1378_out, _1380_out, _1381_2_out, _1381_3_out, _1381_4_out, _1381_5_out, _1381_out,
       _1382_out, _1383_out, _1384_2_out, _1384_3_out, _1384_out, _1391, _1391_3_out, _1391_out, _1396_2_out,
       _1396_3_out, _1396_out, _1398_out, _1399_2_out, _1399_3_out, _1399_4_out, _1399_5_out, _1399_out,
       _1400_2_out, _1400_3_out, _1400_out, _1408, _1408_3_out, _1408_out, _1413_2_out, _1413_3_out,
       _1413_out, _1414_2_out, _1414_3_out, _1414_out, _1416_out, _1417_2_out, _1417_3_out, _1417_out, _1424,
       _1424_3_out, _1424_out, _1429_2_out, _1429_3_out, _1429_out, _1430_2_out, _1430_3_out, _1430_out,
       _1432_out, _1433_2_out, _1433_3_out, _1433_out, _1440, _1440_3_out, _1440_out, _1445_2_out,
       _1445_3_out, _1445_out, _1446_2_out, _1446_3_out, _1446_out, _1448_out, _1455, _1455_3_out, _1455_out,
       _1460_2_out, _1460_3_out, _1460_out, _1461_2_out, _1461_3_out, _1461_out, _1463_out, _1469Q42, _1470,
       _1470_3_out, _1470_out, _1473_2_out, _1473_3_out, _1473_out, _1474_2_out, _1474_3_out, _1474_out,
       _1476_out, _1478_q, _1479_q, _1485_out, _1486_q, _1490_q, _1491_out, _1493_q, _1494_out, _1498_out,
       _1499_q, _1500_out, _1502_q, _1504_out, _1505_2_out, _1505_out, _1506_out, _1507_out, _1508_out,
       _1509_out, _1510_out, _1511_out, _1512_q, _1513_out, _1514_out, _1515_q, _1517_2_out, _1517_3_out,
       _1517_out, _1518_2_out, _1518_3_out, _1518_4_out, _1518_out, _1519_2_out, _1519_3_out, _1519_out,
       _1520_2_out, _1520_3_out, _1520_4_out, _1520_out, _1521_2_out, _1521_3_out, _1521_4_out, _1521_out,
       _1522_2_out, _1522_3_out, _1522_4_out, _1522_out, _1523_2_out, _1523_3_out, _1523_4_out, _1523_out,
       _1524_2_out, _1524_3_out, _1524_4_out, _1524_out, _1525_2_out, _1525_3_out, _1525_out, _1526_2_out,
       _1526_3_out, _1526_4_out, _1526_out, _1527_2_out, _1527_3_out, _1527_out, _1528_2_out, _1528_3_out,
       _1528_4_out, _1528_out, _1529_2_out, _1529_3_out, _1529_out, _1530_out, _1531_2_out, _1531_3_out,
       _1531_4_out, _1531_5_out, _1531_out, _1532_out, _1533_out, _1534_out, _1535_out, _1536_out, _1537_out,
       _1538_out, _1539_out, _1540_out, _1541_out, _1542_out, _1543_out, _1544_out, _1545_out, _1546_out,
       _1547_2_out, _1547_3_out, _1547_4_out, _1547_5_out, _1547_out, _1548_out, _1549_out, _1550_out,
       _1551_out, _1552_2_out, _1552_3_out, _1552_out, _1553_2_out, _1553_3_out, _1553_out, _1554_out,
       _1555_out, _1556_out, _1557_out, _1558_out, _1580_nq, _1583_out, _1586_out, _1587_out, _1588_out,
       _1596_out, _1597_out, _1598_out, _1603_out, _1614_out, _1655_nq, _1656_nq, _1658_out, _1659_out,
       _1660_out, _1661_out, _1662_out, _1663_out, _1664_out, _1665_out, _1666_out, _1667_out, _1668_out,
       _1670_out, _1671_out, _1672_out, _1673_out, _1674_out, _1675_out, _1676_out, _1677_out, _1684_nq,
       _1685_q, _1687_q, _1688_co, _1689_out, _1690_2_out, _1690_out, _1691_out, _1692_out, _1693_out,
       _1694_out, _1695_nq, _1699_out, _1700_out, _1701_nq, _1702_out, _1703_out, _1704_out, _1705_out,
       _1706_2_out, _1706_out, _1707_out, _1708_out, _1709_out, _1710_2_out, _1710_3_out, _1710_out,
       _1711_out, _1712_2_out, _1712_3_out, _1712_out, _1713_out, _1714_out, _1715_out, _1716_out, _1717_nq,
       _1718_nq, _1719_nq, _1720_nq, _1721_nq, _1723_out, _1724_out, _1725_out, _1726_out, _1727_out,
       _1728_2_out, _1728_out, _1729_out, _1730_nq, _1731_nq, _1732_out, _1733_out, _1734_out, _1735_nq,
       _1736_out, _1737_out, _1738_out, _1739_nq, _1740_out, _1741_out, _1742_out, _1743_out, _1744_out,
       _1749_out, _1750_out, _1751_2_out, _1751_3_out, _1751_out, _1752_nq, _1753_nq, _1754_nq, _1755_q,
       _1756_nq, _1757_nq, _1758_2_out, _1758_3_out, _1758_4_out, _1758_out, _1759_nq, _1760_nq, _1761_2_out,
       _1761_3_out, _1761_4_out, _1761_5_out, _1761_out, _1762_nq, _1763_nq, _1764_2_out, _1764_3_out,
       _1764_4_out, _1764_5_out, _1764_out, _1765_out, _1767_2_out, _1767_out, _1768_2_out, _1768_out,
       _1772_nq, _1776_nq, _1779_nq, _1781_nq, _1786_nq, _1787_nq, _1788_nq, _1789_nq, _1790_q, _1790Q44,
       _1791_q, _1791Q44, _1792_q, _1792Q44, _1793_q, _1798_out, _1799_out, _1800_q, _1801_q, _1802_q,
       _1803_q, _1804_q, _1805_q, _1806_out, _1807_out, _1808_out, _1809_out, _1810_out, _1811_out,
       _1812_out, _1813_q, _1814_out, _1815_out, _1817_2_out, _1817_3_out, _1817_out, _1819_out, _1820_2_out,
       _1820_out, _1821_out, _1822_out, _1823_out, _1826_out, _1828_out, _1829_out, _1831_2_out, _1831_3_out,
       _1831_out, _1832_out, _1833_out, _1834_out, _1835_out, _1836_out, _1837_out, _1838_out, _1839_out,
       _1840_out, _1841_out, _1842_out, _1843_out, _1844_out, _1845_out, _1846_out, _1847_out, _1848_out,
       _1849_out, _1850_out, _1851_out, _1852_out, _1853_out, _1854_q, _1855_q, _1856_q, _1857_q, _1858_q,
       _1859_q, _1860_q, _1861_out, _1862_out, _1863_q, _1864_q, _1865_q, _1866_q, _1867_q, _1868_q,
       _1869_out, _1870_out, _1871_out, _1872_2_out, _1872_out, _1873_out, _1876_out, adder_1_cout,
       adder_1_out, adder_2_cout, adder_2_out, adder_3_cout, adder_3_out, adder_4_cout, adder_4_out,
       adder_5_cout, adder_5_out, adder_6_cout, adder_6_out, adder_7_cout, adder_7_out, adder_8_cout,
       adder_8_out, adder_9_cout, adder_9_out, adder_10_out, adder_11_cout, adder_11_out, adder_12_cout,
       adder_12_out, adder_13_cout, adder_13_out, adder_14_cout, adder_14_out, adder_15_cout, adder_15_out,
       adder_16_cout, adder_16_out, adder_17_cout, adder_17_out, adder_18_cout, adder_18_out, adder_19_cout,
       adder_19_out, adder_20_out, adder_21_out, adder_22_cout, adder_22_out, adder_23_cout, adder_23_out,
       adder_24_cout, adder_24_out, adder_25_cout, adder_25_out, adder_26_cout, adder_26_out, adder_27_cout,
       adder_27_out, adder_28_cout, adder_28_out, adder_29_cout, adder_29_out, adder_30_cout, adder_30_out,
       adder_31_cout, adder_31_out, adder_32_cout, adder_32_out, adder_33_cout, adder_33_out, adder_34_cout,
       adder_34_out, adder_35_cout, adder_35_out, adder_36_cout, adder_36_out, adder_37_cout, adder_37_out,
       adder_38_cout, adder_38_out, and_1_out, and_2_out, and_3_out, and_4_out, and_5_out, and_6_out,
       and_7_out, and_8_out, and_9_out, and_10_out, and_11_out, and_12_out, and_13_out, and_14_out,
       and_15_out, and_16_out, and_17_out, and_18_out, and_19_out, and_20_out, d_latch_1_nq, d_latch_2_nq,
       d_latch_3_nq, d_latch_4_nq, d_latch_5_nq, d_latch_6_nq, d_latch_7_nq, d_latch_8_nq, d_latch_9_nq,
       d_latch_10_nq, d_latch_11_nq, d_latch_12_nq, d_latch_13_nq, d_latch_14_nq, d_latch_15_nq,
       d_latch_16_nq, d_latch_17_nq, d_latch_18_nq, d_latch_19_nq, d_latch_20_nq, d_latch_21_nq,
       d_latch_22_nq, d_latch_23_nq, d_latch_24_nq, d_latch_25_nq, d_latch_26_nq, d_latch_27_nq,
       d_latch_28_nq, d_latch_29_nq, d_latch_30_nq, d_latch_31_nq, d_latch_32_nq, d_latch_33_nq,
       d_latch_34_nq, d_latch_35_nq, d_latch_36_nq, d_latch_37_nq, d_latch_38_nq, d_latch_39_nq,
       d_latch_40_nq, d_latch_41_nq, d_latch_42_nq, d_latch_43_nq, d_latch_44_nq, d_latch_45_nq,
       d_latch_46_nq, d_latch_47_nq, d_latch_48_nq, d_latch_49_nq, d_latch_50_nq, d_latch_51_nq,
       d_latch_52_nq, d_latch_53_nq, d_latch_54_nq, d_latch_55_nq, d_latch_56_nq, d_latch_57_nq,
       d_latch_58_nq, d_latch_59_nq, d_latch_60_nq, d_latch_61_nq, d_latch_62_nq, d_latch_63_nq,
       d_latch_64_nq, d_latch_65_nq, d_latch_66_nq, d_latch_67_nq, d_latch_68_nq, d_latch_69_nq,
       d_latch_70_nq, d_latch_71_nq, d_latch_72_nq, d_latch_73_nq, d_latch_74_nq, d_latch_75_nq, g_1501,
       g_1501Q22, g_1827, nor_1_out, not_1_out, not_2_out, not_3_out, not_4_out, not_5_out, not_6_out,
       not_7_out, not_8_out, not_9_out, not_10_out, not_11_out, not_12_out, not_13_out, not_14_out,
       not_15_out, not_16_out, not_17_out, not_18_out, not_19_out, or_1_out, or_2_out, or_3_out, or_4_out,
       or_5_out, or_6_out, or_7_out, or_8_out, or_9_out, or_10_out, QV0, QV1, QV2, QV3, QV4, QV5, QV6, QV7,
       QV8, QV9, QV10, QV11, SCLK, sdelay23_1_q, sdelay23_1_q42, sdelay23_2_q, sdelay23_2_q42, sdelay23_3_q,
       sdelay23_3_q42, sdelay23_4_q, sdelay23_4_q42, sdelay23_5_q, sdelay23_5_q42, sdelay23_6_q,
       sdelay23_6_q42, sdelay23_7_q, sdelay23_7_q42, sdelay23_8_q, sdelay23_8_q42, sdelay23_9_q,
       sdelay23_9_q42, sdelay23_10_q, sr_bit_1_q, sr_bit_2_q, sr_bit_3_q, sr_bit_4_q, sr_bit_5_q, sr_bit_6_q,
       sr_bit_7_q, sr_bit_8_q, sr_bit_9_q, sr_bit_16_q, sr_bit_17_q, sr_bit_18_q, sr_bit_19_q, sr_bit_20_q,
       sr_bit_21_q, sr_bit_22_q, sr_bit_23_q, sr_bit_24_q, sr_bit_25_q, sr_bit_26_q, sr_bit_27_q,
       sr_bit_28_q, sr_bit_29_q, sr_bit_30_q, sr_bit_31_q, sr_bit_32_q, sr_bit_33_q, sr_bit_34_q,
       sr_bit_35_q, sr_bit_43_q, sr_bit_44_nq, sr_bit_45_q, sr_bit_46_nq, sr_bit_47_q, sr_bit_48_nq,
       sr_bit_49_q, sr_bit_50_nq, sr_bit_51_q, sr_bit_52_nq, sr_bit_53_q, sr_bit_54_nq, sr_bit_55_q,
       sr_bit_56_q, sr_bit_57_q, sr_bit_58_q, sr_bit_59_q, sr_bit_60_q, sr_bit_61_q, sr_bit_62_q,
       sr_bit_63_q, xor_1_out, xor_2_out, xor_3_out, xor_4_out, xor_5_out, xor_6_out, xor_7_out, xor_8_out,
       xor_9_out, xor_10_out;
  wire [5:0] register_1_q;

  and _1691 (_1691_out, TEST_i, g_347);
  buf _1798 (_1798_out, g_69);
  and _1826 (_1826_out, g_2463, g_1878, _1469Q42);
  and _1827 (g_1827, _1469Q42, g_2479, g_1878);
  not _1876 (_1876_out, g_1932);
  nand _1799 (_1799_out, g_1878, g_2461, KEY_ON);
  or _1765 (_1765_out, g_2295, g_2297, g_2299, g_2301, g_2303);
  nor _1510 (_1510_out, g_374, _1876_out);
  not _1768 (_1768_out, _1768_2_out);
  not _1767 (_1767_out, _1767_2_out);
  and _1690 (_1690_out, g_67, _1687_q);
  and _1807 (_1807_out, _1469Q42, g_2462);
  and _1806 (_1806_out, _1469Q42, g_2460);
  nor _1537 (_1537_out, _1327, _1343, _1359, _1373, _1391);
  nor _1549 (_1549_out, _1408, _1424, _1440, _1455, _1470);
  not _1768_2 (_1768_2_out, g_2248);
  not _1767_2 (_1767_2_out, g_2249);
  and _1764 (_1764_out, _1768_out, _1767_out, g_3658);
  and _1764_2 (_1764_2_out, _1767_out, _1768_2_out, g_3660);
  and _1764_3 (_1764_3_out, _1767_2_out, _1768_out, g_3656);
  and _1764_4 (_1764_4_out, _1767_2_out, _1768_2_out, g_3652);
  and _1761 (_1761_out, _1768_out, _1767_out, g_3660);
  and _1761_2 (_1761_2_out, _1767_out, _1768_2_out, g_3656);
  and _1761_3 (_1761_3_out, _1767_2_out, _1768_out, g_3652);
  and _1761_4 (_1761_4_out, _1767_2_out, _1768_2_out, g_3654);
  and _1758 (_1758_out, _1767_out, _1768_out, g_3656);
  and _1758_2 (_1758_2_out, _1767_out, _1768_2_out, g_3652);
  and _1758_3 (_1758_3_out, _1767_2_out, _1768_out, g_3654);
  and _1751 (_1751_out, _1767_out, _1768_out, g_3652);
  and _1751_2 (_1751_2_out, _1767_out, _1768_2_out, g_3654);
  and _1750 (_1750_out, _1767_out, _1768_out, g_3654);
  SR_BIT sr_bit_1 (.C2(FCLK2), .C1(FCLK1), .D(g_74), .Q(sr_bit_1_q));  // open: nQ
  SR_BIT sr_bit_2 (.C2(FCLK2), .C1(FCLK1), .D(g_772), .Q(sr_bit_2_q));  // open: nQ
  SR_BIT sr_bit_3 (.C2(FCLK2), .C1(FCLK1), .D(_1826_out), .Q(sr_bit_3_q));  // open: nQ
  SDELAY12 _1515 (.C2(FCLK2), .C1(FCLK1), .D(g_67), .Q(_1515_q));  // open: Q22
  D_LATCH d_latch_1 (.EN(FCLK1), .D(_1689_out), .nQ(d_latch_1_nq));  // open: Q
  not not_1 (not_1_out, _1689_out);
  nor _1690_2 (_1690_2_out, _1876_out, _1690_out);
  and _1837 (_1837_out, _1851_out, _1850_out);
  and _1532 (_1532_out, _1537_out, _1549_out);
  nand _1741 (_1741_out, _1SEL1, _1SEL2, _1SEL3, _1SEL4, _1SEL5);
  or _1764_5 (_1764_5_out, _1764_out, _1764_2_out, _1764_3_out, _1764_4_out);
  or _1761_5 (_1761_5_out, _1761_out, _1761_2_out, _1761_3_out, _1761_4_out);
  or _1758_4 (_1758_4_out, _1758_out, _1758_2_out, _1758_3_out);
  or _1751_3 (_1751_3_out, _1751_out, _1751_2_out);
  nor nor_1 (nor_1_out, d_latch_1_nq, not_1_out);
  not _1692 (_1692_out, _1690_2_out);
  SR_BIT _1801 (.C2(FCLK2), .C1(FCLK1), .D(g_1878), .Q(_1801_q));  // open: nQ
  SR_BIT _1805 (.C2(FCLK2), .C1(FCLK1), .D(_1799_out), .Q(_1805_q));  // open: nQ
  SR_BIT _1803 (.C2(FCLK2), .C1(FCLK1), .D(KEY_ON), .Q(_1803_q));  // open: nQ
  SR_BIT _1868 (.C2(FCLK2), .C1(FCLK1), .D(g_1827), .Q(_1868_q));  // open: nQ
  SR_BIT _1863 (.C2(FCLK2), .C1(FCLK1), .D(_1741_out), .Q(_1863_q));  // open: nQ
  SR_BIT _1864 (.C2(FCLK2), .C1(FCLK1), .D(g_2252), .Q(_1864_q));  // open: nQ
  SR_BIT _1866 (.C2(FCLK2), .C1(FCLK1), .D(g_2253), .Q(_1866_q));  // open: nQ
  SR_BIT _1860 (.C2(FCLK2), .C1(FCLK1), .D(g_2251), .Q(_1860_q));  // open: nQ
  SR_BIT _1858 (.C2(FCLK2), .C1(FCLK1), .D(g_2250), .Q(_1858_q));  // open: nQ
  SR_BIT _1856 (.C2(FCLK2), .C1(FCLK1), .D(g_1883), .Q(_1856_q));  // open: nQ
  D_LATCH _1776 (.EN(FCLK1), .D(_1764_5_out), .nQ(_1776_nq));  // open: Q
  D_LATCH _1763 (.EN(FCLK1), .D(g_2303), .nQ(_1763_nq));  // open: Q
  D_LATCH _1762 (.EN(FCLK1), .D(_1761_5_out), .nQ(_1762_nq));  // open: Q
  D_LATCH _1760 (.EN(FCLK1), .D(g_2301), .nQ(_1760_nq));  // open: Q
  D_LATCH _1759 (.EN(FCLK1), .D(_1758_4_out), .nQ(_1759_nq));  // open: Q
  D_LATCH _1757 (.EN(FCLK1), .D(g_2299), .nQ(_1757_nq));  // open: Q
  D_LATCH _1756 (.EN(FCLK1), .D(_1751_3_out), .nQ(_1756_nq));  // open: Q
  D_LATCH _1753 (.EN(FCLK1), .D(g_2297), .nQ(_1753_nq));  // open: Q
  D_LATCH _1752 (.EN(FCLK1), .D(_1750_out), .nQ(_1752_nq));  // open: Q
  D_LATCH _1754 (.EN(FCLK1), .D(g_2295), .nQ(_1754_nq));  // open: Q
  SR_BIT _1755 (.C2(FCLK2), .C1(FCLK1), .D(_1765_out), .Q(_1755_q));  // open: nQ
  and _1670 (_1670_out, sr_bit_1_q, g_767);
  not _1500 (_1500_out, nor_1_out);
  SR_BIT sr_bit_4 (.C2(FCLK2), .C1(FCLK1), .D(g_67), .Q(sr_bit_4_q));  // open: nQ
  SR_BIT sr_bit_5 (.C2(FCLK2), .C1(FCLK1), .D(_1687_q), .Q(sr_bit_5_q));  // open: nQ
  CNT_BIT _1688 (.C2(FCLK2), .C1(FCLK1), .CIN(g_67), .RES(_1692_out), .CO(_1688_co));  // open: Q, nQ
  CNT_BIT _1687 (.C2(FCLK2), .C1(FCLK1), .CIN(_1688_co), .RES(_1692_out), .Q(_1687_q));  // open: nQ, CO
  xor _1808 (_1808_out, _1793_q, _1807_out);
  not _1862 (_1862_out, g_1932);
  not _1814 (_1814_out, _1802_q);
  not _1838 (_1838_out, _1837_out);
  not _1823 (_1823_out, _1551_out);
  not _1861 (_1861_out, _1532_out);
  not _1822 (_1822_out, _1817_out);
  SR_BIT sr_bit_6 (.C2(FCLK2), .C1(FCLK1), .D(sr_bit_2_q), .Q(sr_bit_6_q));  // open: nQ
  SR_BIT sr_bit_7 (.C2(FCLK2), .C1(FCLK1), .D(sr_bit_3_q), .Q(sr_bit_7_q));  // open: nQ
  not _1500_2 (SCLK, _1500_out);
  or _1809 (_1809_out, _1808_out, _1806_out);
  SR_BIT _1800 (.C2(FCLK2), .C1(FCLK1), .D(_1801_q), .Q(_1800_q));  // open: nQ
  SR_BIT _1804 (.C2(FCLK2), .C1(FCLK1), .D(_1805_q), .Q(_1804_q));  // open: nQ
  SR_BIT _1802 (.C2(FCLK2), .C1(FCLK1), .D(_1803_q), .Q(_1802_q));  // open: nQ
  SR_BIT _1867 (.C2(FCLK2), .C1(FCLK1), .D(_1868_q), .Q(_1867_q));  // open: nQ
  not _1850 (_1850_out, _1790_q);
  not _1851 (_1851_out, _1791_q);
  Adder #(.width(1)) adder_1 (.a(1'b1), .b(_1776_nq), .out(adder_1_out), .cin(1'b1), .cout(adder_1_cout));
  Adder #(.width(1)) adder_2 (.a(_1763_nq), .b(_1762_nq), .out(adder_2_out), .cin(adder_1_cout), .cout(adder_2_cout));
  Adder #(.width(1)) adder_3 (.a(_1760_nq), .b(_1759_nq), .out(adder_3_out), .cin(adder_2_cout), .cout(adder_3_cout));
  Adder #(.width(1)) adder_4 (.a(_1757_nq), .b(_1756_nq), .out(adder_4_out), .cin(adder_3_cout), .cout(adder_4_cout));
  Adder #(.width(1)) adder_5 (.a(_1753_nq), .b(_1752_nq), .out(adder_5_out), .cin(adder_4_cout), .cout(adder_5_cout));
  Adder #(.width(1)) adder_6 (.a(_1754_nq), .b(1'b1), .out(adder_6_out), .cin(adder_5_cout), .cout(adder_6_cout));
  nor _1514 (_1514_out, _1515_q, _1876_out, g_67);
  and _1689 (_1689_out, sr_bit_4_q, sr_bit_5_q);
  and _1810 (_1810_out, _1809_out, g_1878, _1792Q44);
  SR_BIT _1854 (.C2(FCLK2), .C1(FCLK1), .D(_1864_q), .Q(_1854_q));  // open: nQ
  SR_BIT _1865 (.C2(FCLK2), .C1(FCLK1), .D(_1866_q), .Q(_1865_q));  // open: nQ
  SR_BIT _1859 (.C2(FCLK2), .C1(FCLK1), .D(_1860_q), .Q(_1859_q));  // open: nQ
  SR_BIT _1857 (.C2(FCLK2), .C1(FCLK1), .D(_1858_q), .Q(_1857_q));  // open: nQ
  SR_BIT _1855 (.C2(FCLK2), .C1(FCLK1), .D(_1856_q), .Q(_1855_q));  // open: nQ
  D_LATCH _1772 (.EN(FCLK2), .D(adder_1_out), .nQ(_1772_nq));  // open: Q
  D_LATCH _1779 (.EN(FCLK2), .D(adder_2_out), .nQ(_1779_nq));  // open: Q
  D_LATCH _1781 (.EN(FCLK2), .D(adder_3_out), .nQ(_1781_nq));  // open: Q
  D_LATCH _1789 (.EN(FCLK2), .D(adder_4_out), .nQ(_1789_nq));  // open: Q
  D_LATCH _1788 (.EN(FCLK2), .D(adder_5_out), .nQ(_1788_nq));  // open: Q
  D_LATCH _1787 (.EN(FCLK2), .D(adder_6_out), .nQ(_1787_nq));  // open: Q
  D_LATCH _1786 (.EN(FCLK2), .D(adder_6_cout), .nQ(_1786_nq));  // open: Q
  SDELAY24 _1793 (.C2(FCLK2), .C1(FCLK1), .D(_1810_out), .Q(_1793_q));  // open: Q40, Q44
  and _1845 (_1845_out, _1873_out, _1814_out);
  and _1846 (_1846_out, _1790_q, _1791_q, _1873_out);
  and _1847 (_1847_out, _1850_out, _1791_q, _1873_out);
  and _1848 (_1848_out, _1851_out, _1873_out, _1551_out, _1790_q);
  and _1836 (_1836_out, _1817_out, _1873_out, _1804_q, _1838_out);
  and _1832 (_1832_out, _1823_out, _1790_q, _1851_out, _1873_out);
  and _1852 (_1852_out, _1873_out, _1850_out, _1532_out, _1851_out);
  nand _1840 (_1840_out, _1861_out, _1863_q, _1850_out, _1802_q, _1851_out);
  and _1843 (_1843_out, _1791_q, _1822_out, _1873_out);
  and _1844 (_1844_out, _1822_out, _1823_out, _1790_q, _1851_out, _1873_out);
  or _1773 (_1SEL0, _1772_nq, _1786_nq);
  or _1780 (_1SEL1, _1779_nq, _1786_nq);
  or _1782 (_1SEL2, _1781_nq, _1786_nq);
  or _1783 (_1SEL3, _1789_nq, _1786_nq);
  or _1784 (_1SEL4, _1788_nq, _1786_nq);
  or _1785 (_1SEL5, _1787_nq, _1786_nq);
  nor _1834 (_1834_out, _1862_out, _1836_out);
  not _1839 (_1839_out, _1840_out);
  nor _1842 (_1842_out, _1843_out, _1844_out);
  not _1841 (_1841_out, _1842_out);
  D_Flip_Flop #(.trigger("high")) _1478 (.clk(SCLK), .D(g_1501), .Q(_1478_q));  // open: Qn, preset, en, reset
  D_Flip_Flop #(.trigger("high")) _1479 (.clk(SCLK), .D(g_1501Q22), .Q(_1479_q));  // open: Qn, preset, en, reset
  not _1869 (_1869_out, _1792_q);
  not _1828 (_1828_out, _1834_out);
  or _1833 (_1833_out, _1846_out, _1845_out, _1828_out, _1847_out, _1848_out, _1862_out);
  or _1853 (_1853_out, _1845_out, _1828_out, _1846_out, _1832_out, _1862_out, _1852_out);
  xor _1545 (_1545_out, _1854_q, _1408);
  xor _1542 (_1542_out, _1865_q, _1424);
  xor _1548 (_1548_out, _1859_q, _1440);
  xor _1555 (_1555_out, _1857_q, _1455);
  xor _1556 (_1556_out, _1855_q, _1470);
  not _1736 (_1736_out, _1SEL3);
  xor _1811 (_1811_out, _1793_q, g_1877);
  SDELAY24 _1792 (.C2(FCLK2), .C1(FCLK1), .D(_1802_q), .Q(_1792_q), .Q44(_1792Q44));  // open: Q40
  and _1871 (_1871_out, _1802_q, _1869_out);
  SDELAY24 _1791 (.C2(FCLK2), .C1(FCLK1), .D(_1833_out), .Q(_1791_q), .Q44(_1791Q44));  // open: Q40
  SDELAY24 _1790 (.C2(FCLK2), .C1(FCLK1), .D(_1853_out), .Q(_1790_q), .Q44(_1790Q44));  // open: Q40
  not _1738 (_1738_out, _1SEL2);
  not _1708 (_1708_out, _1478_q);
  not _1694 (_1694_out, _1479_q);
  not _1716 (_1716_out, _1SEL1);
  and _1812 (_1812_out, _1811_out, _1792Q44);
  and _1872 (_1872_out, _1792_q, _1867_q);
  nor _1551 (_1551_out, _1391, _1545_out, _1542_out, _1548_out, _1555_out, _1556_out);
  SR_BIT _1813 (.C2(FCLK2), .C1(FCLK1), .D(_1812_out), .Q(_1813_q));  // open: nQ
  nor _1872_2 (_1872_2_out, _1871_out, _1872_out);
  or _1498 (_1498_out, QV5, QV3, QV1, QV7, QV9, QV11);
  or _1494 (_1494_out, QV5, QV2, QV1, QV6, QV9, QV10);
  or _1491 (_1491_out, QV0, QV5, QV6, QV7, QV8);
  or _1485 (_1485_out, QV0, QV1, QV2, QV3, QV4);
  nand _1733 (_1733_out, _1SEL5, _1SEL4, _1738_out, _1736_out);
  nand _1740 (_1740_out, _1736_out, _1SEL5, _1SEL4, _1SEL2);
  nand _1737 (_1737_out, _1736_out, _1SEL5, _1SEL4, _1738_out);
  nand _1734 (_1734_out, _1SEL4, _1SEL2, _1SEL5, _1736_out);
  and _1700 (_1700_out, _1SEL0, _1478_q, _1694_out, _1SEL1);
  and _1702 (_1702_out, _1SEL0, _1708_out, _1694_out, _1716_out);
  buf _1873 (_1873_out, _1872_2_out);
  D_Flip_Flop #(.trigger("high")) _1499 (.clk(SCLK), .D(_1498_out), .Q(_1499_q));  // open: Qn, preset, en, reset
  D_Flip_Flop #(.trigger("high")) _1493 (.clk(SCLK), .D(_1494_out), .Q(_1493_q));  // open: Qn, preset, en, reset
  D_Flip_Flop #(.trigger("high")) _1490 (.clk(SCLK), .D(_1491_out), .Q(_1490_q));  // open: Qn, preset, en, reset
  D_Flip_Flop #(.trigger("high")) _1486 (.clk(SCLK), .D(_1485_out), .Q(_1486_q));  // open: Qn, preset, en, reset
  D_LATCH _1695 (.EN(FCLK1), .D(_1687_q), .nQ(_1695_nq));  // open: Q
  D_LATCH _1721 (.EN(FCLK1), .D(_1724_out), .nQ(_1721_nq));  // open: Q
  D_LATCH _1731 (.EN(FCLK1), .D(_1733_out), .nQ(_1731_nq));  // open: Q
  D_LATCH _1739 (.EN(FCLK1), .D(_1740_out), .nQ(_1739_nq));  // open: Q
  D_LATCH _1735 (.EN(FCLK1), .D(_1737_out), .nQ(_1735_nq));  // open: Q
  D_LATCH _1730 (.EN(FCLK1), .D(_1734_out), .nQ(_1730_nq));  // open: Q
  D_LATCH _1719 (.EN(FCLK1), .D(_1723_out), .nQ(_1719_nq));  // open: Q
  nor _1723 (_1723_out, _1700_out, _1702_out);
  not _1829 (_1829_out, _1802_q);
  Adder #(.width(1)) adder_7 (.a(_1SEL2), .b(_1499_q), .out(adder_7_out), .cin(1'b0), .cout(adder_7_cout));
  Adder #(.width(1)) adder_8 (.a(_1SEL3), .b(_1493_q), .out(adder_8_out), .cin(adder_7_cout), .cout(adder_8_cout));
  Adder #(.width(1)) adder_9 (.a(_1SEL4), .b(_1490_q), .out(adder_9_out), .cin(adder_8_cout), .cout(adder_9_cout));
  Adder #(.width(1)) adder_10 (.a(_1SEL5), .b(_1486_q), .out(adder_10_out), .cin(adder_9_cout));  // open: cout
  or _1508 (_1508_out, _1691_out, _1509_out);
  and _1509 (_1509_out, _1510_out, xor_1_out);
  and _1505 (_1505_out, sr_bit_4_q, _1687_q);
  and _1835 (_1835_out, _1829_out, _1792_q);
  not _1821 (_1821_out, _1863_q);
  or _1817 (_1817_out, _1817_2_out, _1817_3_out);
  not _1742 (_1742_out, adder_7_out);
  not _1744 (_1744_out, adder_8_out);
  SDELAY12 _1501 (.C2(FCLK2), .C1(FCLK1), .D(_1509_out), .Q(g_1501), .Q22(g_1501Q22));
  nor _1505_2 (_1505_2_out, _1505_out, _1502_q);
  not _1729 (_1729_out, _1719_nq);
  and _1820 (_1820_out, _1821_out, _1873_out);
  and _1817_2 (_1817_2_out, not_2_out, _1550_out);
  and _1817_3 (_1817_3_out, _1470, not_3_out);
  or _1732 (_1732_out, _1SEL0, _1SEL1, _1SEL2, _1SEL3, _1SEL4, _1SEL5);
  nand _1749 (_1749_out, _1SEL4, _1SEL5);
  not _1504 (_1504_out, _1505_2_out);
  and _1728 (_1728_out, _1729_out, _1731_nq);
  and _1706 (_1706_out, _1735_nq, _1719_nq);
  and _1712 (_1712_out, _1719_nq, _1731_nq);
  and _1712_2 (_1712_2_out, _1729_out, _1730_nq);
  and _1710 (_1710_out, _1719_nq, _1730_nq);
  and _1710_2 (_1710_2_out, _1729_out, _1735_nq);
  nor _1820_2 (_1820_2_out, _1863_q, _1820_out);
  and _1550 (_1550_out, _1424, _1408, _1391, _1470, _1440, _1455);
  xor xor_1 (xor_1_out, g_1501, _1504_out);
  and and_1 (and_1_out, g_1501, _1504_out);
  nor _1728_2 (_1728_2_out, _1721_nq, _1728_out);
  nor _1706_2 (_1706_2_out, _1739_nq, _1706_out);
  or _1712_3 (_1712_3_out, _1712_out, _1712_2_out);
  or _1710_3 (_1710_3_out, _1710_out, _1710_2_out);
  not _1819 (_1819_out, _1820_2_out);
  not _1693 (_1693_out, _1695_nq);
  not _1727 (_1727_out, _1728_2_out);
  not _1705 (_1705_out, _1706_2_out);
  and _1726 (_1726_out, _1755_q, _1749_out, adder_10_out, adder_9_out, _1744_out, _1742_out, _1732_out);
  and _1743 (_1743_out, _1755_q, _1749_out, adder_10_out, adder_9_out, _1744_out, adder_7_out, _1SEL1);
  and _1725 (_1725_out, _1755_q, _1749_out, adder_10_out, adder_9_out, adder_8_out, _1742_out, _1SEL0);
  SR_BIT _1502 (.C2(FCLK2), .C1(FCLK1), .D(and_1_out), .Q(_1502_q));  // open: nQ
  and _1711 (_1711_out, _1693_out, _1727_out);
  and _1703 (_1703_out, _1693_out, _1705_out);
  and _1713 (_1713_out, _1693_out, _1712_3_out);
  and _1709 (_1709_out, _1693_out, _1710_3_out);
  nor _1724 (_1724_out, _1726_out, _1743_out, _1725_out);
  D_LATCH _1720 (.EN(FCLK2), .D(_1711_out), .nQ(_1720_nq));  // open: Q
  D_LATCH _1701 (.EN(FCLK2), .D(_1703_out), .nQ(_1701_nq));  // open: Q
  D_LATCH _1718 (.EN(FCLK2), .D(_1713_out), .nQ(_1718_nq));  // open: Q
  D_LATCH _1717 (.EN(FCLK2), .D(_1709_out), .nQ(_1717_nq));  // open: Q
  not not_2 (not_2_out, _1800_q);
  not _1715 (_1715_out, _1720_nq);
  not _1704 (_1704_out, _1701_nq);
  not _1714 (_1714_out, _1718_nq);
  not _1707 (_1707_out, _1717_nq);
  not not_3 (not_3_out, not_2_out);
  or _1511 (_1511_out, _1508_out, _1512_q);
  not _1506 (_1506_out, _1512_q);
  and _1513 (_1513_out, _1514_out, _1511_out);
  and _1507 (_1507_out, _1506_out, _1508_out);
  SR_BIT _1512 (.C2(FCLK2), .C1(FCLK1), .D(_1513_out), .Q(_1512_q));  // open: nQ
  and _1517 (_1517_out, _1841_out, _1715_out, not_2_out);
  and _1517_2 (_1517_2_out, _1382_out, _1839_out, _1704_out);
  and _1518 (_1518_out, _1715_out, _1839_out, _1539_out);
  and _1518_2 (_1518_2_out, _1714_out, _1839_out, _1536_out);
  and _1518_3 (_1518_3_out, _1707_out, _1839_out, _1383_out);
  not _1382 (_1382_out, _1343);
  and _1519 (_1519_out, _1841_out, _1714_out, not_2_out);
  and _1519_2 (_1519_2_out, _1383_out, _1839_out, _1704_out);
  and _1520 (_1520_out, _1715_out, _1839_out, _1541_out);
  and _1520_2 (_1520_2_out, _1714_out, _1839_out, _1539_out);
  and _1520_3 (_1520_3_out, _1707_out, _1839_out, _1536_out);
  not _1383 (_1383_out, _1359);
  and _1521 (_1521_out, _1704_out, _1839_out, _1536_out);
  and _1521_2 (_1521_2_out, not_2_out, _1707_out, _1841_out);
  and _1521_3 (_1521_3_out, not_3_out, _1715_out, _1841_out);
  and _1522 (_1522_out, _1715_out, _1839_out, _1543_out);
  and _1522_2 (_1522_2_out, _1714_out, _1839_out, _1541_out);
  and _1522_3 (_1522_3_out, _1707_out, _1839_out, _1539_out);
  not _1536 (_1536_out, _1373);
  and _1523 (_1523_out, _1704_out, _1839_out, _1539_out);
  and _1523_2 (_1523_2_out, not_2_out, _1704_out, _1841_out);
  and _1523_3 (_1523_3_out, not_3_out, _1714_out, _1841_out);
  and _1524 (_1524_out, _1715_out, _1839_out, _1546_out);
  and _1524_2 (_1524_2_out, _1714_out, _1839_out, _1543_out);
  and _1524_3 (_1524_3_out, _1707_out, _1839_out, _1541_out);
  not _1539 (_1539_out, _1391);
  and _1525 (_1525_out, _1841_out, _1707_out, not_3_out);
  and _1525_2 (_1525_2_out, _1541_out, _1839_out, _1704_out);
  and _1526 (_1526_out, _1715_out, _1839_out, _1557_out);
  and _1526_2 (_1526_2_out, _1714_out, _1839_out, _1546_out);
  and _1526_3 (_1526_3_out, _1707_out, _1839_out, _1543_out);
  not _1541 (_1541_out, _1408);
  and _1527 (_1527_out, _1841_out, _1704_out, not_3_out);
  and _1527_2 (_1527_2_out, _1543_out, _1839_out, _1704_out);
  and _1528 (_1528_out, _1715_out, _1839_out, _1558_out);
  and _1528_2 (_1528_2_out, _1714_out, _1839_out, _1557_out);
  and _1528_3 (_1528_3_out, _1707_out, _1839_out, _1546_out);
  not _1543 (_1543_out, _1424);
  and _1547 (_1547_out, 1'b1, _1715_out, _1839_out);
  and _1547_2 (_1547_2_out, _1714_out, _1839_out, _1558_out);
  and _1547_3 (_1547_3_out, _1707_out, _1839_out, _1557_out);
  and _1547_4 (_1547_4_out, _1704_out, _1839_out, _1546_out);
  not _1546 (_1546_out, _1440);
  and _1553 (_1553_out, _1557_out, _1839_out, _1704_out);
  and _1553_2 (_1553_2_out, _1558_out, _1839_out, _1707_out);
  and _1552 (_1552_out, _1715_out, _1839_out);
  and _1552_2 (_1552_2_out, _1714_out, _1839_out);
  not _1557 (_1557_out, _1455);
  and _1529 (_1529_out, _1558_out, _1839_out, _1704_out);
  and _1529_2 (_1529_2_out, _1839_out, _1707_out, 1'b1);
  not _1558 (_1558_out, _1470);
  and _1531 (_1531_out, _1715_out, _1839_out);
  and _1531_2 (_1531_2_out, _1839_out, _1714_out);
  and _1531_3 (_1531_3_out, _1839_out, _1707_out);
  and _1531_4 (_1531_4_out, _1704_out, _1839_out);
  or _1699 (_1699_out, _1715_out, _1704_out, _1714_out, _1707_out);
  nor _1517_3 (_1517_3_out, _1517_out, _1517_2_out);
  nor _1518_4 (_1518_4_out, _1518_out, _1518_2_out, _1518_3_out);
  nor _1519_3 (_1519_3_out, _1519_out, _1519_2_out);
  nor _1520_4 (_1520_4_out, _1520_out, _1520_2_out, _1520_3_out);
  nor _1521_4 (_1521_4_out, _1521_out, _1521_2_out, _1521_3_out);
  nor _1522_4 (_1522_4_out, _1522_out, _1522_2_out, _1522_3_out);
  nor _1523_4 (_1523_4_out, _1523_out, _1523_2_out, _1523_3_out);
  nor _1524_4 (_1524_4_out, _1524_out, _1524_2_out, _1524_3_out);
  nor _1525_3 (_1525_3_out, _1525_out, _1525_2_out);
  nor _1526_4 (_1526_4_out, _1526_out, _1526_2_out, _1526_3_out);
  nor _1527_3 (_1527_3_out, _1527_out, _1527_2_out);
  nor _1528_4 (_1528_4_out, _1528_out, _1528_2_out, _1528_3_out);
  nor _1553_3 (_1553_3_out, _1553_out, _1553_2_out);
  nor _1552_3 (_1552_3_out, _1552_out, _1552_2_out);
  nor _1529_3 (_1529_3_out, _1529_out, _1529_2_out);
  nand _1533 (_1533_out, _1517_3_out, _1518_4_out);
  nand _1534 (_1534_out, _1519_3_out, _1520_4_out);
  nand _1535 (_1535_out, _1521_4_out, _1522_4_out);
  nand _1538 (_1538_out, _1523_4_out, _1524_4_out);
  nand _1540 (_1540_out, _1525_3_out, _1526_4_out);
  nand _1544 (_1544_out, _1527_3_out, _1528_4_out);
  or _1547_5 (_1547_5_out, _1547_out, _1547_2_out, _1547_3_out, _1547_4_out);
  nand _1554 (_1554_out, _1553_3_out, _1552_3_out);
  nand _1530 (_1530_out, _1552_3_out, _1529_3_out);
  or _1531_5 (_1531_5_out, _1531_out, _1531_2_out, _1531_3_out, _1531_4_out);
  nor _1870 (_1870_out, sr_bit_7_q, _1871_out);
  and _1321 (_1321_out, _1819_out, _1327);
  and _1337 (_1337_out, _1819_out, _1343);
  and _1353 (_1353_out, _1819_out, _1359);
  and _1384 (_1384_out, sr_bit_6_q, sr_bit_44_nq);
  and _1384_2 (_1384_2_out, _1819_out, _1373);
  and _1400 (_1400_out, sr_bit_6_q, sr_bit_46_nq);
  and _1400_2 (_1400_2_out, _1819_out, _1391);
  and _1414 (_1414_out, sr_bit_6_q, sr_bit_48_nq);
  and _1414_2 (_1414_2_out, _1819_out, _1408);
  and _1430 (_1430_out, sr_bit_6_q, sr_bit_50_nq);
  and _1430_2 (_1430_2_out, _1819_out, _1424);
  and _1446 (_1446_out, sr_bit_6_q, sr_bit_52_nq);
  and _1446_2 (_1446_2_out, _1819_out, _1440);
  and _1461 (_1461_out, sr_bit_6_q, sr_bit_54_nq);
  and _1461_2 (_1461_2_out, _1819_out, _1455);
  and _1474 (_1474_out, sr_bit_6_q, _1684_nq);
  and _1474_2 (_1474_2_out, _1819_out, _1470);
  nor _1321_2 (_1321_2_out, _1828_out, _1321_out);
  nor _1337_2 (_1337_2_out, _1828_out, _1337_out);
  nor _1353_2 (_1353_2_out, _1828_out, _1353_out);
  nor _1384_3 (_1384_3_out, _1828_out, _1384_out, _1384_2_out);
  nor _1400_3 (_1400_3_out, _1828_out, _1400_out, _1400_2_out);
  nor _1414_3 (_1414_3_out, _1828_out, _1414_out, _1414_2_out);
  nor _1430_3 (_1430_3_out, _1828_out, _1430_out, _1430_2_out);
  nor _1446_3 (_1446_3_out, _1828_out, _1446_out, _1446_2_out);
  nor _1461_3 (_1461_3_out, _1828_out, _1461_out, _1461_2_out);
  nor _1474_3 (_1474_3_out, _1828_out, _1474_out, _1474_2_out);
  SR_BIT sr_bit_8 (.C2(FCLK2), .C1(FCLK1), .D(_1699_out), .Q(sr_bit_8_q));  // open: nQ
  SR_BIT sr_bit_9 (.C2(FCLK2), .C1(FCLK1), .D(_1870_out), .Q(sr_bit_9_q));  // open: nQ
  SR_BIT sr_bit_10 (.C2(FCLK2), .C1(FCLK1), .D(_1507_out), .Q(QV0));  // open: nQ
  not not_4 (not_4_out, _1321_2_out);
  not not_5 (not_5_out, _1337_2_out);
  not not_6 (not_6_out, _1353_2_out);
  not not_7 (not_7_out, _1384_3_out);
  not not_8 (not_8_out, _1400_3_out);
  not not_9 (not_9_out, _1414_3_out);
  not not_10 (not_10_out, _1430_3_out);
  not not_11 (not_11_out, _1446_3_out);
  not not_12 (not_12_out, _1461_3_out);
  not not_13 (not_13_out, _1474_3_out);
  D_LATCH d_latch_2 (.EN(FCLK1), .D(not_4_out), .nQ(d_latch_2_nq));  // open: Q
  D_LATCH d_latch_3 (.EN(FCLK1), .D(_1533_out), .nQ(d_latch_3_nq));  // open: Q
  D_LATCH d_latch_4 (.EN(FCLK1), .D(not_5_out), .nQ(d_latch_4_nq));  // open: Q
  D_LATCH d_latch_5 (.EN(FCLK1), .D(_1534_out), .nQ(d_latch_5_nq));  // open: Q
  D_LATCH d_latch_6 (.EN(FCLK1), .D(not_6_out), .nQ(d_latch_6_nq));  // open: Q
  D_LATCH d_latch_7 (.EN(FCLK1), .D(_1535_out), .nQ(d_latch_7_nq));  // open: Q
  D_LATCH d_latch_8 (.EN(FCLK1), .D(not_7_out), .nQ(d_latch_8_nq));  // open: Q
  D_LATCH d_latch_9 (.EN(FCLK1), .D(_1538_out), .nQ(d_latch_9_nq));  // open: Q
  D_LATCH d_latch_10 (.EN(FCLK1), .D(not_8_out), .nQ(d_latch_10_nq));  // open: Q
  D_LATCH d_latch_11 (.EN(FCLK1), .D(_1540_out), .nQ(d_latch_11_nq));  // open: Q
  D_LATCH d_latch_12 (.EN(FCLK1), .D(not_9_out), .nQ(d_latch_12_nq));  // open: Q
  D_LATCH d_latch_13 (.EN(FCLK1), .D(_1544_out), .nQ(d_latch_13_nq));  // open: Q
  D_LATCH d_latch_14 (.EN(FCLK1), .D(not_10_out), .nQ(d_latch_14_nq));  // open: Q
  D_LATCH d_latch_15 (.EN(FCLK1), .D(_1547_5_out), .nQ(d_latch_15_nq));  // open: Q
  D_LATCH d_latch_16 (.EN(FCLK1), .D(not_11_out), .nQ(d_latch_16_nq));  // open: Q
  D_LATCH d_latch_17 (.EN(FCLK1), .D(_1554_out), .nQ(d_latch_17_nq));  // open: Q
  D_LATCH d_latch_18 (.EN(FCLK1), .D(not_12_out), .nQ(d_latch_18_nq));  // open: Q
  D_LATCH d_latch_19 (.EN(FCLK1), .D(_1530_out), .nQ(d_latch_19_nq));  // open: Q
  D_LATCH d_latch_20 (.EN(FCLK1), .D(not_13_out), .nQ(d_latch_20_nq));  // open: Q
  D_LATCH d_latch_21 (.EN(FCLK1), .D(_1531_5_out), .nQ(d_latch_21_nq));  // open: Q
  buf _1698 (g_1698, sr_bit_8_q);
  Adder #(.width(1)) adder_11 (
    .a(d_latch_2_nq), .b(d_latch_3_nq), .out(adder_11_out), .cin(1'b1), .cout(adder_11_cout));
  Adder #(.width(1)) adder_12 (
    .a(d_latch_4_nq), .b(d_latch_5_nq), .out(adder_12_out), .cin(adder_11_cout), .cout(adder_12_cout));
  Adder #(.width(1)) adder_13 (
    .a(d_latch_6_nq), .b(d_latch_7_nq), .out(adder_13_out), .cin(adder_12_cout), .cout(adder_13_cout));
  Adder #(.width(1)) adder_14 (
    .a(d_latch_8_nq), .b(d_latch_9_nq), .out(adder_14_out), .cin(adder_13_cout), .cout(adder_14_cout));
  Adder #(.width(1)) adder_15 (
    .a(d_latch_10_nq), .b(d_latch_11_nq), .out(adder_15_out), .cin(adder_14_cout), .cout(adder_15_cout));
  Adder #(.width(1)) adder_16 (
    .a(d_latch_12_nq), .b(d_latch_13_nq), .out(adder_16_out), .cin(adder_15_cout), .cout(adder_16_cout));
  Adder #(.width(1)) adder_17 (
    .a(d_latch_14_nq), .b(d_latch_15_nq), .out(adder_17_out), .cin(adder_16_cout), .cout(adder_17_cout));
  Adder #(.width(1)) adder_18 (
    .a(d_latch_16_nq), .b(d_latch_17_nq), .out(adder_18_out), .cin(adder_17_cout), .cout(adder_18_cout));
  Adder #(.width(1)) adder_19 (
    .a(d_latch_18_nq), .b(d_latch_19_nq), .out(adder_19_out), .cin(adder_18_cout), .cout(adder_19_cout));
  Adder #(.width(1)) adder_20 (
    .a(d_latch_20_nq), .b(d_latch_21_nq), .out(adder_20_out), .cin(adder_19_cout));  // open: cout
  SR_BIT sr_bit_11 (.C2(FCLK2), .C1(FCLK1), .D(sr_bit_9_q), .Q(g_3100));  // open: nQ
  SR_BIT sr_bit_12 (.C2(FCLK2), .C1(FCLK1), .D(QV0), .Q(QV1));  // open: nQ
  D_LATCH d_latch_22 (.EN(FCLK2), .D(adder_11_out), .nQ(d_latch_22_nq));  // open: Q
  D_LATCH d_latch_23 (.EN(FCLK2), .D(adder_12_out), .nQ(d_latch_23_nq));  // open: Q
  D_LATCH d_latch_24 (.EN(FCLK2), .D(adder_13_out), .nQ(d_latch_24_nq));  // open: Q
  D_LATCH d_latch_25 (.EN(FCLK2), .D(adder_14_out), .nQ(d_latch_25_nq));  // open: Q
  D_LATCH d_latch_26 (.EN(FCLK2), .D(adder_15_out), .nQ(d_latch_26_nq));  // open: Q
  D_LATCH d_latch_27 (.EN(FCLK2), .D(adder_16_out), .nQ(d_latch_27_nq));  // open: Q
  D_LATCH d_latch_28 (.EN(FCLK2), .D(adder_17_out), .nQ(d_latch_28_nq));  // open: Q
  D_LATCH d_latch_29 (.EN(FCLK2), .D(adder_18_out), .nQ(d_latch_29_nq));  // open: Q
  D_LATCH d_latch_30 (.EN(FCLK2), .D(adder_19_out), .nQ(d_latch_30_nq));  // open: Q
  D_LATCH d_latch_31 (.EN(FCLK2), .D(adder_20_out), .nQ(d_latch_31_nq));  // open: Q
  SDELAY23 sdelay23_1 (.C2(FCLK2), .C1(FCLK1), .D(d_latch_22_nq), .Q(sdelay23_1_q), .Q42(sdelay23_1_q42));
  SDELAY23 sdelay23_2 (.C2(FCLK2), .C1(FCLK1), .D(d_latch_23_nq), .Q(sdelay23_2_q), .Q42(sdelay23_2_q42));
  SDELAY23 sdelay23_3 (.C2(FCLK2), .C1(FCLK1), .D(d_latch_24_nq), .Q(sdelay23_3_q), .Q42(sdelay23_3_q42));
  SDELAY23 sdelay23_4 (.C2(FCLK2), .C1(FCLK1), .D(d_latch_25_nq), .Q(sdelay23_4_q), .Q42(sdelay23_4_q42));
  SDELAY23 sdelay23_5 (.C2(FCLK2), .C1(FCLK1), .D(d_latch_26_nq), .Q(sdelay23_5_q), .Q42(sdelay23_5_q42));
  SDELAY23 sdelay23_6 (.C2(FCLK2), .C1(FCLK1), .D(d_latch_27_nq), .Q(sdelay23_6_q), .Q42(sdelay23_6_q42));
  SDELAY23 sdelay23_7 (.C2(FCLK2), .C1(FCLK1), .D(d_latch_28_nq), .Q(sdelay23_7_q), .Q42(sdelay23_7_q42));
  SDELAY23 sdelay23_8 (.C2(FCLK2), .C1(FCLK1), .D(d_latch_29_nq), .Q(sdelay23_8_q), .Q42(sdelay23_8_q42));
  SDELAY23 sdelay23_9 (.C2(FCLK2), .C1(FCLK1), .D(d_latch_30_nq), .Q(sdelay23_9_q), .Q42(sdelay23_9_q42));
  SDELAY23 sdelay23_10 (.C2(FCLK2), .C1(FCLK1), .D(d_latch_31_nq), .Q(sdelay23_10_q), .Q42(_1469Q42));
  SR_BIT sr_bit_13 (.C2(FCLK2), .C1(FCLK1), .D(QV1), .Q(QV2));  // open: nQ
  not not_14 (not_14_out, _1835_out);
  not not_15 (not_15_out, not_14_out);
  SR_BIT sr_bit_14 (.C2(FCLK2), .C1(FCLK1), .D(QV2), .Q(QV3));  // open: nQ
  and u__1327 (_1327_out, sr_bit_16_q, not_15_out);
  or _1327_2 (_1327, _1327_out, _1327_3_out);
  and _1327_3 (_1327_3_out, not_14_out, sdelay23_1_q);
  and u__1343 (_1343_out, sr_bit_18_q, not_15_out);
  or _1343_2 (_1343, _1343_out, _1343_3_out);
  and _1343_3 (_1343_3_out, not_14_out, sdelay23_2_q);
  and u__1359 (_1359_out, sr_bit_20_q, not_15_out);
  or _1359_2 (_1359, _1359_out, _1359_3_out);
  and _1359_3 (_1359_3_out, not_14_out, sdelay23_3_q);
  and u__1373 (_1373_out, sr_bit_22_q, not_15_out);
  or _1373_2 (_1373, _1373_out, _1373_3_out);
  and _1373_3 (_1373_3_out, not_14_out, sdelay23_4_q);
  and u__1391 (_1391_out, sr_bit_24_q, not_15_out);
  or _1391_2 (_1391, _1391_out, _1391_3_out);
  and _1391_3 (_1391_3_out, not_14_out, sdelay23_5_q);
  and u__1408 (_1408_out, sr_bit_26_q, not_15_out);
  or _1408_2 (_1408, _1408_out, _1408_3_out);
  and _1408_3 (_1408_3_out, not_14_out, sdelay23_6_q);
  and u__1424 (_1424_out, sr_bit_28_q, not_15_out);
  or _1424_2 (_1424, _1424_out, _1424_3_out);
  and _1424_3 (_1424_3_out, not_14_out, sdelay23_7_q);
  and u__1440 (_1440_out, sr_bit_30_q, not_15_out);
  or _1440_2 (_1440, _1440_out, _1440_3_out);
  and _1440_3 (_1440_3_out, not_14_out, sdelay23_8_q);
  and u__1455 (_1455_out, sr_bit_32_q, not_15_out);
  or _1455_2 (_1455, _1455_out, _1455_3_out);
  and _1455_3 (_1455_3_out, not_14_out, sdelay23_9_q);
  and u__1470 (_1470_out, sr_bit_34_q, not_15_out);
  or _1470_2 (_1470, _1470_out, _1470_3_out);
  and _1470_3 (_1470_3_out, not_14_out, sdelay23_10_q);
  SR_BIT sr_bit_15 (.C2(FCLK2), .C1(FCLK1), .D(QV3), .Q(QV4));  // open: nQ
  SR_BIT sr_bit_16 (.C2(FCLK2), .C1(FCLK1), .D(_1332_3_out), .Q(sr_bit_16_q));  // open: nQ
  SR_BIT sr_bit_17 (.C2(FCLK2), .C1(FCLK1), .D(sdelay23_1_q42), .Q(sr_bit_17_q));  // open: nQ
  D_LATCH d_latch_32 (.EN(FCLK1), .D(sdelay23_1_q42), .nQ(d_latch_32_nq));  // open: Q
  SR_BIT sr_bit_18 (.C2(FCLK2), .C1(FCLK1), .D(_1348_3_out), .Q(sr_bit_18_q));  // open: nQ
  SR_BIT sr_bit_19 (.C2(FCLK2), .C1(FCLK1), .D(sdelay23_2_q42), .Q(sr_bit_19_q));  // open: nQ
  D_LATCH d_latch_33 (.EN(FCLK1), .D(sdelay23_2_q42), .nQ(d_latch_33_nq));  // open: Q
  SR_BIT sr_bit_20 (.C2(FCLK2), .C1(FCLK1), .D(_1364_3_out), .Q(sr_bit_20_q));  // open: nQ
  SR_BIT sr_bit_21 (.C2(FCLK2), .C1(FCLK1), .D(sdelay23_3_q42), .Q(sr_bit_21_q));  // open: nQ
  D_LATCH d_latch_34 (.EN(FCLK1), .D(sdelay23_3_q42), .nQ(d_latch_34_nq));  // open: Q
  SR_BIT sr_bit_22 (.C2(FCLK2), .C1(FCLK1), .D(_1378_3_out), .Q(sr_bit_22_q));  // open: nQ
  SR_BIT sr_bit_23 (.C2(FCLK2), .C1(FCLK1), .D(sdelay23_4_q42), .Q(sr_bit_23_q));  // open: nQ
  D_LATCH d_latch_35 (.EN(FCLK1), .D(sdelay23_4_q42), .nQ(d_latch_35_nq));  // open: Q
  SR_BIT sr_bit_24 (.C2(FCLK2), .C1(FCLK1), .D(_1396_3_out), .Q(sr_bit_24_q));  // open: nQ
  SR_BIT sr_bit_25 (.C2(FCLK2), .C1(FCLK1), .D(sdelay23_5_q42), .Q(sr_bit_25_q));  // open: nQ
  D_LATCH d_latch_36 (.EN(FCLK1), .D(sdelay23_5_q42), .nQ(d_latch_36_nq));  // open: Q
  SR_BIT sr_bit_26 (.C2(FCLK2), .C1(FCLK1), .D(_1413_3_out), .Q(sr_bit_26_q));  // open: nQ
  SR_BIT sr_bit_27 (.C2(FCLK2), .C1(FCLK1), .D(sdelay23_6_q42), .Q(sr_bit_27_q));  // open: nQ
  D_LATCH d_latch_37 (.EN(FCLK1), .D(sdelay23_6_q42), .nQ(d_latch_37_nq));  // open: Q
  SR_BIT sr_bit_28 (.C2(FCLK2), .C1(FCLK1), .D(_1429_3_out), .Q(sr_bit_28_q));  // open: nQ
  SR_BIT sr_bit_29 (.C2(FCLK2), .C1(FCLK1), .D(sdelay23_7_q42), .Q(sr_bit_29_q));  // open: nQ
  D_LATCH d_latch_38 (.EN(FCLK1), .D(sdelay23_7_q42), .nQ(d_latch_38_nq));  // open: Q
  SR_BIT sr_bit_30 (.C2(FCLK2), .C1(FCLK1), .D(_1445_3_out), .Q(sr_bit_30_q));  // open: nQ
  SR_BIT sr_bit_31 (.C2(FCLK2), .C1(FCLK1), .D(sdelay23_8_q42), .Q(sr_bit_31_q));  // open: nQ
  D_LATCH d_latch_39 (.EN(FCLK1), .D(sdelay23_8_q42), .nQ(d_latch_39_nq));  // open: Q
  SR_BIT sr_bit_32 (.C2(FCLK2), .C1(FCLK1), .D(_1460_3_out), .Q(sr_bit_32_q));  // open: nQ
  SR_BIT sr_bit_33 (.C2(FCLK2), .C1(FCLK1), .D(sdelay23_9_q42), .Q(sr_bit_33_q));  // open: nQ
  D_LATCH d_latch_40 (.EN(FCLK1), .D(sdelay23_9_q42), .nQ(d_latch_40_nq));  // open: Q
  SR_BIT sr_bit_34 (.C2(FCLK2), .C1(FCLK1), .D(_1473_3_out), .Q(sr_bit_34_q));  // open: nQ
  SR_BIT sr_bit_35 (.C2(FCLK2), .C1(FCLK1), .D(_1469Q42), .Q(sr_bit_35_q));  // open: nQ
  D_LATCH d_latch_41 (.EN(FCLK1), .D(_1469Q42), .nQ(d_latch_41_nq));  // open: Q
  SR_BIT sr_bit_36 (.C2(FCLK2), .C1(FCLK1), .D(QV4), .Q(QV5));  // open: nQ
  Adder #(.width(1)) adder_21 (.a(d_latch_41_nq), .b(1'b1), .out(adder_21_out), .cin(and_10_out));  // open: cout
  xor xor_2 (xor_2_out, 1'b1, d_latch_32_nq);
  and and_2 (and_2_out, 1'b1, d_latch_32_nq);
  xor xor_3 (xor_3_out, and_2_out, d_latch_33_nq);
  and and_3 (and_3_out, and_2_out, d_latch_33_nq);
  xor xor_4 (xor_4_out, and_3_out, d_latch_34_nq);
  and and_4 (and_4_out, and_3_out, d_latch_34_nq);
  xor xor_5 (xor_5_out, and_4_out, d_latch_35_nq);
  and and_5 (and_5_out, and_4_out, d_latch_35_nq);
  xor xor_6 (xor_6_out, and_5_out, d_latch_36_nq);
  and and_6 (and_6_out, and_5_out, d_latch_36_nq);
  xor xor_7 (xor_7_out, and_6_out, d_latch_37_nq);
  and and_7 (and_7_out, and_6_out, d_latch_37_nq);
  xor xor_8 (xor_8_out, and_7_out, d_latch_38_nq);
  and and_8 (and_8_out, and_7_out, d_latch_38_nq);
  xor xor_9 (xor_9_out, and_8_out, d_latch_39_nq);
  and and_9 (and_9_out, and_8_out, d_latch_39_nq);
  xor xor_10 (xor_10_out, and_9_out, d_latch_40_nq);
  and and_10 (and_10_out, and_9_out, d_latch_40_nq);
  SR_BIT sr_bit_37 (.C2(FCLK2), .C1(FCLK1), .D(QV5), .Q(QV6));  // open: nQ
  not not_16 (not_16_out, _1813_q);
  D_LATCH d_latch_42 (.EN(FCLK2), .D(xor_2_out), .nQ(d_latch_42_nq));  // open: Q
  D_LATCH d_latch_43 (.EN(FCLK2), .D(xor_3_out), .nQ(d_latch_43_nq));  // open: Q
  D_LATCH d_latch_44 (.EN(FCLK2), .D(xor_4_out), .nQ(d_latch_44_nq));  // open: Q
  D_LATCH d_latch_45 (.EN(FCLK2), .D(xor_5_out), .nQ(d_latch_45_nq));  // open: Q
  D_LATCH d_latch_46 (.EN(FCLK2), .D(xor_6_out), .nQ(d_latch_46_nq));  // open: Q
  D_LATCH d_latch_47 (.EN(FCLK2), .D(xor_7_out), .nQ(d_latch_47_nq));  // open: Q
  D_LATCH d_latch_48 (.EN(FCLK2), .D(xor_8_out), .nQ(d_latch_48_nq));  // open: Q
  D_LATCH d_latch_49 (.EN(FCLK2), .D(xor_9_out), .nQ(d_latch_49_nq));  // open: Q
  D_LATCH d_latch_50 (.EN(FCLK2), .D(xor_10_out), .nQ(d_latch_50_nq));  // open: Q
  D_LATCH d_latch_51 (.EN(FCLK2), .D(adder_21_out), .nQ(d_latch_51_nq));  // open: Q
  not not_17 (not_17_out, not_16_out);
  not _1815 (_1815_out, d_latch_51_nq);
  D_LATCH d_latch_52 (.EN(FCLK1), .D(g_3065), .nQ(d_latch_52_nq));  // open: Q
  D_LATCH d_latch_53 (.EN(FCLK1), .D(g_3066), .nQ(d_latch_53_nq));  // open: Q
  and _1332 (_1332_out, sr_bit_17_q, not_16_out);
  and _1332_2 (_1332_2_out, not_17_out, d_latch_42_nq);
  and _1348 (_1348_out, sr_bit_19_q, not_16_out);
  and _1348_2 (_1348_2_out, not_17_out, d_latch_43_nq);
  and _1364 (_1364_out, sr_bit_21_q, not_16_out);
  and _1364_2 (_1364_2_out, not_17_out, d_latch_44_nq);
  and _1378 (_1378_out, sr_bit_23_q, not_16_out);
  and _1378_2 (_1378_2_out, not_17_out, d_latch_45_nq);
  and _1396 (_1396_out, sr_bit_25_q, not_16_out);
  and _1396_2 (_1396_2_out, not_17_out, d_latch_46_nq);
  and _1413 (_1413_out, sr_bit_27_q, not_16_out);
  and _1413_2 (_1413_2_out, not_17_out, d_latch_47_nq);
  and _1429 (_1429_out, sr_bit_29_q, not_16_out);
  and _1429_2 (_1429_2_out, not_17_out, d_latch_48_nq);
  and _1445 (_1445_out, sr_bit_31_q, not_16_out);
  and _1445_2 (_1445_2_out, not_17_out, d_latch_49_nq);
  and _1460 (_1460_out, sr_bit_33_q, not_16_out);
  and _1460_2 (_1460_2_out, not_17_out, d_latch_50_nq);
  and _1473 (_1473_out, sr_bit_35_q, not_16_out);
  and _1473_2 (_1473_2_out, not_17_out, _1815_out);
  SR_BIT sr_bit_38 (.C2(FCLK2), .C1(FCLK1), .D(QV6), .Q(QV7));  // open: nQ
  not _1667 (_1667_out, d_latch_52_nq);
  not _1668 (_1668_out, d_latch_53_nq);
  Register #(.width(6), .trigger("high")) register_1 (
    .D({LFO5, LFO4, LFO3, LFO2, LFO1, LFO0}), .Q(register_1_q), .clk(FCLK1));  // open: en, clr
  or _1332_3 (_1332_3_out, _1332_out, _1332_2_out);
  or _1348_3 (_1348_3_out, _1348_out, _1348_2_out);
  or _1364_3 (_1364_3_out, _1364_out, _1364_2_out);
  or _1378_3 (_1378_3_out, _1378_out, _1378_2_out);
  or _1396_3 (_1396_3_out, _1396_out, _1396_2_out);
  or _1413_3 (_1413_3_out, _1413_out, _1413_2_out);
  or _1429_3 (_1429_3_out, _1429_out, _1429_2_out);
  or _1445_3 (_1445_3_out, _1445_out, _1445_2_out);
  or _1460_3 (_1460_3_out, _1460_out, _1460_2_out);
  or _1473_3 (_1473_3_out, _1473_out, _1473_2_out);
  not _1597 (_1597_out, _1667_out);
  not _1596 (_1596_out, _1668_out);
  SR_BIT sr_bit_39 (.C2(FCLK2), .C1(FCLK1), .D(QV7), .Q(QV8));  // open: nQ
  and _1587 (_1587_out, _1597_out, _1668_out);
  and _1598 (_1598_out, _1597_out, _1596_out);
  and _1586 (_1586_out, _1596_out, _1667_out);
  and _1588 (_1588_out, _1667_out, _1668_out);
  and _1335 (_1335_out, register_1_q[2], _1587_out);
  and _1335_2 (_1335_2_out, 1'b0, register_1_q[1]);
  and _1335_3 (_1335_3_out, register_1_q[0], _1586_out);
  and _1335_4 (_1335_4_out, _1588_out, 1'b0);
  and _1351 (_1351_out, register_1_q[3], _1587_out);
  and _1351_2 (_1351_2_out, 1'b0, register_1_q[2]);
  and _1351_3 (_1351_3_out, register_1_q[1], _1586_out);
  and _1351_4 (_1351_4_out, _1588_out, register_1_q[0]);
  and _1367 (_1367_out, register_1_q[4], _1587_out);
  and _1367_2 (_1367_2_out, 1'b0, register_1_q[3]);
  and _1367_3 (_1367_3_out, register_1_q[2], _1586_out);
  and _1367_4 (_1367_4_out, _1588_out, register_1_q[1]);
  and _1381 (_1381_out, register_1_q[5], _1587_out);
  and _1381_2 (_1381_2_out, 1'b0, register_1_q[4]);
  and _1381_3 (_1381_3_out, register_1_q[3], _1586_out);
  and _1381_4 (_1381_4_out, _1588_out, register_1_q[2]);
  and _1399 (_1399_out, 1'b0, _1587_out);
  and _1399_2 (_1399_2_out, 1'b0, register_1_q[5]);
  and _1399_3 (_1399_3_out, register_1_q[4], _1586_out);
  and _1399_4 (_1399_4_out, _1588_out, register_1_q[3]);
  and _1417 (_1417_out, register_1_q[5], _1586_out);
  and _1417_2 (_1417_2_out, _1588_out, register_1_q[4]);
  and _1433 (_1433_out, 1'b0, _1586_out);
  and _1433_2 (_1433_2_out, _1588_out, register_1_q[5]);
  SR_BIT sr_bit_40 (.C2(FCLK2), .C1(FCLK1), .D(QV8), .Q(QV9));  // open: nQ
  nor _1417_3 (_1417_3_out, _1417_out, _1417_2_out);
  nor _1433_3 (_1433_3_out, _1433_out, _1433_2_out);
  D_LATCH d_latch_54 (.EN(FCLK2), .D(_1335_5_out), .nQ(d_latch_54_nq));  // open: Q
  nor _1335_5 (_1335_5_out, _1335_out, _1335_2_out, _1335_3_out, _1335_4_out);
  D_LATCH d_latch_55 (.EN(FCLK2), .D(_1351_5_out), .nQ(d_latch_55_nq));  // open: Q
  nor _1351_5 (_1351_5_out, _1351_out, _1351_2_out, _1351_3_out, _1351_4_out);
  D_LATCH d_latch_56 (.EN(FCLK2), .D(_1367_5_out), .nQ(d_latch_56_nq));  // open: Q
  nor _1367_5 (_1367_5_out, _1367_out, _1367_2_out, _1367_3_out, _1367_4_out);
  D_LATCH d_latch_57 (.EN(FCLK2), .D(_1381_5_out), .nQ(d_latch_57_nq));  // open: Q
  nor _1381_5 (_1381_5_out, _1381_out, _1381_2_out, _1381_3_out, _1381_4_out);
  D_LATCH d_latch_58 (.EN(FCLK2), .D(_1399_5_out), .nQ(d_latch_58_nq));  // open: Q
  nor _1399_5 (_1399_5_out, _1399_out, _1399_2_out, _1399_3_out, _1399_4_out);
  D_LATCH d_latch_59 (.EN(FCLK2), .D(_1417_3_out), .nQ(d_latch_59_nq));  // open: Q
  D_LATCH d_latch_60 (.EN(FCLK2), .D(_1433_3_out), .nQ(d_latch_60_nq));  // open: Q
  SR_BIT sr_bit_41 (.C2(FCLK2), .C1(FCLK1), .D(QV9), .Q(QV10));  // open: nQ
  not _1614 (_1614_out, g_374);
  and _1334 (_1334_out, _1614_out, _1332_3_out);
  and _1350 (_1350_out, _1614_out, _1348_3_out);
  and _1366 (_1366_out, _1614_out, _1364_3_out);
  and _1380 (_1380_out, _1614_out, _1378_3_out);
  and _1398 (_1398_out, _1614_out, _1396_3_out);
  and _1416 (_1416_out, _1614_out, _1413_3_out);
  and _1432 (_1432_out, _1614_out, _1429_3_out);
  and _1448 (_1448_out, _1614_out, _1445_3_out);
  and _1463 (_1463_out, _1614_out, _1460_3_out);
  and _1476 (_1476_out, _1614_out, _1473_3_out);
  Adder #(.width(1)) adder_22 (.a(d_latch_54_nq), .b(_1334_out), .out(adder_22_out), .cin(1'b0), .cout(adder_22_cout));
  Adder #(.width(1)) adder_23 (
    .a(d_latch_55_nq), .b(_1350_out), .out(adder_23_out), .cin(adder_22_cout), .cout(adder_23_cout));
  Adder #(.width(1)) adder_24 (
    .a(d_latch_56_nq), .b(_1366_out), .out(adder_24_out), .cin(adder_23_cout), .cout(adder_24_cout));
  Adder #(.width(1)) adder_25 (
    .a(d_latch_57_nq), .b(_1380_out), .out(adder_25_out), .cin(adder_24_cout), .cout(adder_25_cout));
  Adder #(.width(1)) adder_26 (
    .a(d_latch_58_nq), .b(_1398_out), .out(adder_26_out), .cin(adder_25_cout), .cout(adder_26_cout));
  Adder #(.width(1)) adder_27 (
    .a(d_latch_59_nq), .b(_1416_out), .out(adder_27_out), .cin(adder_26_cout), .cout(adder_27_cout));
  Adder #(.width(1)) adder_28 (
    .a(d_latch_60_nq), .b(_1432_out), .out(adder_28_out), .cin(adder_27_cout), .cout(adder_28_cout));
  Adder #(.width(1)) adder_29 (.a(1'b0), .b(_1448_out), .out(adder_29_out), .cin(adder_28_cout), .cout(adder_29_cout));
  Adder #(.width(1)) adder_30 (.a(1'b0), .b(_1463_out), .out(adder_30_out), .cin(adder_29_cout), .cout(adder_30_cout));
  Adder #(.width(1)) adder_31 (.a(1'b0), .b(_1476_out), .out(adder_31_out), .cin(adder_30_cout), .cout(adder_31_cout));
  SR_BIT sr_bit_42 (.C2(FCLK2), .C1(FCLK1), .D(QV10), .Q(QV11));  // open: nQ
  SR_BIT sr_bit_43 (.C2(FCLK2), .C1(FCLK1), .D(g_2270), .Q(sr_bit_43_q));  // open: nQ
  SR_BIT sr_bit_44 (.C2(FCLK2), .C1(FCLK1), .D(sr_bit_43_q), .nQ(sr_bit_44_nq));  // open: Q
  SR_BIT sr_bit_45 (.C2(FCLK2), .C1(FCLK1), .D(g_2269), .Q(sr_bit_45_q));  // open: nQ
  SR_BIT sr_bit_46 (.C2(FCLK2), .C1(FCLK1), .D(sr_bit_45_q), .nQ(sr_bit_46_nq));  // open: Q
  SR_BIT sr_bit_47 (.C2(FCLK2), .C1(FCLK1), .D(g_2268), .Q(sr_bit_47_q));  // open: nQ
  SR_BIT sr_bit_48 (.C2(FCLK2), .C1(FCLK1), .D(sr_bit_47_q), .nQ(sr_bit_48_nq));  // open: Q
  SR_BIT sr_bit_49 (.C2(FCLK2), .C1(FCLK1), .D(g_2267), .Q(sr_bit_49_q));  // open: nQ
  SR_BIT sr_bit_50 (.C2(FCLK2), .C1(FCLK1), .D(sr_bit_49_q), .nQ(sr_bit_50_nq));  // open: Q
  SR_BIT sr_bit_51 (.C2(FCLK2), .C1(FCLK1), .D(g_2266), .Q(sr_bit_51_q));  // open: nQ
  SR_BIT sr_bit_52 (.C2(FCLK2), .C1(FCLK1), .D(sr_bit_51_q), .nQ(sr_bit_52_nq));  // open: Q
  SR_BIT sr_bit_53 (.C2(FCLK2), .C1(FCLK1), .D(g_2265), .Q(sr_bit_53_q));  // open: nQ
  SR_BIT sr_bit_54 (.C2(FCLK2), .C1(FCLK1), .D(sr_bit_53_q), .nQ(sr_bit_54_nq));  // open: Q
  SR_BIT _1685 (.C2(FCLK2), .C1(FCLK1), .D(g_2264), .Q(_1685_q));  // open: nQ
  SR_BIT _1684 (.C2(FCLK2), .C1(FCLK1), .D(_1685_q), .nQ(_1684_nq));  // open: Q
  not not_18 (not_18_out, _1670_out);
  D_LATCH d_latch_61 (.EN(FCLK1), .D(adder_22_out), .nQ(d_latch_61_nq));  // open: Q
  D_LATCH d_latch_62 (.EN(FCLK1), .D(adder_23_out), .nQ(d_latch_62_nq));  // open: Q
  D_LATCH d_latch_63 (.EN(FCLK1), .D(adder_24_out), .nQ(d_latch_63_nq));  // open: Q
  D_LATCH d_latch_64 (.EN(FCLK1), .D(adder_25_out), .nQ(d_latch_64_nq));  // open: Q
  D_LATCH d_latch_65 (.EN(FCLK1), .D(_1671_out), .nQ(d_latch_65_nq));  // open: Q
  and _1671 (_1671_out, not_18_out, sr_bit_43_q);
  D_LATCH d_latch_66 (.EN(FCLK1), .D(adder_26_out), .nQ(d_latch_66_nq));  // open: Q
  D_LATCH d_latch_67 (.EN(FCLK1), .D(_1672_out), .nQ(d_latch_67_nq));  // open: Q
  and _1672 (_1672_out, not_18_out, sr_bit_45_q);
  D_LATCH d_latch_68 (.EN(FCLK1), .D(adder_27_out), .nQ(d_latch_68_nq));  // open: Q
  D_LATCH d_latch_69 (.EN(FCLK1), .D(_1673_out), .nQ(d_latch_69_nq));  // open: Q
  and _1673 (_1673_out, not_18_out, sr_bit_47_q);
  D_LATCH d_latch_70 (.EN(FCLK1), .D(adder_28_out), .nQ(d_latch_70_nq));  // open: Q
  D_LATCH d_latch_71 (.EN(FCLK1), .D(_1674_out), .nQ(d_latch_71_nq));  // open: Q
  and _1674 (_1674_out, not_18_out, sr_bit_49_q);
  D_LATCH d_latch_72 (.EN(FCLK1), .D(adder_29_out), .nQ(d_latch_72_nq));  // open: Q
  D_LATCH d_latch_73 (.EN(FCLK1), .D(_1675_out), .nQ(d_latch_73_nq));  // open: Q
  and _1675 (_1675_out, not_18_out, sr_bit_51_q);
  D_LATCH d_latch_74 (.EN(FCLK1), .D(adder_30_out), .nQ(d_latch_74_nq));  // open: Q
  D_LATCH d_latch_75 (.EN(FCLK1), .D(_1676_out), .nQ(d_latch_75_nq));  // open: Q
  and _1676 (_1676_out, not_18_out, sr_bit_53_q);
  D_LATCH _1655 (.EN(FCLK1), .D(adder_31_out), .nQ(_1655_nq));  // open: Q
  D_LATCH _1656 (.EN(FCLK1), .D(_1677_out), .nQ(_1656_nq));  // open: Q
  and _1677 (_1677_out, not_18_out, _1685_q);
  D_LATCH _1580 (.EN(FCLK1), .D(adder_31_cout), .nQ(_1580_nq));  // open: Q
  Adder #(.width(1)) adder_32 (
    .a(d_latch_64_nq), .b(d_latch_65_nq), .out(adder_32_out), .cin(1'b1), .cout(adder_32_cout));
  Adder #(.width(1)) adder_33 (
    .a(d_latch_66_nq), .b(d_latch_67_nq), .out(adder_33_out), .cin(adder_32_cout), .cout(adder_33_cout));
  Adder #(.width(1)) adder_34 (
    .a(d_latch_68_nq), .b(d_latch_69_nq), .out(adder_34_out), .cin(adder_33_cout), .cout(adder_34_cout));
  Adder #(.width(1)) adder_35 (
    .a(d_latch_70_nq), .b(d_latch_71_nq), .out(adder_35_out), .cin(adder_34_cout), .cout(adder_35_cout));
  Adder #(.width(1)) adder_36 (
    .a(d_latch_72_nq), .b(d_latch_73_nq), .out(adder_36_out), .cin(adder_35_cout), .cout(adder_36_cout));
  Adder #(.width(1)) adder_37 (
    .a(d_latch_74_nq), .b(d_latch_75_nq), .out(adder_37_out), .cin(adder_36_cout), .cout(adder_37_cout));
  Adder #(.width(1)) adder_38 (
    .a(_1655_nq), .b(_1656_nq), .out(adder_38_out), .cin(adder_37_cout), .cout(adder_38_cout));
  nand _1583 (_1583_out, adder_38_cout, _1580_nq);
  and _1603 (_1603_out, d_latch_61_nq, not_19_out);
  and _1666 (_1666_out, d_latch_62_nq, not_19_out);
  and _1665 (_1665_out, d_latch_63_nq, not_19_out);
  and _1664 (_1664_out, adder_32_out, not_19_out);
  and _1663 (_1663_out, adder_33_out, not_19_out);
  and _1662 (_1662_out, adder_34_out, not_19_out);
  and _1661 (_1661_out, adder_35_out, not_19_out);
  and _1660 (_1660_out, adder_36_out, not_19_out);
  and _1659 (_1659_out, adder_37_out, not_19_out);
  and _1658 (_1658_out, adder_38_out, not_19_out);
  not not_19 (not_19_out, _1583_out);
  D_LATCH d_latch_76 (.EN(FCLK2), .D(_1603_out), .nQ(ENV0));  // open: Q
  D_LATCH d_latch_77 (.EN(FCLK2), .D(_1666_out), .nQ(ENV1));  // open: Q
  D_LATCH d_latch_78 (.EN(FCLK2), .D(_1665_out), .nQ(ENV2));  // open: Q
  D_LATCH d_latch_79 (.EN(FCLK2), .D(_1664_out), .nQ(ENV3));  // open: Q
  D_LATCH d_latch_80 (.EN(FCLK2), .D(_1663_out), .nQ(ENV4));  // open: Q
  D_LATCH d_latch_81 (.EN(FCLK2), .D(_1662_out), .nQ(ENV5));  // open: Q
  D_LATCH d_latch_82 (.EN(FCLK2), .D(_1661_out), .nQ(ENV6));  // open: Q
  D_LATCH d_latch_83 (.EN(FCLK2), .D(_1660_out), .nQ(ENV7));  // open: Q
  D_LATCH d_latch_84 (.EN(FCLK2), .D(_1659_out), .nQ(ENV8));  // open: Q
  D_LATCH _1648 (.EN(FCLK2), .D(_1658_out), .nQ(ENV9));  // open: Q
  not _1849 (_1849_out, _1792Q44);
  or or_1 (or_1_out, 1'b0, and_11_out);
  and and_11 (and_11_out, ENV0, _1798_out);
  or or_2 (or_2_out, sr_bit_55_q, and_12_out);
  and and_12 (and_12_out, ENV1, _1798_out);
  or or_3 (or_3_out, sr_bit_56_q, and_13_out);
  and and_13 (and_13_out, ENV2, _1798_out);
  or or_4 (or_4_out, sr_bit_57_q, and_14_out);
  and and_14 (and_14_out, ENV3, _1798_out);
  or or_5 (or_5_out, sr_bit_58_q, and_15_out);
  and and_15 (and_15_out, ENV4, _1798_out);
  or or_6 (or_6_out, sr_bit_59_q, and_16_out);
  and and_16 (and_16_out, ENV5, _1798_out);
  or or_7 (or_7_out, sr_bit_60_q, and_17_out);
  and and_17 (and_17_out, ENV6, _1798_out);
  or or_8 (or_8_out, sr_bit_61_q, and_18_out);
  and and_18 (and_18_out, ENV7, _1798_out);
  or or_9 (or_9_out, sr_bit_62_q, and_19_out);
  and and_19 (and_19_out, ENV8, _1798_out);
  or or_10 (or_10_out, sr_bit_63_q, and_20_out);
  and and_20 (and_20_out, ENV9, _1798_out);
  and _1831 (_1831_out, _1849_out, KEY_ON);
  and _1831_2 (_1831_2_out, _1792Q44, g_1827);
  SR_BIT sr_bit_55 (.C2(FCLK2), .C1(FCLK1), .D(or_1_out), .Q(sr_bit_55_q));  // open: nQ
  SR_BIT sr_bit_56 (.C2(FCLK2), .C1(FCLK1), .D(or_2_out), .Q(sr_bit_56_q));  // open: nQ
  SR_BIT sr_bit_57 (.C2(FCLK2), .C1(FCLK1), .D(or_3_out), .Q(sr_bit_57_q));  // open: nQ
  SR_BIT sr_bit_58 (.C2(FCLK2), .C1(FCLK1), .D(or_4_out), .Q(sr_bit_58_q));  // open: nQ
  SR_BIT sr_bit_59 (.C2(FCLK2), .C1(FCLK1), .D(or_5_out), .Q(sr_bit_59_q));  // open: nQ
  SR_BIT sr_bit_60 (.C2(FCLK2), .C1(FCLK1), .D(or_6_out), .Q(sr_bit_60_q));  // open: nQ
  SR_BIT sr_bit_61 (.C2(FCLK2), .C1(FCLK1), .D(or_7_out), .Q(sr_bit_61_q));  // open: nQ
  SR_BIT sr_bit_62 (.C2(FCLK2), .C1(FCLK1), .D(or_8_out), .Q(sr_bit_62_q));  // open: nQ
  SR_BIT sr_bit_63 (.C2(FCLK2), .C1(FCLK1), .D(or_9_out), .Q(sr_bit_63_q));  // open: nQ
  SR_BIT sr_bit_64 (.C2(FCLK2), .C1(FCLK1), .D(or_10_out), .Q(g_1613));  // open: nQ
  nor _1831_3 (_1831_3_out, _1831_out, _1831_2_out);
  and _1795 (g_1795, _1791Q44, _1831_3_out);
  and _1796 (g_1796, _1831_3_out, _1790Q44);

  // Other names for the same wires on the sheet: LFO0_5[5:0] = {LFO5, LFO4, LFO3, LFO2, LFO1, LFO0}

  // Notes on the sheet:
  //   1690
  //   B
  //   A1
  //   A2
  //   AOI21
  //   1634
  //   1584
  //   1825
  //   1686
  //   1771
  //   1774
  //   1775
  //   1776
  //   1777
  //   1778
  //   1582
  //   1824
  //   1516
  //   1696
  //   SLATCH
  //   SLATCH
  //   1872
  //   B
  //   A1
  //   A2
  //   AOI21
  //   SLATCH
  //   SLATCH
  //   SLATCH
  //   SLATCH
  //   1748
  //   1747
  //   1746
  //   1745
  //   1505
  //   A1
  //   A2
  //   AOI21
  //   B
  //   1820
  //   B
  //   A2
  //   A1
  //   A
  //   HA
  //   1728
  //   B
  //   A1
  //   A2
  //   1706
  //   B
  //   A1
  //   A2
  //   AOI21
  //   1503
  //   B
  //   CO
  //   AOI21
  //   AOI21
  //   S
  //   1818
  //   1818
  //   A1
  //   A2
  //   A1
  //   A2
  //   A1
  //   A2
  //   C2
  //   C1
  //   B2
  //   B1
  //   C2
  //   C1
  //   B2
  //   B1
  //   C2
  //   C1
  //   B2
  //   B1
  //   C2
  //   C1
  //   B2
  //   B1
  //   C2
  //   C1
  //   B2
  //   B1
  //   C2
  //   C1
  //   B2
  //   B1
  //   C2
  //   C1
  //   B2
  //   B1
  //   AOI21
  //   B
  //   AOI21
  //   B
  //   AOI21
  //   B
  //   AOI221
  //   A
  //   AOI221
  //   A
  //   AOI221
  //   A
  //   AOI221
  //   A
  //   AOI221
  //   A
  //   AOI221
  //   A
  //   AOI221
  //   A
  //   1322
  //   1338
  //   1354
  //   1368
  //   1386
  //   1403
  //   1419
  //   1435
  //   1450
  //   1465
  //   1697
  //   1874
  //   1480
  //   1323
  //   1320
  //   1339
  //   1336
  //   1355
  //   1336
  //   1369
  //   1385
  //   1387
  //   1401
  //   1404
  //   1402
  //   1420
  //   1418
  //   1436
  //   1434
  //   1451
  //   1449
  //   1466
  //   1464
  //   1324
  //   1340
  //   1356
  //   1370
  //   1388
  //   1405
  //   1421
  //   1437
  //   1452
  //   1467
  //   1875
  //   1481
  //   1325
  //   1341
  //   1357
  //   1371
  //   1389
  //   1406
  //   1422
  //   1438
  //   1453
  //   1468
  //   1482
  //   1830
  //   1326
  //   1342
  //   1358
  //   1372
  //   1390
  //   1407
  //   1423
  //   1439
  //   1454
  //   1469
  //   1830
  //   1483
  //   1484
  //   1329
  //   1345
  //   1361
  //   1375
  //   1393
  //   1410
  //   1426
  //   1442
  //   1457
  //   1472
  //   1333
  //   1328
  //   1349
  //   1344
  //   1365
  //   1360
  //   1379
  //   1374
  //   1397
  //   1392
  //   1415
  //   1409
  //   1431
  //   1425
  //   1447
  //   1441
  //   1462
  //   1456
  //   1475
  //   1471
  //   1487
  //   1330
  //   A
  //   B
  //   HA
  //   1346
  //   A
  //   B
  //   HA
  //   1362
  //   A
  //   B
  //   HA
  //   1376
  //   A
  //   B
  //   HA
  //   1394
  //   A
  //   B
  //   HA
  //   1411
  //   A
  //   B
  //   HA
  //   1427
  //   A
  //   B
  //   HA
  //   1443
  //   A
  //   B
  //   HA
  //   1458
  //   A
  //   B
  //   HA
  //   2316
  //   S
  //   CO
  //   S
  //   CO
  //   S
  //   CO
  //   S
  //   CO
  //   S
  //   CO
  //   S
  //   CO
  //   S
  //   CO
  //   S
  //   CO
  //   S
  //   CO
  //   1816
  //   1331
  //   1347
  //   1363
  //   1377
  //   1395
  //   1412
  //   1428
  //   1444
  //   1459
  //   1477
  //   1488
  //   1592, 1593, 1600, 1615
  //   1616, 1579, 1594, 1595
  //   1599, 1617, 1519, 1585
  //   1816
  //   1489
  //   1633
  //   1632
  //   DLATCH 6 BIT
  //   1492
  //   1495
  //   1591
  //   1590
  //   1589
  //   1575
  //   1576
  //   1577
  //   1578
  //   1496
  //   1559
  //   1560
  //   1561
  //   1562
  //   1563
  //   1564
  //   1565
  //   1566
  //   1567
  //   1568
  //   1497
  //   1636
  //   1635
  //   1642
  //   1641
  //   1644
  //   1643
  //   1678
  //   1679
  //   1681
  //   1680
  //   1683
  //   1682
  //   1669
  //   1601
  //   1630
  //   1631
  //   1638
  //   1637
  //   1639
  //   1640
  //   1646
  //   1645
  //   1650
  //   1649
  //   1651
  //   1652
  //   1654
  //   1653
  //   1569
  //   1570
  //   1571
  //   1572
  //   1573
  //   1574
  //   1657
  //   1581
  //   1602
  //   1623
  //   1624
  //   1625
  //   1626
  //   1627
  //   1628
  //   1629
  //   1647
  //   1604
  //   A2
  //   A1
  //   1605
  //   A2
  //   A1
  //   1606
  //   A2
  //   A1
  //   1607
  //   A2
  //   A1
  //   1608
  //   A2
  //   A1
  //   1609
  //   A2
  //   A1
  //   1610
  //   A2
  //   A1
  //   1611
  //   A2
  //   A1
  //   1612
  //   A2
  //   A1
  //   1613
  //   A2
  //   A1
  //   B
  //   B
  //   B
  //   B
  //   B
  //   B
  //   B
  //   B
  //   B
  //   B
  //   AON21SR
  //   AON21SR
  //   AON21SR
  //   AON21SR
  //   AON21SR
  //   AON21SR
  //   AON21SR
  //   AON21SR
  //   AON21SR
  //   AON21SR
endmodule

module SDELAY23 (
  input  C2,
  input  C1,
  input  D,
  output Q,
  output Q42
);

  wire d_ff_1_q, d_ff_2_q, d_ff_3_q, d_ff_4_q, d_ff_5_q, d_ff_6_q, d_ff_7_q, d_ff_8_q, d_ff_9_q, d_ff_10_q,
       d_ff_11_q, d_ff_13_q, d_ff_14_q, d_ff_15_q, d_ff_16_q, d_ff_17_q, d_ff_18_q, d_ff_19_q, d_ff_20_q,
       d_ff_21_q, d_ff_22_q, d_ff_23_q, d_ff_24_q, d_ff_25_q, d_ff_26_q, d_ff_27_q, d_ff_28_q, d_ff_29_q,
       d_ff_30_q, d_ff_31_q, d_ff_32_q, d_ff_33_q, d_ff_34_q, d_ff_35_q, d_ff_37_q, d_ff_38_q, d_ff_39_q,
       d_ff_40_q, d_ff_41_q, d_ff_42_q, d_ff_43_q, d_ff_44_q, d_ff_45_q, d_ff_46_q;

  D_Flip_Flop #(.trigger("high")) d_ff_1 (.clk(C1), .D(D), .Q(d_ff_1_q));  // open: Qn, preset, en, reset
  D_Flip_Flop #(.trigger("high")) d_ff_2 (.clk(C1), .D(d_ff_42_q), .Q(d_ff_2_q));  // open: Qn, preset, en, reset
  D_Flip_Flop #(.trigger("high")) d_ff_3 (.clk(C1), .D(d_ff_43_q), .Q(d_ff_3_q));  // open: Qn, preset, en, reset
  D_Flip_Flop #(.trigger("high")) d_ff_4 (.clk(C1), .D(d_ff_44_q), .Q(d_ff_4_q));  // open: Qn, preset, en, reset
  D_Flip_Flop #(.trigger("high")) d_ff_5 (.clk(C1), .D(d_ff_45_q), .Q(d_ff_5_q));  // open: Qn, preset, en, reset
  D_Flip_Flop #(.trigger("high")) d_ff_6 (.clk(C1), .D(d_ff_46_q), .Q(d_ff_6_q));  // open: Qn, preset, en, reset
  D_Flip_Flop #(.trigger("high")) d_ff_7 (.clk(C2), .D(d_ff_1_q), .Q(d_ff_7_q));  // open: Qn, preset, en, reset
  D_Flip_Flop #(.trigger("high")) d_ff_8 (.clk(C2), .D(d_ff_2_q), .Q(d_ff_8_q));  // open: Qn, preset, en, reset
  D_Flip_Flop #(.trigger("high")) d_ff_9 (.clk(C2), .D(d_ff_3_q), .Q(d_ff_9_q));  // open: Qn, preset, en, reset
  D_Flip_Flop #(.trigger("high")) d_ff_10 (.clk(C2), .D(d_ff_4_q), .Q(d_ff_10_q));  // open: Qn, preset, en, reset
  D_Flip_Flop #(.trigger("high")) d_ff_11 (.clk(C2), .D(d_ff_5_q), .Q(d_ff_11_q));  // open: Qn, preset, en, reset
  D_Flip_Flop #(.trigger("high")) d_ff_12 (.clk(C2), .D(d_ff_6_q), .Q(Q42));  // open: Qn, preset, en, reset
  D_Flip_Flop #(.trigger("high")) d_ff_13 (.clk(C1), .D(d_ff_7_q), .Q(d_ff_13_q));  // open: Qn, preset, en, reset
  D_Flip_Flop #(.trigger("high")) d_ff_14 (.clk(C1), .D(d_ff_8_q), .Q(d_ff_14_q));  // open: Qn, preset, en, reset
  D_Flip_Flop #(.trigger("high")) d_ff_15 (.clk(C1), .D(d_ff_9_q), .Q(d_ff_15_q));  // open: Qn, preset, en, reset
  D_Flip_Flop #(.trigger("high")) d_ff_16 (.clk(C1), .D(d_ff_10_q), .Q(d_ff_16_q));  // open: Qn, preset, en, reset
  D_Flip_Flop #(.trigger("high")) d_ff_17 (.clk(C1), .D(d_ff_11_q), .Q(d_ff_17_q));  // open: Qn, preset, en, reset
  D_Flip_Flop #(.trigger("high")) d_ff_18 (.clk(C1), .D(Q42), .Q(d_ff_18_q));  // open: Qn, preset, en, reset
  D_Flip_Flop #(.trigger("high")) d_ff_19 (.clk(C2), .D(d_ff_13_q), .Q(d_ff_19_q));  // open: Qn, preset, en, reset
  D_Flip_Flop #(.trigger("high")) d_ff_20 (.clk(C2), .D(d_ff_14_q), .Q(d_ff_20_q));  // open: Qn, preset, en, reset
  D_Flip_Flop #(.trigger("high")) d_ff_21 (.clk(C2), .D(d_ff_15_q), .Q(d_ff_21_q));  // open: Qn, preset, en, reset
  D_Flip_Flop #(.trigger("high")) d_ff_22 (.clk(C2), .D(d_ff_16_q), .Q(d_ff_22_q));  // open: Qn, preset, en, reset
  D_Flip_Flop #(.trigger("high")) d_ff_23 (.clk(C2), .D(d_ff_17_q), .Q(d_ff_23_q));  // open: Qn, preset, en, reset
  D_Flip_Flop #(.trigger("high")) d_ff_24 (.clk(C2), .D(d_ff_18_q), .Q(d_ff_24_q));  // open: Qn, preset, en, reset
  D_Flip_Flop #(.trigger("high")) d_ff_25 (.clk(C1), .D(d_ff_19_q), .Q(d_ff_25_q));  // open: Qn, preset, en, reset
  D_Flip_Flop #(.trigger("high")) d_ff_26 (.clk(C1), .D(d_ff_20_q), .Q(d_ff_26_q));  // open: Qn, preset, en, reset
  D_Flip_Flop #(.trigger("high")) d_ff_27 (.clk(C1), .D(d_ff_21_q), .Q(d_ff_27_q));  // open: Qn, preset, en, reset
  D_Flip_Flop #(.trigger("high")) d_ff_28 (.clk(C1), .D(d_ff_22_q), .Q(d_ff_28_q));  // open: Qn, preset, en, reset
  D_Flip_Flop #(.trigger("high")) d_ff_29 (.clk(C1), .D(d_ff_23_q), .Q(d_ff_29_q));  // open: Qn, preset, en, reset
  D_Flip_Flop #(.trigger("high")) d_ff_30 (.clk(C1), .D(d_ff_24_q), .Q(d_ff_30_q));  // open: Qn, preset, en, reset
  D_Flip_Flop #(.trigger("high")) d_ff_31 (.clk(C2), .D(d_ff_25_q), .Q(d_ff_31_q));  // open: Qn, preset, en, reset
  D_Flip_Flop #(.trigger("high")) d_ff_32 (.clk(C2), .D(d_ff_26_q), .Q(d_ff_32_q));  // open: Qn, preset, en, reset
  D_Flip_Flop #(.trigger("high")) d_ff_33 (.clk(C2), .D(d_ff_27_q), .Q(d_ff_33_q));  // open: Qn, preset, en, reset
  D_Flip_Flop #(.trigger("high")) d_ff_34 (.clk(C2), .D(d_ff_28_q), .Q(d_ff_34_q));  // open: Qn, preset, en, reset
  D_Flip_Flop #(.trigger("high")) d_ff_35 (.clk(C2), .D(d_ff_29_q), .Q(d_ff_35_q));  // open: Qn, preset, en, reset
  D_Flip_Flop #(.trigger("high")) d_ff_36 (.clk(C2), .D(d_ff_30_q), .Q(Q));  // open: Qn, preset, en, reset
  D_Flip_Flop #(.trigger("high")) d_ff_37 (.clk(C1), .D(d_ff_31_q), .Q(d_ff_37_q));  // open: Qn, preset, en, reset
  D_Flip_Flop #(.trigger("high")) d_ff_38 (.clk(C1), .D(d_ff_32_q), .Q(d_ff_38_q));  // open: Qn, preset, en, reset
  D_Flip_Flop #(.trigger("high")) d_ff_39 (.clk(C1), .D(d_ff_33_q), .Q(d_ff_39_q));  // open: Qn, preset, en, reset
  D_Flip_Flop #(.trigger("high")) d_ff_40 (.clk(C1), .D(d_ff_34_q), .Q(d_ff_40_q));  // open: Qn, preset, en, reset
  D_Flip_Flop #(.trigger("high")) d_ff_41 (.clk(C1), .D(d_ff_35_q), .Q(d_ff_41_q));  // open: Qn, preset, en, reset
  D_Flip_Flop #(.trigger("high")) d_ff_42 (.clk(C2), .D(d_ff_37_q), .Q(d_ff_42_q));  // open: Qn, preset, en, reset
  D_Flip_Flop #(.trigger("high")) d_ff_43 (.clk(C2), .D(d_ff_38_q), .Q(d_ff_43_q));  // open: Qn, preset, en, reset
  D_Flip_Flop #(.trigger("high")) d_ff_44 (.clk(C2), .D(d_ff_39_q), .Q(d_ff_44_q));  // open: Qn, preset, en, reset
  D_Flip_Flop #(.trigger("high")) d_ff_45 (.clk(C2), .D(d_ff_40_q), .Q(d_ff_45_q));  // open: Qn, preset, en, reset
  D_Flip_Flop #(.trigger("high")) d_ff_46 (.clk(C2), .D(d_ff_41_q), .Q(d_ff_46_q));  // open: Qn, preset, en, reset
endmodule

module TIMERS (
  input  FCLK2,
  input  FCLK1,
  input  g_68,
  input  g_368,
  input  g_1932,
  input  g_66,
  input  g_1913,
  input  g_1947,
  input  g_1917,
  input  g_1946,
  input  g_1945,
  input  g_1944,
  input  g_1943,
  input  g_1942,
  input  g_1941,
  input  g_1940,
  input  g_1939,
  input  g_77,
  input  g_74,
  output g_800,
  output g_805,
  output g_566,
  output g_770,
  output g_767,
  output KEY_ON,
  output g_655,
  output g_654,
  output g_763,
  output g_764
);

  wire _524_out, _525_out, _526_out, _527_q, _528_2_out, _528_out, _529_out, _530_out, _531_out, _532_out,
       _533_q, _534_2_out, _534_out, _535_out, _536_out, _537_q, _538_2_out, _538_out, _539_out, _540_out,
       _541_q, _542_2_out, _542_out, _543_out, _544_out, _545_q, _546_2_out, _546_out, _547_out, _548_out,
       _549_q, _550_2_out, _550_out, _551_out, _552_out, _553_out, _554_out, _555_out, _556_out, _557_out,
       _558_out, _559_out, _560_out, _561_q, _562_out, _563_co, _563_q, _564_out, _565_co, _565_q, _567_q,
       _568_out, _569_co, _569_q, _570_out, _571_out, _572_out, _573_out, _574_out, _575_out, _576_out,
       _577_out, _578_out, _579_out, _580_2_out, _580_3_out, _580_out, _581_out, _582_out, _583_2_out,
       _583_3_out, _583_out, _584_out, _585_2_out, _585_3_out, _585_out, _586_2_out, _586_3_out, _586_out,
       _587_out, _588_2_out, _588_out, _589_out, _590_2_out, _590_3_out, _590_out, _592_2_out, _592_3_out,
       _592_out, _593_out, _594_2_out, _594_3_out, _594_out, _595_out, _596_out, _597_out, _598_2_out,
       _598_3_out, _598_out, _599_2_out, _599_3_out, _599_out, _600_out, _601_out, _602_2_out, _602_3_out,
       _602_out, _603_out, _604_2_out, _604_3_out, _604_out, _605_out, _606_2_out, _606_3_out, _606_out,
       _607_out, _608_2_out, _608_3_out, _608_out, _609_out, _610_2_out, _610_3_out, _610_out, _611_out,
       _612_2_out, _612_3_out, _612_out, _613_out, _614_2_out, _614_3_out, _614_out, _615_out, _616_2_out,
       _616_3_out, _616_out, _617_2_out, _617_3_out, _617_out, _618_out, _619_2_out, _619_3_out, _619_out,
       _620_out, _621_2_out, _621_3_out, _621_out, _622_out, _623_2_out, _623_3_out, _623_out, _624_out,
       _625_2_out, _625_3_out, _625_out, _626_out, _627_2_out, _627_3_out, _627_out, _628_out, _629_2_out,
       _629_3_out, _629_out, _630_out, _631_2_out, _631_3_out, _631_out, _632_out, _633_2_out, _633_3_out,
       _633_out, _634_out, _635_2_out, _635_3_out, _635_out, _636_out, _637_2_out, _637_3_out, _637_out,
       _638_out, _639_2_out, _639_3_out, _639_out, _640_out, _641_2_out, _641_3_out, _641_out, _642_out,
       _643_2_out, _643_3_out, _643_out, _644_out, _645_2_out, _645_3_out, _645_out, _646_out, _647_2_out,
       _647_3_out, _647_4_out, _647_out, _648_out, _649_2_out, _649_3_out, _649_out, _650_out, _656_q,
       _657_q, _658_q, _659_2_q, _659_q, _660_q, _661_q, _662_out, _663_out, _664_out, _665_out, _666_out,
       _667_q, _668_out, _670_2_q, _670_out, _671_q, _672_out, _673_q, _674_out, _675_q, _676_out, _677_q,
       _678_out, _680_out, _681_q, _682_out, _683_out, _684_q, _685_out, _686_q, _687_out, _688_q, _689_out,
       _690_q, _691_2_out, _691_out, _692_q, _694_q, _695_out, _696_2_out, _696_out, _697_q, _698_q,
       _699_out, _700_out, _701_out, _702_q, _703_out, _704_q, _705_2_out, _705_out, _706_q, _708_q,
       _709_out, _710_q, _711_out, _712_q, _713_out, _714_q, _715_out, _716_q, _717_out, _718_out, _719_q,
       _720_out, _721_q, _722_out, _723_q, _724_out, _725_q, _726_out, _727_q, _728_out, _729_q, _730_out,
       _731_q, _732_out, _733_out, _734_2_out, _734_out, _737_out, _741_2_out, _741_3_out, _741_out,
       _742_2_out, _742_3_out, _742_out, _743_2_out, _743_3_out, _743_out, _744_2_out, _744_3_out, _744_out,
       _745_co, _746_co, _747_co, _748_co, _749_co, _750_co, _751_co, _752_co, _753_co, _754_co, _755_co,
       _756_co, _757_co, _758_co, _759_co, _760_co, _761_co, _762_co, _765_out, _766_out, _768_out, _769_out,
       _771_out, _773_out, _774_out, _776_q, _777_q, _778_q, _779_q, _780_q, _782_out, _783_q, _784_q,
       _785_q, _787_out, _788_out, _790_out, _791_out, _793_q, _794_out, _795_out, _796_2_out, _796_out,
       _797_out, _798_out, _799_q, _801_out, _802_2_out, _802_out, _803_q, _804_out, _806_out, _807_out,
       _809_q, _810_nq, _811_q, _812_q, _813_out, _814_out, _815_out, _816_co, _817_co, _818_co, _819_co,
       _820_out, _821_out, _822_out, _823_out, _824_out, _825_q, g_786, not_1_out;

  not _579 (_579_out, g_1932);
  nor _556 (_556_out, g_1940, g_1942, g_1945, g_1943, g_1946);
  nor _555 (_555_out, g_1939, g_1942, g_1940, g_1943, g_1945, g_1946);
  nor _530 (_530_out, g_1939, g_1942, g_1943, g_1945, g_1946);
  nor _558 (_558_out, g_1943, g_1942, g_1945, g_1946);
  nor _553 (_553_out, g_1941, g_1940, g_1939, g_1943, g_1945, g_1946);
  nor _524 (_524_out, g_1939, g_1941, g_1942, g_1943, g_1945, g_1946);
  and _557 (_557_out, g_1917, g_1947, g_1939, g_1941, g_1944, _556_out);
  and _554 (_554_out, g_1917, g_1947, g_1941, g_1944, _555_out);
  and _531 (_531_out, g_1917, g_1947, g_1940, g_1944, g_1941, _530_out);
  and _559 (_559_out, g_1917, g_1940, g_1939, g_1947, g_1944, g_1941, _558_out);
  and _552 (_552_out, g_1917, g_1947, g_1942, g_1944, _553_out);
  and _525 (_525_out, g_1917, g_1947, g_1944, g_1940, _524_out);
  not _547 (_547_out, g_1917);
  not _543 (_543_out, g_1917);
  not _535 (_535_out, g_1917);
  not _539 (_539_out, g_1917);
  not _551 (_551_out, g_1917);
  not _529 (_529_out, g_1917);
  and _542 (_542_out, _547_out, _540_out);
  and _546 (_546_out, _543_out, _544_out);
  and _534 (_534_out, _535_out, _532_out);
  and _538 (_538_out, _539_out, _536_out);
  and _550 (_550_out, _551_out, _548_out);
  and _528 (_528_out, _529_out, _526_out);
  nor _542_2 (_542_2_out, _557_out, _542_out);
  nor _546_2 (_546_2_out, _554_out, _546_out);
  nor _534_2 (_534_2_out, _531_out, _534_out);
  nor _538_2 (_538_2_out, _559_out, _538_out);
  nor _550_2 (_550_2_out, _552_out, _550_out);
  nor _528_2 (_528_2_out, _525_out, _528_out);
  SR_BIT _541 (.C2(FCLK2), .C1(FCLK1), .D(_542_2_out), .Q(_541_q));  // open: nQ
  SR_BIT _545 (.C2(FCLK2), .C1(FCLK1), .D(_546_2_out), .Q(_545_q));  // open: nQ
  SR_BIT _533 (.C2(FCLK2), .C1(FCLK1), .D(_534_2_out), .Q(_533_q));  // open: nQ
  SR_BIT _537 (.C2(FCLK2), .C1(FCLK1), .D(_538_2_out), .Q(_537_q));  // open: nQ
  SR_BIT _549 (.C2(FCLK2), .C1(FCLK1), .D(_550_2_out), .Q(_549_q));  // open: nQ
  SR_BIT _527 (.C2(FCLK2), .C1(FCLK1), .D(_528_2_out), .Q(_527_q));  // open: nQ
  not _540 (_540_out, _541_q);
  not _544 (_544_out, _545_q);
  not _532 (_532_out, _533_q);
  not _536 (_536_out, _537_q);
  not _548 (_548_out, _549_q);
  not _526 (_526_out, _527_q);
  and _782 (_782_out, g_786, g_767);
  D_Flip_Flop #(.trigger("high")) _809 (.clk(g_66), .D(_692_q), .Q(_809_q));  // open: Qn, preset, en, reset
  D_Flip_Flop #(.trigger("high")) _780 (.clk(g_66), .D(_782_out), .Q(_780_q));  // open: Qn, preset, en, reset
  and _650 (_650_out, g_1913, g_1947, _540_out);
  and _611 (_611_out, g_1913, g_1947, _544_out);
  and _634 (_634_out, g_1913, g_1947, _532_out);
  and _646 (_646_out, g_1913, g_1947, _536_out);
  and _597 (_597_out, g_1913, g_1947, _548_out);
  and _582 (_582_out, g_1913, g_1947, _526_out);
  and _773 (_773_out, _780_q, g_74);
  D_Flip_Flop #(.trigger("high")) _793 (.clk(g_66), .D(_694_q), .Q(_793_q));  // open: Qn, preset, en, reset
  not _699 (_699_out, _650_out);
  not _700 (_700_out, _650_out);
  not _703 (_703_out, _611_out);
  not _705 (_705_out, _611_out);
  not _705_2 (_705_2_out, _611_out);
  not _709 (_709_out, _611_out);
  not _711 (_711_out, _611_out);
  not _713 (_713_out, _611_out);
  not _715 (_715_out, _611_out);
  not _718 (_718_out, _611_out);
  not _668 (_668_out, _634_out);
  not _670 (_670_out, _634_out);
  not _672 (_672_out, _634_out);
  not _674 (_674_out, _634_out);
  not _676 (_676_out, _634_out);
  not _678 (_678_out, _634_out);
  not _680 (_680_out, _634_out);
  not _683 (_683_out, _634_out);
  not _696 (_696_out, _646_out);
  not _696_2 (_696_2_out, _646_out);
  not _691 (_691_out, _646_out);
  not _689 (_689_out, _646_out);
  not _687 (_687_out, _646_out);
  not _685 (_685_out, _646_out);
  not _720 (_720_out, _597_out);
  not _722 (_722_out, _597_out);
  not _724 (_724_out, _597_out);
  not _726 (_726_out, _597_out);
  not _728 (_728_out, _597_out);
  not _730 (_730_out, _597_out);
  not _733 (_733_out, _597_out);
  not _663 (_663_out, _582_out);
  not _664 (_664_out, _582_out);
  not _665 (_665_out, _582_out);
  not _666 (_666_out, _582_out);
  and _578 (_578_out, _646_out, g_1943);
  and _647 (_647_out, _699_out, _697_q);
  and _647_2 (_647_2_out, _650_out, g_1939);
  and _649 (_649_out, _700_out, _698_q);
  and _649_2 (_649_2_out, _650_out, g_1940);
  and _617 (_617_out, _703_out, _702_q);
  and _617_2 (_617_2_out, _611_out, g_1939);
  and _625 (_625_out, _705_out, _704_q);
  and _625_2 (_625_2_out, _611_out, g_1940);
  and _623 (_623_out, _705_2_out, _706_q);
  and _623_2 (_623_2_out, _611_out, g_1941);
  and _621 (_621_out, _709_out, _708_q);
  and _621_2 (_621_2_out, _611_out, g_1942);
  and _619 (_619_out, _711_out, _710_q);
  and _619_2 (_619_2_out, _611_out, g_1943);
  and _616 (_616_out, _713_out, _712_q);
  and _616_2 (_616_2_out, _611_out, g_1944);
  and _614 (_614_out, _715_out, _714_q);
  and _614_2 (_614_2_out, _611_out, g_1945);
  and _612 (_612_out, _718_out, _716_q);
  and _612_2 (_612_2_out, _611_out, g_1946);
  and _577 (_577_out, _646_out, g_1944);
  and _588 (_588_out, _668_out, _667_q);
  and _588_2 (_588_2_out, _634_out, g_1939);
  and _590 (_590_out, _670_out, _659_q);
  and _590_2 (_590_2_out, _634_out, g_1940);
  and _592 (_592_out, _672_out, _671_q);
  and _592_2 (_592_2_out, _634_out, g_1941);
  and _594 (_594_out, _674_out, _673_q);
  and _594_2 (_594_2_out, _634_out, g_1942);
  and _627 (_627_out, _676_out, _675_q);
  and _627_2 (_627_2_out, _634_out, g_1943);
  and _629 (_629_out, _678_out, _677_q);
  and _629_2 (_629_2_out, _634_out, g_1944);
  and _631 (_631_out, _680_out, _670_2_q);
  and _631_2 (_631_2_out, _634_out, g_1945);
  and _633 (_633_out, _683_out, _681_q);
  and _633_2 (_633_2_out, _634_out, g_1946);
  and _645 (_645_out, _696_out, _694_q);
  and _645_2 (_645_2_out, _646_out, g_1939);
  and _643 (_643_out, _696_2_out, _692_q);
  and _643_2 (_643_2_out, _646_out, g_1940);
  and _641 (_641_out, _691_out, _690_q);
  and _641_2 (_641_2_out, _646_out, g_1941);
  and _639 (_639_out, _689_out, _688_q);
  and _639_2 (_639_2_out, _646_out, g_1942);
  and _637 (_637_out, _687_out, _686_q);
  and _637_2 (_637_2_out, _646_out, g_1945);
  and _635 (_635_out, _685_out, _684_q);
  and _635_2 (_635_2_out, _646_out, g_1946);
  and _610 (_610_out, _720_out, _719_q);
  and _610_2 (_610_2_out, _597_out, g_1945);
  and _608 (_608_out, _722_out, _721_q);
  and _608_2 (_608_2_out, _597_out, g_1944);
  and _606 (_606_out, _724_out, _723_q);
  and _606_2 (_606_2_out, _597_out, g_1946);
  and _604 (_604_out, _726_out, _725_q);
  and _604_2 (_604_2_out, _597_out, g_1943);
  and _602 (_602_out, _728_out, _727_q);
  and _602_2 (_602_2_out, _597_out, g_1941);
  and _599 (_599_out, _730_out, _729_q);
  and _599_2 (_599_2_out, _597_out, g_1940);
  and _598 (_598_out, _733_out, _731_q);
  and _598_2 (_598_2_out, _597_out, g_1939);
  and _580 (_580_out, _663_out, _658_q);
  and _580_2 (_580_2_out, _582_out, g_1942);
  and _586 (_586_out, _664_out, _659_2_q);
  and _586_2 (_586_2_out, _582_out, g_1941);
  and _585 (_585_out, _665_out, _660_q);
  and _585_2 (_585_2_out, _582_out, g_1940);
  and _583 (_583_out, _666_out, _661_q);
  and _583_2 (_583_2_out, _582_out, g_1939);
  nor _647_3 (_647_3_out, _647_out, _647_2_out);
  nor _649_3 (_649_3_out, _649_out, _649_2_out);
  nor _617_3 (_617_3_out, _617_out, _617_2_out);
  nor _625_3 (_625_3_out, _625_out, _625_2_out);
  nor _623_3 (_623_3_out, _623_out, _623_2_out);
  nor _621_3 (_621_3_out, _621_out, _621_2_out);
  nor _619_3 (_619_3_out, _619_out, _619_2_out);
  nor _616_3 (_616_3_out, _616_out, _616_2_out);
  nor _614_3 (_614_3_out, _614_out, _614_2_out);
  nor _612_3 (_612_3_out, _612_out, _612_2_out);
  nor _647_4 (_647_4_out, _588_out, _588_2_out);
  nor _590_3 (_590_3_out, _590_out, _590_2_out);
  nor _592_3 (_592_3_out, _592_out, _592_2_out);
  nor _594_3 (_594_3_out, _594_out, _594_2_out);
  nor _627_3 (_627_3_out, _627_out, _627_2_out);
  nor _629_3 (_629_3_out, _629_out, _629_2_out);
  nor _631_3 (_631_3_out, _631_out, _631_2_out);
  nor _633_3 (_633_3_out, _633_out, _633_2_out);
  nor _645_3 (_645_3_out, _645_out, _645_2_out);
  nor _643_3 (_643_3_out, _643_out, _643_2_out);
  nor _641_3 (_641_3_out, _641_out, _641_2_out);
  nor _639_3 (_639_3_out, _639_out, _639_2_out);
  nor _637_3 (_637_3_out, _637_out, _637_2_out);
  nor _635_3 (_635_3_out, _635_out, _635_2_out);
  nor _610_3 (_610_3_out, _610_out, _610_2_out);
  nor _608_3 (_608_3_out, _608_out, _608_2_out);
  nor _606_3 (_606_3_out, _606_out, _606_2_out);
  nor _604_3 (_604_3_out, _604_out, _604_2_out);
  nor _602_3 (_602_3_out, _602_out, _602_2_out);
  nor _599_3 (_599_3_out, _599_out, _599_2_out);
  nor _598_3 (_598_3_out, _598_out, _598_2_out);
  nor _580_3 (_580_3_out, _580_out, _580_2_out);
  nor _586_3 (_586_3_out, _586_out, _586_2_out);
  nor _585_3 (_585_3_out, _585_out, _585_2_out);
  nor _583_3 (_583_3_out, _583_out, _583_2_out);
  nor _648 (_648_out, _579_out, _647_3_out);
  nor _701 (_701_out, _579_out, _649_3_out);
  nor _626 (_626_out, _579_out, _617_3_out);
  nor _624 (_624_out, _579_out, _625_3_out);
  nor _622 (_622_out, _579_out, _623_3_out);
  nor _620 (_620_out, _579_out, _621_3_out);
  nor _618 (_618_out, _579_out, _619_3_out);
  nor _615 (_615_out, _579_out, _616_3_out);
  nor _613 (_613_out, _579_out, _614_3_out);
  nor _717 (_717_out, _579_out, _612_3_out);
  nor _589 (_589_out, _579_out, _647_4_out);
  nor _691_2 (_691_2_out, _579_out, _590_3_out);
  nor _593 (_593_out, _579_out, _592_3_out);
  nor _595 (_595_out, _579_out, _594_3_out);
  nor _628 (_628_out, _579_out, _627_3_out);
  nor _630 (_630_out, _579_out, _629_3_out);
  nor _632 (_632_out, _579_out, _631_3_out);
  nor _682 (_682_out, _579_out, _633_3_out);
  or _570 (_570_out, _579_out, g_77);
  nor _695 (_695_out, _579_out, _645_3_out);
  nor _644 (_644_out, _579_out, _643_3_out);
  nor _642 (_642_out, _579_out, _641_3_out);
  nor _640 (_640_out, _579_out, _639_3_out);
  nor _638 (_638_out, _579_out, _637_3_out);
  nor _636 (_636_out, _579_out, _635_3_out);
  nor _609 (_609_out, _579_out, _610_3_out);
  nor _607 (_607_out, _579_out, _608_3_out);
  nor _605 (_605_out, _579_out, _606_3_out);
  nor _603 (_603_out, _579_out, _604_3_out);
  nor _601 (_601_out, _579_out, _602_3_out);
  nor _600 (_600_out, _579_out, _599_3_out);
  nor _732 (_732_out, _579_out, _598_3_out);
  nor _581 (_581_out, _579_out, _580_3_out);
  nor _587 (_587_out, _579_out, _586_3_out);
  nor _584 (_584_out, _579_out, _585_3_out);
  nor _662 (_662_out, _579_out, _583_3_out);
  and _790 (_790_out, g_68, _793_q);
  SR_BIT _657 (.C2(FCLK2), .C1(FCLK1), .D(_578_out), .Q(_657_q));  // open: nQ
  SR_BIT _785 (.C2(FCLK2), .C1(FCLK1), .D(_793_q), .Q(_785_q));  // open: nQ
  SR_BIT _784 (.C2(FCLK2), .C1(FCLK1), .D(g_786), .Q(_784_q));  // open: nQ
  or _786 (g_786, _787_out, _783_q);
  SR_BIT _697 (.C2(FCLK2), .C1(FCLK1), .D(_648_out), .Q(_697_q));  // open: nQ
  SR_BIT _698 (.C2(FCLK2), .C1(FCLK1), .D(_701_out), .Q(_698_q));  // open: nQ
  SR_BIT _702 (.C2(FCLK2), .C1(FCLK1), .D(_626_out), .Q(_702_q));  // open: nQ
  SR_BIT _704 (.C2(FCLK2), .C1(FCLK1), .D(_624_out), .Q(_704_q));  // open: nQ
  SR_BIT _706 (.C2(FCLK2), .C1(FCLK1), .D(_622_out), .Q(_706_q));  // open: nQ
  SR_BIT _708 (.C2(FCLK2), .C1(FCLK1), .D(_620_out), .Q(_708_q));  // open: nQ
  SR_BIT _710 (.C2(FCLK2), .C1(FCLK1), .D(_618_out), .Q(_710_q));  // open: nQ
  SR_BIT _712 (.C2(FCLK2), .C1(FCLK1), .D(_615_out), .Q(_712_q));  // open: nQ
  SR_BIT _714 (.C2(FCLK2), .C1(FCLK1), .D(_613_out), .Q(_714_q));  // open: nQ
  SR_BIT _716 (.C2(FCLK2), .C1(FCLK1), .D(_717_out), .Q(_716_q));  // open: nQ
  SR_BIT _783 (.C2(FCLK2), .C1(FCLK1), .D(_745_co), .Q(_783_q));  // open: nQ
  SR_BIT _825 (.C2(FCLK2), .C1(FCLK1), .D(_819_co), .Q(_825_q));  // open: nQ
  SR_BIT _811 (.C2(FCLK2), .C1(FCLK1), .D(_809_q), .Q(_811_q));  // open: nQ
  SR_BIT _812 (.C2(FCLK2), .C1(FCLK1), .D(_813_out), .Q(_812_q));  // open: nQ
  or _813 (_813_out, _814_out, _810_nq);
  SR_BIT _667 (.C2(FCLK2), .C1(FCLK1), .D(_589_out), .Q(_667_q));  // open: nQ
  SR_BIT _659 (.C2(FCLK2), .C1(FCLK1), .D(_691_2_out), .Q(_659_q));  // open: nQ
  SR_BIT _671 (.C2(FCLK2), .C1(FCLK1), .D(_593_out), .Q(_671_q));  // open: nQ
  SR_BIT _673 (.C2(FCLK2), .C1(FCLK1), .D(_595_out), .Q(_673_q));  // open: nQ
  SR_BIT _675 (.C2(FCLK2), .C1(FCLK1), .D(_628_out), .Q(_675_q));  // open: nQ
  SR_BIT _677 (.C2(FCLK2), .C1(FCLK1), .D(_630_out), .Q(_677_q));  // open: nQ
  SR_BIT _670_2 (.C2(FCLK2), .C1(FCLK1), .D(_632_out), .Q(_670_2_q));  // open: nQ
  SR_BIT _681 (.C2(FCLK2), .C1(FCLK1), .D(_682_out), .Q(_681_q));  // open: nQ
  SR_BIT _810 (.C2(FCLK2), .C1(FCLK1), .D(_755_co), .nQ(_810_nq));  // open: Q
  SR_BIT _694 (.C2(FCLK2), .C1(FCLK1), .D(_695_out), .Q(_694_q));  // open: nQ
  SR_BIT _692 (.C2(FCLK2), .C1(FCLK1), .D(_644_out), .Q(_692_q));  // open: nQ
  SR_BIT _690 (.C2(FCLK2), .C1(FCLK1), .D(_642_out), .Q(_690_q));  // open: nQ
  SR_BIT _688 (.C2(FCLK2), .C1(FCLK1), .D(_640_out), .Q(_688_q));  // open: nQ
  SR_BIT _686 (.C2(FCLK2), .C1(FCLK1), .D(_638_out), .Q(_686_q));  // open: nQ
  SR_BIT _684 (.C2(FCLK2), .C1(FCLK1), .D(_636_out), .Q(_684_q));  // open: nQ
  SR_BIT _719 (.C2(FCLK2), .C1(FCLK1), .D(_609_out), .Q(_719_q));  // open: nQ
  SR_BIT _721 (.C2(FCLK2), .C1(FCLK1), .D(_607_out), .Q(_721_q));  // open: nQ
  SR_BIT _723 (.C2(FCLK2), .C1(FCLK1), .D(_605_out), .Q(_723_q));  // open: nQ
  SR_BIT _725 (.C2(FCLK2), .C1(FCLK1), .D(_603_out), .Q(_725_q));  // open: nQ
  SR_BIT _727 (.C2(FCLK2), .C1(FCLK1), .D(_601_out), .Q(_727_q));  // open: nQ
  SR_BIT _729 (.C2(FCLK2), .C1(FCLK1), .D(_600_out), .Q(_729_q));  // open: nQ
  SR_BIT _731 (.C2(FCLK2), .C1(FCLK1), .D(_732_out), .Q(_731_q));  // open: nQ
  SR_BIT _658 (.C2(FCLK2), .C1(FCLK1), .D(_581_out), .Q(_658_q));  // open: nQ
  SR_BIT _659_2 (.C2(FCLK2), .C1(FCLK1), .D(_587_out), .Q(_659_2_q));  // open: nQ
  SR_BIT _660 (.C2(FCLK2), .C1(FCLK1), .D(_584_out), .Q(_660_q));  // open: nQ
  SR_BIT _661 (.C2(FCLK2), .C1(FCLK1), .D(_662_out), .Q(_661_q));  // open: nQ
  not _824 (_824_out, _809_q);
  not _788 (_788_out, _785_q);
  not not_1 (not_1_out, _793_q);
  and _823 (_823_out, _809_q, _825_q);
  not _815 (_815_out, _811_q);
  buf _655 (g_655, _658_q);
  buf _654 (g_654, _659_2_q);
  buf _763 (g_763, _660_q);
  buf _764 (g_764, _661_q);
  or _791 (_791_out, g_368, _790_out);
  or _821 (_821_out, _657_q, _579_out);
  and _787 (_787_out, _788_out, _793_q);
  not _771 (_771_out, _784_q);
  CNT_BIT_LD _754 (
    .C2(FCLK2), .C1(FCLK1), .RES(not_1_out), .CIN(_791_out), .L(_784_q), .D(_697_q), .CO(_754_co));  // open: Q, nQ
  CNT_BIT_LD _753 (
    .C2(FCLK2), .C1(FCLK1), .RES(not_1_out), .CIN(_754_co), .L(_784_q), .D(_698_q), .CO(_753_co));  // open: Q, nQ
  CNT_BIT_LD _752 (
    .C2(FCLK2), .C1(FCLK1), .RES(not_1_out), .CIN(_753_co), .L(_784_q), .D(_702_q), .CO(_752_co));  // open: Q, nQ
  CNT_BIT_LD _751 (
    .C2(FCLK2), .C1(FCLK1), .RES(not_1_out), .CIN(_752_co), .L(_784_q), .D(_704_q), .CO(_751_co));  // open: Q, nQ
  CNT_BIT_LD _750 (
    .C2(FCLK2), .C1(FCLK1), .RES(not_1_out), .CIN(_751_co), .L(_784_q), .D(_706_q), .CO(_750_co));  // open: Q, nQ
  CNT_BIT_LD _749 (
    .C2(FCLK2), .C1(FCLK1), .RES(not_1_out), .CIN(_750_co), .L(_784_q), .D(_708_q), .CO(_749_co));  // open: Q, nQ
  CNT_BIT_LD _748 (
    .C2(FCLK2), .C1(FCLK1), .RES(not_1_out), .CIN(_749_co), .L(_784_q), .D(_710_q), .CO(_748_co));  // open: Q, nQ
  CNT_BIT_LD _747 (
    .C2(FCLK2), .C1(FCLK1), .RES(not_1_out), .CIN(_748_co), .L(_784_q), .D(_712_q), .CO(_747_co));  // open: Q, nQ
  CNT_BIT_LD _746 (
    .C2(FCLK2), .C1(FCLK1), .RES(not_1_out), .CIN(_747_co), .L(_784_q), .D(_714_q), .CO(_746_co));  // open: Q, nQ
  CNT_BIT_LD _745 (
    .C2(FCLK2), .C1(FCLK1), .RES(not_1_out), .CIN(_746_co), .L(_784_q), .D(_716_q), .CO(_745_co));  // open: Q, nQ
  or _822 (_822_out, g_368, _823_out);
  and _814 (_814_out, _815_out, _809_q);
  not _765 (_765_out, _812_q);
  CNT_BIT_LD _762 (
    .C2(FCLK2), .C1(FCLK1), .RES(_824_out), .CIN(_822_out), .L(_812_q), .D(_667_q), .CO(_762_co));  // open: Q, nQ
  CNT_BIT_LD _761 (
    .C2(FCLK2), .C1(FCLK1), .RES(_824_out), .CIN(_762_co), .L(_812_q), .D(_659_q), .CO(_761_co));  // open: Q, nQ
  CNT_BIT_LD _760 (
    .C2(FCLK2), .C1(FCLK1), .RES(_824_out), .CIN(_761_co), .L(_812_q), .D(_671_q), .CO(_760_co));  // open: Q, nQ
  CNT_BIT_LD _759 (
    .C2(FCLK2), .C1(FCLK1), .RES(_824_out), .CIN(_760_co), .L(_812_q), .D(_673_q), .CO(_759_co));  // open: Q, nQ
  CNT_BIT_LD _758 (
    .C2(FCLK2), .C1(FCLK1), .RES(_824_out), .CIN(_759_co), .L(_812_q), .D(_675_q), .CO(_758_co));  // open: Q, nQ
  CNT_BIT_LD _757 (
    .C2(FCLK2), .C1(FCLK1), .RES(_824_out), .CIN(_758_co), .L(_812_q), .D(_677_q), .CO(_757_co));  // open: Q, nQ
  CNT_BIT_LD _756 (
    .C2(FCLK2), .C1(FCLK1), .RES(_824_out), .CIN(_757_co), .L(_812_q), .D(_670_2_q), .CO(_756_co));  // open: Q, nQ
  CNT_BIT_LD _755 (
    .C2(FCLK2), .C1(FCLK1), .RES(_824_out), .CIN(_756_co), .L(_812_q), .D(_681_q), .CO(_755_co));  // open: Q, nQ
  not _766 (_766_out, _686_q);
  nor _769 (_769_out, _686_q, _684_q);
  nand _768 (_768_out, _766_out, _684_q);
  not _770 (g_770, _769_out);
  not _767 (g_767, _768_out);
  not _734 (_734_out, _734_2_out);
  not _737 (_737_out, _579_out);
  not _797 (_797_out, _821_out);
  not _794 (_794_out, _821_out);
  not _801 (_801_out, _820_out);
  not _807 (_807_out, _820_out);
  or _571 (_571_out, _570_out, g_566);
  not _734_2 (_734_2_out, _596_out);
  and _741 (_741_out, _734_2_out, _778_q);
  and _741_2 (_741_2_out, _719_q, _734_out);
  and _742 (_742_out, _734_2_out, _777_q);
  and _742_2 (_742_2_out, _721_q, _734_out);
  and _743 (_743_out, _734_2_out, _776_q);
  and _743_2 (_743_2_out, _723_q, _734_out);
  and _744 (_744_out, _734_2_out, _737_out, _779_q);
  and _744_2 (_744_2_out, _725_q, _734_out);
  nor _774 (_774_out, _779_q, _773_out);
  and _796 (_796_out, _798_out, _797_out);
  and _795 (_795_out, _794_out, _783_q, _690_q);
  and _802 (_802_out, _804_out, _801_out);
  and _806 (_806_out, _807_out, _810_nq, _688_q);
  CNT_BIT _816 (.C2(FCLK2), .C1(FCLK1), .CIN(g_68), .RES(_579_out), .CO(_816_co));  // open: Q, nQ
  CNT_BIT _817 (.C2(FCLK2), .C1(FCLK1), .CIN(_816_co), .RES(_579_out), .CO(_817_co));  // open: Q, nQ
  CNT_BIT _818 (.C2(FCLK2), .C1(FCLK1), .CIN(_817_co), .RES(_579_out), .CO(_818_co));  // open: Q, nQ
  CNT_BIT _819 (.C2(FCLK2), .C1(FCLK1), .CIN(_818_co), .RES(_579_out), .CO(_819_co));  // open: Q, nQ
  CNT_BIT _569 (.C2(FCLK2), .C1(FCLK1), .CIN(1'b1), .RES(_571_out), .Q(_569_q), .CO(_569_co));  // open: nQ
  CNT_BIT _567 (.C2(FCLK2), .C1(FCLK1), .CIN(_569_co), .RES(_571_out), .Q(_567_q));  // open: nQ, CO
  CNT_BIT _565 (.C2(FCLK2), .C1(FCLK1), .CIN(g_566), .RES(_570_out), .Q(_565_q), .CO(_565_co));  // open: nQ
  CNT_BIT _563 (.C2(FCLK2), .C1(FCLK1), .CIN(_565_co), .RES(_570_out), .Q(_563_q), .CO(_563_co));  // open: nQ
  CNT_BIT _561 (.C2(FCLK2), .C1(FCLK1), .CIN(_563_co), .RES(_570_out), .Q(_561_q));  // open: nQ, CO
  or _741_3 (_741_3_out, _741_out, _741_2_out);
  or _742_3 (_742_3_out, _742_out, _742_2_out);
  or _743_3 (_743_3_out, _743_out, _743_2_out);
  or _744_3 (_744_3_out, _744_out, _744_2_out);
  not _775 (KEY_ON, _774_out);
  nor _796_2 (_796_2_out, _796_out, _795_out);
  nor _802_2 (_802_2_out, _802_out, _806_out);
  SDELAY6 _779 (.C2(FCLK2), .C1(FCLK1), .D(_741_3_out), .Q(_779_q));
  SDELAY6 _778 (.C2(FCLK2), .C1(FCLK1), .D(_742_3_out), .Q(_778_q));
  SDELAY6 _777 (.C2(FCLK2), .C1(FCLK1), .D(_743_3_out), .Q(_777_q));
  SDELAY6 _776 (.C2(FCLK2), .C1(FCLK1), .D(_744_3_out), .Q(_776_q));
  SR_BIT _799 (.C2(FCLK2), .C1(FCLK1), .D(_796_2_out), .Q(_799_q));  // open: nQ
  SR_BIT _656 (.C2(FCLK2), .C1(FCLK1), .D(_577_out), .Q(_656_q));  // open: nQ
  SR_BIT _803 (.C2(FCLK2), .C1(FCLK1), .D(_802_2_out), .Q(_803_q));  // open: nQ
  not _568 (_568_out, _569_q);
  not _566 (g_566, _567_q);
  not _564 (_564_out, _565_q);
  not _562 (_562_out, _563_q);
  not _560 (_560_out, _561_q);
  not _800 (g_800, _798_out);
  not _798 (_798_out, _799_q);
  or _820 (_820_out, _656_q, _579_out);
  not _804 (_804_out, _803_q);
  not _805 (g_805, _804_out);
  xor _576 (_576_out, _731_q, _568_out);
  xor _575 (_575_out, _729_q, g_566);
  xor _574 (_574_out, _727_q, _564_out);
  xor _573 (_573_out, 1'b0, _562_out);
  xor _572 (_572_out, 1'b0, _560_out);
  nor _596 (_596_out, _576_out, _575_out, _574_out, _573_out, _572_out);

  // Other names for the same wires on the sheet: DB0 = g_1939; DB1 = g_1940; DB2 = g_1941; DB3 = g_1942; DB4 = g_1943;
  //   DB5 = g_1944; DB6 = g_1945; DB7 = g_1946

  // Notes on the sheet:
  //   542
  //   A2
  //   A1
  //   546
  //   A2
  //   A1
  //   534
  //   A2
  //   A1
  //   538
  //   A2
  //   A1
  //   550
  //   A2
  //   A1
  //   528
  //   A2
  //   A1
  //   AOI21
  //   B
  //   AOI21
  //   B
  //   AOI21
  //   B
  //   AOI21
  //   B
  //   AOI21
  //   B
  //   AOI21
  //   B
  //   SLATCH
  //   SLATCH
  //   SLATCH
  //   789
  //   /L
  //   /L
  //   A1
  //   A2
  //   A1
  //   A2
  //   796
  //   B
  //   802
  //   B
  //   AOI21
  //   AOI21
endmodule

// CNT BIT LD
module CNT_BIT_LD (
  input  C2,
  input  C1,
  input  RES,
  input  CIN,
  input  L,
  input  D,
  output Q,
  output nQ,
  output CO
);

  wire d_ff_1_q, multiplexer_1_out, not_1_out, xor_1_out;

  not not_1 (not_1_out, RES);
  xor xor_1 (xor_1_out, Q, CIN);
  and and_1 (CO, Q, CIN);
  Multiplexer #(.disabled(0)) multiplexer_1 (
    .in0(xor_1_out), .in1(D), .out(multiplexer_1_out), .sel(L), .en(not_1_out));
  D_Flip_Flop #(.trigger("high")) d_ff_1 (
    .clk(C1), .D(multiplexer_1_out), .Q(d_ff_1_q));  // open: Qn, preset, en, reset
  D_Flip_Flop #(.trigger("high")) d_ff_2 (.clk(C2), .D(d_ff_1_q), .Q(Q), .Qn(nQ));  // open: preset, en, reset
endmodule
