// Logisim project regblock_idu_ff.circ as structural Verilog: 2 circuits, main circuit main
module main (
  input  idu_ck,
  input  idu_cck,
  input  idu_ck2,
  input  idu_cck2,
  input  n_from_regs,
  input  n_idu_clr,
  input  ci,
  output n_to_regs,
  output co,
  output xi
);

  wire multiplexer_1_out, multiplexer_2_out, nand_2_out, nand_3_out, not_1_out, not_2_out, not_3_out,
       not_4_out, not_5_out, not_6_out, or_1_out, transp_latch_1_out_2;

  transp_latch transp_latch_1 (.in_1(n_from_regs), .out_2(transp_latch_1_out_2));
  nand nand_1 (n_to_regs, n_idu_clr, multiplexer_1_out);
  not not_1 (not_1_out, multiplexer_1_out);
  not not_2 (not_2_out, nand_2_out);
  Multiplexer multiplexer_1 (.in0(not_2_out), .in1(not_3_out), .out(multiplexer_1_out), .sel(idu_ck));
  not not_3 (not_3_out, not_1_out);
  not not_4 (not_4_out, transp_latch_1_out_2);
  Multiplexer multiplexer_2 (.in0(not_4_out), .in1(not_5_out), .out(multiplexer_2_out), .sel(idu_ck2));
  not not_5 (not_5_out, not_6_out);
  not not_6 (not_6_out, multiplexer_2_out);
  not not_7 (co, not_6_out);
  or or_1 (or_1_out, co, ci);
  nand nand_2 (nand_2_out, or_1_out, nand_3_out);
  nand nand_3 (nand_3_out, ci, co);
  not not_8 (xi, co);

  // Notes on the sheet:
  //   tri-state
  //   __
  //   bl
  //   to_idu1
  //   from carry lookahead
  //   ck=0: Save result to Slave FF
  //   Slave
  //   ck2 = 0: Load Input to Master FF
  //   Master
  //   in1
  //   out
  //   in2
  //   xnor
  //   to reg array
  //   to carry lookahead
  //   to right side xor
endmodule

module transp_latch (
  input  in_1,
  output out_2
);

  D_Flip_Flop #(.trigger("high")) d_ff_1 (.D(in_1), .clk(1'b1), .Q(out_2));  // open: Qn, preset, reset
endmodule
