// Logisim project SEGA_VDP_315-5313.circ as structural Verilog
module D_Latch (
  input  in_1,
  input  in_2,
  output out_3,
  output out_4
);

  D_Flip_Flop #(.trigger("high")) d_ff_1 (.clk(in_1), .D(in_2), .Q(out_3), .Qn(out_4));  // open: preset, en, reset
endmodule

module RGB_DECODER (
  input  in_1,
  input  in_2,
  input  in_3,
  input  in_4,
  input  in_5,
  input  in_6,
  input  in_7,
  input  in_8,
  input  in_9,
  input  in_10,
  input  in_11,
  input  in_12,
  input  in_13,
  input  in_14,
  output out_15,
  output out_16,
  output out_17,
  output out_18,
  output out_19,
  output out_20,
  output out_21,
  output out_22,
  output out_23,
  output out_24,
  output out_25,
  output out_26,
  output out_27,
  output out_28,
  output out_29,
  output out_30,
  output out_31,
  output out_32,
  output out_33,
  output out_34,
  output out_35,
  output out_36,
  output out_37,
  output out_38,
  output out_39,
  output out_40,
  output out_41,
  output out_42,
  output out_43,
  output out_44,
  output out_45,
  output out_46,
  output out_47,
  output out_48,
  output out_49,
  output out_50,
  output out_51,
  output out_52,
  output out_53,
  output out_54,
  output out_55,
  output out_56,
  output out_57,
  output out_58,
  output out_59,
  output out_60,
  output out_61,
  output out_62,
  output out_63,
  output out_64,
  output out_65
);

  wire _54_out, _72_out, _91_out, _100_out, _101_out, and_1_out, and_2_out, and_3_out, and_4_out, and_5_out,
       and_6_out, and_7_out, and_8_out, and_9_out, and_10_out, and_11_out, and_12_out, and_13_out,
       and_14_out, and_15_out, and_16_out, and_17_out, and_18_out, and_19_out, and_20_out, and_21_out,
       and_22_out, and_23_out, and_24_out, and_25_out, and_26_out, and_27_out, and_28_out, and_29_out,
       and_30_out, and_31_out, and_32_out, and_33_out, and_34_out, and_35_out, and_36_out, and_37_out,
       and_38_out, and_39_out, and_40_out, and_41_out, and_42_out, and_43_out, and_44_out, and_45_out,
       and_46_out, and_47_out, and_48_out, and_49_out, and_50_out, and_51_out, and_52_out, and_53_out,
       and_54_out, and_55_out, and_56_out, and_57_out, and_58_out, and_59_out, and_60_out, and_61_out,
       and_62_out, and_63_out, and_64_out, and_65_out, and_66_out, and_67_out, and_68_out, and_69_out,
       and_70_out, and_71_out, and_72_out, and_73_out, and_74_out, and_75_out, and_76_out, and_77_out,
       and_78_out, buffer_1_out, d_latch_1_out_4, d_latch_2_out_4, d_latch_3_out_4, d_latch_4_out_4,
       d_latch_5_out_4, d_latch_6_out_4, d_latch_7_out_4, d_latch_8_out_4, d_latch_9_out_4, d_latch_10_out_4,
       d_latch_11_out_4, d_latch_12_out_4, d_latch_13_out_4, decoder_1_out0, decoder_1_out1, decoder_1_out2,
       decoder_1_out3, decoder_1_out4, decoder_1_out5, decoder_1_out6, decoder_1_out7, decoder_2_out0,
       decoder_2_out1, decoder_2_out2, decoder_2_out3, decoder_2_out4, decoder_2_out5, decoder_2_out6,
       decoder_2_out7, decoder_3_out0, decoder_3_out1, decoder_3_out2, decoder_3_out3, decoder_3_out4,
       decoder_3_out5, decoder_3_out6, decoder_3_out7, not_1_out;
  wire [2:0] d_latch_14_out_4, d_latch_17_out_4, d_latch_20_out_4;

  buf buffer_1 (buffer_1_out, in_3);
  D_Latch d_latch_1 (.in_1(in_2), .in_2(in_4), .out_4(d_latch_1_out_4));  // open: out_3
  D_Latch d_latch_2 (.in_1(in_2), .in_2(in_5), .out_4(d_latch_2_out_4));  // open: out_3
  D_Latch d_latch_3 (.in_1(in_2), .in_2(in_6), .out_4(d_latch_3_out_4));  // open: out_3
  D_Latch d_latch_4 (.in_1(in_2), .in_2(in_7), .out_4(d_latch_4_out_4));  // open: out_3
  D_Latch d_latch_5 (.in_1(in_2), .in_2(in_8), .out_4(d_latch_5_out_4));  // open: out_3
  D_Latch d_latch_6 (.in_1(in_2), .in_2(in_9), .out_4(d_latch_6_out_4));  // open: out_3
  D_Latch d_latch_7 (.in_1(in_2), .in_2(in_10), .out_4(d_latch_7_out_4));  // open: out_3
  D_Latch d_latch_8 (.in_1(in_2), .in_2(in_11), .out_4(d_latch_8_out_4));  // open: out_3
  D_Latch d_latch_9 (.in_1(in_2), .in_2(in_12), .out_4(d_latch_9_out_4));  // open: out_3
  D_Latch d_latch_10 (.in_1(in_2), .in_2(in_13), .out_4(d_latch_10_out_4));  // open: out_3
  D_Latch d_latch_11 (.in_1(in_2), .in_2(in_14), .out_4(d_latch_11_out_4));  // open: out_3
  D_Latch d_latch_12 (.in_1(in_1), .in_2(d_latch_1_out_4), .out_4(d_latch_12_out_4));  // open: out_3
  D_Latch d_latch_13 (.in_1(in_1), .in_2(d_latch_2_out_4), .out_4(d_latch_13_out_4));  // open: out_3
  D_Latch d_latch_14 (.in_1(in_1), .in_2(d_latch_3_out_4), .out_4(d_latch_14_out_4[0]));  // open: out_3
  D_Latch d_latch_15 (.in_1(in_1), .in_2(d_latch_4_out_4), .out_4(d_latch_14_out_4[1]));  // open: out_3
  D_Latch d_latch_16 (.in_1(in_1), .in_2(d_latch_5_out_4), .out_4(d_latch_14_out_4[2]));  // open: out_3
  D_Latch d_latch_17 (.in_1(in_1), .in_2(d_latch_6_out_4), .out_4(d_latch_17_out_4[0]));  // open: out_3
  D_Latch d_latch_18 (.in_1(in_1), .in_2(d_latch_7_out_4), .out_4(d_latch_17_out_4[1]));  // open: out_3
  D_Latch d_latch_19 (.in_1(in_1), .in_2(d_latch_8_out_4), .out_4(d_latch_17_out_4[2]));  // open: out_3
  D_Latch d_latch_20 (.in_1(in_1), .in_2(d_latch_9_out_4), .out_4(d_latch_20_out_4[0]));  // open: out_3
  D_Latch d_latch_21 (.in_1(in_1), .in_2(d_latch_10_out_4), .out_4(d_latch_20_out_4[1]));  // open: out_3
  D_Latch d_latch_22 (.in_1(in_1), .in_2(d_latch_11_out_4), .out_4(d_latch_20_out_4[2]));  // open: out_3
  not not_1 (not_1_out, d_latch_13_out_4);
  Decoder #(.select(3), .disabled(0), .enable("false")) decoder_1 (
    .out0(decoder_1_out0), .out1(decoder_1_out1), .out2(decoder_1_out2), .out3(decoder_1_out3),
    .out4(decoder_1_out4), .out5(decoder_1_out5), .out6(decoder_1_out6), .out7(decoder_1_out7),
    .sel(d_latch_20_out_4));
  nand _101 (_101_out, d_latch_12_out_4, not_1_out);
  nor _100 (_100_out, buffer_1_out, d_latch_12_out_4, d_latch_13_out_4);
  and and_1 (and_1_out, _100_out, decoder_1_out6);
  and and_2 (and_2_out, decoder_1_out5, d_latch_13_out_4);
  and and_3 (and_3_out, _100_out, decoder_1_out4);
  and and_4 (and_4_out, decoder_1_out1, d_latch_13_out_4);
  and and_5 (and_5_out, d_latch_13_out_4, decoder_1_out0);
  and and_6 (and_6_out, decoder_1_out7, _101_out);
  and _49 (out_24, d_latch_13_out_4, decoder_1_out4);
  and _50 (out_27, d_latch_13_out_4, decoder_1_out6);
  and _51 (out_30, d_latch_13_out_4, decoder_1_out2);
  and and_7 (and_7_out, buffer_1_out, decoder_1_out5);
  and and_8 (and_8_out, decoder_1_out4, buffer_1_out);
  and and_9 (and_9_out, _100_out, decoder_1_out5);
  and and_10 (and_10_out, decoder_1_out3, d_latch_13_out_4);
  and and_11 (and_11_out, _100_out, decoder_1_out1);
  and and_12 (and_12_out, decoder_1_out2, _101_out);
  and and_13 (and_13_out, _100_out, decoder_1_out3);
  and and_14 (and_14_out, decoder_1_out6, _101_out);
  and _57 (out_47, decoder_1_out5, _101_out);
  and _58 (out_50, _101_out, decoder_1_out3);
  and _59 (out_52, decoder_1_out1, _101_out);
  and and_15 (and_15_out, buffer_1_out, decoder_1_out3);
  and and_16 (and_16_out, decoder_1_out2, buffer_1_out);
  and and_17 (and_17_out, _100_out, decoder_1_out2);
  and and_18 (and_18_out, decoder_1_out4, _101_out);
  and and_19 (and_19_out, _100_out, decoder_1_out0);
  and and_20 (and_20_out, decoder_1_out0, _101_out);
  and and_21 (and_21_out, buffer_1_out, decoder_1_out1);
  and and_22 (and_22_out, decoder_1_out0, buffer_1_out);
  and and_23 (and_23_out, _100_out, decoder_1_out7);
  and and_24 (and_24_out, decoder_1_out7, d_latch_13_out_4);
  and and_25 (and_25_out, buffer_1_out, decoder_1_out7);
  and and_26 (and_26_out, decoder_1_out6, buffer_1_out);
  or or_1 (out_15, and_1_out, and_2_out);
  or or_2 (out_18, and_3_out, and_4_out);
  or or_3 (out_21, and_5_out, and_6_out);
  or or_4 (out_33, and_7_out, and_8_out);
  or or_5 (out_36, and_9_out, and_10_out);
  or or_6 (out_41, and_11_out, and_12_out);
  or or_7 (out_44, and_13_out, and_14_out);
  or or_8 (out_56, and_15_out, and_16_out);
  or or_9 (out_59, and_17_out, and_18_out);
  or _62 (out_62, and_19_out, and_20_out, and_21_out, and_22_out);
  or _54 (_54_out, and_23_out, and_24_out, and_25_out, and_26_out);
  not not_2 (out_65, _54_out);
  Decoder #(.select(3), .disabled(0), .enable("false")) decoder_2 (
    .out0(decoder_2_out0), .out1(decoder_2_out1), .out2(decoder_2_out2), .out3(decoder_2_out3),
    .out4(decoder_2_out4), .out5(decoder_2_out5), .out6(decoder_2_out6), .out7(decoder_2_out7),
    .sel(d_latch_17_out_4));
  and and_27 (and_27_out, _100_out, decoder_2_out6);
  and and_28 (and_28_out, decoder_2_out5, d_latch_13_out_4);
  and and_29 (and_29_out, _100_out, decoder_2_out4);
  and and_30 (and_30_out, decoder_2_out1, d_latch_13_out_4);
  and and_31 (and_31_out, d_latch_13_out_4, decoder_2_out0);
  and and_32 (and_32_out, decoder_2_out7, _101_out);
  and _67 (out_25, d_latch_13_out_4, decoder_2_out4);
  and _68 (out_28, d_latch_13_out_4, decoder_2_out6);
  and _69 (out_31, d_latch_13_out_4, decoder_2_out2);
  and and_33 (and_33_out, buffer_1_out, decoder_2_out5);
  and and_34 (and_34_out, decoder_2_out4, buffer_1_out);
  and and_35 (and_35_out, _100_out, decoder_2_out5);
  and and_36 (and_36_out, decoder_2_out3, d_latch_13_out_4);
  and and_37 (and_37_out, _100_out, decoder_2_out1);
  and and_38 (and_38_out, decoder_2_out2, _101_out);
  and and_39 (and_39_out, _100_out, decoder_2_out3);
  and and_40 (and_40_out, decoder_2_out6, _101_out);
  and _75 (out_48, decoder_2_out5, _101_out);
  and _76 (out_51, _101_out, decoder_2_out3);
  and _77 (out_53, decoder_2_out1, _101_out);
  and and_41 (and_41_out, buffer_1_out, decoder_2_out3);
  and and_42 (and_42_out, decoder_2_out2, buffer_1_out);
  and and_43 (and_43_out, _100_out, decoder_2_out2);
  and and_44 (and_44_out, decoder_2_out4, _101_out);
  and and_45 (and_45_out, _100_out, decoder_2_out0);
  and and_46 (and_46_out, decoder_2_out0, _101_out);
  and and_47 (and_47_out, buffer_1_out, decoder_2_out1);
  and and_48 (and_48_out, decoder_2_out0, buffer_1_out);
  and and_49 (and_49_out, _100_out, decoder_2_out7);
  and and_50 (and_50_out, decoder_2_out7, d_latch_13_out_4);
  and and_51 (and_51_out, buffer_1_out, decoder_2_out7);
  and and_52 (and_52_out, decoder_2_out6, buffer_1_out);
  or or_10 (out_16, and_27_out, and_28_out);
  or or_11 (out_19, and_29_out, and_30_out);
  or or_12 (out_22, and_31_out, and_32_out);
  or or_13 (out_34, and_33_out, and_34_out);
  or or_14 (out_37, and_35_out, and_36_out);
  or or_15 (out_42, and_37_out, and_38_out);
  or or_16 (out_45, and_39_out, and_40_out);
  or or_17 (out_57, and_41_out, and_42_out);
  or or_18 (out_60, and_43_out, and_44_out);
  or _80 (out_63, and_45_out, and_46_out, and_47_out, and_48_out);
  or _72 (_72_out, and_49_out, and_50_out, and_51_out, and_52_out);
  not not_3 (out_39, _72_out);
  Decoder #(.select(3), .disabled(0), .enable("false")) decoder_3 (
    .out0(decoder_3_out0), .out1(decoder_3_out1), .out2(decoder_3_out2), .out3(decoder_3_out3),
    .out4(decoder_3_out4), .out5(decoder_3_out5), .out6(decoder_3_out6), .out7(decoder_3_out7),
    .sel(d_latch_14_out_4));
  and and_53 (and_53_out, _100_out, decoder_3_out6);
  and and_54 (and_54_out, decoder_3_out5, d_latch_13_out_4);
  and and_55 (and_55_out, _100_out, decoder_3_out4);
  and and_56 (and_56_out, decoder_3_out1, d_latch_13_out_4);
  and and_57 (and_57_out, d_latch_13_out_4, decoder_3_out0);
  and and_58 (and_58_out, decoder_3_out7, _101_out);
  and _86 (out_26, d_latch_13_out_4, decoder_3_out4);
  and _87 (out_29, d_latch_13_out_4, decoder_3_out6);
  and _88 (out_32, d_latch_13_out_4, decoder_3_out2);
  and and_59 (and_59_out, buffer_1_out, decoder_3_out5);
  and and_60 (and_60_out, decoder_3_out4, buffer_1_out);
  and and_61 (and_61_out, _100_out, decoder_3_out5);
  and and_62 (and_62_out, decoder_3_out3, d_latch_13_out_4);
  and and_63 (and_63_out, _100_out, decoder_3_out1);
  and and_64 (and_64_out, decoder_3_out2, _101_out);
  and and_65 (and_65_out, buffer_1_out, decoder_3_out3);
  and and_66 (and_66_out, decoder_3_out2, buffer_1_out);
  and and_67 (and_67_out, _100_out, decoder_3_out3);
  and and_68 (and_68_out, decoder_3_out6, _101_out);
  and _95 (out_54, decoder_3_out5, _101_out);
  and _96 (out_55, _101_out, decoder_3_out3);
  and _97 (out_58, decoder_3_out1, _101_out);
  and and_69 (and_69_out, _100_out, decoder_3_out2);
  and and_70 (and_70_out, decoder_3_out4, _101_out);
  and and_71 (and_71_out, _100_out, decoder_3_out0);
  and and_72 (and_72_out, decoder_3_out0, _101_out);
  and and_73 (and_73_out, buffer_1_out, decoder_3_out1);
  and and_74 (and_74_out, decoder_3_out0, buffer_1_out);
  and and_75 (and_75_out, _100_out, decoder_3_out7);
  and and_76 (and_76_out, decoder_3_out7, d_latch_13_out_4);
  and and_77 (and_77_out, buffer_1_out, decoder_3_out7);
  and and_78 (and_78_out, decoder_3_out6, buffer_1_out);
  or or_19 (out_17, and_53_out, and_54_out);
  or or_20 (out_20, and_55_out, and_56_out);
  or or_21 (out_23, and_57_out, and_58_out);
  or or_22 (out_35, and_59_out, and_60_out);
  or or_23 (out_38, and_61_out, and_62_out);
  or or_24 (out_43, and_63_out, and_64_out);
  or or_25 (out_46, and_65_out, and_66_out);
  or or_26 (out_49, and_67_out, and_68_out);
  or or_27 (out_61, and_69_out, and_70_out);
  or _99 (out_64, and_71_out, and_72_out, and_73_out, and_74_out);
  not not_4 (out_40, _91_out);
  or _91 (_91_out, and_75_out, and_76_out, and_77_out, and_78_out);

  // Notes on the sheet:
  //   44
  //   45
  //   39
  //   41
  //   43
  //   24
  //   26
  //   28
  //   10
  //   12
  //   14
  //   1 - 9, 11,13
  //   102
  //   46
  //   47
  //   48
  //   52
  //   53
  //   55
  //   56
  //   60
  //   61
  //   62
  //   54
  //   63
  //   15 - 23,25,27
  //   64
  //   65
  //   66
  //   70
  //   71
  //   73
  //   74
  //   78
  //   79
  //   80
  //   72
  //   81
  //   3 - 38, 40,42
  //   83
  //   84
  //   85
  //   89
  //   90
  //   92
  //   93
  //   94
  //   98
  //   99
  //   91
  //   82
endmodule
