// Logisim project CMOS_CELLS_TA.circ as structural Verilog
module DFF_POSEDGE (
  input  EN,
  input  D,
  output Q,
  output nQ
);

  wire d_ff_1_q, d_ff_1_qn, multiplexer_1_out, multiplexer_2_out, not_1_out, not_2_out, not_3_out, not_4_out,
       not_5_out, not_7_out;

  not not_1 (not_1_out, not_2_out);
  not not_2 (not_2_out, D);
  not not_3 (not_3_out, not_4_out);
  Multiplexer #(.disabled(0), .enable("false")) multiplexer_1 (
    .in0(not_1_out), .in1(not_3_out), .out(multiplexer_1_out), .sel(EN));
  not not_4 (not_4_out, multiplexer_1_out);
  not not_5 (not_5_out, not_7_out);
  Multiplexer #(.disabled(0), .enable("false")) multiplexer_2 (
    .in0(not_5_out), .in1(not_4_out), .out(multiplexer_2_out), .sel(EN));
  not not_6 (Q, multiplexer_2_out);
  not not_7 (not_7_out, multiplexer_2_out);
  not not_8 (nQ, not_7_out);
  D_Flip_Flop d_ff_1 (.clk(EN), .D(D), .Q(d_ff_1_q), .Qn(d_ff_1_qn));  // open: preset, en, reset

  // Notes on the sheet:
  //   DFF POSEDGE
endmodule

module CNT_BIT (
  input  nRES,
  input  CLK,
  input  LOAD,
  input  VAL,
  input  C_IN,
  output Q,
  output nQ,
  output C_OUT
);

  wire multiplexer_1_out, multiplexer_2_out, multiplexer_3_out, multiplexer_4_out, nand_1_out, nand_2_out,
       nand_3_out, nor_1_out, not_1_out, not_2_out, not_3_out, not_4_out, not_5_out, not_7_out;

  not not_1 (not_1_out, VAL);
  nand nand_1 (nand_1_out, not_7_out, C_IN);
  Multiplexer #(.disabled(0), .enable("false")) multiplexer_1 (
    .in0(1'b1), .in1(nor_1_out), .out(multiplexer_1_out), .sel(nand_1_out));
  nor nor_1 (nor_1_out, C_IN, not_7_out);
  Multiplexer #(.disabled(0), .enable("false")) multiplexer_2 (
    .in0(multiplexer_1_out), .in1(not_1_out), .out(multiplexer_2_out), .sel(LOAD));
  not not_2 (not_2_out, nand_2_out);
  not not_3 (not_3_out, multiplexer_2_out);
  Multiplexer #(.disabled(0), .enable("false")) multiplexer_3 (
    .in0(not_2_out), .in1(not_3_out), .out(multiplexer_3_out), .sel(CLK));
  nand nand_2 (nand_2_out, nRES, multiplexer_3_out);
  not not_4 (not_4_out, nand_2_out);
  Multiplexer #(.disabled(0), .enable("false")) multiplexer_4 (
    .in0(not_4_out), .in1(not_5_out), .out(multiplexer_4_out), .sel(CLK));
  not not_5 (not_5_out, nand_3_out);
  nand nand_3 (nand_3_out, nRES, multiplexer_4_out);
  not not_6 (Q, nand_3_out);
  not not_7 (not_7_out, nand_3_out);
  not not_8 (nQ, not_7_out);
  not not_9 (C_OUT, nand_1_out);

  // Notes on the sheet:
  //   COUNTER BIT
endmodule

module DFF_POSEDGE__RES (
  input  nRES,
  input  EN,
  input  D,
  output Q,
  output nQ
);

  wire d_ff_1_q, d_ff_1_qn, multiplexer_1_out, multiplexer_2_out, nand_1_out, nand_2_out, not_1_out,
       not_2_out, not_3_out, not_4_out, not_5_out, not_6_out, not_9_out;

  not not_1 (not_1_out, D);
  not not_2 (not_2_out, nand_1_out);
  not not_3 (not_3_out, not_1_out);
  Multiplexer #(.disabled(0), .enable("false")) multiplexer_1 (
    .in0(not_3_out), .in1(not_2_out), .out(multiplexer_1_out), .sel(EN));
  nand nand_1 (nand_1_out, nRES, multiplexer_1_out);
  not not_4 (not_4_out, nRES);
  not not_5 (not_5_out, nand_2_out);
  not not_6 (not_6_out, nand_1_out);
  D_Flip_Flop d_ff_1 (.clk(EN), .D(D), .Q(d_ff_1_q), .Qn(d_ff_1_qn), .reset(not_4_out));  // open: preset, en
  Multiplexer #(.disabled(0), .enable("false")) multiplexer_2 (
    .in0(not_5_out), .in1(not_6_out), .out(multiplexer_2_out), .sel(EN));
  nand nand_2 (nand_2_out, nRES, multiplexer_2_out);
  not not_7 (Q, nand_2_out);
  not not_8 (nQ, not_9_out);
  not not_9 (not_9_out, nand_2_out);

  // Notes on the sheet:
  //   DFF POSEDGE #RES
endmodule

module NAND (
  input  A,
  input  B,
  output Q
);

  wire nand_1_out, transistor_3_out;

  Transistor transistor_1 (.in(1'b1), .out(Q), .gate(A));
  Transistor #(.\type ("n")) transistor_2 (.in(transistor_3_out), .out(Q), .gate(A));
  Transistor #(.\type ("n")) transistor_3 (.in(1'b0), .out(transistor_3_out), .gate(B));
  Transistor transistor_4 (.in(1'b1), .out(Q), .gate(B));
  nand nand_1 (nand_1_out, A, B);

  // Notes on the sheet:
  //   NAND
endmodule

module _3NAND (
  input  A,
  input  B,
  input  C,
  output Q
);

  wire nand_1_out, transistor_3_out, transistor_4_out;

  Transistor transistor_1 (.in(1'b1), .out(Q), .gate(A));
  Transistor #(.\type ("n")) transistor_2 (.in(transistor_3_out), .out(Q), .gate(A));
  Transistor #(.\type ("n")) transistor_3 (.in(transistor_4_out), .out(transistor_3_out), .gate(B));
  Transistor #(.\type ("n")) transistor_4 (.in(1'b0), .out(transistor_4_out), .gate(C));
  Transistor transistor_5 (.in(1'b1), .out(Q), .gate(B));
  nand nand_1 (nand_1_out, C, A, B);
  Transistor transistor_6 (.in(1'b1), .out(Q), .gate(C));

  // Notes on the sheet:
  //   3NAND
endmodule

module dffs_latch (
  input  clk,
  input  d,
  input  nset,
  output nq,
  output q
);

  wire multiplexer_1_out, multiplexer_2_out, nand_1_out, nand_2_out, not_1_out, not_2_out, not_3_out,
       not_4_out, not_5_out, not_6_out, not_8_out;

  not not_1 (not_1_out, d);
  not not_2 (not_2_out, not_1_out);
  not not_3 (not_3_out, nand_1_out);
  not not_4 (not_4_out, not_2_out);
  Multiplexer #(.enable("false")) multiplexer_1 (.in0(not_3_out), .in1(not_4_out), .out(multiplexer_1_out), .sel(clk));
  nand nand_1 (nand_1_out, multiplexer_1_out, nset);
  not not_5 (not_5_out, nand_2_out);
  not not_6 (not_6_out, nand_1_out);
  Multiplexer #(.enable("false")) multiplexer_2 (.in0(not_5_out), .in1(not_6_out), .out(multiplexer_2_out), .sel(clk));
  nand nand_2 (nand_2_out, multiplexer_2_out, nset);
  not not_7 (nq, nand_2_out);
  not not_8 (not_8_out, nand_2_out);
  not not_9 (q, not_8_out);

  // Notes on the sheet:
  //   clk = enable
  //   Master
  //   from negedge DFF
  //   Slave
  //   from posedge DFF
  //   DFF active-low async Set, fuckedge
  //   Works by level (effectively as latch)
endmodule

module jksneg (
  input  clk,
  input  J,
  input  K,
  input  nset,
  output nq,
  output q
);

  wire and_1_out, multiplexer_1_out, multiplexer_2_out, nand_1_out, nand_2_out, nor_1_out, nor_2_out,
       not_1_out, not_2_out, not_3_out, not_5_out;

  and and_1 (and_1_out, J, not_5_out);
  nor nor_1 (nor_1_out, K, not_5_out);
  nor nor_2 (nor_2_out, and_1_out, nor_1_out);
  not not_1 (not_1_out, nand_1_out);
  Multiplexer #(.enable("false")) multiplexer_1 (.in0(not_1_out), .in1(nor_2_out), .out(multiplexer_1_out), .sel(clk));
  nand nand_1 (nand_1_out, multiplexer_1_out, nset);
  not not_2 (not_2_out, nand_1_out);
  not not_3 (not_3_out, nand_2_out);
  Multiplexer #(.enable("false")) multiplexer_2 (.in0(not_2_out), .in1(not_3_out), .out(multiplexer_2_out), .sel(clk));
  nand nand_2 (nand_2_out, multiplexer_2_out, nset);
  not not_4 (nq, nand_2_out);
  not not_5 (not_5_out, nand_2_out);
  not not_6 (q, not_5_out);

  // Notes on the sheet:
  //   Master
  //   Slave
  //   JK with active-low async Set, negedge
endmodule
